// Logisim project Sokoban.circ as structural Verilog: 21 circuits, main circuit ◇单周期RISC-V
module \单周期RISC_V  (
  input  IR1,
  input  IR2,
  input  IR3,
  output RegWrite,
  output MemWrite,
  output [31:0] PC,
  output [31:0] IR,
  output [31:0] RDin,
  output [31:0] MDin,
  output [31:0] LedData
);

  wire AluSrcB, and_1_out, and_2_out, and_3_out, and_4_out, and_5_out, B, Beq, BLTU, Bne, CLK, clock_1_out,
       comparator_1_eq, comparator_2_eq, comparator_3_eq, comparator_4_eq, comparator_4_lt, CSRRCI, CSRRSI,
       d_ff_1_q, ecall, equal, Go, halt, IR1_t, IR2_t, IR3_t, IRA, IRB, IRC, J, JAL, JALR, less, LUI,
       MemToReg, nand_1_out, not_1_out, not_2_out, not_3_out, not_4_out, not_5_out, not_6_out, not_7_out,
       RST, S_type, SB, URET, W1, W2, W3;
  wire [3:0] AluOP, multiplexer_11_out, Select;
  wire [4:0] multiplexer_1_out, multiplexer_2_out, multiplexer_12_out;
  wire [11:0] multiplexer_3_out, shifter_2_out;
  wire [12:0] CNT_num;
  wire [15:0] \总周期数 ;
  wire [19:0] shifter_3_out;
  wire [31:0] adder_2_out, adder_3_out, bit_extender_1_out, bit_extender_2_out, bit_extender_3_out,
       bit_extender_4_out, mips_ram_1_p8, multiplexer_5_out, multiplexer_6_out, multiplexer_7_out,
       multiplexer_8_out, multiplexer_9_out, PC_4, PCin, R1, R2, Result, shifter_1_out, shifter_4_out;

  Button \u_继续运行  (.out(Go));
  Button _1 (.out(IRA));
  Button _2 (.out(IRB));
  Button _3 (.out(IRC));
  LED #(.active("true")) led_1 (.in(W1));
  LED #(.active("true")) led_2 (.in(W2));
  LED #(.active("true")) led_3 (.in(W3));
  Comparator #(.width(32), .mode("twosComplement")) comparator_1 (
    .a(R2), .b(32'h22), .eq(comparator_1_eq));  // open: gt, lt
  Comparator #(.width(32), .mode("twosComplement")) comparator_2 (
    .a(R2), .b(32'h22), .eq(comparator_2_eq));  // open: gt, lt
  Button button_1 (.out(RST));
  Hex_Digit_Display hex_digit_display_1 (.value(LedData[31:28]));  // open: dp
  and and_1 (and_1_out, ecall, comparator_1_eq);
  and and_2 (and_2_out, ecall, not_1_out);
  not not_1 (not_1_out, comparator_2_eq);
  not not_2 (not_2_out, halt);
  Counter #(.width(16), .max('hffff), .ongoal("wrap"), .trigger("rising"), .behavior("new")) counter_1 (
    .count(not_2_out), .Q(\总周期数 ), .clk(CLK), .clr(RST));  // open: load, D, carry, preset, down
  Comparator #(.width(32), .mode("twosComplement")) comparator_3 (
    .a(32'h1), .b(Result), .eq(comparator_3_eq));  // open: gt, lt
  Hex_Digit_Display hex_digit_display_2 (.value(LedData[23:20]));  // open: dp
  Hex_Digit_Display hex_digit_display_3 (.value(LedData[27:24]));  // open: dp
  Register #(.width(32), .trigger("rising"), .Select("low")) register_1 (
    .D(R1), .en(and_1_out), .Q(LedData), .clk(CLK), .clr(RST));
  Register #(.width(1), .trigger("rising"), .Select("low")) register_2 (
    .D(and_2_out), .Q(halt), .clk(not_3_out), .clr(Go));  // open: en
  not not_3 (not_3_out, CLK);
  Register #(.width(32), .trigger("rising"), .Select("low")) u_PC (
    .D(PCin), .en(not_4_out), .Q(PC), .clk(CLK), .clr(RST));
  not not_4 (not_4_out, halt);
  and and_3 (and_3_out, BLTU, comparator_3_eq);
  Hex_Digit_Display hex_digit_display_4 (.value(LedData[15:12]));  // open: dp
  Hex_Digit_Display hex_digit_display_5 (.value(LedData[19:16]));  // open: dp
  not not_5 (not_5_out, equal);
  Hex_Digit_Display hex_digit_display_6 (.value(LedData[7:4]));  // open: dp
  Hex_Digit_Display hex_digit_display_7 (.value(LedData[11:8]));  // open: dp
  // Probe on \总周期数 
  and and_4 (and_4_out, Beq, equal);
  and and_5 (and_5_out, not_5_out, Bne);
  or or_1 (J, JAL, JALR);
  Hex_Digit_Display hex_digit_display_8 (.value(LedData[3:0]));  // open: dp
  // RiscV_Probe riscv_probe_1: pin names not known; wires that end beside it: IR
  or or_2 (B, and_4_out, and_3_out, and_5_out);
  ROM #(.addrWidth(10), .dataWidth(32), .Select("high")) rom_1 (.addr(PC[11:2]), .data(IR));
  or or_3 (IR1_t, IR1, IRA);
  or or_4 (IR2_t, IR2, IRB);
  \单周期硬布线控制器  \u_单周期硬布线控制器_1  (
    .Funct({IR[30], IR[25], IR[14:12]}), .OP(IR[6:2]), .ALU_OP(AluOP), .MemToReg(MemToReg),
    .MemWrite(MemWrite), .ALU_SRC(AluSrcB), .RegWrite(RegWrite), .ecall(ecall), .S_type(S_type), .Jalr(JALR),
    .Beq(Beq), .JAL(JAL), .Bne(Bne), .in_3(IR[21]), .uret(URET), .SB(SB), .BLTU(BLTU), .CSRRSI(CSRRSI),
    .CSRRCI(CSRRCI), .LUI(LUI));  // open: BLT, BGE, AUIPC
  Multiplexer #(.select(1), .width(5), .disabled("Z"), .enable("false")) multiplexer_1 (
    .in0(IR[19:15]), .in1(5'b01010), .out(multiplexer_1_out), .sel(ecall));
  Multiplexer #(.select(1), .width(5), .disabled("Z"), .enable("false")) multiplexer_2 (
    .in0(IR[24:20]), .in1(5'b10001), .out(multiplexer_2_out), .sel(ecall));
  Multiplexer #(.select(1), .width(12), .disabled("Z"), .enable("false")) multiplexer_3 (
    .in0(IR[31:20]), .in1({IR[31:25], IR[11:7]}), .out(multiplexer_3_out), .sel(S_type));
  assign bit_extender_1_out = {{12{1'b0}}, IR[31:12]};  // Bit_Extender bit_extender_1
  Shifter #(.width(32), .shift("ll")) shifter_1 (.in(bit_extender_1_out), .\dist (5'b01100), .out(shifter_1_out));
  Shifter #(.width(12), .shift("ll")) shifter_2 (
    .in({IR[31], IR[7], IR[30:25], IR[11:8]}), .\dist (4'b0001), .out(shifter_2_out));
  Shifter #(.width(20), .shift("ll")) shifter_3 (
    .in({IR[31], IR[19:12], IR[20], IR[30:21]}), .\dist (5'b00001), .out(shifter_3_out));
  Multiplexer #(.select(1), .width(32), .disabled("Z"), .enable("false")) multiplexer_4 (
    .in0(shifter_1_out), .in1(multiplexer_7_out), .out(RDin), .sel(not_6_out));
  not not_6 (not_6_out, LUI);
  Adder #(.width(32)) adder_1 (.a(PC), .b(32'h4), .out(PC_4));  // open: cin, cout
  assign bit_extender_2_out = {{20{shifter_2_out[11]}}, shifter_2_out};  // Bit_Extender bit_extender_2
  assign bit_extender_3_out = {{12{shifter_3_out[19]}}, shifter_3_out};  // Bit_Extender bit_extender_3
  or or_5 (IR3_t, IR3, IRC);
  Regifile regifile_1 (
    .Din(RDin), .Clk(CLK), .R1(R1), .R2(R2), .WE(RegWrite), .W_num(IR[11:7]), .R1_num(multiplexer_1_out),
    .R2_num(multiplexer_2_out));
  assign bit_extender_4_out = {{20{multiplexer_3_out[11]}}, multiplexer_3_out};  // Bit_Extender bit_extender_4
  Multiplexer #(.select(1), .width(32), .disabled("Z"), .enable("false")) multiplexer_5 (
    .in0(PC_4), .in1(adder_2_out), .out(multiplexer_5_out), .sel(B));
  Adder #(.width(32)) adder_2 (.a(PC), .b(bit_extender_2_out), .out(adder_2_out));  // open: cin, cout
  Adder #(.width(32)) adder_3 (.a(PC), .b(bit_extender_3_out), .out(adder_3_out));  // open: cin, cout
  Multiplexer #(.select(1), .width(32), .disabled("Z"), .enable("false")) multiplexer_6 (
    .in0(R2), .in1(bit_extender_4_out), .out(multiplexer_6_out), .sel(AluSrcB));
  Multiplexer #(.select(1), .width(32), .disabled("Z"), .enable("false")) multiplexer_7 (
    .in0(multiplexer_8_out), .in1(PC_4), .out(multiplexer_7_out), .sel(J));
  ALU alu_1 (
    .X(R1), .Y(multiplexer_6_out), .AluOP(AluOP), .Equal(equal), .Result(Result), .out_6(less));  // open: Result_2, out_4
  Multiplexer #(.select(1), .width(32), .disabled("Z"), .enable("false")) multiplexer_8 (
    .in0(Result), .in1(mips_ram_1_p8), .out(multiplexer_8_out), .sel(MemToReg));
  Multiplexer #(.select(1), .width(32), .disabled("Z"), .enable("false")) multiplexer_9 (
    .in0(multiplexer_5_out), .in1(adder_3_out), .out(multiplexer_9_out), .sel(JAL));
  Multiplexer #(.select(1), .width(32), .disabled("Z"), .enable("false")) multiplexer_10 (
    .in0(multiplexer_9_out), .in1(Result), .out(PCin), .sel(JALR));
  not not_7 (not_7_out, MemWrite);
  Multiplexer #(.select(2), .width(4), .disabled("Z"), .enable("false")) multiplexer_11 (
    .in0(4'b0001), .in1(4'b0010), .in2(4'b0100), .in3(4'b1000), .out(multiplexer_11_out), .sel(Result[1:0]));
  Multiplexer #(.select(2), .width(5), .disabled("Z"), .enable("false")) multiplexer_12 (
    .in0({5{1'b0}}), .in1(5'b01000), .in2(5'b10000), .in3(5'b11000), .out(multiplexer_12_out),
    .sel(Result[1:0]));
  // MIPS_RAM mips_ram_1: pin names not known; wires that end beside it: Result[11:2], MDin, MemWrite, Select, CLK, not_7_out, RST, mips_ram_1_p8
  Multiplexer #(.select(1), .width(4), .disabled("Z"), .enable("false")) multiplexer_13 (
    .in0(4'b1111), .in1(multiplexer_11_out), .out(Select), .sel(SB));
  Multiplexer #(.select(1), .width(32), .disabled("Z"), .enable("false")) multiplexer_14 (
    .in0(R2), .in1(shifter_4_out), .out(MDin), .sel(SB));
  Shifter #(.width(32), .shift("ll")) shifter_4 (.in(R2), .\dist (multiplexer_12_out), .out(shifter_4_out));
  D_Flip_Flop #(.trigger("high"), .Pre_Clr_Positions("LEGACY"), .NegatePresetClear("false"), .enable("true"), .NewFFLayout("false")) d_ff_1 (.Q(d_ff_1_q));  // open: clk, D, Qn, preset, en, reset
  // Probe on 13'hc
  Comparator #(.width(13), .mode("twosComplement")) comparator_4 (
    .a(CNT_num), .b(13'hc), .eq(comparator_4_eq), .lt(comparator_4_lt));  // open: gt
  Clock #(.highDuration(1), .lowDuration(1)) clock_1 (.out(clock_1_out));
  Counter #(.width(13), .max('h1fff), .ongoal("stay"), .trigger("rising"), .behavior("old")) counter_2 (
    .count(comparator_4_lt), .Q(CNT_num), .clk(clock_1_out));  // open: load, D, carry, clr, preset
  nand nand_1 (nand_1_out, d_ff_1_q, comparator_4_eq);
  assign CLK = nand_1_out ? clock_1_out : 1'bz;  // Controlled_Buffer controlled_buffer_1
  Pull_Resistor #(.pull(1)) pull_resistor_1 (.node(CLK));

  // Notes on the sheet:
  //   中断源
  //   中断等待指示
  //   数码管输出应该用寄存器锁存，否则显示数据只能一闪而过
  //   数码管输出
  //   指令探针
  //   指令存储器
  //   指令字
  //   contents of rom_1 (hex, n*v repeats v):
  //   100493 100006f 100493 200913 300993 100006f 100493 200913 300993 100006f 100493 200913 300993
  //   100006f 100493 200913 300993 3ac000ef 100413 100493 1f49493 900533 2200893 73 24d493 48463 fedff06f
  //   900533 2200893 73 100493 249493 900533 2200893 73 48463 fedff06f 100493 1f49493 900533 2200893 73
  //   4034d493 900533 2200893 73 4044d493 900533 2200893 73 4044d493 900533 2200893 73 4044d493 900533
  //   2200893 73 4044d493 900533 2200893 73 4044d493 900533 2200893 73 4044d493 900533 2200893 73 4044d493
  //   900533 2200893 73 100413 1f41993 41f9d993 433 c00913 300b13 140413 f47413 800293 100313 499993
  //   89e9b3 1300533 2200893 73 406282b3 fe0294e3 140413 f00f93 1f47433 1c41413 800293 100313 49d993
  //   89e9b3 1300533 2200893 73 406282b3 fe0294e3 1c45413 406b0b33 b0463 f95ff06f 2b3 fff2c293 829293
  //   ff2e293 500533 2200893 73 fff00413 493 84a023 140413 448493 84a023 140413 448493 84a023 140413
  //   448493 84a023 140413 448493 84a023 140413 448493 84a023 140413 448493 84a023 140413 448493 84a023
  //   140413 448493 84a023 140413 448493 84a023 140413 448493 84a023 140413 448493 84a023 140413 448493
  //   84a023 140413 448493 84a023 140413 448493 84a023 140413 448493 84a023 140413 448493 140413 433
  //   3c00493 42983 4aa03 149a2b3 28663 134a023 1442023 ffc48493 fe9412e3 800533 2200893 73 440413 3c00493
  //   fc9416e3 a00893 73 800e13 fedc04b7 fff00413 1045413 84e4b3 900533 2200893 73 ba984b7 900533 73
  //   76544b7 900533 73 32104b7 900533 73 fffe0e13 fa0e1ee3 a00893 73 fff00293 313 1900413 841413 9700493
  //   940533 2200893 73 5484b3 494b313 fe0306e3 a00893 73 313 2000e13 493 100913 930023 900533 2200893 73
  //   12484b3 130313 fffe0e13 fe0e12e3 800e13 313 32483 900533 2200893 73 430313 fffe0e13 fe0e14e3 a00893
  //   73 ff100493 900533 2200893 73 148493 fe9068e3 900533 2200893 73 a00893 73 413 140413 800533 2200893
  //   73 240413 800533 2200893 73 340413 800533 2200893 73 440413 800533 2200893 73 540413 800533 2200893
  //   73 640413 800533 2200893 73 740413 800533 2200893 73 840413 800533 2200893 2200893 73 8067
  //   JAL
  //   JALR
  //   URET
  //   I型
  //   S型
  //   U型
  //   B型
  //   J型
  //   Beq
  //   Bne
  //   MemToReg
  //   MemWrite
  //   AluOP
  //   AluSrcB
  //   RegWrite
  //   为方便自动评测，需要输出PC，IR，寄存器堆写如数据RDin
  //   RAM写使能MemWrite、RAM写入数据MDin等信号
  //   数据存储器
  //   控制位
  //   暂停节拍，不能为0
  //   戳工具置1进入计数暂停模式，ctrl+k时钟自动运行到对应节拍暂停
  //   ctrl+k关闭时钟连续运行，将控制位置零，进入单步调试模式调试
  //   用这个时钟源需要去掉电路中的其他时钟源
  //   可计数暂停的时钟源
endmodule

// 单周期硬布线控制器
module \单周期硬布线控制器  (
  input  [4:0] OP,
  input  [4:0] Funct,
  input  in_3,
  output [3:0] ALU_OP,
  output uret,
  output MemToReg,
  output ecall,
  output MemWrite,
  output ALU_SRC,
  output RegWrite,
  output S_type,
  output Beq,
  output Bne,
  output Jalr,
  output JAL,
  output SB,
  output BLTU,
  output CSRRSI,
  output CSRRCI,
  output LUI,
  output BLT,
  output BGE,
  output AUIPC
);

  wire \控制信号自动生成_1_ecall ;

  \运算控制器自动生成  \u_运算控制器自动生成_1  (
    .OP2(OP[0]), .OP3(OP[1]), .OP4(OP[2]), .OP5(OP[3]), .OP6(OP[4]), .F12(Funct[0]), .F13(Funct[1]),
    .F14(Funct[2]), .F25(Funct[3]), .F30(Funct[4]), .S0(ALU_OP[0]), .S1(ALU_OP[1]), .S2(ALU_OP[2]),
    .S3(ALU_OP[3]));
  \控制信号自动生成  \u_控制信号自动生成_1  (
    .OP2(OP[0]), .OP3(OP[1]), .MemToReg(MemToReg), .OP4(OP[2]), .OP5(OP[3]), .OP6(OP[4]), .F12(Funct[0]),
    .MemWrite(MemWrite), .F13(Funct[1]), .F14(Funct[2]), .F25(Funct[3]), .F30(Funct[4]), .ALU_SRC(ALU_SRC),
    .RegWrite(RegWrite), .ecall(\控制信号自动生成_1_ecall ), .S_Type(S_type), .BEQ(Beq), .BNE(Bne), .JALR(Jalr),
    .JAL(JAL), .SB(SB), .BLTU(BLTU), .CSRRSI(CSRRSI), .CSRRCI(CSRRCI), .LUI(LUI), .BLT(BLT), .BGE(BGE),
    .AUIPC(AUIPC));
  and and_1 (uret, in_3, \控制信号自动生成_1_ecall );
  and and_2 (ecall, ~in_3, \控制信号自动生成_1_ecall );  // AND_Gate

  // Other names for the same wires on the sheet: IR21 = in_3; OP_CODE[4:0] = OP

  // Notes on the sheet:
  //   运算器控制器，根据指令生成运算器功能选择信号
  //   控制信号生成，产生数据通路需要的其他控制信号
endmodule

// 运算器控制器
module \运算控制器自动生成  (
  input  OP2,
  input  OP3,
  input  OP4,
  input  OP5,
  input  OP6,
  input  F12,
  input  F13,
  input  F14,
  input  F25,
  input  F30,
  output S0,
  output S1,
  output S2,
  output S3
);

  wire and_1_out, and_2_out, and_3_out, and_4_out, and_5_out, and_6_out, and_7_out, and_8_out, and_9_out,
       and_10_out, and_11_out, and_12_out, and_13_out, and_14_out, and_15_out, and_16_out, and_17_out,
       and_18_out, and_19_out, and_20_out, and_21_out, and_22_out, and_23_out, and_24_out, and_25_out,
       and_26_out, and_27_out, and_28_out, and_29_out, and_30_out, and_31_out, and_32_out, and_33_out,
       and_34_out, and_35_out, and_36_out, and_37_out, and_38_out, and_39_out, and_40_out, and_41_out,
       and_42_out, and_43_out, and_44_out, and_45_out, and_46_out, and_47_out, and_48_out, and_49_out,
       and_50_out, and_51_out, and_52_out, and_53_out, and_54_out, not_1_out, not_2_out, not_3_out,
       not_4_out, not_5_out, not_6_out, not_7_out, not_8_out, not_9_out, not_10_out, not_11_out, not_12_out,
       not_13_out, not_14_out, not_15_out, not_16_out, not_17_out, not_18_out, not_19_out, not_20_out,
       not_21_out, not_22_out, not_23_out, not_24_out, not_25_out, not_26_out, not_27_out, not_28_out,
       not_29_out, not_30_out, not_31_out, not_32_out, not_33_out, not_34_out, not_35_out, not_36_out,
       not_37_out, not_38_out, not_39_out, not_40_out, not_41_out, not_42_out, not_43_out, not_44_out,
       not_45_out, not_46_out, not_47_out, not_48_out, not_49_out, not_50_out, not_51_out, not_52_out,
       not_53_out, not_54_out, not_55_out, not_56_out, not_57_out, not_58_out, not_59_out, not_60_out,
       not_61_out, not_62_out, not_63_out, not_64_out, not_65_out, not_66_out, not_67_out, not_68_out,
       not_69_out, not_70_out, not_71_out, not_72_out, not_73_out, not_74_out, not_75_out, not_76_out,
       not_77_out, not_78_out, not_79_out, not_80_out, not_81_out, not_82_out, not_83_out, not_84_out,
       not_85_out, not_86_out, not_87_out, not_88_out, not_89_out, not_90_out, not_91_out, not_92_out,
       not_93_out, not_94_out, not_95_out, not_96_out, not_97_out, not_98_out, not_99_out, not_100_out,
       not_101_out, not_102_out, not_103_out, not_104_out, not_105_out, not_106_out, not_107_out,
       not_108_out, not_109_out, not_110_out, not_111_out, not_112_out, not_113_out, not_114_out,
       not_115_out, not_116_out, not_117_out, not_118_out, not_119_out, not_120_out, not_121_out,
       not_122_out, not_123_out, not_124_out, not_125_out, not_126_out, not_127_out, not_128_out,
       not_129_out, not_130_out, not_131_out, not_132_out, not_133_out, not_134_out, not_135_out,
       not_136_out, not_137_out, not_138_out, not_139_out, not_140_out, not_141_out, not_142_out,
       not_143_out, not_144_out, not_145_out, not_146_out, not_147_out, not_148_out, not_149_out,
       not_150_out, not_151_out, not_152_out, not_153_out, not_154_out, not_155_out, not_156_out,
       not_157_out, not_158_out, not_159_out, not_160_out, not_161_out, not_162_out, not_163_out,
       not_164_out, not_165_out, not_166_out, not_167_out, not_168_out, not_169_out, not_170_out,
       not_171_out, not_172_out, not_173_out, not_174_out, not_175_out, not_176_out, not_177_out,
       not_178_out, not_179_out, not_180_out, not_181_out, not_182_out, not_183_out, not_184_out,
       not_185_out, not_186_out, not_187_out, not_188_out, not_189_out, not_190_out, not_191_out,
       not_192_out, not_193_out, not_194_out, not_195_out, not_196_out, not_197_out, not_198_out,
       not_199_out, not_200_out, not_201_out, not_202_out, not_203_out, not_204_out, not_205_out,
       not_206_out, not_207_out, not_208_out, not_209_out, not_210_out, not_211_out, not_212_out,
       not_213_out, not_214_out, not_215_out, not_216_out, not_217_out, not_218_out, not_219_out,
       not_220_out, not_221_out, not_222_out, not_223_out, not_224_out, not_225_out, not_226_out,
       not_227_out, not_228_out, not_229_out, not_230_out, not_231_out, not_232_out, not_233_out,
       not_234_out, not_235_out, not_236_out, not_237_out, not_238_out, not_239_out, not_240_out,
       not_241_out, not_242_out, not_243_out, not_244_out, not_245_out, not_246_out, not_247_out,
       not_248_out, not_249_out, not_250_out, not_251_out, not_252_out, not_253_out, not_254_out,
       not_255_out, not_256_out, not_257_out, not_258_out, not_259_out, not_260_out, not_261_out,
       not_262_out, not_263_out, not_264_out, not_265_out, not_266_out, not_267_out, not_268_out,
       not_269_out, not_270_out, not_271_out, not_272_out, not_273_out, not_274_out, not_275_out,
       not_276_out, not_277_out, not_278_out, not_279_out, not_280_out, not_281_out, not_282_out,
       not_283_out, not_284_out, not_285_out, not_286_out, not_287_out, not_288_out, not_289_out,
       not_290_out, not_291_out, not_292_out, not_293_out, not_294_out, not_295_out, not_296_out,
       not_297_out, not_298_out, not_299_out, not_300_out;

  not not_1 (not_1_out, F30);
  not not_2 (not_2_out, F25);
  not not_3 (not_3_out, F14);
  not not_4 (not_4_out, F13);
  not not_5 (not_5_out, F12);
  not not_6 (not_6_out, OP6);
  not not_7 (not_7_out, OP3);
  not not_8 (not_8_out, OP2);
  not not_9 (not_9_out, F30);
  not not_10 (not_10_out, F25);
  not not_11 (not_11_out, OP6);
  not not_12 (not_12_out, OP3);
  not not_13 (not_13_out, OP2);
  not not_14 (not_14_out, F30);
  not not_15 (not_15_out, F25);
  not not_16 (not_16_out, F14);
  not not_17 (not_17_out, F12);
  not not_18 (not_18_out, OP6);
  not not_19 (not_19_out, OP3);
  not not_20 (not_20_out, OP2);
  not not_21 (not_21_out, F14);
  not not_22 (not_22_out, F13);
  not not_23 (not_23_out, F12);
  not not_24 (not_24_out, OP6);
  not not_25 (not_25_out, OP5);
  not not_26 (not_26_out, OP3);
  not not_27 (not_27_out, OP2);
  not not_28 (not_28_out, OP6);
  not not_29 (not_29_out, OP5);
  not not_30 (not_30_out, OP3);
  not not_31 (not_31_out, OP2);
  not not_32 (not_32_out, F13);
  not not_33 (not_33_out, F12);
  not not_34 (not_34_out, OP6);
  not not_35 (not_35_out, OP5);
  not not_36 (not_36_out, OP3);
  not not_37 (not_37_out, OP2);
  not not_38 (not_38_out, F14);
  not not_39 (not_39_out, F12);
  not not_40 (not_40_out, OP6);
  not not_41 (not_41_out, OP5);
  not not_42 (not_42_out, OP3);
  not not_43 (not_43_out, OP2);
  not not_44 (not_44_out, F25);
  not not_45 (not_45_out, F13);
  not not_46 (not_46_out, OP6);
  not not_47 (not_47_out, OP5);
  not not_48 (not_48_out, OP3);
  not not_49 (not_49_out, OP2);
  not not_50 (not_50_out, F14);
  not not_51 (not_51_out, F12);
  not not_52 (not_52_out, OP6);
  not not_53 (not_53_out, OP5);
  not not_54 (not_54_out, OP4);
  not not_55 (not_55_out, OP3);
  not not_56 (not_56_out, OP2);
  not not_57 (not_57_out, F14);
  not not_58 (not_58_out, F12);
  not not_59 (not_59_out, OP6);
  not not_60 (not_60_out, OP4);
  not not_61 (not_61_out, OP3);
  not not_62 (not_62_out, OP2);
  not not_63 (not_63_out, F14);
  not not_64 (not_64_out, F13);
  not not_65 (not_65_out, F12);
  not not_66 (not_66_out, OP4);
  not not_67 (not_67_out, OP3);
  not not_68 (not_68_out, F12);
  not not_69 (not_69_out, OP3);
  not not_70 (not_70_out, OP2);
  not not_71 (not_71_out, F14);
  not not_72 (not_72_out, F13);
  not not_73 (not_73_out, F12);
  not not_74 (not_74_out, OP6);
  not not_75 (not_75_out, OP4);
  not not_76 (not_76_out, OP3);
  not not_77 (not_77_out, OP2);
  not not_78 (not_78_out, F13);
  not not_79 (not_79_out, F12);
  not not_80 (not_80_out, OP4);
  not not_81 (not_81_out, OP3);
  not not_82 (not_82_out, OP2);
  not not_83 (not_83_out, F13);
  not not_84 (not_84_out, OP4);
  not not_85 (not_85_out, OP3);
  not not_86 (not_86_out, OP2);
  not not_87 (not_87_out, F30);
  not not_88 (not_88_out, F14);
  not not_89 (not_89_out, F13);
  not not_90 (not_90_out, F12);
  not not_91 (not_91_out, OP6);
  not not_92 (not_92_out, OP3);
  not not_93 (not_93_out, OP2);
  not not_94 (not_94_out, F25);
  not not_95 (not_95_out, F14);
  not not_96 (not_96_out, F13);
  not not_97 (not_97_out, F12);
  not not_98 (not_98_out, OP6);
  not not_99 (not_99_out, OP3);
  not not_100 (not_100_out, OP2);
  not not_101 (not_101_out, F30);
  not not_102 (not_102_out, F25);
  not not_103 (not_103_out, OP6);
  not not_104 (not_104_out, OP3);
  not not_105 (not_105_out, OP2);
  not not_106 (not_106_out, F30);
  not not_107 (not_107_out, F25);
  not not_108 (not_108_out, F14);
  not not_109 (not_109_out, F12);
  not not_110 (not_110_out, OP6);
  not not_111 (not_111_out, OP3);
  not not_112 (not_112_out, OP2);
  not not_113 (not_113_out, OP6);
  not not_114 (not_114_out, OP5);
  not not_115 (not_115_out, OP3);
  not not_116 (not_116_out, OP2);
  not not_117 (not_117_out, F14);
  not not_118 (not_118_out, F12);
  not not_119 (not_119_out, OP6);
  not not_120 (not_120_out, OP5);
  not not_121 (not_121_out, OP3);
  not not_122 (not_122_out, OP2);
  not not_123 (not_123_out, F30);
  not not_124 (not_124_out, F25);
  not not_125 (not_125_out, F13);
  not not_126 (not_126_out, OP6);
  not not_127 (not_127_out, OP5);
  not not_128 (not_128_out, OP3);
  not not_129 (not_129_out, OP2);
  not not_130 (not_130_out, F14);
  not not_131 (not_131_out, F13);
  not not_132 (not_132_out, F12);
  not not_133 (not_133_out, OP4);
  not not_134 (not_134_out, OP3);
  not not_135 (not_135_out, OP2);
  not not_136 (not_136_out, F14);
  not not_137 (not_137_out, F13);
  not not_138 (not_138_out, OP4);
  not not_139 (not_139_out, OP3);
  not not_140 (not_140_out, OP2);
  not not_141 (not_141_out, F12);
  not not_142 (not_142_out, OP3);
  not not_143 (not_143_out, OP2);
  not not_144 (not_144_out, F13);
  not not_145 (not_145_out, F12);
  not not_146 (not_146_out, OP4);
  not not_147 (not_147_out, OP3);
  not not_148 (not_148_out, OP2);
  not not_149 (not_149_out, F13);
  not not_150 (not_150_out, OP4);
  not not_151 (not_151_out, OP3);
  not not_152 (not_152_out, OP2);
  not not_153 (not_153_out, F30);
  not not_154 (not_154_out, F14);
  not not_155 (not_155_out, F13);
  not not_156 (not_156_out, F12);
  not not_157 (not_157_out, OP6);
  not not_158 (not_158_out, OP3);
  not not_159 (not_159_out, OP2);
  not not_160 (not_160_out, F30);
  not not_161 (not_161_out, F25);
  not not_162 (not_162_out, F14);
  not not_163 (not_163_out, F13);
  not not_164 (not_164_out, F12);
  not not_165 (not_165_out, OP6);
  not not_166 (not_166_out, OP3);
  not not_167 (not_167_out, OP2);
  not not_168 (not_168_out, F25);
  not not_169 (not_169_out, F14);
  not not_170 (not_170_out, F13);
  not not_171 (not_171_out, F12);
  not not_172 (not_172_out, OP6);
  not not_173 (not_173_out, OP3);
  not not_174 (not_174_out, OP2);
  not not_175 (not_175_out, F30);
  not not_176 (not_176_out, F25);
  not not_177 (not_177_out, OP6);
  not not_178 (not_178_out, OP3);
  not not_179 (not_179_out, OP2);
  not not_180 (not_180_out, F30);
  not not_181 (not_181_out, F25);
  not not_182 (not_182_out, F14);
  not not_183 (not_183_out, OP6);
  not not_184 (not_184_out, OP3);
  not not_185 (not_185_out, OP2);
  not not_186 (not_186_out, F14);
  not not_187 (not_187_out, F13);
  not not_188 (not_188_out, F12);
  not not_189 (not_189_out, OP6);
  not not_190 (not_190_out, OP5);
  not not_191 (not_191_out, OP3);
  not not_192 (not_192_out, OP2);
  not not_193 (not_193_out, OP6);
  not not_194 (not_194_out, OP5);
  not not_195 (not_195_out, OP3);
  not not_196 (not_196_out, OP2);
  not not_197 (not_197_out, F14);
  not not_198 (not_198_out, F12);
  not not_199 (not_199_out, OP6);
  not not_200 (not_200_out, OP5);
  not not_201 (not_201_out, OP4);
  not not_202 (not_202_out, OP3);
  not not_203 (not_203_out, OP2);
  not not_204 (not_204_out, F14);
  not not_205 (not_205_out, F12);
  not not_206 (not_206_out, OP6);
  not not_207 (not_207_out, OP4);
  not not_208 (not_208_out, OP3);
  not not_209 (not_209_out, OP2);
  not not_210 (not_210_out, F14);
  not not_211 (not_211_out, F13);
  not not_212 (not_212_out, F12);
  not not_213 (not_213_out, OP4);
  not not_214 (not_214_out, OP3);
  not not_215 (not_215_out, OP2);
  not not_216 (not_216_out, F14);
  not not_217 (not_217_out, F13);
  not not_218 (not_218_out, OP4);
  not not_219 (not_219_out, OP3);
  not not_220 (not_220_out, OP2);
  not not_221 (not_221_out, F14);
  not not_222 (not_222_out, F13);
  not not_223 (not_223_out, F12);
  not not_224 (not_224_out, OP4);
  not not_225 (not_225_out, OP3);
  not not_226 (not_226_out, F12);
  not not_227 (not_227_out, OP3);
  not not_228 (not_228_out, OP2);
  not not_229 (not_229_out, F14);
  not not_230 (not_230_out, OP6);
  not not_231 (not_231_out, OP5);
  not not_232 (not_232_out, OP3);
  not not_233 (not_233_out, OP2);
  not not_234 (not_234_out, F14);
  not not_235 (not_235_out, F13);
  not not_236 (not_236_out, F12);
  not not_237 (not_237_out, OP6);
  not not_238 (not_238_out, OP4);
  not not_239 (not_239_out, OP3);
  not not_240 (not_240_out, OP2);
  not not_241 (not_241_out, F12);
  not not_242 (not_242_out, OP4);
  not not_243 (not_243_out, OP3);
  not not_244 (not_244_out, OP2);
  not not_245 (not_245_out, F30);
  not not_246 (not_246_out, F25);
  not not_247 (not_247_out, F12);
  not not_248 (not_248_out, OP6);
  not not_249 (not_249_out, OP3);
  not not_250 (not_250_out, OP2);
  not not_251 (not_251_out, F30);
  not not_252 (not_252_out, F25);
  not not_253 (not_253_out, F14);
  not not_254 (not_254_out, F12);
  not not_255 (not_255_out, OP6);
  not not_256 (not_256_out, OP3);
  not not_257 (not_257_out, OP2);
  not not_258 (not_258_out, F30);
  not not_259 (not_259_out, F25);
  not not_260 (not_260_out, F14);
  not not_261 (not_261_out, OP6);
  not not_262 (not_262_out, OP3);
  not not_263 (not_263_out, OP2);
  not not_264 (not_264_out, F12);
  not not_265 (not_265_out, OP6);
  not not_266 (not_266_out, OP5);
  not not_267 (not_267_out, OP3);
  not not_268 (not_268_out, OP2);
  not not_269 (not_269_out, F13);
  not not_270 (not_270_out, F12);
  not not_271 (not_271_out, OP6);
  not not_272 (not_272_out, OP5);
  not not_273 (not_273_out, OP3);
  not not_274 (not_274_out, OP2);
  not not_275 (not_275_out, F14);
  not not_276 (not_276_out, F12);
  not not_277 (not_277_out, OP6);
  not not_278 (not_278_out, OP5);
  not not_279 (not_279_out, OP3);
  not not_280 (not_280_out, OP2);
  not not_281 (not_281_out, OP3);
  not not_282 (not_282_out, OP2);
  not not_283 (not_283_out, F14);
  not not_284 (not_284_out, OP6);
  not not_285 (not_285_out, OP5);
  not not_286 (not_286_out, OP3);
  not not_287 (not_287_out, OP2);
  not not_288 (not_288_out, F12);
  not not_289 (not_289_out, OP4);
  not not_290 (not_290_out, OP3);
  not not_291 (not_291_out, OP2);
  not not_292 (not_292_out, F13);
  not not_293 (not_293_out, F12);
  not not_294 (not_294_out, OP4);
  not not_295 (not_295_out, OP3);
  not not_296 (not_296_out, OP2);
  not not_297 (not_297_out, F13);
  not not_298 (not_298_out, OP4);
  not not_299 (not_299_out, OP3);
  not not_300 (not_300_out, OP2);
  and and_1 (and_1_out, not_1_out, not_2_out, not_3_out, not_4_out, not_5_out, not_6_out, OP5, OP4, not_7_out, not_8_out);
  and and_2 (and_2_out, not_9_out, not_10_out, F14, F13, F12, not_11_out, OP5, OP4, not_12_out, not_13_out);
  and and_3 (and_3_out, not_14_out, not_15_out, not_16_out, F13, not_17_out, not_18_out, OP5, OP4, not_19_out, not_20_out);
  and and_4 (and_4_out, not_21_out, not_22_out, not_23_out, not_24_out, not_25_out, OP4, not_26_out, not_27_out);
  and and_5 (and_5_out, F14, F13, F12, not_28_out, not_29_out, OP4, not_30_out, not_31_out);
  and and_6 (and_6_out, F14, not_32_out, not_33_out, not_34_out, not_35_out, OP4, not_36_out, not_37_out);
  and and_7 (and_7_out, not_38_out, F13, not_39_out, not_40_out, not_41_out, OP4, not_42_out, not_43_out);
  and and_8 (and_8_out, F30, not_44_out, F14, not_45_out, F12, not_46_out, not_47_out, OP4, not_48_out, not_49_out);
  and and_9 (and_9_out, not_50_out, F13, not_51_out, not_52_out, not_53_out, not_54_out, not_55_out, not_56_out);
  and and_10 (and_10_out, not_57_out, F13, not_58_out, not_59_out, OP5, not_60_out, not_61_out, not_62_out);
  and and_11 (and_11_out, not_63_out, not_64_out, not_65_out, OP6, OP5, not_66_out, not_67_out, OP2);
  and and_12 (and_12_out, F14, F13, not_68_out, OP6, OP5, OP4, not_69_out, not_70_out);
  and and_13 (and_13_out, not_71_out, not_72_out, not_73_out, not_74_out, OP5, not_75_out, not_76_out, not_77_out);
  and and_14 (and_14_out, F14, not_78_out, not_79_out, OP6, OP5, not_80_out, not_81_out, not_82_out);
  and and_15 (and_15_out, F14, not_83_out, F12, OP6, OP5, not_84_out, not_85_out, not_86_out);
  and and_16 (and_16_out, not_87_out, F25, not_88_out, not_89_out, not_90_out, not_91_out, OP5, OP4, not_92_out, not_93_out);
  and and_17 (and_17_out, F30, not_94_out, not_95_out, not_96_out, not_97_out, not_98_out, OP5, OP4, not_99_out, not_100_out);
  and and_18 (and_18_out, not_101_out, not_102_out, F14, F13, F12, not_103_out, OP5, OP4, not_104_out, not_105_out);
  and and_19 (and_19_out, not_106_out, not_107_out, not_108_out, F13, not_109_out, not_110_out, OP5, OP4, not_111_out, not_112_out);
  and and_20 (and_20_out, F14, F13, F12, not_113_out, not_114_out, OP4, not_115_out, not_116_out);
  and and_21 (and_21_out, not_117_out, F13, not_118_out, not_119_out, not_120_out, OP4, not_121_out, not_122_out);
  and and_22 (and_22_out, not_123_out, not_124_out, F14, not_125_out, F12, not_126_out, not_127_out, OP4, not_128_out, not_129_out);
  and and_23 (and_23_out, not_130_out, not_131_out, not_132_out, OP6, OP5, not_133_out, not_134_out, not_135_out);
  and and_24 (and_24_out, not_136_out, not_137_out, F12, OP6, OP5, not_138_out, not_139_out, not_140_out);
  and and_25 (and_25_out, F14, F13, not_141_out, OP6, OP5, OP4, not_142_out, not_143_out);
  and and_26 (and_26_out, F14, not_144_out, not_145_out, OP6, OP5, not_146_out, not_147_out, not_148_out);
  and and_27 (and_27_out, F14, not_149_out, F12, OP6, OP5, not_150_out, not_151_out, not_152_out);
  and and_28 (and_28_out, not_153_out, F25, not_154_out, not_155_out, not_156_out, not_157_out, OP5, OP4, not_158_out, not_159_out);
  and and_29 (and_29_out, not_160_out, not_161_out, not_162_out, not_163_out, not_164_out, not_165_out, OP5, OP4, not_166_out, not_167_out);
  and and_30 (and_30_out, F30, not_168_out, not_169_out, not_170_out, not_171_out, not_172_out, OP5, OP4, not_173_out, not_174_out);
  and and_31 (and_31_out, not_175_out, not_176_out, F14, F13, F12, not_177_out, OP5, OP4, not_178_out, not_179_out);
  and and_32 (and_32_out, not_180_out, not_181_out, not_182_out, F13, F12, not_183_out, OP5, OP4, not_184_out, not_185_out);
  and and_33 (and_33_out, not_186_out, not_187_out, not_188_out, not_189_out, not_190_out, OP4, not_191_out, not_192_out);
  and and_34 (and_34_out, F14, F13, F12, not_193_out, not_194_out, OP4, not_195_out, not_196_out);
  and and_35 (and_35_out, not_197_out, F13, not_198_out, not_199_out, not_200_out, not_201_out, not_202_out, not_203_out);
  and and_36 (and_36_out, not_204_out, F13, not_205_out, not_206_out, OP5, not_207_out, not_208_out, not_209_out);
  and and_37 (and_37_out, not_210_out, not_211_out, not_212_out, OP6, OP5, not_213_out, not_214_out, not_215_out);
  and and_38 (and_38_out, not_216_out, not_217_out, F12, OP6, OP5, not_218_out, not_219_out, not_220_out);
  and and_39 (and_39_out, not_221_out, not_222_out, not_223_out, OP6, OP5, not_224_out, not_225_out, OP2);
  and and_40 (and_40_out, F14, F13, not_226_out, OP6, OP5, OP4, not_227_out, not_228_out);
  and and_41 (and_41_out, not_229_out, F13, F12, not_230_out, not_231_out, OP4, not_232_out, not_233_out);
  and and_42 (and_42_out, not_234_out, not_235_out, not_236_out, not_237_out, OP5, not_238_out, not_239_out, not_240_out);
  and and_43 (and_43_out, F14, F13, not_241_out, OP6, OP5, not_242_out, not_243_out, not_244_out);
  and and_44 (and_44_out, not_245_out, not_246_out, F14, F13, not_247_out, not_248_out, OP5, OP4, not_249_out, not_250_out);
  and and_45 (and_45_out, not_251_out, not_252_out, not_253_out, F13, not_254_out, not_255_out, OP5, OP4, not_256_out, not_257_out);
  and and_46 (and_46_out, not_258_out, not_259_out, not_260_out, F13, F12, not_261_out, OP5, OP4, not_262_out, not_263_out);
  and and_47 (and_47_out, F14, F13, not_264_out, not_265_out, not_266_out, OP4, not_267_out, not_268_out);
  and and_48 (and_48_out, F14, not_269_out, not_270_out, not_271_out, not_272_out, OP4, not_273_out, not_274_out);
  and and_49 (and_49_out, not_275_out, F13, not_276_out, not_277_out, not_278_out, OP4, not_279_out, not_280_out);
  and and_50 (and_50_out, F14, F13, F12, OP6, OP5, OP4, not_281_out, not_282_out);
  and and_51 (and_51_out, not_283_out, F13, F12, not_284_out, not_285_out, OP4, not_286_out, not_287_out);
  and and_52 (and_52_out, F14, F13, not_288_out, OP6, OP5, not_289_out, not_290_out, not_291_out);
  and and_53 (and_53_out, F14, not_292_out, not_293_out, OP6, OP5, not_294_out, not_295_out, not_296_out);
  and and_54 (and_54_out, F14, not_297_out, F12, OP6, OP5, not_298_out, not_299_out, not_300_out);
  or or_1 (S0, and_1_out, and_2_out, and_3_out, and_4_out, and_5_out, and_6_out, and_7_out, and_8_out, and_9_out, and_10_out, and_11_out, and_12_out, and_13_out, and_14_out, and_15_out, and_16_out);
  or or_2 (S1, and_17_out, and_18_out, and_19_out, and_20_out, and_21_out, and_22_out, and_23_out, and_24_out, and_25_out, and_26_out, and_27_out, and_28_out);
  or or_3 (S2, and_29_out, and_30_out, and_31_out, and_32_out, and_33_out, and_34_out, and_35_out, and_36_out, and_37_out, and_38_out, and_39_out, and_40_out, and_41_out, and_42_out, and_43_out);
  or or_4 (S3, and_44_out, and_45_out, and_46_out, and_47_out, and_48_out, and_49_out, and_50_out, and_51_out, and_52_out, and_53_out, and_54_out);
endmodule

// 控制信号生成
module \控制信号自动生成  (
  input  OP2,
  input  OP3,
  input  OP4,
  input  OP5,
  input  OP6,
  input  F12,
  input  F13,
  input  F14,
  input  F25,
  input  F30,
  output MemToReg,
  output MemWrite,
  output ALU_SRC,
  output RegWrite,
  output ecall,
  output S_Type,
  output BEQ,
  output BNE,
  output JALR,
  output JAL,
  output SB,
  output BLTU,
  output CSRRSI,
  output CSRRCI,
  output LUI,
  output BLT,
  output BGE,
  output AUIPC
);

  wire and_3_out, and_4_out, and_5_out, and_6_out, and_7_out, and_8_out, and_9_out, and_10_out, and_11_out,
       and_12_out, and_13_out, and_14_out, and_15_out, and_16_out, and_17_out, and_18_out, and_19_out,
       and_20_out, and_21_out, and_22_out, and_23_out, and_24_out, and_25_out, and_26_out, and_27_out,
       and_28_out, and_29_out, and_30_out, not_1_out, not_2_out, not_3_out, not_4_out, not_5_out, not_6_out,
       not_7_out, not_8_out, not_9_out, not_10_out, not_11_out, not_12_out, not_13_out, not_14_out,
       not_15_out, not_16_out, not_17_out, not_18_out, not_19_out, not_20_out, not_21_out, not_22_out,
       not_23_out, not_24_out, not_25_out, not_26_out, not_27_out, not_28_out, not_29_out, not_30_out,
       not_31_out, not_32_out, not_33_out, not_34_out, not_35_out, not_36_out, not_37_out, not_38_out,
       not_39_out, not_40_out, not_41_out, not_42_out, not_43_out, not_44_out, not_45_out, not_46_out,
       not_47_out, not_48_out, not_49_out, not_50_out, not_51_out, not_52_out, not_53_out, not_54_out,
       not_55_out, not_56_out, not_57_out, not_58_out, not_59_out, not_60_out, not_61_out, not_62_out,
       not_63_out, not_64_out, not_65_out, not_66_out, not_67_out, not_68_out, not_69_out, not_70_out,
       not_71_out, not_72_out, not_73_out, not_74_out, not_75_out, not_76_out, not_77_out, not_78_out,
       not_79_out, not_80_out, not_81_out, not_82_out, not_83_out, not_84_out, not_85_out, not_86_out,
       not_87_out, not_88_out, not_89_out, not_90_out, not_91_out, not_92_out, not_93_out, not_94_out,
       not_95_out, not_96_out, not_97_out, not_98_out, not_99_out, not_100_out, not_101_out, not_102_out,
       not_103_out, not_104_out, not_105_out, not_106_out, not_107_out, not_108_out, not_109_out,
       not_110_out, not_111_out, not_112_out, not_113_out, not_114_out, not_115_out, not_116_out,
       not_117_out, not_118_out, not_119_out, not_120_out, not_121_out, not_122_out, not_123_out,
       not_124_out, not_125_out, not_126_out, not_127_out, not_128_out, not_129_out, not_130_out,
       not_131_out, not_132_out, not_133_out, not_134_out, not_135_out, not_136_out, not_137_out,
       not_138_out, not_139_out, not_140_out, not_141_out, not_142_out, not_143_out, not_144_out,
       not_145_out, not_146_out, not_147_out, not_148_out, not_149_out, not_150_out, not_151_out,
       not_152_out, not_153_out, not_154_out, not_155_out, not_156_out, not_157_out, not_158_out,
       not_159_out, not_160_out, not_161_out, not_162_out, not_163_out, not_164_out, not_165_out,
       not_166_out, not_167_out, not_168_out, not_169_out, not_170_out, not_171_out, not_172_out,
       not_173_out, not_174_out, not_175_out, not_176_out, not_177_out, not_178_out, not_179_out,
       not_180_out, not_181_out, not_182_out, not_183_out, not_184_out, not_185_out, not_186_out,
       not_187_out, not_188_out, not_189_out, not_190_out, not_191_out, not_192_out, not_193_out,
       not_194_out, not_195_out, not_196_out, not_197_out, not_198_out, not_199_out, not_200_out,
       not_201_out, not_202_out, not_203_out, not_204_out, not_205_out, not_206_out, not_207_out,
       not_208_out, not_209_out, not_210_out, not_211_out, not_212_out, not_213_out, not_214_out,
       not_215_out, not_216_out, not_217_out, not_218_out, not_219_out, not_220_out, not_221_out,
       not_222_out, not_223_out, not_224_out, not_225_out, not_226_out, not_227_out, not_228_out;

  not not_1 (not_1_out, OP2);
  not not_2 (not_2_out, OP3);
  not not_3 (not_3_out, OP4);
  not not_4 (not_4_out, OP5);
  not not_5 (not_5_out, OP6);
  not not_6 (not_6_out, F12);
  not not_7 (not_7_out, F14);
  not not_8 (not_8_out, OP2);
  not not_9 (not_9_out, OP3);
  not not_10 (not_10_out, OP4);
  not not_11 (not_11_out, OP6);
  not not_12 (not_12_out, F12);
  not not_13 (not_13_out, F14);
  not not_14 (not_14_out, OP2);
  not not_15 (not_15_out, OP3);
  not not_16 (not_16_out, OP5);
  not not_17 (not_17_out, OP6);
  not not_18 (not_18_out, F12);
  not not_19 (not_19_out, F14);
  not not_20 (not_20_out, OP2);
  not not_21 (not_21_out, OP3);
  not not_22 (not_22_out, OP4);
  not not_23 (not_23_out, OP6);
  not not_24 (not_24_out, F12);
  not not_25 (not_25_out, F14);
  not not_26 (not_26_out, OP2);
  not not_27 (not_27_out, OP3);
  not not_28 (not_28_out, OP5);
  not not_29 (not_29_out, OP6);
  not not_30 (not_30_out, F12);
  not not_31 (not_31_out, OP2);
  not not_32 (not_32_out, OP3);
  not not_33 (not_33_out, OP5);
  not not_34 (not_34_out, OP6);
  not not_35 (not_35_out, F25);
  not not_36 (not_36_out, F30);
  not not_37 (not_37_out, OP2);
  not not_38 (not_38_out, OP3);
  not not_39 (not_39_out, OP5);
  not not_40 (not_40_out, OP6);
  not not_41 (not_41_out, F25);
  not not_42 (not_42_out, OP2);
  not not_43 (not_43_out, OP3);
  not not_44 (not_44_out, OP5);
  not not_45 (not_45_out, OP6);
  not not_46 (not_46_out, OP3);
  not not_47 (not_47_out, OP4);
  not not_48 (not_48_out, F12);
  not not_49 (not_49_out, F13);
  not not_50 (not_50_out, F14);
  not not_51 (not_51_out, F30);
  not not_52 (not_52_out, F25);
  not not_53 (not_53_out, F14);
  not not_54 (not_54_out, F13);
  not not_55 (not_55_out, F12);
  not not_56 (not_56_out, OP6);
  not not_57 (not_57_out, OP3);
  not not_58 (not_58_out, OP2);
  not not_59 (not_59_out, F25);
  not not_60 (not_60_out, F14);
  not not_61 (not_61_out, F13);
  not not_62 (not_62_out, F12);
  not not_63 (not_63_out, OP6);
  not not_64 (not_64_out, OP3);
  not not_65 (not_65_out, OP2);
  not not_66 (not_66_out, F30);
  not not_67 (not_67_out, F25);
  not not_68 (not_68_out, OP6);
  not not_69 (not_69_out, OP3);
  not not_70 (not_70_out, OP2);
  not not_71 (not_71_out, F30);
  not not_72 (not_72_out, F25);
  not not_73 (not_73_out, F12);
  not not_74 (not_74_out, OP6);
  not not_75 (not_75_out, OP3);
  not not_76 (not_76_out, OP2);
  not not_77 (not_77_out, F30);
  not not_78 (not_78_out, F25);
  not not_79 (not_79_out, F14);
  not not_80 (not_80_out, F12);
  not not_81 (not_81_out, OP6);
  not not_82 (not_82_out, OP3);
  not not_83 (not_83_out, OP2);
  not not_84 (not_84_out, F30);
  not not_85 (not_85_out, F25);
  not not_86 (not_86_out, F14);
  not not_87 (not_87_out, OP6);
  not not_88 (not_88_out, OP3);
  not not_89 (not_89_out, OP2);
  not not_90 (not_90_out, F14);
  not not_91 (not_91_out, F13);
  not not_92 (not_92_out, F12);
  not not_93 (not_93_out, OP6);
  not not_94 (not_94_out, OP5);
  not not_95 (not_95_out, OP3);
  not not_96 (not_96_out, OP2);
  not not_97 (not_97_out, OP6);
  not not_98 (not_98_out, OP5);
  not not_99 (not_99_out, OP3);
  not not_100 (not_100_out, OP2);
  not not_101 (not_101_out, F12);
  not not_102 (not_102_out, OP6);
  not not_103 (not_103_out, OP5);
  not not_104 (not_104_out, OP3);
  not not_105 (not_105_out, OP2);
  not not_106 (not_106_out, F13);
  not not_107 (not_107_out, F12);
  not not_108 (not_108_out, OP6);
  not not_109 (not_109_out, OP5);
  not not_110 (not_110_out, OP3);
  not not_111 (not_111_out, OP2);
  not not_112 (not_112_out, F14);
  not not_113 (not_113_out, F12);
  not not_114 (not_114_out, OP6);
  not not_115 (not_115_out, OP5);
  not not_116 (not_116_out, OP3);
  not not_117 (not_117_out, OP2);
  not not_118 (not_118_out, F30);
  not not_119 (not_119_out, F25);
  not not_120 (not_120_out, F14);
  not not_121 (not_121_out, F13);
  not not_122 (not_122_out, OP6);
  not not_123 (not_123_out, OP5);
  not not_124 (not_124_out, OP3);
  not not_125 (not_125_out, OP2);
  not not_126 (not_126_out, F30);
  not not_127 (not_127_out, F25);
  not not_128 (not_128_out, F13);
  not not_129 (not_129_out, OP6);
  not not_130 (not_130_out, OP5);
  not not_131 (not_131_out, OP3);
  not not_132 (not_132_out, OP2);
  not not_133 (not_133_out, F25);
  not not_134 (not_134_out, F13);
  not not_135 (not_135_out, OP6);
  not not_136 (not_136_out, OP5);
  not not_137 (not_137_out, OP3);
  not not_138 (not_138_out, OP2);
  not not_139 (not_139_out, F14);
  not not_140 (not_140_out, F12);
  not not_141 (not_141_out, OP6);
  not not_142 (not_142_out, OP5);
  not not_143 (not_143_out, OP4);
  not not_144 (not_144_out, OP3);
  not not_145 (not_145_out, OP2);
  not not_146 (not_146_out, OP4);
  not not_147 (not_147_out, F14);
  not not_148 (not_148_out, F13);
  not not_149 (not_149_out, F12);
  not not_150 (not_150_out, OP4);
  not not_151 (not_151_out, OP3);
  not not_152 (not_152_out, OP6);
  not not_153 (not_153_out, OP3);
  not not_154 (not_154_out, F14);
  not not_155 (not_155_out, OP6);
  not not_156 (not_156_out, OP5);
  not not_157 (not_157_out, OP3);
  not not_158 (not_158_out, OP2);
  not not_159 (not_159_out, OP6);
  not not_160 (not_160_out, OP5);
  not not_161 (not_161_out, OP3);
  not not_162 (not_162_out, F30);
  not not_163 (not_163_out, F14);
  not not_164 (not_164_out, F13);
  not not_165 (not_165_out, F12);
  not not_166 (not_166_out, OP6);
  not not_167 (not_167_out, OP3);
  not not_168 (not_168_out, OP2);
  not not_169 (not_169_out, OP2);
  not not_170 (not_170_out, OP3);
  not not_171 (not_171_out, F12);
  not not_172 (not_172_out, F13);
  not not_173 (not_173_out, F14);
  not not_174 (not_174_out, F25);
  not not_175 (not_175_out, F30);
  not not_176 (not_176_out, OP2);
  not not_177 (not_177_out, OP3);
  not not_178 (not_178_out, OP4);
  not not_179 (not_179_out, OP6);
  not not_180 (not_180_out, F12);
  not not_181 (not_181_out, F14);
  not not_182 (not_182_out, OP2);
  not not_183 (not_183_out, OP3);
  not not_184 (not_184_out, OP4);
  not not_185 (not_185_out, F12);
  not not_186 (not_186_out, F13);
  not not_187 (not_187_out, F14);
  not not_188 (not_188_out, OP2);
  not not_189 (not_189_out, OP3);
  not not_190 (not_190_out, OP4);
  not not_191 (not_191_out, F13);
  not not_192 (not_192_out, F14);
  not not_193 (not_193_out, OP3);
  not not_194 (not_194_out, OP4);
  not not_195 (not_195_out, F12);
  not not_196 (not_196_out, F13);
  not not_197 (not_197_out, F14);
  not not_198 (not_198_out, OP4);
  not not_199 (not_199_out, OP2);
  not not_200 (not_200_out, OP3);
  not not_201 (not_201_out, OP4);
  not not_202 (not_202_out, OP6);
  not not_203 (not_203_out, F12);
  not not_204 (not_204_out, F13);
  not not_205 (not_205_out, F14);
  not not_206 (not_206_out, OP2);
  not not_207 (not_207_out, OP3);
  not not_208 (not_208_out, OP4);
  not not_209 (not_209_out, F12);
  not not_210 (not_210_out, OP2);
  not not_211 (not_211_out, OP3);
  not not_212 (not_212_out, F12);
  not not_213 (not_213_out, OP2);
  not not_214 (not_214_out, OP3);
  not not_215 (not_215_out, OP3);
  not not_216 (not_216_out, OP6);
  not not_217 (not_217_out, OP2);
  not not_218 (not_218_out, OP3);
  not not_219 (not_219_out, OP4);
  not not_220 (not_220_out, F12);
  not not_221 (not_221_out, F13);
  not not_222 (not_222_out, OP2);
  not not_223 (not_223_out, OP3);
  not not_224 (not_224_out, OP4);
  not not_225 (not_225_out, F13);
  not not_226 (not_226_out, OP3);
  not not_227 (not_227_out, OP5);
  not not_228 (not_228_out, OP6);
  and and_1 (MemToReg, not_1_out, not_2_out, not_3_out, not_4_out, not_5_out, not_6_out, F13, not_7_out);
  and and_2 (MemWrite, not_8_out, not_9_out, not_10_out, OP5, not_11_out, not_12_out, not_13_out);
  and and_3 (and_3_out, not_14_out, not_15_out, not_16_out, not_17_out, not_18_out, F13, not_19_out);
  and and_4 (and_4_out, not_20_out, not_21_out, not_22_out, OP5, not_23_out, not_24_out, not_25_out);
  and and_5 (and_5_out, not_26_out, not_27_out, OP4, not_28_out, not_29_out, not_30_out);
  and and_6 (and_6_out, not_31_out, not_32_out, OP4, not_33_out, not_34_out, not_35_out, not_36_out);
  and and_7 (and_7_out, not_37_out, not_38_out, OP4, not_39_out, not_40_out, F14, not_41_out);
  and and_8 (and_8_out, not_42_out, not_43_out, OP4, not_44_out, not_45_out, F13);
  and and_9 (and_9_out, OP2, not_46_out, not_47_out, OP5, OP6, not_48_out, not_49_out, not_50_out);
  and and_10 (and_10_out, not_51_out, not_52_out, not_53_out, not_54_out, not_55_out, not_56_out, OP5, OP4, not_57_out, not_58_out);
  and and_11 (and_11_out, F30, not_59_out, not_60_out, not_61_out, not_62_out, not_63_out, OP5, OP4, not_64_out, not_65_out);
  and and_12 (and_12_out, not_66_out, not_67_out, F14, F13, F12, not_68_out, OP5, OP4, not_69_out, not_70_out);
  and and_13 (and_13_out, not_71_out, not_72_out, F14, F13, not_73_out, not_74_out, OP5, OP4, not_75_out, not_76_out);
  and and_14 (and_14_out, not_77_out, not_78_out, not_79_out, F13, not_80_out, not_81_out, OP5, OP4, not_82_out, not_83_out);
  and and_15 (and_15_out, not_84_out, not_85_out, not_86_out, F13, F12, not_87_out, OP5, OP4, not_88_out, not_89_out);
  and and_16 (and_16_out, not_90_out, not_91_out, not_92_out, not_93_out, not_94_out, OP4, not_95_out, not_96_out);
  and and_17 (and_17_out, F14, F13, F12, not_97_out, not_98_out, OP4, not_99_out, not_100_out);
  and and_18 (and_18_out, F14, F13, not_101_out, not_102_out, not_103_out, OP4, not_104_out, not_105_out);
  and and_19 (and_19_out, F14, not_106_out, not_107_out, not_108_out, not_109_out, OP4, not_110_out, not_111_out);
  and and_20 (and_20_out, not_112_out, F13, not_113_out, not_114_out, not_115_out, OP4, not_116_out, not_117_out);
  and and_21 (and_21_out, not_118_out, not_119_out, not_120_out, not_121_out, F12, not_122_out, not_123_out, OP4, not_124_out, not_125_out);
  and and_22 (and_22_out, not_126_out, not_127_out, F14, not_128_out, F12, not_129_out, not_130_out, OP4, not_131_out, not_132_out);
  and and_23 (and_23_out, F30, not_133_out, F14, not_134_out, F12, not_135_out, not_136_out, OP4, not_137_out, not_138_out);
  and and_24 (and_24_out, not_139_out, F13, not_140_out, not_141_out, not_142_out, not_143_out, not_144_out, not_145_out);
  and and_25 (and_25_out, OP6, OP5, not_146_out, OP3, OP2);
  and and_26 (and_26_out, not_147_out, not_148_out, not_149_out, OP6, OP5, not_150_out, not_151_out, OP2);
  and and_27 (and_27_out, not_152_out, OP5, OP4, not_153_out, OP2);
  and and_28 (and_28_out, not_154_out, F13, F12, not_155_out, not_156_out, OP4, not_157_out, not_158_out);
  and and_29 (and_29_out, not_159_out, not_160_out, OP4, not_161_out, OP2);
  and and_30 (and_30_out, not_162_out, F25, not_163_out, not_164_out, not_165_out, not_166_out, OP5, OP4, not_167_out, not_168_out);
  and and_31 (ecall, not_169_out, not_170_out, OP4, OP5, OP6, not_171_out, not_172_out, not_173_out, not_174_out, not_175_out);
  and and_32 (S_Type, not_176_out, not_177_out, not_178_out, OP5, not_179_out, not_180_out, not_181_out);
  and and_33 (BEQ, not_182_out, not_183_out, not_184_out, OP5, OP6, not_185_out, not_186_out, not_187_out);
  and and_34 (BNE, not_188_out, not_189_out, not_190_out, OP5, OP6, F12, not_191_out, not_192_out);
  and and_35 (JALR, OP2, not_193_out, not_194_out, OP5, OP6, not_195_out, not_196_out, not_197_out);
  and and_36 (JAL, OP2, OP3, not_198_out, OP5, OP6);
  and and_37 (SB, not_199_out, not_200_out, not_201_out, OP5, not_202_out, not_203_out, not_204_out, not_205_out);
  and and_38 (BLTU, not_206_out, not_207_out, not_208_out, OP5, OP6, not_209_out, F13, F14);
  and and_39 (CSRRSI, not_210_out, not_211_out, OP4, OP5, OP6, not_212_out, F13, F14);
  and and_40 (CSRRCI, not_213_out, not_214_out, OP4, OP5, OP6, F12, F13, F14);
  and and_41 (LUI, OP2, not_215_out, OP4, OP5, not_216_out);
  and and_42 (BLT, not_217_out, not_218_out, not_219_out, OP5, OP6, not_220_out, not_221_out, F14);
  and and_43 (BGE, not_222_out, not_223_out, not_224_out, OP5, OP6, F12, not_225_out, F14);
  and and_44 (AUIPC, OP2, not_226_out, OP4, not_227_out, not_228_out);
  or or_1 (ALU_SRC, and_3_out, and_4_out, and_5_out, and_6_out, and_7_out, and_8_out, and_9_out);
  or or_2 (RegWrite, and_10_out, and_11_out, and_12_out, and_13_out, and_14_out, and_15_out, and_16_out, and_17_out, and_18_out, and_19_out, and_20_out, and_21_out, and_22_out, and_23_out, and_24_out, and_25_out, and_26_out, and_27_out, and_28_out, and_29_out, and_30_out);
endmodule

// ALU
module ALU (
  input  [31:0] X,
  input  [31:0] Y,
  input  [3:0] AluOP,
  output out_4,
  output Equal,
  output out_6,
  output [31:0] Result,
  output [31:0] Result_2
);

  wire [0:0] comparator_1_lt, comparator_2_lt;
  wire [31:0] adder_1_out, AND_out, divider_1_out, divider_1_rem, multiplier_1_cout, multiplier_1_out,
       NOR_out, OR_out, shifter_1_out, shifter_2_out, shifter_3_out, subtractor_1_out, XOR_out;

  assign AND_out = X & Y;  // AND_Gate AND, 32 bits wide
  assign OR_out = X | Y;  // OR_Gate OR, 32 bits wide
  Shifter #(.width(32), .shift("ll")) shifter_1 (.in(X), .\dist (Y[4:0]), .out(shifter_1_out));
  Shifter #(.width(32), .shift("ar")) shifter_2 (.in(X), .\dist (Y[4:0]), .out(shifter_2_out));
  Shifter #(.width(32), .shift("lr")) shifter_3 (.in(X), .\dist (Y[4:0]), .out(shifter_3_out));
  Multiplier #(.width(32)) multiplier_1 (.a(X), .b(Y), .out(multiplier_1_out), .cout(multiplier_1_cout));  // open: cin
  Divider #(.width(32)) divider_1 (.a(X), .b(Y), .out(divider_1_out), .rem(divider_1_rem));  // open: upper
  Adder #(.width(32)) adder_1 (.a(X), .b(Y), .out(adder_1_out));  // open: cin, cout
  Subtractor #(.width(32)) subtractor_1 (.a(X), .b(Y), .out(subtractor_1_out));  // open: bin, bout
  assign XOR_out = X ^ Y;  // XOR_Gate XOR, 32 bits wide
  assign NOR_out = ~(X | Y);  // NOR_Gate NOR, 32 bits wide
  Comparator #(.width(32), .mode("twosComplement")) comparator_1 (
    .a(X), .b(Y), .eq(Equal), .lt(comparator_1_lt[0]));  // open: gt
  Comparator #(.width(32), .mode("unsigned")) comparator_2 (.a(X), .b(Y), .lt(comparator_2_lt[0]));  // open: gt, eq
  Multiplexer #(.select(4), .width(32), .disabled("Z"), .enable("false")) multiplexer_1 (
    .in0(shifter_1_out), .in1(shifter_2_out), .in2(shifter_3_out), .in3(multiplier_1_out),
    .in4(divider_1_out), .in5(adder_1_out), .in6(subtractor_1_out), .in7(AND_out), .in8(OR_out),
    .in9(XOR_out), .in10(NOR_out), .in11({{31{1'b0}}, comparator_1_lt[0]}),
    .in12({{31{1'b0}}, comparator_2_lt[0]}), .in13({32{1'b0}}), .in14({32{1'b0}}), .in15({32{1'b0}}),
    .out(Result), .sel(AluOP));
  Multiplexer #(.select(4), .width(32), .disabled("Z"), .enable("false")) multiplexer_2 (
    .in0({32{1'b0}}), .in1({32{1'b0}}), .in2({32{1'b0}}), .in3(multiplier_1_cout), .in4(divider_1_rem),
    .in5({32{1'b0}}), .in6({32{1'b0}}), .in7({32{1'b0}}), .in8({32{1'b0}}), .in9({32{1'b0}}),
    .in10({32{1'b0}}), .in11({32{1'b0}}), .in12({32{1'b0}}), .in13({32{1'b0}}), .in14({32{1'b0}}),
    .in15({32{1'b0}}), .out(Result_2), .sel(AluOP));
  Multiplexer #(.select(4), .width(1), .disabled("Z"), .enable("false")) multiplexer_3 (
    .in0(1'b0), .in1(1'b0), .in2(1'b0), .in3(1'b0), .in4(1'b0), .in5(1'b0), .in6(1'b0), .in7(1'b0),
    .in8(1'b0), .in9(1'b0), .in10(1'b0), .in11(comparator_1_lt[0]), .in12(comparator_2_lt[0]), .in13(1'b0),
    .in14(1'b0), .in15(1'b0), .out(out_6), .sel(AluOP));
  not not_1 (out_4, out_6);

  // Other names for the same wires on the sheet: Result2[31:0] = Result_2; S[3:0] = AluOP; tunnel = out_6;
  //   tunnel_t = out_4

  // Notes on the sheet:
  //   不要改变此引脚区域内容，也不要改变ALU封装形式
  //   输入引脚
  //   输出引脚
endmodule

module Regifile (
  input  [31:0] Din,
  input  Clk,
  input  WE,
  input  [4:0] R1_num,
  input  [4:0] W_num,
  input  [4:0] R2_num,
  output [31:0] R1,
  output [31:0] R2
);

  // RegisterFile registerfile_1: pin names not known; wires that end beside it: Din, Clk, WE, W_num, R1_num, R2_num, R1, R2
endmodule

module \理想流水线  (
  output RegWrite,
  output MemWrite,
  output [31:0] IF_PC,
  output [31:0] ID_PC,
  output [31:0] EX_PC,
  output [31:0] M_PC,
  output [31:0] WB_PC,
  output [31:0] RDin,
  output [31:0] MDin,
  output [31:0] LedData
);

  wire and_1_out, and_2_out, and_3_out, and_4_out, and_5_out, B, CLK, clock_1_out, comparator_1_eq,
       comparator_1_lt, comparator_2_eq, comparator_3_eq, comparator_4_eq, d_ff_1_q, ecall, en, equal,
       ex_mem_1_haltout, ex_mem_1_jout, ex_mem_1_luiout, ex_mem_1_memtoregout, ex_mem_1_regwriteout, Go,
       halt, id_ex_1_alusrcbout, id_ex_1_beqout, id_ex_1_bltuout, id_ex_1_bneout, id_ex_1_haltout,
       id_ex_1_luiout, id_ex_1_memtoregout, id_ex_1_memwriteout, id_ex_1_regwriteout, id_ex_1_sbout,
       id_ex_1_stypeout, IR1, IR2, IR3, JAL, JALR, less, mem_wb_1_haltout, mem_wb_1_jout, mem_wb_1_luiout,
       mem_wb_1_memtoregout, nand_1_out, not_1_out, not_2_out, not_3_out, not_4_out, not_5_out, or_1_out,
       RST, W1, W2, W3, \单周期硬布线控制器_1_alu_src , \单周期硬布线控制器_1_beq , \单周期硬布线控制器_1_bltu , \单周期硬布线控制器_1_bne ,
       \单周期硬布线控制器_1_csrrci , \单周期硬布线控制器_1_csrrsi , \单周期硬布线控制器_1_jal , \单周期硬布线控制器_1_jalr , \单周期硬布线控制器_1_lui ,
       \单周期硬布线控制器_1_memtoreg , \单周期硬布线控制器_1_memwrite , \单周期硬布线控制器_1_regwrite , \单周期硬布线控制器_1_s_type ,
       \单周期硬布线控制器_1_sb , \单周期硬布线控制器_1_uret ;
  wire [3:0] ex_mem_1_selectout, id_ex_1_aluopout, multiplexer_8_out, multiplexer_10_out,
       \单周期硬布线控制器_1_alu_op ;
  wire [4:0] ex_mem_1_w_out, id_ex_1_w_out_2, multiplexer_4_out, multiplexer_5_out, multiplexer_9_out, W_num;
  wire [11:0] shifter_1_out;
  wire [12:0] CNT_num;
  wire [15:0] \LoadUse次数 , \总周期数 , \插入气泡数 , \无条件分支数 , \条件分支成功数 ;
  wire [19:0] shifter_2_out;
  wire [31:0] adder_4_out, bit_extender_1_out, bit_extender_2_out, bit_extender_3_out, bit_extender_4_out,
       bit_extender_5_out, BPC, EX_IR, ex_mem_1_resultout, ex_mem_1_uout, EX_R2, id_ex_1_bout, id_ex_1_iout,
       id_ex_1_jout, id_ex_1_r1out, id_ex_1_sout, id_ex_1_uout, ID_IR, IF_IR, JPC, MEM_IR,
       mem_wb_1_mddateout, mem_wb_1_resultout, mem_wb_1_uout, mips_ram_1_p8, multiplexer_1_out,
       multiplexer_2_out, multiplexer_6_out, multiplexer_7_out, multiplexer_11_out, multiplexer_12_out,
       multiplexer_13_out, PC_4, PCin, R1, R2, Result, shifter_3_out, shifter_4_out, WB_IR;

  Button \u_总复位  (.out(RST));
  Button _1 (.out(IR1));
  Button _2 (.out(IR2));
  Button _3 (.out(IR3));
  // Probe on \总周期数 
  // Probe on \总周期数 
  Button \u_继续运行  (.out(Go));
  LED #(.active("true")) led_1 (.in(W1));
  LED #(.active("true")) led_2 (.in(W2));
  LED #(.active("true")) led_3 (.in(W3));
  Hex_Digit_Display hex_digit_display_1 (.value(LedData[31:28]));  // open: dp
  // Probe on IF_PC[19:0]
  // RiscV_Probe riscv_probe_1: pin names not known; wires that end beside it: IF_IR
  not not_1 (not_1_out, halt);
  Counter #(.width(16), .max('hffff), .ongoal("wrap"), .trigger("rising"), .behavior("new")) counter_1 (
    .count(not_1_out), .Q(\总周期数 ), .clk(CLK), .clr(RST));  // open: load, D, carry, preset, down
  Hex_Digit_Display hex_digit_display_2 (.value(LedData[23:20]));  // open: dp
  Hex_Digit_Display hex_digit_display_3 (.value(LedData[27:24]));  // open: dp
  // Probe on ID_PC[19:0]
  // RiscV_Probe riscv_probe_2: pin names not known; wires that end beside it: ID_IR
  not not_2 (not_2_out, halt);
  Hex_Digit_Display hex_digit_display_4 (.value(LedData[19:16]));  // open: dp
  Hex_Digit_Display hex_digit_display_5 (.value(LedData[15:12]));  // open: dp
  Register #(.width(32), .trigger("rising"), .Select("low")) PC (
    .D(PCin), .en(not_2_out), .Q(IF_PC), .clk(CLK), .clr(RST));
  Multiplexer #(.select(1), .width(32), .disabled("Z"), .enable("false")) multiplexer_1 (
    .in0(PC_4), .in1(BPC), .out(multiplexer_1_out), .sel(B));
  Hex_Digit_Display hex_digit_display_6 (.value(LedData[11:8]));  // open: dp
  Hex_Digit_Display hex_digit_display_7 (.value(LedData[7:4]));  // open: dp
  // Probe on EX_PC[19:0]
  // RiscV_Probe riscv_probe_3: pin names not known; wires that end beside it: EX_IR
  Adder #(.width(32)) adder_1 (.a(IF_PC), .b(32'h4), .out(PC_4));  // open: cin, cout
  Multiplexer #(.select(1), .width(32), .disabled("Z"), .enable("false")) multiplexer_2 (
    .in0(multiplexer_1_out), .in1(JPC), .out(multiplexer_2_out), .sel(JAL));
  Hex_Digit_Display hex_digit_display_8 (.value(LedData[3:0]));  // open: dp
  // Probe on \总周期数 
  // Probe on M_PC[19:0]
  // RiscV_Probe riscv_probe_4: pin names not known; wires that end beside it: MEM_IR
  ROM #(.addrWidth(10), .dataWidth(32), .Select("high")) rom_1 (.addr(IF_PC[11:2]), .data(IF_IR));
  Multiplexer #(.select(1), .width(32), .disabled("Z"), .enable("false")) multiplexer_3 (
    .in0(multiplexer_2_out), .in1(Result), .out(PCin), .sel(JALR));
  // Probe on \总周期数 
  // Probe on \无条件分支数 
  // Probe on \条件分支成功数 
  // Probe on \插入气泡数 
  // Probe on \LoadUse次数 
  IF_ID if_id_1 (.IRin(IF_IR), .PCin(IF_PC), .IRout(ID_IR), .PCout(ID_PC), .RST(RST), .EN(en), .CLK(CLK));
  // Probe on IF_PC[11:0]
  // Probe on WB_PC[19:0]
  // RiscV_Probe riscv_probe_5: pin names not known; wires that end beside it: WB_IR
  // Probe on EX_PC[11:0]
  // Probe on ID_PC[11:0]
  // RiscV_Probe riscv_probe_6: pin names not known; wires that end beside it: ID_IR
  // Probe on M_PC[11:0]
  D_Flip_Flop #(.trigger("high"), .Pre_Clr_Positions("LEGACY"), .NegatePresetClear("false"), .enable("true"), .NewFFLayout("false")) d_ff_1 (.Q(d_ff_1_q));  // open: clk, D, Qn, preset, en, reset
  // Probe on 13'hc
  // Probe on WB_PC[11:0]
  Comparator #(.width(13), .mode("twosComplement")) comparator_1 (
    .a(CNT_num), .b(13'hc), .eq(comparator_1_eq), .lt(comparator_1_lt));  // open: gt
  Clock #(.highDuration(1), .lowDuration(1)) clock_1 (.out(clock_1_out));
  Comparator #(.width(32), .mode("twosComplement")) comparator_2 (
    .a(R2), .b(32'h22), .eq(comparator_2_eq));  // open: gt, lt
  nand nand_1 (nand_1_out, d_ff_1_q, comparator_1_eq);
  Counter #(.width(13), .max('h1fff), .ongoal("stay"), .trigger("rising"), .behavior("old")) counter_2 (
    .count(comparator_1_lt), .Q(CNT_num), .clk(clock_1_out));  // open: load, D, carry, clr, preset
  and and_1 (and_1_out, ecall, comparator_2_eq);
  \单周期硬布线控制器  \u_单周期硬布线控制器_1  (
    .Funct({ID_IR[30], ID_IR[25], ID_IR[14:12]}), .OP(ID_IR[6:2]), .ALU_OP(\单周期硬布线控制器_1_alu_op ),
    .MemToReg(\单周期硬布线控制器_1_memtoreg ), .MemWrite(\单周期硬布线控制器_1_memwrite ), .ALU_SRC(\单周期硬布线控制器_1_alu_src ),
    .RegWrite(\单周期硬布线控制器_1_regwrite ), .ecall(ecall), .S_type(\单周期硬布线控制器_1_s_type ),
    .Jalr(\单周期硬布线控制器_1_jalr ), .Beq(\单周期硬布线控制器_1_beq ), .JAL(\单周期硬布线控制器_1_jal ), .Bne(\单周期硬布线控制器_1_bne ),
    .in_3(ID_IR[21]), .uret(\单周期硬布线控制器_1_uret ), .SB(\单周期硬布线控制器_1_sb ), .BLTU(\单周期硬布线控制器_1_bltu ),
    .CSRRSI(\单周期硬布线控制器_1_csrrsi ), .CSRRCI(\单周期硬布线控制器_1_csrrci ), .LUI(\单周期硬布线控制器_1_lui ));  // open: BLT, BGE, AUIPC
  Multiplexer #(.select(1), .width(5), .disabled("Z"), .enable("false")) multiplexer_4 (
    .in0(ID_IR[19:15]), .in1(5'b01010), .out(multiplexer_4_out), .sel(ecall));
  Multiplexer #(.select(1), .width(5), .disabled("Z"), .enable("false")) multiplexer_5 (
    .in0(ID_IR[24:20]), .in1(5'b10001), .out(multiplexer_5_out), .sel(ecall));
  assign bit_extender_1_out = {{20{ID_IR[31]}}, ID_IR[31:20]};  // Bit_Extender bit_extender_1
  assign bit_extender_2_out = {{20{ID_IR[31]}}, {ID_IR[31:25], ID_IR[11:7]}};  // Bit_Extender bit_extender_2
  assign bit_extender_3_out = {{12{1'b0}}, ID_IR[31:12]};  // Bit_Extender bit_extender_3
  Shifter #(.width(12), .shift("ll")) shifter_1 (
    .in({ID_IR[31], ID_IR[7], ID_IR[30:25], ID_IR[11:8]}), .\dist (4'b0001), .out(shifter_1_out));
  Shifter #(.width(20), .shift("ll")) shifter_2 (
    .in({ID_IR[31], ID_IR[19:12], ID_IR[20], ID_IR[30:21]}), .\dist (5'b00001), .out(shifter_2_out));
  assign CLK = nand_1_out ? clock_1_out : 1'bz;  // Controlled_Buffer controlled_buffer_1
  Register #(.width(32), .trigger("rising"), .Select("low")) register_1 (
    .D(R1), .en(and_1_out), .Q(LedData), .clk(CLK), .clr(RST));
  Regifile regifile_1 (
    .Din(RDin), .Clk(CLK), .R1(R1), .R2(R2), .WE(RegWrite), .W_num(W_num), .R1_num(multiplexer_4_out),
    .R2_num(multiplexer_5_out));
  Shifter #(.width(32), .shift("ll")) shifter_3 (.in(bit_extender_3_out), .\dist (5'b01100), .out(shifter_3_out));
  assign bit_extender_4_out = {{20{shifter_1_out[11]}}, shifter_1_out};  // Bit_Extender bit_extender_4
  assign bit_extender_5_out = {{12{shifter_2_out[19]}}, shifter_2_out};  // Bit_Extender bit_extender_5
  Pull_Resistor #(.pull(1)) pull_resistor_1 (.node(CLK));
  not not_3 (not_3_out, comparator_3_eq);
  Comparator #(.width(32), .mode("twosComplement")) comparator_3 (
    .a(R2), .b(32'h22), .eq(comparator_3_eq));  // open: gt, lt
  ID_EX id_ex_1 (
    .JALin(\单周期硬布线控制器_1_jal ), .JALRin(\单周期硬布线控制器_1_jalr ), .SBin(\单周期硬布线控制器_1_sb ),
    .BLTUin(\单周期硬布线控制器_1_bltu ), .URETin(\单周期硬布线控制器_1_uret ), .CSRRSIin(\单周期硬布线控制器_1_csrrsi ), .RST(RST),
    .EN(en), .CLK(CLK), .JALout(JAL), .SBout(id_ex_1_sbout), .JALRout(JALR), .BLTUout(id_ex_1_bltuout),
    .LUIout(id_ex_1_luiout), .LUIin(\单周期硬布线控制器_1_lui ), .Beqin(\单周期硬布线控制器_1_beq ), .Beqout(id_ex_1_beqout),
    .Bnein(\单周期硬布线控制器_1_bne ), .Bneout(id_ex_1_bneout), .MemToRegin(\单周期硬布线控制器_1_memtoreg ),
    .MemToRegout(id_ex_1_memtoregout), .MemWritein(\单周期硬布线控制器_1_memwrite ),
    .MemWriteout(id_ex_1_memwriteout), .AluOPin(\单周期硬布线控制器_1_alu_op ), .AluOPout(id_ex_1_aluopout),
    .AluSrcBin(\单周期硬布线控制器_1_alu_src ), .AluSrcBout(id_ex_1_alusrcbout), .RegWritein(\单周期硬布线控制器_1_regwrite ),
    .RegWriteout(id_ex_1_regwriteout), .Stypein(\单周期硬布线控制器_1_s_type ), .Stypeout(id_ex_1_stypeout),
    .haltin(and_2_out), .haltout(id_ex_1_haltout), .R1out(id_ex_1_r1out), .R1in(R1), .R2out(EX_R2),
    .R2in(R2), .PCin(ID_PC), .PCout(EX_PC), .Iin(bit_extender_1_out), .Iout(id_ex_1_iout),
    .Sin(bit_extender_2_out), .Sout(id_ex_1_sout), .Uin(shifter_3_out), .Uout(id_ex_1_uout),
    .Bin(bit_extender_4_out), .Bout(id_ex_1_bout), .Jin(bit_extender_5_out), .Jout(id_ex_1_jout),
    .IRin(ID_IR), .IRout(EX_IR), .CSRRCIin(\单周期硬布线控制器_1_csrrci ), .W_out_2(id_ex_1_w_out_2),
    .W_out(ID_IR[11:7]));  // open: URETout, CSRRSIout, CSRRCIout, R1Forwardin, R1forwardout, R2Forwardin, R2forwardout
  and and_2 (and_2_out, ecall, not_3_out);
  or or_1 (or_1_out, JAL, JALR);
  Comparator #(.width(32), .mode("twosComplement")) comparator_4 (
    .a(32'h1), .b(Result), .eq(comparator_4_eq));  // open: gt, lt
  not not_4 (not_4_out, equal);
  and and_3 (and_3_out, id_ex_1_bltuout, comparator_4_eq);
  and and_4 (and_4_out, id_ex_1_beqout, equal);
  and and_5 (and_5_out, not_4_out, id_ex_1_bneout);
  Multiplexer #(.select(1), .width(32), .disabled("Z"), .enable("false")) multiplexer_6 (
    .in0(id_ex_1_iout), .in1(id_ex_1_sout), .out(multiplexer_6_out), .sel(id_ex_1_stypeout));
  or or_2 (B, and_3_out, and_4_out, and_5_out);
  Multiplexer #(.select(1), .width(32), .disabled("Z"), .enable("false")) multiplexer_7 (
    .in0(EX_R2), .in1(multiplexer_6_out), .out(multiplexer_7_out), .sel(id_ex_1_alusrcbout));
  Adder #(.width(32)) adder_2 (.a(EX_PC), .b(id_ex_1_bout), .out(BPC));  // open: cin, cout
  Adder #(.width(32)) adder_3 (.a(id_ex_1_jout), .b(EX_PC), .out(JPC));  // open: cin, cout
  Multiplexer #(.select(2), .width(4), .disabled("Z"), .enable("false")) multiplexer_8 (
    .in0(4'b0001), .in1(4'b0010), .in2(4'b0100), .in3(4'b1000), .out(multiplexer_8_out), .sel(Result[1:0]));
  Shifter #(.width(32), .shift("ll")) shifter_4 (.in(EX_R2), .\dist (multiplexer_9_out), .out(shifter_4_out));
  Multiplexer #(.select(2), .width(5), .disabled("Z"), .enable("false")) multiplexer_9 (
    .in0({5{1'b0}}), .in1(5'b01000), .in2(5'b10000), .in3(5'b11000), .out(multiplexer_9_out),
    .sel(Result[1:0]));
  ALU alu_1 (
    .X(id_ex_1_r1out), .Y(multiplexer_7_out), .AluOP(id_ex_1_aluopout), .Equal(equal), .Result(Result),
    .out_6(less));  // open: Result_2, out_4
  Multiplexer #(.select(1), .width(4), .disabled("Z"), .enable("false")) multiplexer_10 (
    .in0(4'b1111), .in1(multiplexer_8_out), .out(multiplexer_10_out), .sel(id_ex_1_sbout));
  Multiplexer #(.select(1), .width(32), .disabled("Z"), .enable("false")) multiplexer_11 (
    .in0(EX_R2), .in1(shifter_4_out), .out(multiplexer_11_out), .sel(id_ex_1_sbout));
  EX_MEM ex_mem_1 (
    .IRin(EX_IR), .PCin(EX_PC), .haltin(id_ex_1_haltout), .Jin(or_1_out), .W_in(id_ex_1_w_out_2),
    .Resultin(Result), .MemToRegin(id_ex_1_memtoregout), .MemWritein(id_ex_1_memwriteout),
    .RegWritein(id_ex_1_regwriteout), .Selectin(multiplexer_10_out), .MDin(multiplexer_11_out),
    .IRout(MEM_IR), .PCout(M_PC), .haltout(ex_mem_1_haltout), .Jout(ex_mem_1_jout), .W_out(ex_mem_1_w_out),
    .Resultout(ex_mem_1_resultout), .MemToRegout(ex_mem_1_memtoregout), .MemWriteout(MemWrite),
    .RegWriteout(ex_mem_1_regwriteout), .Selectout(ex_mem_1_selectout), .MDout(MDin), .RST(RST), .EN(en),
    .CLK(CLK), .LUIout(ex_mem_1_luiout), .LUIin(id_ex_1_luiout), .Uout(ex_mem_1_uout), .Uin(id_ex_1_uout));
  not not_5 (not_5_out, MemWrite);
  // MIPS_RAM mips_ram_1: pin names not known; wires that end beside it: ex_mem_1_resultout[11:2], MDin, MemWrite, ex_mem_1_selectout, CLK, not_5_out, RST, mips_ram_1_p8
  MEM_WB mem_wb_1 (
    .IRin(MEM_IR), .PCin(M_PC), .haltin(ex_mem_1_haltout), .Jin(ex_mem_1_jout), .W_in(ex_mem_1_w_out),
    .Resultin(ex_mem_1_resultout), .MemToRegin(ex_mem_1_memtoregout), .RegWritein(ex_mem_1_regwriteout),
    .MDdatein(mips_ram_1_p8), .LUIin(ex_mem_1_luiout), .Uin(ex_mem_1_uout), .IRout(WB_IR), .PCout(WB_PC),
    .haltout(mem_wb_1_haltout), .Jout(mem_wb_1_jout), .W_out(W_num), .Resultout(mem_wb_1_resultout),
    .MemToRegout(mem_wb_1_memtoregout), .RegWriteout(RegWrite), .MDdateout(mem_wb_1_mddateout),
    .LUIout(mem_wb_1_luiout), .Uout(mem_wb_1_uout), .RST(RST), .EN(en), .CLK(CLK));
  Adder #(.width(32)) adder_4 (.a(WB_PC), .b(32'h4), .out(adder_4_out));  // open: cin, cout
  Multiplexer #(.select(1), .width(32), .disabled("Z"), .enable("false")) multiplexer_12 (
    .in0(mem_wb_1_resultout), .in1(mem_wb_1_mddateout), .out(multiplexer_12_out), .sel(mem_wb_1_memtoregout));
  Multiplexer #(.select(1), .width(32), .disabled("Z"), .enable("false")) multiplexer_13 (
    .in0(multiplexer_12_out), .in1(adder_4_out), .out(multiplexer_13_out), .sel(mem_wb_1_jout));
  and and_6 (halt, mem_wb_1_haltout, ~Go);  // AND_Gate
  not not_6 (en, halt);
  Multiplexer #(.select(1), .width(32), .disabled("Z"), .enable("false")) multiplexer_14 (
    .in0(multiplexer_13_out), .in1(mem_wb_1_uout), .out(RDin), .sel(mem_wb_1_luiout));

  // Other names for the same wires on the sheet: MEM_PC[31:0] = M_PC

  // Notes on the sheet:
  //   中断源
  //   时空图监测，可删除
  //   中断等待指示
  //   数码管输出
  //   指令存储器
  //   contents of rom_1 (hex, n*v repeats v):
  //   413 493 913 993 46413 14e493 296913 39e993 842023 942223 1242423 1342623 a00893 493 913 993 73
  //   控制位
  //   指令探针
  //   流水调试日志用
  //   暂停节拍，不能为0
  //   指令字
  //   戳工具置1进入计数暂停模式，ctrl+k时钟自动运行到对应节拍暂停
  //   ctrl+k关闭时钟连续运行，将控制位置零，进入单步调试模式调试
  //   用这个时钟源需要去掉电路中的其他时钟源
  //   JAL
  //   JALR
  //   URET
  //   I型
  //   S型
  //   U型
  //   B型
  //   J型
  //   Beq
  //   Bne
  //   MemToReg
  //   MemWrite
  //   AluOP
  //   AluSrcB
  //   RegWrite
  //   可计数暂停的时钟源
  //   为方便自动评测，需要输出流水线各段保存的PC值，注意是PC不是PC+4，另外ID段寄存器写入信息，Mem段内存写入信息也要输出
  //   数据存储器
endmodule

module \气泡流水线  (
  output RegWrite,
  output MemWrite,
  output [31:0] IF_PC,
  output [31:0] ID_PC,
  output [31:0] EX_PC,
  output [31:0] M_PC,
  output [31:0] WB_PC,
  output [31:0] RDin,
  output [31:0] MDin,
  output [31:0] LedData
);

  wire and_1_out, and_2_out, and_3_out, and_4_out, and_5_out, and_6_out, and_7_out, B, CLK, clock_1_out,
       comparator_1_eq, comparator_1_lt, comparator_2_eq, comparator_3_eq, comparator_4_eq, d_ff_1_q,
       DataHazzard, ecall, en, equal, EX_ecall, ex_mem_1_haltout, ex_mem_1_jout, ex_mem_1_luiout,
       ex_mem_1_memtoregout, EX_RegWrite, Go, halt, id_ex_1_alusrcbout, id_ex_1_beqout, id_ex_1_bltuout,
       id_ex_1_bneout, id_ex_1_luiout, id_ex_1_memtoregout, id_ex_1_memwriteout, id_ex_1_sbout,
       id_ex_1_stypeout, IR1, IR2, IR3, JAL, JALR, less, MEM_RegWrite, mem_wb_1_haltout, mem_wb_1_jout,
       mem_wb_1_luiout, mem_wb_1_memtoregout, nand_1_out, not_1_out, not_2_out, not_3_out, not_4_out,
       not_5_out, not_6_out, not_7_out, not_8_out, not_9_out, or_1_out, or_2_out, or_3_out, or_4_out,
       register_3_q, RST, W1, W2, W3, \单周期硬布线控制器_1_alu_src , \单周期硬布线控制器_1_beq , \单周期硬布线控制器_1_bltu ,
       \单周期硬布线控制器_1_bne , \单周期硬布线控制器_1_csrrci , \单周期硬布线控制器_1_csrrsi , \单周期硬布线控制器_1_jal , \单周期硬布线控制器_1_jalr ,
       \单周期硬布线控制器_1_lui , \单周期硬布线控制器_1_memtoreg , \单周期硬布线控制器_1_memwrite , \单周期硬布线控制器_1_regwrite ,
       \单周期硬布线控制器_1_s_type , \单周期硬布线控制器_1_sb , \单周期硬布线控制器_1_uret ;
  wire [3:0] ex_mem_1_selectout, id_ex_1_aluopout, multiplexer_8_out, multiplexer_10_out,
       \单周期硬布线控制器_1_alu_op ;
  wire [4:0] EX_W_num, ID_Func, ID_R1_num, ID_R2_num, MEM_W_num, multiplexer_9_out, W_num;
  wire [11:0] shifter_2_out;
  wire [12:0] CNT_num;
  wire [15:0] adder_2_out, counter_4_q, \LoadUse次数 , shifter_1_out, \总周期数 , \插入气泡数 , \无条件分支数 , \条件分支成功数 ;
  wire [19:0] shifter_3_out;
  wire [31:0] adder_6_out, bit_extender_1_out, bit_extender_2_out, bit_extender_3_out, bit_extender_4_out,
       bit_extender_5_out, BPC, EX_IR, ex_mem_1_resultout, ex_mem_1_uout, EX_R1, EX_R2, id_ex_1_bout,
       id_ex_1_iout, id_ex_1_jout, id_ex_1_sout, id_ex_1_uout, ID_IR, IF_IR, JPC, MEM_IR, mem_wb_1_mddateout,
       mem_wb_1_resultout, mem_wb_1_uout, mips_ram_1_p8, multiplexer_1_out, multiplexer_2_out,
       multiplexer_6_out, multiplexer_7_out, multiplexer_11_out, multiplexer_12_out, multiplexer_13_out,
       PC_4, PCin, R1, R2, Result, shifter_4_out, shifter_5_out, WB_IR;

  Button \u_总复位  (.out(RST));
  Button _1 (.out(IR1));
  Button _2 (.out(IR2));
  Button _3 (.out(IR3));
  // Probe on \总周期数 
  // Probe on \总周期数 
  Button \u_继续运行  (.out(Go));
  LED #(.active("true")) led_1 (.in(W1));
  LED #(.active("true")) led_2 (.in(W2));
  LED #(.active("true")) led_3 (.in(W3));
  not not_1 (not_1_out, DataHazzard);
  not not_2 (not_2_out, halt);
  Hex_Digit_Display hex_digit_display_1 (.value(LedData[31:28]));  // open: dp
  // Probe on IF_PC[19:0]
  // RiscV_Probe riscv_probe_1: pin names not known; wires that end beside it: IF_IR
  not not_3 (not_3_out, halt);
  Counter #(.width(16), .max('hffff), .ongoal("wrap"), .trigger("rising"), .behavior("new")) counter_1 (
    .count(not_3_out), .Q(\总周期数 ), .clk(CLK), .clr(RST));  // open: load, D, carry, preset, down
  Hex_Digit_Display hex_digit_display_2 (.value(LedData[23:20]));  // open: dp
  Hex_Digit_Display hex_digit_display_3 (.value(LedData[27:24]));  // open: dp
  // Probe on ID_PC[19:0]
  // RiscV_Probe riscv_probe_2: pin names not known; wires that end beside it: {ID_IR[31], ID_Func[4], ID_IR[29:26], ID_Func[3], ID_IR[24:15], ID_Func[2:0], ID_IR[11:0]}
  and and_1 (and_1_out, not_1_out, not_2_out);
  Hex_Digit_Display hex_digit_display_4 (.value(LedData[15:12]));  // open: dp
  Hex_Digit_Display hex_digit_display_5 (.value(LedData[19:16]));  // open: dp
  Counter #(.width(16), .max('hffff), .ongoal("wrap"), .trigger("rising"), .behavior("new")) counter_2 (
    .count(B), .Q(\条件分支成功数 ), .clk(CLK), .clr(RST));  // open: load, D, carry, preset, down
  Register #(.width(32), .trigger("rising"), .Select("low")) PC (
    .D(PCin), .en(and_1_out), .Q(IF_PC), .clk(CLK), .clr(RST));
  Multiplexer #(.select(1), .width(32), .disabled("Z"), .enable("false")) multiplexer_1 (
    .in0(PC_4), .in1(BPC), .out(multiplexer_1_out), .sel(B));
  Hex_Digit_Display hex_digit_display_6 (.value(LedData[11:8]));  // open: dp
  Hex_Digit_Display hex_digit_display_7 (.value(LedData[7:4]));  // open: dp
  // Probe on EX_PC[19:0]
  // RiscV_Probe riscv_probe_3: pin names not known; wires that end beside it: EX_IR
  \数据冲突判断  \u_数据冲突判断_1  (
    .ID_R1_num(ID_R1_num), .EX_W_num(EX_W_num), .EX_RegWrite(EX_RegWrite), .ID_R2_num(ID_R2_num),
    .MEM_W_num(MEM_W_num), .MEM_RegWrite(MEM_RegWrite), .OP(ID_IR[6:2]), .Func(ID_Func),
    .DataHazzard(DataHazzard), .ecall(ecall));
  Adder #(.width(32)) adder_1 (.a(IF_PC), .b(32'h4), .out(PC_4));  // open: cin, cout
  Multiplexer #(.select(1), .width(32), .disabled("Z"), .enable("false")) multiplexer_2 (
    .in0(multiplexer_1_out), .in1(JPC), .out(multiplexer_2_out), .sel(JAL));
  Hex_Digit_Display hex_digit_display_8 (.value(LedData[3:0]));  // open: dp
  or or_1 (or_1_out, JALR, JAL);
  Register #(.width(1), .trigger("falling"), .Select("low")) register_1 (.en(en), .clk(CLK));  // open: D, Q, clr
  // Probe on \总周期数 
  // Probe on M_PC[19:0]
  // RiscV_Probe riscv_probe_4: pin names not known; wires that end beside it: MEM_IR
  Counter #(.width(16), .max('hffff), .ongoal("wrap"), .trigger("rising"), .behavior("new")) counter_3 (
    .count(or_1_out), .Q(\无条件分支数 ), .clk(CLK), .clr(RST));  // open: load, D, carry, preset, down
  ROM #(.addrWidth(10), .dataWidth(32), .Select("high")) rom_1 (.addr(IF_PC[11:2]), .data(IF_IR));
  Multiplexer #(.select(1), .width(32), .disabled("Z"), .enable("false")) multiplexer_3 (
    .in0(multiplexer_2_out), .in1(Result), .out(PCin), .sel(JALR));
  // Probe on \总周期数 
  // Probe on \无条件分支数 
  // Probe on \条件分支成功数 
  // Probe on \插入气泡数 
  // Probe on \LoadUse次数 
  Adder #(.width(16)) adder_2 (.a(\条件分支成功数 ), .b(\无条件分支数 ), .out(adder_2_out));  // open: cin, cout
  not not_4 (not_4_out, halt);
  IF_ID if_id_1 (
    .IRin(IF_IR), .PCin(IF_PC),
    .IRout({ID_IR[31], ID_Func[4], ID_IR[29:26], ID_Func[3], ID_IR[24:15], ID_Func[2:0], ID_IR[11:0]}),
    .PCout(ID_PC), .RST(or_2_out), .EN(and_2_out), .CLK(CLK));
  or or_2 (or_2_out, JAL, RST, B, JALR);
  and and_2 (and_2_out, en, not_5_out);
  not not_5 (not_5_out, DataHazzard);
  // Probe on IF_PC[11:0]
  // Probe on WB_PC[19:0]
  // RiscV_Probe riscv_probe_5: pin names not known; wires that end beside it: WB_IR
  Shifter #(.width(16), .shift("ll")) shifter_1 (.in(adder_2_out), .\dist (4'b0001), .out(shifter_1_out));
  and and_3 (and_3_out, not_4_out, DataHazzard);
  Counter #(.width(16), .max('hffff), .ongoal("wrap"), .trigger("rising"), .behavior("new")) counter_4 (
    .count(and_3_out), .Q(counter_4_q), .clk(CLK), .clr(RST));  // open: load, D, carry, preset, down
  // Probe on ID_PC[11:0]
  // Probe on EX_PC[11:0]
  Adder #(.width(16)) adder_3 (.a(shifter_1_out), .b(counter_4_q), .out(\插入气泡数 ));  // open: cin, cout
  // RiscV_Probe riscv_probe_6: pin names not known; wires that end beside it: {ID_IR[31], ID_Func[4], ID_IR[29:26], ID_Func[3], ID_IR[24:15], ID_Func[2:0], ID_IR[11:0]}
  // Probe on M_PC[11:0]
  D_Flip_Flop #(.trigger("high"), .Pre_Clr_Positions("LEGACY"), .NegatePresetClear("false"), .enable("true"), .NewFFLayout("false")) d_ff_1 (.Q(d_ff_1_q));  // open: clk, D, Qn, preset, en, reset
  // Probe on 13'hc
  // Probe on WB_PC[11:0]
  Comparator #(.width(13), .mode("twosComplement")) comparator_1 (
    .a(CNT_num), .b(13'hc), .eq(comparator_1_eq), .lt(comparator_1_lt));  // open: gt
  Clock #(.highDuration(1), .lowDuration(1)) clock_1 (.out(clock_1_out));
  nand nand_1 (nand_1_out, d_ff_1_q, comparator_1_eq);
  Counter #(.width(13), .max('h1fff), .ongoal("stay"), .trigger("rising"), .behavior("old")) counter_5 (
    .count(comparator_1_lt), .Q(CNT_num), .clk(clock_1_out));  // open: load, D, carry, clr, preset
  \单周期硬布线控制器  \u_单周期硬布线控制器_1  (
    .Funct(ID_Func), .OP(ID_IR[6:2]), .ALU_OP(\单周期硬布线控制器_1_alu_op ), .MemToReg(\单周期硬布线控制器_1_memtoreg ),
    .MemWrite(\单周期硬布线控制器_1_memwrite ), .ALU_SRC(\单周期硬布线控制器_1_alu_src ), .RegWrite(\单周期硬布线控制器_1_regwrite ),
    .ecall(ecall), .S_type(\单周期硬布线控制器_1_s_type ), .Jalr(\单周期硬布线控制器_1_jalr ), .Beq(\单周期硬布线控制器_1_beq ),
    .JAL(\单周期硬布线控制器_1_jal ), .Bne(\单周期硬布线控制器_1_bne ), .in_3(ID_IR[21]), .uret(\单周期硬布线控制器_1_uret ),
    .SB(\单周期硬布线控制器_1_sb ), .BLTU(\单周期硬布线控制器_1_bltu ), .CSRRSI(\单周期硬布线控制器_1_csrrsi ),
    .CSRRCI(\单周期硬布线控制器_1_csrrci ), .LUI(\单周期硬布线控制器_1_lui ));  // open: BLT, BGE, AUIPC
  Multiplexer #(.select(1), .width(5), .disabled("Z"), .enable("false")) multiplexer_4 (
    .in0(ID_IR[19:15]), .in1(5'b01010), .out(ID_R1_num), .sel(ecall));
  Multiplexer #(.select(1), .width(5), .disabled("Z"), .enable("false")) multiplexer_5 (
    .in0(ID_IR[24:20]), .in1(5'b10001), .out(ID_R2_num), .sel(ecall));
  assign bit_extender_1_out = {{20{ID_IR[31]}}, {ID_IR[31], ID_Func[4], ID_IR[29:26], ID_Func[3], ID_IR[24:20]}};  // Bit_Extender bit_extender_1
  assign bit_extender_2_out = {{20{ID_IR[31]}}, {ID_IR[31], ID_Func[4], ID_IR[29:26], ID_Func[3], ID_IR[11:7]}};  // Bit_Extender bit_extender_2
  assign bit_extender_3_out = {{12{1'b0}}, {ID_IR[31], ID_Func[4], ID_IR[29:26], ID_Func[3], ID_IR[24:15], ID_Func[2:0]}};  // Bit_Extender bit_extender_3
  Shifter #(.width(12), .shift("ll")) shifter_2 (
    .in({ID_IR[31], ID_IR[7], ID_Func[4], ID_IR[29:26], ID_Func[3], ID_IR[11:8]}), .\dist (4'b0001),
    .out(shifter_2_out));
  Shifter #(.width(20), .shift("ll")) shifter_3 (
    .in({ID_IR[31], ID_IR[19:15], ID_Func[2:0], ID_IR[20], ID_Func[4], ID_IR[29:26], ID_Func[3], ID_IR[24:21]}),
    .\dist (5'b00001), .out(shifter_3_out));
  assign CLK = nand_1_out ? clock_1_out : 1'bz;  // Controlled_Buffer controlled_buffer_1
  not not_6 (not_6_out, CLK);
  Regifile regifile_1 (
    .Din(RDin), .Clk(not_6_out), .R1(R1), .R2(R2), .WE(RegWrite), .W_num(W_num), .R1_num(ID_R1_num),
    .R2_num(ID_R2_num));
  Shifter #(.width(32), .shift("ll")) shifter_4 (.in(bit_extender_3_out), .\dist (5'b01100), .out(shifter_4_out));
  assign bit_extender_4_out = {{20{shifter_2_out[11]}}, shifter_2_out};  // Bit_Extender bit_extender_4
  assign bit_extender_5_out = {{12{shifter_3_out[19]}}, shifter_3_out};  // Bit_Extender bit_extender_5
  Pull_Resistor #(.pull(1)) pull_resistor_1 (.node(CLK));
  ID_EX id_ex_1 (
    .JALin(\单周期硬布线控制器_1_jal ), .JALRin(\单周期硬布线控制器_1_jalr ), .SBin(\单周期硬布线控制器_1_sb ),
    .BLTUin(\单周期硬布线控制器_1_bltu ), .URETin(\单周期硬布线控制器_1_uret ), .CSRRSIin(\单周期硬布线控制器_1_csrrsi ),
    .RST(or_3_out), .EN(en), .CLK(CLK), .JALout(JAL), .SBout(id_ex_1_sbout), .JALRout(JALR),
    .BLTUout(id_ex_1_bltuout), .LUIout(id_ex_1_luiout), .LUIin(\单周期硬布线控制器_1_lui ), .Beqin(\单周期硬布线控制器_1_beq ),
    .Beqout(id_ex_1_beqout), .Bnein(\单周期硬布线控制器_1_bne ), .Bneout(id_ex_1_bneout),
    .MemToRegin(\单周期硬布线控制器_1_memtoreg ), .MemToRegout(id_ex_1_memtoregout),
    .MemWritein(\单周期硬布线控制器_1_memwrite ), .MemWriteout(id_ex_1_memwriteout), .AluOPin(\单周期硬布线控制器_1_alu_op ),
    .AluOPout(id_ex_1_aluopout), .AluSrcBin(\单周期硬布线控制器_1_alu_src ), .AluSrcBout(id_ex_1_alusrcbout),
    .RegWritein(\单周期硬布线控制器_1_regwrite ), .RegWriteout(EX_RegWrite), .Stypein(\单周期硬布线控制器_1_s_type ),
    .Stypeout(id_ex_1_stypeout), .haltin(ecall), .haltout(EX_ecall), .R1out(EX_R1), .R1in(R1), .R2out(EX_R2),
    .R2in(R2), .PCin(ID_PC), .PCout(EX_PC), .Iin(bit_extender_1_out), .Iout(id_ex_1_iout),
    .Sin(bit_extender_2_out), .Sout(id_ex_1_sout), .Uin(shifter_4_out), .Uout(id_ex_1_uout),
    .Bin(bit_extender_4_out), .Bout(id_ex_1_bout), .Jin(bit_extender_5_out), .Jout(id_ex_1_jout),
    .IRin({ID_IR[31], ID_Func[4], ID_IR[29:26], ID_Func[3], ID_IR[24:15], ID_Func[2:0], ID_IR[11:0]}),
    .IRout(EX_IR), .CSRRCIin(\单周期硬布线控制器_1_csrrci ), .W_out_2(EX_W_num), .W_out(ID_IR[11:7]));  // open: URETout, CSRRSIout, CSRRCIout, R1Forwardin, R1forwardout, R2Forwardin, R2forwardout
  or or_3 (or_3_out, JAL, RST, DataHazzard, B, JALR);
  or or_4 (or_4_out, JAL, JALR);
  Comparator #(.width(32), .mode("twosComplement")) comparator_2 (
    .a(32'h1), .b(Result), .eq(comparator_2_eq));  // open: gt, lt
  not not_7 (not_7_out, equal);
  Comparator #(.width(32), .mode("twosComplement")) comparator_3 (
    .a(EX_R2), .b(32'h22), .eq(comparator_3_eq));  // open: gt, lt
  and and_4 (and_4_out, id_ex_1_bltuout, comparator_2_eq);
  and and_5 (and_5_out, id_ex_1_beqout, equal);
  and and_6 (and_6_out, not_7_out, id_ex_1_bneout);
  Multiplexer #(.select(1), .width(32), .disabled("Z"), .enable("false")) multiplexer_6 (
    .in0(id_ex_1_iout), .in1(id_ex_1_sout), .out(multiplexer_6_out), .sel(id_ex_1_stypeout));
  and and_7 (and_7_out, EX_ecall, comparator_3_eq);
  or or_5 (B, and_4_out, and_5_out, and_6_out);
  Multiplexer #(.select(1), .width(32), .disabled("Z"), .enable("false")) multiplexer_7 (
    .in0(EX_R2), .in1(multiplexer_6_out), .out(multiplexer_7_out), .sel(id_ex_1_alusrcbout));
  Adder #(.width(32)) adder_4 (.a(EX_PC), .b(id_ex_1_bout), .out(BPC));  // open: cin, cout
  Adder #(.width(32)) adder_5 (.a(id_ex_1_jout), .b(EX_PC), .out(JPC));  // open: cin, cout
  Register #(.width(32), .trigger("rising"), .Select("low")) register_2 (
    .D(EX_R1), .en(and_7_out), .Q(LedData), .clk(CLK), .clr(RST));
  Multiplexer #(.select(2), .width(4), .disabled("Z"), .enable("false")) multiplexer_8 (
    .in0(4'b0001), .in1(4'b0010), .in2(4'b0100), .in3(4'b1000), .out(multiplexer_8_out), .sel(Result[1:0]));
  Multiplexer #(.select(2), .width(5), .disabled("Z"), .enable("false")) multiplexer_9 (
    .in0({5{1'b0}}), .in1(5'b01000), .in2(5'b10000), .in3(5'b11000), .out(multiplexer_9_out),
    .sel(Result[1:0]));
  Shifter #(.width(32), .shift("ll")) shifter_5 (.in(EX_R2), .\dist (multiplexer_9_out), .out(shifter_5_out));
  ALU alu_1 (
    .X(EX_R1), .Y(multiplexer_7_out), .AluOP(id_ex_1_aluopout), .Equal(equal), .Result(Result), .out_6(less));  // open: Result_2, out_4
  Multiplexer #(.select(1), .width(4), .disabled("Z"), .enable("false")) multiplexer_10 (
    .in0(4'b1111), .in1(multiplexer_8_out), .out(multiplexer_10_out), .sel(id_ex_1_sbout));
  Multiplexer #(.select(1), .width(32), .disabled("Z"), .enable("false")) multiplexer_11 (
    .in0(EX_R2), .in1(shifter_5_out), .out(multiplexer_11_out), .sel(id_ex_1_sbout));
  not not_8 (not_8_out, comparator_4_eq);
  Comparator #(.width(32), .mode("twosComplement")) comparator_4 (
    .a(EX_R2), .b(32'h22), .eq(comparator_4_eq));  // open: gt, lt
  Register #(.width(1), .trigger("rising"), .Select("low")) register_3 (
    .D(not_8_out), .en(EX_ecall), .Q(register_3_q), .clk(CLK));  // open: clr
  EX_MEM ex_mem_1 (
    .IRin(EX_IR), .PCin(EX_PC), .haltin(register_3_q), .Jin(or_4_out), .W_in(EX_W_num), .Resultin(Result),
    .MemToRegin(id_ex_1_memtoregout), .MemWritein(id_ex_1_memwriteout), .RegWritein(EX_RegWrite),
    .Selectin(multiplexer_10_out), .MDin(multiplexer_11_out), .IRout(MEM_IR), .PCout(M_PC),
    .haltout(ex_mem_1_haltout), .Jout(ex_mem_1_jout), .W_out(MEM_W_num), .Resultout(ex_mem_1_resultout),
    .MemToRegout(ex_mem_1_memtoregout), .MemWriteout(MemWrite), .RegWriteout(MEM_RegWrite),
    .Selectout(ex_mem_1_selectout), .MDout(MDin), .RST(RST), .EN(en), .CLK(CLK), .LUIout(ex_mem_1_luiout),
    .LUIin(id_ex_1_luiout), .Uout(ex_mem_1_uout), .Uin(id_ex_1_uout));
  not not_9 (not_9_out, MemWrite);
  // MIPS_RAM mips_ram_1: pin names not known; wires that end beside it: ex_mem_1_resultout[11:2], MDin, MemWrite, ex_mem_1_selectout, CLK, not_9_out, RST, mips_ram_1_p8
  MEM_WB mem_wb_1 (
    .IRin(MEM_IR), .PCin(M_PC), .haltin(ex_mem_1_haltout), .Jin(ex_mem_1_jout), .W_in(MEM_W_num),
    .Resultin(ex_mem_1_resultout), .MemToRegin(ex_mem_1_memtoregout), .RegWritein(MEM_RegWrite),
    .MDdatein(mips_ram_1_p8), .LUIin(ex_mem_1_luiout), .Uin(ex_mem_1_uout), .IRout(WB_IR), .PCout(WB_PC),
    .haltout(mem_wb_1_haltout), .Jout(mem_wb_1_jout), .W_out(W_num), .Resultout(mem_wb_1_resultout),
    .MemToRegout(mem_wb_1_memtoregout), .RegWriteout(RegWrite), .MDdateout(mem_wb_1_mddateout),
    .LUIout(mem_wb_1_luiout), .Uout(mem_wb_1_uout), .RST(RST), .EN(en), .CLK(CLK));
  Adder #(.width(32)) adder_6 (.a(WB_PC), .b(32'h4), .out(adder_6_out));  // open: cin, cout
  Multiplexer #(.select(1), .width(32), .disabled("Z"), .enable("false")) multiplexer_12 (
    .in0(mem_wb_1_resultout), .in1(mem_wb_1_mddateout), .out(multiplexer_12_out), .sel(mem_wb_1_memtoregout));
  Multiplexer #(.select(1), .width(32), .disabled("Z"), .enable("false")) multiplexer_13 (
    .in0(multiplexer_12_out), .in1(adder_6_out), .out(multiplexer_13_out), .sel(mem_wb_1_jout));
  and and_8 (halt, mem_wb_1_haltout, ~Go);  // AND_Gate
  not not_10 (en, halt);
  Multiplexer #(.select(1), .width(32), .disabled("Z"), .enable("false")) multiplexer_14 (
    .in0(multiplexer_13_out), .in1(mem_wb_1_uout), .out(RDin), .sel(mem_wb_1_luiout));

  // Other names for the same wires on the sheet: ID_IR (some bits) = ID_Func; ID_OP[4:0] = ID_IR[6:2];
  //   MEM_PC[31:0] = M_PC

  // Notes on the sheet:
  //   中断源
  //   时空图监测，可删除
  //   中断等待指示
  //   数码管输出
  //   指令存储器
  //   contents of rom_1 (hex, n*v repeats v):
  //   800e13 fedc04b7 fff00413 1045413 84e4b3 900533 2200893 73 ba984b7 900533 73 76544b7 900533 73
  //   32104b7 900533 73 fffe0e13 fa0e1ee3 a00893 73
  //   控制位
  //   指令探针
  //   流水调试日志用
  //   暂停节拍，不能为0
  //   指令字
  //   戳工具置1进入计数暂停模式，ctrl+k时钟自动运行到对应节拍暂停
  //   ctrl+k关闭时钟连续运行，将控制位置零，进入单步调试模式调试
  //   JAL
  //   JALR
  //   URET
  //   I型
  //   S型
  //   U型
  //   B型
  //   J型
  //   Beq
  //   Bne
  //   MemToReg
  //   MemWrite
  //   AluOP
  //   AluSrcB
  //   RegWrite
  //   可计数暂停的时钟源
  //   为方便自动评测，需要输出流水线各段保存的PC值，注意是PC不是PC+4，另外ID段寄存器写入信息，Mem段内存写入信息也要输出
  //   数据存储器
endmodule
module \重定向流水线  (
  output RegWrite,
  output MemWrite,
  output [31:0] IF_PC,
  output [31:0] ID_PC,
  output [31:0] EX_PC,
  output [31:0] M_PC,
  output [31:0] WB_PC,
  output [31:0] RDin,
  output [31:0] MDin,
  output [31:0] LedData
);

  wire and_1_out, and_2_out, and_3_out, and_4_out, and_5_out, and_6_out, and_7_out, B, CLK, clock_1_out,
       comparator_1_eq, comparator_1_lt, comparator_2_eq, comparator_3_eq, comparator_4_eq, d_ff_1_q,
       DataHazzard, ecall, en, equal, EX_ecall, ex_mem_1_haltout, ex_mem_1_jout, ex_mem_1_luiout,
       ex_mem_1_memtoregout, EX_MemToReg, EX_RegWrite, Go, halt, id_ex_1_alusrcbout, id_ex_1_beqout,
       id_ex_1_bltuout, id_ex_1_bneout, id_ex_1_luiout, id_ex_1_memwriteout, id_ex_1_sbout, id_ex_1_stypeout,
       IR1, IR2, IR3, JAL, JALR, less, Load_Used, MEM_RegWrite, mem_wb_1_haltout, mem_wb_1_jout,
       mem_wb_1_luiout, mem_wb_1_memtoregout, nand_1_out, not_1_out, not_2_out, not_3_out, not_4_out,
       not_5_out, not_6_out, not_7_out, not_8_out, not_9_out, or_1_out, or_2_out, or_3_out, or_4_out,
       register_2_q, RST, W1, W2, W3, \单周期硬布线控制器_1_alu_src , \单周期硬布线控制器_1_beq , \单周期硬布线控制器_1_bltu ,
       \单周期硬布线控制器_1_bne , \单周期硬布线控制器_1_csrrci , \单周期硬布线控制器_1_csrrsi , \单周期硬布线控制器_1_jal , \单周期硬布线控制器_1_jalr ,
       \单周期硬布线控制器_1_lui , \单周期硬布线控制器_1_memtoreg , \单周期硬布线控制器_1_memwrite , \单周期硬布线控制器_1_regwrite ,
       \单周期硬布线控制器_1_s_type , \单周期硬布线控制器_1_sb , \单周期硬布线控制器_1_uret ;
  wire [1:0] id_ex_1_r1forwardout, id_ex_1_r2forwardout, R1Forward, R2Forward;
  wire [3:0] ex_mem_1_selectout, id_ex_1_aluopout, multiplexer_10_out, multiplexer_12_out,
       \单周期硬布线控制器_1_alu_op ;
  wire [4:0] EX_W_num, ID_Func, ID_R1_num, ID_R2_num, MEM_W_num, multiplexer_11_out, W_num;
  wire [11:0] shifter_2_out;
  wire [12:0] CNT_num;
  wire [15:0] adder_2_out, \LoadUse次数 , shifter_1_out, \总周期数 , \插入气泡数 , \无条件分支数 , \条件分支成功数 ;
  wire [19:0] shifter_3_out;
  wire [31:0] adder_6_out, adder_7_out, bit_extender_1_out, bit_extender_2_out, bit_extender_3_out,
       bit_extender_4_out, bit_extender_5_out, BPC, EX_IR, ex_mem_1_resultout, ex_mem_1_uout, EX_R1, EX_R2,
       id_ex_1_bout, id_ex_1_iout, id_ex_1_jout, id_ex_1_r1out, id_ex_1_r2out, id_ex_1_sout, id_ex_1_uout,
       ID_IR, IF_IR, JPC, MEM_IR, MEM_Rin, mem_wb_1_mddateout, mem_wb_1_resultout, mem_wb_1_uout,
       mips_ram_1_p8, multiplexer_1_out, multiplexer_2_out, multiplexer_7_out, multiplexer_8_out,
       multiplexer_13_out, multiplexer_14_out, multiplexer_15_out, multiplexer_17_out, multiplexer_18_out,
       PC_4, PCin, R1, R2, Result, shifter_4_out, shifter_5_out, WB_IR;

  Button \u_总复位  (.out(RST));
  Button _1 (.out(IR1));
  Button _2 (.out(IR2));
  Button _3 (.out(IR3));
  // Probe on \总周期数 
  // Probe on \总周期数 
  Button \u_继续运行  (.out(Go));
  LED #(.active("true")) led_1 (.in(W1));
  LED #(.active("true")) led_2 (.in(W2));
  LED #(.active("true")) led_3 (.in(W3));
  not not_1 (not_1_out, Load_Used);
  not not_2 (not_2_out, halt);
  Hex_Digit_Display hex_digit_display_1 (.value(LedData[31:28]));  // open: dp
  // Probe on IF_PC[19:0]
  // RiscV_Probe riscv_probe_1: pin names not known; wires that end beside it: IF_IR
  not not_3 (not_3_out, halt);
  Counter #(.width(16), .max('hffff), .ongoal("wrap"), .trigger("rising"), .behavior("new")) counter_1 (
    .count(not_3_out), .Q(\总周期数 ), .clk(CLK), .clr(RST));  // open: load, D, carry, preset, down
  Hex_Digit_Display hex_digit_display_2 (.value(LedData[23:20]));  // open: dp
  Hex_Digit_Display hex_digit_display_3 (.value(LedData[27:24]));  // open: dp
  // Probe on ID_PC[19:0]
  // RiscV_Probe riscv_probe_2: pin names not known; wires that end beside it: {ID_IR[31], ID_Func[4], ID_IR[29:26], ID_Func[3], ID_IR[24:15], ID_Func[2:0], ID_IR[11:0]}
  and and_1 (and_1_out, not_1_out, not_2_out);
  Hex_Digit_Display hex_digit_display_4 (.value(LedData[15:12]));  // open: dp
  Hex_Digit_Display hex_digit_display_5 (.value(LedData[19:16]));  // open: dp
  Counter #(.width(16), .max('hffff), .ongoal("wrap"), .trigger("rising"), .behavior("new")) counter_2 (
    .count(B), .Q(\条件分支成功数 ), .clk(CLK), .clr(RST));  // open: load, D, carry, preset, down
  Register #(.width(32), .trigger("rising"), .Select("low")) PC (
    .D(PCin), .en(and_1_out), .Q(IF_PC), .clk(CLK), .clr(RST));
  Multiplexer #(.select(1), .width(32), .disabled("Z"), .enable("false")) multiplexer_1 (
    .in0(PC_4), .in1(BPC), .out(multiplexer_1_out), .sel(B));
  Hex_Digit_Display hex_digit_display_6 (.value(LedData[11:8]));  // open: dp
  Hex_Digit_Display hex_digit_display_7 (.value(LedData[7:4]));  // open: dp
  // Probe on EX_PC[19:0]
  // RiscV_Probe riscv_probe_3: pin names not known; wires that end beside it: EX_IR
  Adder #(.width(32)) adder_1 (.a(IF_PC), .b(32'h4), .out(PC_4));  // open: cin, cout
  Multiplexer #(.select(1), .width(32), .disabled("Z"), .enable("false")) multiplexer_2 (
    .in0(multiplexer_1_out), .in1(JPC), .out(multiplexer_2_out), .sel(JAL));
  Hex_Digit_Display hex_digit_display_8 (.value(LedData[3:0]));  // open: dp
  or or_1 (or_1_out, JALR, JAL);
  // Probe on \总周期数 
  // Probe on M_PC[19:0]
  // RiscV_Probe riscv_probe_4: pin names not known; wires that end beside it: MEM_IR
  Counter #(.width(16), .max('hffff), .ongoal("wrap"), .trigger("rising"), .behavior("new")) counter_3 (
    .count(or_1_out), .Q(\无条件分支数 ), .clk(CLK), .clr(RST));  // open: load, D, carry, preset, down
  ROM #(.addrWidth(10), .dataWidth(32), .Select("high")) rom_1 (.addr(IF_PC[11:2]), .data(IF_IR));
  Multiplexer #(.select(1), .width(32), .disabled("Z"), .enable("false")) multiplexer_3 (
    .in0(multiplexer_2_out), .in1(Result), .out(PCin), .sel(JALR));
  // Probe on \总周期数 
  // Probe on \无条件分支数 
  // Probe on \条件分支成功数 
  // Probe on \插入气泡数 
  // Probe on \LoadUse次数 
  Adder #(.width(16)) adder_2 (.a(\条件分支成功数 ), .b(\无条件分支数 ), .out(adder_2_out));  // open: cin, cout
  not not_4 (not_4_out, halt);
  IF_ID if_id_1 (
    .IRin(IF_IR), .PCin(IF_PC),
    .IRout({ID_IR[31], ID_Func[4], ID_IR[29:26], ID_Func[3], ID_IR[24:15], ID_Func[2:0], ID_IR[11:0]}),
    .PCout(ID_PC), .RST(or_2_out), .EN(and_2_out), .CLK(CLK));
  or or_2 (or_2_out, JAL, RST, B, JALR);
  and and_2 (and_2_out, en, not_5_out);
  not not_5 (not_5_out, Load_Used);
  // Probe on IF_PC[11:0]
  // Probe on WB_PC[19:0]
  // RiscV_Probe riscv_probe_5: pin names not known; wires that end beside it: WB_IR
  Shifter #(.width(16), .shift("ll")) shifter_1 (.in(adder_2_out), .\dist (4'b0001), .out(shifter_1_out));
  and and_3 (and_3_out, not_4_out, Load_Used);
  Counter #(.width(16), .max('hffff), .ongoal("wrap"), .trigger("rising"), .behavior("new")) counter_4 (
    .count(and_3_out), .Q(\LoadUse次数 ), .clk(CLK), .clr(RST));  // open: load, D, carry, preset, down
  // Probe on ID_PC[11:0]
  // Probe on EX_PC[11:0]
  Adder #(.width(16)) adder_3 (.a(shifter_1_out), .b(\LoadUse次数 ), .out(\插入气泡数 ));  // open: cin, cout
  // RiscV_Probe riscv_probe_6: pin names not known; wires that end beside it: {ID_IR[31], ID_Func[4], ID_IR[29:26], ID_Func[3], ID_IR[24:15], ID_Func[2:0], ID_IR[11:0]}
  // Probe on M_PC[11:0]
  D_Flip_Flop #(.trigger("high"), .Pre_Clr_Positions("LEGACY"), .NegatePresetClear("false"), .enable("true"), .NewFFLayout("false")) d_ff_1 (.Q(d_ff_1_q));  // open: clk, D, Qn, preset, en, reset
  // Probe on 13'hc
  // Probe on WB_PC[11:0]
  Comparator #(.width(13), .mode("twosComplement")) comparator_1 (
    .a(CNT_num), .b(13'hc), .eq(comparator_1_eq), .lt(comparator_1_lt));  // open: gt
  Clock #(.highDuration(1), .lowDuration(1)) clock_1 (.out(clock_1_out));
  nand nand_1 (nand_1_out, d_ff_1_q, comparator_1_eq);
  Counter #(.width(13), .max('h1fff), .ongoal("stay"), .trigger("rising"), .behavior("old")) counter_5 (
    .count(comparator_1_lt), .Q(CNT_num), .clk(clock_1_out));  // open: load, D, carry, clr, preset
  \单周期硬布线控制器  \u_单周期硬布线控制器_1  (
    .Funct(ID_Func), .OP(ID_IR[6:2]), .ALU_OP(\单周期硬布线控制器_1_alu_op ), .MemToReg(\单周期硬布线控制器_1_memtoreg ),
    .MemWrite(\单周期硬布线控制器_1_memwrite ), .ALU_SRC(\单周期硬布线控制器_1_alu_src ), .RegWrite(\单周期硬布线控制器_1_regwrite ),
    .ecall(ecall), .S_type(\单周期硬布线控制器_1_s_type ), .Jalr(\单周期硬布线控制器_1_jalr ), .Beq(\单周期硬布线控制器_1_beq ),
    .JAL(\单周期硬布线控制器_1_jal ), .Bne(\单周期硬布线控制器_1_bne ), .in_3(ID_IR[21]), .uret(\单周期硬布线控制器_1_uret ),
    .SB(\单周期硬布线控制器_1_sb ), .BLTU(\单周期硬布线控制器_1_bltu ), .CSRRSI(\单周期硬布线控制器_1_csrrsi ),
    .CSRRCI(\单周期硬布线控制器_1_csrrci ), .LUI(\单周期硬布线控制器_1_lui ));  // open: BLT, BGE, AUIPC
  Multiplexer #(.select(1), .width(5), .disabled("Z"), .enable("false")) multiplexer_4 (
    .in0(ID_IR[19:15]), .in1(5'b01010), .out(ID_R1_num), .sel(ecall));
  Multiplexer #(.select(1), .width(5), .disabled("Z"), .enable("false")) multiplexer_5 (
    .in0(ID_IR[24:20]), .in1(5'b10001), .out(ID_R2_num), .sel(ecall));
  assign bit_extender_1_out = {{20{ID_IR[31]}}, {ID_IR[31], ID_Func[4], ID_IR[29:26], ID_Func[3], ID_IR[24:20]}};  // Bit_Extender bit_extender_1
  assign bit_extender_2_out = {{20{ID_IR[31]}}, {ID_IR[31], ID_Func[4], ID_IR[29:26], ID_Func[3], ID_IR[11:7]}};  // Bit_Extender bit_extender_2
  assign bit_extender_3_out = {{12{1'b0}}, {ID_IR[31], ID_Func[4], ID_IR[29:26], ID_Func[3], ID_IR[24:15], ID_Func[2:0]}};  // Bit_Extender bit_extender_3
  Shifter #(.width(12), .shift("ll")) shifter_2 (
    .in({ID_IR[31], ID_IR[7], ID_Func[4], ID_IR[29:26], ID_Func[3], ID_IR[11:8]}), .\dist (4'b0001),
    .out(shifter_2_out));
  Shifter #(.width(20), .shift("ll")) shifter_3 (
    .in({ID_IR[31], ID_IR[19:15], ID_Func[2:0], ID_IR[20], ID_Func[4], ID_IR[29:26], ID_Func[3], ID_IR[24:21]}),
    .\dist (5'b00001), .out(shifter_3_out));
  assign CLK = nand_1_out ? clock_1_out : 1'bz;  // Controlled_Buffer controlled_buffer_1
  not not_6 (not_6_out, CLK);
  Regifile regifile_1 (
    .Din(RDin), .Clk(not_6_out), .R1(R1), .R2(R2), .WE(RegWrite), .W_num(W_num), .R1_num(ID_R1_num),
    .R2_num(ID_R2_num));
  Shifter #(.width(32), .shift("ll")) shifter_4 (.in(bit_extender_3_out), .\dist (5'b01100), .out(shifter_4_out));
  assign bit_extender_4_out = {{20{shifter_2_out[11]}}, shifter_2_out};  // Bit_Extender bit_extender_4
  assign bit_extender_5_out = {{12{shifter_3_out[19]}}, shifter_3_out};  // Bit_Extender bit_extender_5
  Pull_Resistor #(.pull(1)) pull_resistor_1 (.node(CLK));
  ID_EX id_ex_1 (
    .JALin(\单周期硬布线控制器_1_jal ), .JALRin(\单周期硬布线控制器_1_jalr ), .SBin(\单周期硬布线控制器_1_sb ),
    .BLTUin(\单周期硬布线控制器_1_bltu ), .URETin(\单周期硬布线控制器_1_uret ), .CSRRSIin(\单周期硬布线控制器_1_csrrsi ),
    .RST(or_3_out), .EN(en), .CLK(CLK), .JALout(JAL), .SBout(id_ex_1_sbout), .JALRout(JALR),
    .BLTUout(id_ex_1_bltuout), .LUIout(id_ex_1_luiout), .LUIin(\单周期硬布线控制器_1_lui ), .Beqin(\单周期硬布线控制器_1_beq ),
    .Beqout(id_ex_1_beqout), .Bnein(\单周期硬布线控制器_1_bne ), .Bneout(id_ex_1_bneout),
    .MemToRegin(\单周期硬布线控制器_1_memtoreg ), .MemToRegout(EX_MemToReg), .MemWritein(\单周期硬布线控制器_1_memwrite ),
    .MemWriteout(id_ex_1_memwriteout), .AluOPin(\单周期硬布线控制器_1_alu_op ), .AluOPout(id_ex_1_aluopout),
    .AluSrcBin(\单周期硬布线控制器_1_alu_src ), .AluSrcBout(id_ex_1_alusrcbout), .RegWritein(\单周期硬布线控制器_1_regwrite ),
    .RegWriteout(EX_RegWrite), .Stypein(\单周期硬布线控制器_1_s_type ), .Stypeout(id_ex_1_stypeout), .haltin(ecall),
    .haltout(EX_ecall), .R1out(id_ex_1_r1out), .R1in(R1), .R2out(id_ex_1_r2out), .R2in(R2), .PCin(ID_PC),
    .PCout(EX_PC), .Iin(bit_extender_1_out), .Iout(id_ex_1_iout), .Sin(bit_extender_2_out),
    .Sout(id_ex_1_sout), .Uin(shifter_4_out), .Uout(id_ex_1_uout), .Bin(bit_extender_4_out),
    .Bout(id_ex_1_bout), .Jin(bit_extender_5_out), .Jout(id_ex_1_jout),
    .IRin({ID_IR[31], ID_Func[4], ID_IR[29:26], ID_Func[3], ID_IR[24:15], ID_Func[2:0], ID_IR[11:0]}),
    .IRout(EX_IR), .CSRRCIin(\单周期硬布线控制器_1_csrrci ), .W_out_2(EX_W_num), .W_out(ID_IR[11:7]),
    .R1Forwardin(R1Forward), .R1forwardout(id_ex_1_r1forwardout), .R2Forwardin(R2Forward),
    .R2forwardout(id_ex_1_r2forwardout));  // open: URETout, CSRRSIout, CSRRCIout
  or or_3 (or_3_out, JAL, RST, Load_Used, B, JALR);
  or or_4 (or_4_out, JAL, JALR);
  Comparator #(.width(32), .mode("twosComplement")) comparator_2 (
    .a(32'h1), .b(Result), .eq(comparator_2_eq));  // open: gt, lt
  not not_7 (not_7_out, equal);
  Multiplexer #(.select(2), .width(32), .disabled("Z"), .enable("false")) multiplexer_6 (
    .in0(id_ex_1_r1out), .in1(RDin), .in2(MEM_Rin), .out(EX_R1), .sel(id_ex_1_r1forwardout));  // open: in3
  \数据相关检测  \u_数据相关检测_1  (
    .ID_R1_num(ID_R1_num), .EX_W_num(EX_W_num), .EX_RegWrite(EX_RegWrite), .EX_MemToReg(EX_MemToReg),
    .ID_R2_num(ID_R2_num), .MEM_W_num(MEM_W_num), .MEM_RegWrite(MEM_RegWrite), .OP(ID_IR[6:2]),
    .ecall(ecall), .Func(ID_Func), .R1Forward(R1Forward), .DataHazzard(DataHazzard), .R2Forward(R2Forward),
    .Load_Used(Load_Used));
  and and_4 (and_4_out, id_ex_1_bltuout, comparator_2_eq);
  and and_5 (and_5_out, id_ex_1_beqout, equal);
  and and_6 (and_6_out, not_7_out, id_ex_1_bneout);
  Multiplexer #(.select(1), .width(32), .disabled("Z"), .enable("false")) multiplexer_7 (
    .in0(id_ex_1_iout), .in1(id_ex_1_sout), .out(multiplexer_7_out), .sel(id_ex_1_stypeout));
  Comparator #(.width(32), .mode("twosComplement")) comparator_3 (
    .a(EX_R2), .b(32'h22), .eq(comparator_3_eq));  // open: gt, lt
  or or_5 (B, and_4_out, and_5_out, and_6_out);
  Multiplexer #(.select(1), .width(32), .disabled("Z"), .enable("false")) multiplexer_8 (
    .in0(EX_R2), .in1(multiplexer_7_out), .out(multiplexer_8_out), .sel(id_ex_1_alusrcbout));
  Adder #(.width(32)) adder_4 (.a(EX_PC), .b(id_ex_1_bout), .out(BPC));  // open: cin, cout
  Adder #(.width(32)) adder_5 (.a(id_ex_1_jout), .b(EX_PC), .out(JPC));  // open: cin, cout
  Multiplexer #(.select(2), .width(32), .disabled("Z"), .enable("false")) multiplexer_9 (
    .in0(id_ex_1_r2out), .in1(RDin), .in2(MEM_Rin), .out(EX_R2), .sel(id_ex_1_r2forwardout));  // open: in3
  and and_7 (and_7_out, EX_ecall, comparator_3_eq);
  Multiplexer #(.select(2), .width(4), .disabled("Z"), .enable("false")) multiplexer_10 (
    .in0(4'b0001), .in1(4'b0010), .in2(4'b0100), .in3(4'b1000), .out(multiplexer_10_out), .sel(Result[1:0]));
  Shifter #(.width(32), .shift("ll")) shifter_5 (.in(EX_R2), .\dist (multiplexer_11_out), .out(shifter_5_out));
  Multiplexer #(.select(2), .width(5), .disabled("Z"), .enable("false")) multiplexer_11 (
    .in0({5{1'b0}}), .in1(5'b01000), .in2(5'b10000), .in3(5'b11000), .out(multiplexer_11_out),
    .sel(Result[1:0]));
  ALU alu_1 (
    .X(EX_R1), .Y(multiplexer_8_out), .AluOP(id_ex_1_aluopout), .Equal(equal), .Result(Result), .out_6(less));  // open: Result_2, out_4
  Register #(.width(32), .trigger("rising"), .Select("low")) register_1 (
    .D(EX_R1), .en(and_7_out), .Q(LedData), .clk(CLK), .clr(RST));
  Multiplexer #(.select(1), .width(4), .disabled("Z"), .enable("false")) multiplexer_12 (
    .in0(4'b1111), .in1(multiplexer_10_out), .out(multiplexer_12_out), .sel(id_ex_1_sbout));
  Multiplexer #(.select(1), .width(32), .disabled("Z"), .enable("false")) multiplexer_13 (
    .in0(EX_R2), .in1(shifter_5_out), .out(multiplexer_13_out), .sel(id_ex_1_sbout));
  not not_8 (not_8_out, comparator_4_eq);
  Comparator #(.width(32), .mode("twosComplement")) comparator_4 (
    .a(EX_R2), .b(32'h22), .eq(comparator_4_eq));  // open: gt, lt
  Register #(.width(1), .trigger("rising"), .Select("low")) register_2 (
    .D(not_8_out), .en(EX_ecall), .Q(register_2_q), .clk(CLK));  // open: clr
  EX_MEM ex_mem_1 (
    .IRin(EX_IR), .PCin(EX_PC), .haltin(register_2_q), .Jin(or_4_out), .W_in(EX_W_num), .Resultin(Result),
    .MemToRegin(EX_MemToReg), .MemWritein(id_ex_1_memwriteout), .RegWritein(EX_RegWrite),
    .Selectin(multiplexer_12_out), .MDin(multiplexer_13_out), .IRout(MEM_IR), .PCout(M_PC),
    .haltout(ex_mem_1_haltout), .Jout(ex_mem_1_jout), .W_out(MEM_W_num), .Resultout(ex_mem_1_resultout),
    .MemToRegout(ex_mem_1_memtoregout), .MemWriteout(MemWrite), .RegWriteout(MEM_RegWrite),
    .Selectout(ex_mem_1_selectout), .MDout(MDin), .RST(RST), .EN(en), .CLK(CLK), .LUIout(ex_mem_1_luiout),
    .LUIin(id_ex_1_luiout), .Uout(ex_mem_1_uout), .Uin(id_ex_1_uout));
  not not_9 (not_9_out, MemWrite);
  Adder #(.width(32)) adder_6 (.a(M_PC), .b(32'h4), .out(adder_6_out));  // open: cin, cout
  Multiplexer #(.select(1), .width(32), .disabled("Z"), .enable("false")) multiplexer_14 (
    .in0(ex_mem_1_resultout), .in1(mips_ram_1_p8), .out(multiplexer_14_out), .sel(ex_mem_1_memtoregout));
  Multiplexer #(.select(1), .width(32), .disabled("Z"), .enable("false")) multiplexer_15 (
    .in0(multiplexer_14_out), .in1(adder_6_out), .out(multiplexer_15_out), .sel(ex_mem_1_jout));
  // MIPS_RAM mips_ram_1: pin names not known; wires that end beside it: ex_mem_1_resultout[11:2], MDin, MemWrite, ex_mem_1_selectout, CLK, not_9_out, RST, mips_ram_1_p8
  Multiplexer #(.select(1), .width(32), .disabled("Z"), .enable("false")) multiplexer_16 (
    .in0(multiplexer_15_out), .in1(ex_mem_1_uout), .out(MEM_Rin), .sel(ex_mem_1_luiout));
  MEM_WB mem_wb_1 (
    .IRin(MEM_IR), .PCin(M_PC), .haltin(ex_mem_1_haltout), .Jin(ex_mem_1_jout), .W_in(MEM_W_num),
    .Resultin(ex_mem_1_resultout), .MemToRegin(ex_mem_1_memtoregout), .RegWritein(MEM_RegWrite),
    .MDdatein(mips_ram_1_p8), .LUIin(ex_mem_1_luiout), .Uin(ex_mem_1_uout), .IRout(WB_IR), .PCout(WB_PC),
    .haltout(mem_wb_1_haltout), .Jout(mem_wb_1_jout), .W_out(W_num), .Resultout(mem_wb_1_resultout),
    .MemToRegout(mem_wb_1_memtoregout), .RegWriteout(RegWrite), .MDdateout(mem_wb_1_mddateout),
    .LUIout(mem_wb_1_luiout), .Uout(mem_wb_1_uout), .RST(RST), .EN(en), .CLK(CLK));
  Adder #(.width(32)) adder_7 (.a(WB_PC), .b(32'h4), .out(adder_7_out));  // open: cin, cout
  Multiplexer #(.select(1), .width(32), .disabled("Z"), .enable("false")) multiplexer_17 (
    .in0(mem_wb_1_resultout), .in1(mem_wb_1_mddateout), .out(multiplexer_17_out), .sel(mem_wb_1_memtoregout));
  Multiplexer #(.select(1), .width(32), .disabled("Z"), .enable("false")) multiplexer_18 (
    .in0(multiplexer_17_out), .in1(adder_7_out), .out(multiplexer_18_out), .sel(mem_wb_1_jout));
  and and_8 (halt, mem_wb_1_haltout, ~Go);  // AND_Gate
  not not_10 (en, halt);
  Multiplexer #(.select(1), .width(32), .disabled("Z"), .enable("false")) multiplexer_19 (
    .in0(multiplexer_18_out), .in1(mem_wb_1_uout), .out(RDin), .sel(mem_wb_1_luiout));

  // Other names for the same wires on the sheet: ID_IR (some bits) = ID_Func; ID_OP[4:0] = ID_IR[6:2];
  //   MEM_PC[31:0] = M_PC; WB_Rin[31:0] = RDin

  // Notes on the sheet:
  //   中断源
  //   时空图监测，可删除
  //   中断等待指示
  //   数码管输出
  //   指令存储器
  //   contents of rom_1 (hex, n*v repeats v):
  //   100493 100006f 100493 200913 300993 100006f 100493 200913 300993 100006f 100493 200913 300993
  //   100006f 100493 200913 300993 3ac000ef 100413 100493 1f49493 900533 2200893 73 24d493 48463 fedff06f
  //   900533 2200893 73 100493 249493 900533 2200893 73 48463 fedff06f 100493 1f49493 900533 2200893 73
  //   4034d493 900533 2200893 73 4044d493 900533 2200893 73 4044d493 900533 2200893 73 4044d493 900533
  //   2200893 73 4044d493 900533 2200893 73 4044d493 900533 2200893 73 4044d493 900533 2200893 73 4044d493
  //   900533 2200893 73 100413 1f41993 41f9d993 433 c00913 300b13 140413 f47413 800293 100313 499993
  //   89e9b3 1300533 2200893 73 406282b3 fe0294e3 140413 f00f93 1f47433 1c41413 800293 100313 49d993
  //   89e9b3 1300533 2200893 73 406282b3 fe0294e3 1c45413 406b0b33 b0463 f95ff06f 2b3 fff2c293 829293
  //   ff2e293 500533 2200893 73 fff00413 493 84a023 140413 448493 84a023 140413 448493 84a023 140413
  //   448493 84a023 140413 448493 84a023 140413 448493 84a023 140413 448493 84a023 140413 448493 84a023
  //   140413 448493 84a023 140413 448493 84a023 140413 448493 84a023 140413 448493 84a023 140413 448493
  //   84a023 140413 448493 84a023 140413 448493 84a023 140413 448493 84a023 140413 448493 140413 433
  //   3c00493 42983 4aa03 149a2b3 28663 134a023 1442023 ffc48493 fe9412e3 800533 2200893 73 440413 3c00493
  //   fc9416e3 a00893 73 800e13 fedc04b7 fff00413 1045413 84e4b3 900533 2200893 73 ba984b7 900533 73
  //   76544b7 900533 73 32104b7 900533 73 fffe0e13 fa0e1ee3 a00893 73 fff00293 313 1900413 841413 9700493
  //   940533 2200893 73 5484b3 494b313 fe0306e3 a00893 73 313 2000e13 493 100913 930023 900533 2200893 73
  //   12484b3 130313 fffe0e13 fe0e12e3 800e13 313 32483 900533 2200893 73 430313 fffe0e13 fe0e14e3 a00893
  //   73 ff100493 900533 2200893 73 148493 fe9068e3 900533 2200893 73 a00893 73 413 140413 800533 2200893
  //   73 240413 800533 2200893 73 340413 800533 2200893 73 440413 800533 2200893 73 540413 800533 2200893
  //   73 640413 800533 2200893 73 740413 800533 2200893 73 840413 800533 2200893 2200893 73 8067
  //   控制位
  //   指令探针
  //   流水调试日志用
  //   暂停节拍，不能为0
  //   指令字
  //   戳工具置1进入计数暂停模式，ctrl+k时钟自动运行到对应节拍暂停
  //   ctrl+k关闭时钟连续运行，将控制位置零，进入单步调试模式调试
  //   JAL
  //   JALR
  //   URET
  //   I型
  //   S型
  //   U型
  //   B型
  //   J型
  //   Beq
  //   Bne
  //   MemToReg
  //   MemWrite
  //   AluOP
  //   AluSrcB
  //   RegWrite
  //   可计数暂停的时钟源
  //   为方便自动评测，需要输出流水线各段保存的PC值，注意是PC不是PC+4，另外ID段寄存器写入信息，Mem段内存写入信息也要输出
  //   数据存储器
endmodule

module \中断按键参考电路  (
  input  \同步清零信号 ,
  output \与中断屏蔽位与 
);

  wire \_1号中断_out , and_1_out, clock_1_out, d_ff_1_q, or_1_out, or_2_out;

  Clock #(.highDuration(1), .lowDuration(1)) clock_1 (.out(clock_1_out));
  Button \_1号中断  (.out(\_1号中断_out ));
  or or_1 (or_1_out, \与中断屏蔽位与 , d_ff_1_q);
  LED #(.active("true")) \_1号中断等待指示灯  (.in(or_1_out));
  D_Flip_Flop #(.trigger("rising"), .Pre_Clr_Positions("LEGACY"), .NegatePresetClear("false"), .enable("true"), .NewFFLayout("false")) d_ff_1 (
    .clk(\_1号中断_out ), .D(1'b1), .Q(d_ff_1_q), .reset(\与中断屏蔽位与 ));  // open: Qn, preset, en
  or or_2 (or_2_out, d_ff_1_q, \与中断屏蔽位与 );
  and and_1 (and_1_out, or_2_out, ~\同步清零信号 );  // AND_Gate
  D_Flip_Flop #(.trigger("rising"), .Pre_Clr_Positions("LEGACY"), .NegatePresetClear("false"), .enable("true"), .NewFFLayout("false")) IR1 (
    .clk(clock_1_out), .D(and_1_out), .Q(\与中断屏蔽位与 ));  // open: Qn, preset, en, reset

  // Notes on the sheet:
  //   中断信号采样参考电路
  //   Reset 
endmodule

module \单周期_单级中断  (
  input  IR1,
  input  IR2,
  input  IR3,
  input  IR4,
  input  CLK,
  input  RST,
  input  [6:0] Stage,
  input  FIFO,
  input  Go,
  input  [15:0] MAP_LENGTH,
  output [15:0] LOAD_LINE,
  output ecall,
  output [6:0] x,
  output [6:0] y,
  output [15:0] rgb
);

  wire AluSrcB, and_1_out, and_2_out, and_3_out, and_4_out, and_5_out, and_6_out, and_7_out, and_8_out,
       and_9_out, and_10_out, and_11_out, and_17_out, and_18_out, and_19_out, and_21_out, and_22_out, AUIPC,
       B, Beq, BGE, BLT, BLTU, Bne, comparator_1_eq, comparator_2_eq, comparator_3_eq, comparator_4_eq,
       comparator_5_eq, comparator_6_eq, comparator_7_eq, comparator_8_eq, comparator_9_eq, comparator_10_eq,
       comparator_11_eq, comparator_12_eq, comparator_13_eq, comparator_13_lt, comparator_14_eq,
       comparator_14_gt, comparator_14_lt, controlled_inverter_1_out, controlled_inverter_2_out,
       controlled_inverter_3_out, CSRRCI, CSRRSI, d_ff_1_q, d_ff_2_q, d_ff_3_q, d_ff_4_q, d_ff_5_q, d_ff_6_q,
       d_ff_7_q, d_ff_8_q, decoder_1_out0, decoder_1_out1, decoder_1_out2, decoder_1_out3, ecall_t, equal,
       FIFO_RST, greater, guan, halt, IE, Int, Intq, IR1_t, IR2_t, IR3_t, IR4_t, IRA, IRB, IRC, IRD, J, JAL,
       JALR, less, LUI, MemToReg, MemWrite, mips_ram_1_p6, multiplexer_17_out, multiplexer_18_out, not_1_out,
       not_2_out, not_3_out, not_4_out, not_5_out, not_6_out, not_7_out, not_8_out, not_10_out, not_11_out,
       or_1_out, or_10_out, or_11_out, or_12_out, or_13_out, or_16_out, or_17_out, RegWrite, Ret1, Ret2,
       Ret3, Ret4, ROM_IN, S_type, SB, URET, W1, W2, W3, W4;
  wire [1:0] priority_encoder_1_out, register_3_q;
  wire [3:0] AluOP, multiplexer_15_out, Select;
  wire [4:0] multiplexer_1_out, multiplexer_2_out, multiplexer_16_out;
  wire [6:0] bit_extender_5_out, bit_extender_6_out, subtractor_1_out;
  wire [9:0] bit_extender_9_out, FAI, multiplexer_13_out;
  wire [11:0] multiplexer_4_out, shifter_2_out;
  wire [15:0] bit_extender_7_out, bit_extender_8_out, counter_3_q, multiplier_1_out, subtractor_2_out,
       subtractor_3_out, subtractor_4_out, TEMP, TEMP_ADDRESS, UP_ADDRESS, \总周期数 ;
  wire [19:0] shifter_3_out;
  wire [31:0] adder_2_out, adder_4_out, aui, bit_extender_1_out, bit_extender_2_out, bit_extender_3_out,
       bit_extender_4_out, EPC, FIFO_DATA, InterAddr, IR, LedData, MDin, mips_ram_1_p8, multiplexer_5_out,
       multiplexer_6_out, multiplexer_7_out, multiplexer_8_out, multiplexer_9_out, multiplexer_10_out,
       multiplexer_14_out, multiplexer_19_out, nextPC, PC, PC_4, PCin, R1, R2, RDin, Result, shifter_1_out,
       shifter_4_out;

  Hex_Digit_Display hex_digit_display_1 (.value(LedData[31:28]));  // open: dp
  Comparator #(.width(16), .mode("twosComplement")) comparator_1 (
    .a(16'h23b), .b(\总周期数 ), .eq(comparator_1_eq));  // open: gt, lt
  Comparator #(.width(16), .mode("twosComplement")) comparator_2 (
    .a(\总周期数 ), .b(16'h1), .eq(comparator_2_eq));  // open: gt, lt
  Comparator #(.width(16), .mode("twosComplement")) comparator_3 (
    .a(\总周期数 ), .b(16'h4), .eq(comparator_3_eq));  // open: gt, lt
  Comparator #(.width(16), .mode("twosComplement")) comparator_4 (
    .a(\总周期数 ), .b(16'h7), .eq(comparator_4_eq));  // open: gt, lt
  Comparator #(.width(32), .mode("twosComplement")) comparator_5 (
    .a(R2), .b(32'h22), .eq(comparator_5_eq));  // open: gt, lt
  Comparator #(.width(32), .mode("twosComplement")) comparator_6 (
    .a(R2), .b(32'h22), .eq(comparator_6_eq));  // open: gt, lt
  not not_1 (not_1_out, halt);
  Hex_Digit_Display hex_digit_display_2 (.value(LedData[23:20]));  // open: dp
  Hex_Digit_Display hex_digit_display_3 (.value(LedData[27:24]));  // open: dp
  or or_1 (or_1_out, comparator_1_eq, comparator_2_eq);
  assign controlled_inverter_1_out = or_1_out ? ~CLK : 1'bz;  // Controlled_Inverter controlled_inverter_1
  assign controlled_inverter_2_out = comparator_3_eq ? ~CLK : 1'bz;  // Controlled_Inverter controlled_inverter_2
  assign controlled_inverter_3_out = comparator_4_eq ? ~CLK : 1'bz;  // Controlled_Inverter controlled_inverter_3
  and and_1 (and_1_out, ecall_t, comparator_5_eq);
  and and_2 (and_2_out, ecall_t, not_2_out);
  not not_2 (not_2_out, comparator_6_eq);
  not not_3 (not_3_out, halt);
  Counter #(.width(16), .max('hffff), .ongoal("wrap"), .trigger("rising"), .behavior("new")) counter_1 (
    .count(not_1_out), .Q(\总周期数 ), .clk(CLK), .clr(RST));  // open: load, D, carry, preset, down
  Comparator #(.width(32), .mode("twosComplement")) comparator_7 (
    .a(32'h1), .b(Result), .eq(comparator_7_eq));  // open: gt, lt
  Hex_Digit_Display hex_digit_display_4 (.value(LedData[15:12]));  // open: dp
  Hex_Digit_Display hex_digit_display_5 (.value(LedData[19:16]));  // open: dp
  Pull_Resistor #(.pull(0)) pull_resistor_1 (.node(controlled_inverter_1_out));
  Pull_Resistor #(.pull(0)) pull_resistor_2 (.node(controlled_inverter_2_out));
  Pull_Resistor #(.pull(0)) pull_resistor_3 (.node(controlled_inverter_3_out));
  Register #(.width(32), .trigger("rising"), .Select("low")) register_1 (
    .D(R1), .en(and_1_out), .Q(LedData), .clk(CLK), .clr(RST));
  Register #(.width(1), .trigger("rising"), .Select("low")) register_2 (
    .D(and_2_out), .en(not_3_out), .Q(halt), .clk(not_4_out), .clr(Go));
  not not_4 (not_4_out, CLK);
  Register #(.width(32), .trigger("rising"), .Select("low")) u_PC (
    .D(PCin), .en(not_5_out), .Q(PC), .clk(CLK), .clr(RST));
  not not_5 (not_5_out, halt);
  and and_3 (and_3_out, BLTU, comparator_7_eq);
  Hex_Digit_Display hex_digit_display_6 (.value(LedData[7:4]));  // open: dp
  Hex_Digit_Display hex_digit_display_7 (.value(LedData[11:8]));  // open: dp
  // Probe on \总周期数 
  and and_4 (and_4_out, BGE, greater);
  not not_6 (not_6_out, equal);
  and and_5 (and_5_out, less, BLT);
  Hex_Digit_Display hex_digit_display_8 (.value(LedData[3:0]));  // open: dp
  and and_6 (and_6_out, Beq, equal);
  and and_7 (and_7_out, not_6_out, Bne);
  or or_2 (J, JAL, JALR);
  D_Flip_Flop #(.trigger("rising"), .Pre_Clr_Positions("LEGACY"), .NegatePresetClear("false"), .enable("true"), .NewFFLayout("false")) d_ff_1 (
    .clk(IR1_t), .D(1'b1), .Q(d_ff_1_q), .en(guan), .reset(d_ff_5_q));  // open: Qn, preset
  or or_3 (W1, d_ff_5_q, d_ff_1_q);
  D_Flip_Flop #(.trigger("rising"), .Pre_Clr_Positions("LEGACY"), .NegatePresetClear("false"), .enable("true"), .NewFFLayout("false")) d_ff_2 (
    .clk(IR2_t), .D(1'b1), .Q(d_ff_2_q), .en(guan), .reset(d_ff_6_q));  // open: Qn, preset
  or or_4 (W2, d_ff_6_q, d_ff_2_q);
  D_Flip_Flop #(.trigger("rising"), .Pre_Clr_Positions("LEGACY"), .NegatePresetClear("false"), .enable("true"), .NewFFLayout("false")) d_ff_3 (
    .clk(IR3_t), .D(1'b1), .Q(d_ff_3_q), .en(guan), .reset(d_ff_7_q));  // open: Qn, preset
  or or_5 (W3, d_ff_7_q, d_ff_3_q);
  D_Flip_Flop #(.trigger("rising"), .Pre_Clr_Positions("LEGACY"), .NegatePresetClear("false"), .enable("true"), .NewFFLayout("false")) d_ff_4 (
    .clk(IR4_t), .D(1'b1), .Q(d_ff_4_q), .en(guan), .reset(d_ff_8_q));  // open: Qn, preset
  or or_6 (W4, d_ff_8_q, d_ff_4_q);
  // RiscV_Probe riscv_probe_1: pin names not known; wires that end beside it: IR
  or or_7 (B, and_4_out, and_6_out, and_3_out, and_7_out, and_5_out);
  or or_8 (IR1_t, IR1, IRA);
  ROM #(.addrWidth(10), .dataWidth(32), .Select("high")) rom_1 (.addr(PC[11:2]), .data(IR));
  or or_9 (IR2_t, IR2, IRB);
  or or_10 (or_10_out, d_ff_1_q, d_ff_5_q);
  and and_8 (and_8_out, or_10_out, ~Ret1);  // AND_Gate
  or or_11 (or_11_out, d_ff_2_q, d_ff_6_q);
  and and_9 (and_9_out, or_11_out, ~Ret2);  // AND_Gate
  or or_12 (or_12_out, d_ff_3_q, d_ff_7_q);
  and and_10 (and_10_out, or_12_out, ~Ret3);  // AND_Gate
  or or_13 (or_13_out, d_ff_4_q, d_ff_8_q);
  and and_11 (and_11_out, or_13_out, ~Ret4);  // AND_Gate
  D_Flip_Flop #(.trigger("rising"), .Pre_Clr_Positions("LEGACY"), .NegatePresetClear("false"), .enable("true"), .NewFFLayout("false")) d_ff_5 (
    .clk(CLK), .D(and_8_out), .Q(d_ff_5_q));  // open: Qn, preset, en, reset
  D_Flip_Flop #(.trigger("rising"), .Pre_Clr_Positions("LEGACY"), .NegatePresetClear("false"), .enable("true"), .NewFFLayout("false")) d_ff_6 (
    .clk(CLK), .D(and_9_out), .Q(d_ff_6_q));  // open: Qn, preset, en, reset
  D_Flip_Flop #(.trigger("rising"), .Pre_Clr_Positions("LEGACY"), .NegatePresetClear("false"), .enable("true"), .NewFFLayout("false")) d_ff_7 (
    .clk(CLK), .D(and_10_out), .Q(d_ff_7_q));  // open: Qn, preset, en, reset
  D_Flip_Flop #(.trigger("rising"), .Pre_Clr_Positions("LEGACY"), .NegatePresetClear("false"), .enable("true"), .NewFFLayout("false")) d_ff_8 (
    .clk(CLK), .D(and_11_out), .Q(d_ff_8_q));  // open: Qn, preset, en, reset
  \单周期硬布线控制器  \u_单周期硬布线控制器_1  (
    .Funct({IR[30], IR[25], IR[14:12]}), .OP(IR[6:2]), .ALU_OP(AluOP), .MemToReg(MemToReg),
    .MemWrite(MemWrite), .ALU_SRC(AluSrcB), .RegWrite(RegWrite), .ecall(ecall_t), .S_type(S_type),
    .Jalr(JALR), .Beq(Beq), .JAL(JAL), .Bne(Bne), .in_3(IR[21]), .uret(URET), .SB(SB), .BLTU(BLTU),
    .CSRRSI(CSRRSI), .CSRRCI(CSRRCI), .LUI(LUI), .BLT(BLT), .BGE(BGE), .AUIPC(AUIPC));
  Multiplexer #(.select(1), .width(5), .disabled("Z"), .enable("false")) multiplexer_1 (
    .in0(IR[19:15]), .in1(5'b01010), .out(multiplexer_1_out), .sel(ecall_t));
  Multiplexer #(.select(1), .width(5), .disabled("Z"), .enable("false")) multiplexer_2 (
    .in0(IR[24:20]), .in1(5'b10001), .out(multiplexer_2_out), .sel(ecall_t));
  Multiplexer #(.select(1), .width(32), .disabled("Z"), .enable("false")) multiplexer_3 (
    .in0(aui), .in1(multiplexer_5_out), .out(RDin), .sel(not_7_out));
  Multiplexer #(.select(1), .width(12), .disabled("Z"), .enable("false")) multiplexer_4 (
    .in0(IR[31:20]), .in1({IR[31:25], IR[11:7]}), .out(multiplexer_4_out), .sel(S_type));
  assign bit_extender_1_out = {{12{1'b0}}, IR[31:12]};  // Bit_Extender bit_extender_1
  Shifter #(.width(32), .shift("ll")) shifter_1 (.in(bit_extender_1_out), .\dist (5'b01100), .out(shifter_1_out));
  Shifter #(.width(12), .shift("ll")) shifter_2 (
    .in({IR[31], IR[7], IR[30:25], IR[11:8]}), .\dist (4'b0001), .out(shifter_2_out));
  Shifter #(.width(20), .shift("ll")) shifter_3 (
    .in({IR[31], IR[19:12], IR[20], IR[30:21]}), .\dist (5'b00001), .out(shifter_3_out));
  or or_14 (IR3_t, IR3, IRC);
  or or_15 (IR4_t, IR4, IRD);
  not not_7 (not_7_out, AUIPC);
  Multiplexer #(.select(1), .width(32), .disabled("Z"), .enable("false")) multiplexer_5 (
    .in0(shifter_1_out), .in1(multiplexer_8_out), .out(multiplexer_5_out), .sel(not_8_out));
  not not_8 (not_8_out, LUI);
  Adder #(.width(32)) adder_1 (.a(PC), .b(32'h4), .out(PC_4));  // open: cin, cout
  Adder #(.width(32)) adder_2 (.a(PC), .b(bit_extender_2_out), .out(adder_2_out));  // open: cin, cout
  assign bit_extender_2_out = {{20{shifter_2_out[11]}}, shifter_2_out};  // Bit_Extender bit_extender_2
  Adder #(.width(32)) adder_3 (.a(shifter_1_out), .b(PC), .out(aui));  // open: cin, cout
  Adder #(.width(32)) adder_4 (.a(PC), .b(bit_extender_3_out), .out(adder_4_out));  // open: cin, cout
  assign bit_extender_3_out = {{12{shifter_3_out[19]}}, shifter_3_out};  // Bit_Extender bit_extender_3
  Regifile regifile_1 (
    .Din(RDin), .Clk(CLK), .R1(R1), .R2(R2), .WE(RegWrite), .W_num(IR[11:7]), .R1_num(multiplexer_1_out),
    .R2_num(multiplexer_2_out));
  assign bit_extender_4_out = {{20{multiplexer_4_out[11]}}, multiplexer_4_out};  // Bit_Extender bit_extender_4
  Multiplexer #(.select(1), .width(32), .disabled("Z"), .enable("false")) multiplexer_6 (
    .in0(PC_4), .in1(adder_2_out), .out(multiplexer_6_out), .sel(B));
  Priority_Encoder #(.select(2), .disabled("Z")) priority_encoder_1 (
    .in0(d_ff_5_q), .in1(d_ff_6_q), .in2(d_ff_7_q), .in3(d_ff_8_q), .out(priority_encoder_1_out), .gs(Intq),
    .en_in(guan));  // open: en_out
  D_Flip_Flop #(.trigger("falling"), .Pre_Clr_Positions("LEGACY"), .NegatePresetClear("false"), .enable("true"), .NewFFLayout("false")) d_ff_9 (
    .clk(CSRRCI), .D(1'b1), .Qn(guan), .reset(CSRRSI));  // open: Q, preset, en
  and and_12 (Int, IE, Intq);
  D_Flip_Flop #(.trigger("rising"), .Pre_Clr_Positions("LEGACY"), .NegatePresetClear("false"), .enable("true"), .NewFFLayout("false")) d_ff_10 (
    .clk(CLK), .D(Int), .Qn(IE), .en(or_16_out));  // open: Q, preset, reset
  or or_16 (or_16_out, Int, URET);
  Multiplexer #(.select(1), .width(32), .disabled("Z"), .enable("false")) multiplexer_7 (
    .in0(R2), .in1(bit_extender_4_out), .out(multiplexer_7_out), .sel(AluSrcB));
  Multiplexer #(.select(1), .width(32), .disabled("Z"), .enable("false")) multiplexer_8 (
    .in0(multiplexer_9_out), .in1(PC_4), .out(multiplexer_8_out), .sel(J));
  ALU alu_1 (
    .X(R1), .Y(multiplexer_7_out), .AluOP(AluOP), .Equal(equal), .Result(Result), .out_4(greater),
    .out_6(less));  // open: Result_2
  Multiplexer #(.select(1), .width(32), .disabled("Z"), .enable("false")) multiplexer_9 (
    .in0(Result), .in1(mips_ram_1_p8), .out(multiplexer_9_out), .sel(MemToReg));
  Multiplexer #(.select(1), .width(32), .disabled("Z"), .enable("false")) multiplexer_10 (
    .in0(multiplexer_6_out), .in1(adder_4_out), .out(multiplexer_10_out), .sel(JAL));
  Multiplexer #(.select(2), .width(32), .disabled("Z"), .enable("false")) multiplexer_11 (
    .in0(32'h37f8), .in1(32'h380c), .in2(32'h3820), .in3(32'h3834), .out(InterAddr),
    .sel(priority_encoder_1_out));
  // Probe on multiplexer_14_out
  Multiplexer #(.select(1), .width(32), .disabled("Z"), .enable("false")) multiplexer_12 (
    .in0(multiplexer_10_out), .in1(Result), .out(nextPC), .sel(JALR));
  Decoder #(.select(2), .tristate("false"), .disabled("Z"), .enable("false")) decoder_1 (
    .out0(decoder_1_out0), .out1(decoder_1_out1), .out2(decoder_1_out2), .out3(decoder_1_out3),
    .sel(register_3_q));
  Register #(.width(2), .trigger("rising"), .Select("low")) register_3 (
    .D(priority_encoder_1_out), .en(Int), .Q(register_3_q), .clk(CLK));  // open: clr
  // Probe on multiplexer_13_out
  Multiplexer #(.select(1), .width(10), .disabled("Z"), .enable("false")) multiplexer_13 (
    .in0(Result[11:2]), .in1(FAI), .out(multiplexer_13_out), .sel(ROM_IN));
  Multiplexer #(.select(1), .width(32), .disabled("Z"), .enable("false")) multiplexer_14 (
    .in0(MDin), .in1(FIFO_DATA), .out(multiplexer_14_out), .sel(ROM_IN));
  Register #(.width(32), .trigger("rising"), .Select("low")) register_4 (
    .D(nextPC), .en(Int), .Q(EPC), .clk(CLK), .clr(RST));
  Multiplexer #(.select(2), .width(4), .disabled("Z"), .enable("false")) multiplexer_15 (
    .in0(4'b0001), .in1(4'b0010), .in2(4'b0100), .in3(4'b1000), .out(multiplexer_15_out), .sel(Result[1:0]));
  Multiplexer #(.select(2), .width(5), .disabled("Z"), .enable("false")) multiplexer_16 (
    .in0({5{1'b0}}), .in1(5'b01000), .in2(5'b10000), .in3(5'b11000), .out(multiplexer_16_out),
    .sel(Result[1:0]));
  Shifter #(.width(32), .shift("ll")) shifter_4 (.in(R2), .\dist (multiplexer_16_out), .out(shifter_4_out));
  Multiplexer #(.select(1), .width(1), .disabled("Z"), .enable("false")) multiplexer_17 (
    .in0(MemWrite), .in1(ROM_IN), .out(multiplexer_17_out), .sel(ROM_IN));
  Multiplexer #(.select(1), .width(1), .disabled("Z"), .enable("false")) multiplexer_18 (
    .in0(MemWrite), .in1(ROM_IN), .out(multiplexer_18_out), .sel(ROM_IN));
  Multiplexer #(.select(1), .width(32), .disabled("Z"), .enable("false")) multiplexer_19 (
    .in0(nextPC), .in1(InterAddr), .out(multiplexer_19_out), .sel(Int));
  and and_13 (Ret1, decoder_1_out0, URET);
  and and_14 (Ret2, decoder_1_out1, URET);
  and and_15 (Ret3, decoder_1_out2, URET);
  and and_16 (Ret4, decoder_1_out3, URET);
  Multiplexer #(.select(1), .width(4), .disabled("Z"), .enable("false")) multiplexer_20 (
    .in0(4'b1111), .in1(multiplexer_15_out), .out(Select), .sel(SB));
  Multiplexer #(.select(1), .width(32), .disabled("Z"), .enable("false")) multiplexer_21 (
    .in0(R2), .in1(shifter_4_out), .out(MDin), .sel(SB));
  // MIPS_RAM mips_ram_1: pin names not known; wires that end beside it: multiplexer_13_out, multiplexer_14_out, multiplexer_17_out, Select, CLK, mips_ram_1_p6, RST, mips_ram_1_p8
  not not_9 (mips_ram_1_p6, multiplexer_18_out);
  Multiplexer #(.select(1), .width(32), .disabled("Z"), .enable("false")) multiplexer_22 (
    .in0(multiplexer_19_out), .in1(EPC), .out(PCin), .sel(URET));
  Bit_Extender #(.in_width(32), .out_width(7), .\type ("zero")) bit_extender_5 (.in(RDin), .out(bit_extender_5_out));
  Comparator #(.width(5), .mode("twosComplement")) comparator_8 (
    .a(IR[11:7]), .b(5'b10010), .eq(comparator_8_eq));  // open: gt, lt
  Bit_Extender #(.in_width(32), .out_width(7), .\type ("zero")) bit_extender_6 (.in(RDin), .out(bit_extender_6_out));
  Comparator #(.width(5), .mode("twosComplement")) comparator_9 (
    .a(IR[11:7]), .b(5'b01001), .eq(comparator_9_eq));  // open: gt, lt
  Bit_Extender #(.in_width(32), .out_width(16), .\type ("zero")) bit_extender_7 (.in(RDin), .out(bit_extender_7_out));
  Comparator #(.width(5), .mode("twosComplement")) comparator_10 (
    .a(IR[11:7]), .b(5'b10100), .eq(comparator_10_eq));  // open: gt, lt
  Comparator #(.width(32), .mode("twosComplement")) comparator_11 (
    .a(R2), .b(32'h22), .eq(comparator_11_eq));  // open: gt, lt
  and and_17 (and_17_out, comparator_8_eq, RegWrite);
  and and_18 (and_18_out, comparator_9_eq, RegWrite);
  and and_19 (and_19_out, comparator_10_eq, RegWrite);
  and and_20 (ecall, ecall_t, comparator_11_eq);
  Register #(.width(7), .trigger("rising"), .Select("low")) register_5 (
    .D(bit_extender_5_out), .en(and_17_out), .Q(x), .clk(CLK));  // open: clr
  Register #(.width(7), .trigger("rising"), .Select("low")) register_6 (
    .D(bit_extender_6_out), .en(and_18_out), .Q(y), .clk(CLK));  // open: clr
  Register #(.width(16), .trigger("rising"), .Select("low")) register_7 (
    .D(bit_extender_7_out), .en(and_19_out), .Q(rgb), .clk(CLK));  // open: clr
  Button UP (.out(IRA));
  Button DOWN (.out(IRB));
  Button LEFT (.out(IRC));
  Button RIGHT (.out(IRD));
  LED #(.active("true")) led_1 (.in(W1));
  LED #(.active("true")) led_2 (.in(W2));
  LED #(.active("true")) led_3 (.in(W3));
  LED #(.active("true")) led_4 (.in(W4));
  // Probe on subtractor_1_out
  Subtractor #(.width(7)) subtractor_1 (.a(Stage), .b(7'b0110000), .out(subtractor_1_out));  // open: bin, bout
  // Probe on bit_extender_8_out
  assign bit_extender_8_out = {{9{1'b0}}, subtractor_1_out};  // Bit_Extender bit_extender_8
  Multiplier #(.width(16)) multiplier_1 (
    .a(MAP_LENGTH), .b(bit_extender_8_out), .out(multiplier_1_out));  // open: cin, cout
  // Probe on multiplier_1_out
  Subtractor #(.width(16)) subtractor_2 (.a(MAP_LENGTH), .b(TEMP), .out(subtractor_2_out));  // open: bin, bout
  Register #(.width(16), .trigger("rising"), .Select("low")) register_8 (
    .D(multiplier_1_out), .en(FIFO), .Q(UP_ADDRESS), .clk(CLK), .clr(RST));
  Subtractor #(.width(16)) subtractor_3 (.a(UP_ADDRESS), .b(TEMP), .out(subtractor_3_out));  // open: bin, bout
  not not_10 (not_10_out, FIFO);
  Comparator #(.width(16), .mode("twosComplement")) comparator_12 (
    .a(UP_ADDRESS), .b({16{1'b0}}), .eq(comparator_12_eq));  // open: gt, lt
  Comparator #(.width(16), .mode("twosComplement")) comparator_13 (
    .a(TEMP), .b(16'h200), .eq(comparator_13_eq), .lt(comparator_13_lt));  // open: gt
  Bit_Extender #(.in_width(16), .out_width(10), .\type ("zero")) bit_extender_9 (
    .in(subtractor_2_out), .out(bit_extender_9_out));
  // Probe on UP_ADDRESS
  Register #(.width(16), .trigger("falling"), .Select("low")) register_9 (
    .D(subtractor_3_out), .en(not_10_out), .Q(TEMP_ADDRESS), .clk(CLK), .clr(RST));
  // Probe on TEMP_ADDRESS
  Subtractor #(.width(16)) subtractor_4 (.a(UP_ADDRESS), .b(TEMP_ADDRESS), .out(subtractor_4_out));  // open: bin, bout
  not not_11 (not_11_out, comparator_12_eq);
  or or_17 (or_17_out, comparator_13_eq, comparator_13_lt);
  Register #(.width(10), .trigger("falling"), .Select("low")) register_10 (
    .D(bit_extender_9_out), .en(ROM_IN), .Q(FAI), .clk(CLK), .clr(RST));
  // Probe on FAI
  Comparator #(.width(16), .mode("twosComplement")) comparator_14 (
    .a(subtractor_4_out), .b(MAP_LENGTH), .gt(comparator_14_gt), .eq(comparator_14_eq), .lt(comparator_14_lt));
  Counter #(.width(16), .max('hffff), .ongoal("wrap"), .trigger("rising"), .behavior("new")) counter_2 (
    .count(ROM_IN), .Q(TEMP), .clk(CLK), .clr(RST));  // open: load, D, carry, preset, down
  and and_21 (and_21_out, comparator_14_eq, comparator_14_lt);
  and and_22 (and_22_out, not_11_out, or_17_out);
  // Probe on bit_extender_9_out
  // Probe on TEMP
  ROM #(.addrWidth(16), .dataWidth(32), .Select("high")) rom_2 (.addr(TEMP_ADDRESS), .data(FIFO_DATA), .sel(ROM_IN));
  and and_23 (ROM_IN, ~comparator_14_gt, ~and_21_out, and_22_out);  // AND_Gate
  // Probe on FIFO_DATA
  Subtractor #(.width(16)) subtractor_5 (.a(TEMP), .b(16'h1), .out(LOAD_LINE));  // open: bin, bout
  Counter #(.width(16), .max('hffff), .ongoal("wrap"), .trigger("falling"), .behavior("new")) counter_3 (
    .count(1'b1), .Q(counter_3_q), .clk(ROM_IN), .clr(RST));  // open: load, D, carry, preset, down
  // Probe on counter_3_q
  Comparator #(.width(16), .mode("twosComplement")) comparator_15 (
    .a(16'h1), .b(counter_3_q), .eq(FIFO_RST));  // open: gt, lt

  // Other names for the same wires on the sheet: W[4:0] = IR[11:7]; unit[15:0] = MAP_LENGTH

  // Notes on the sheet:
  //   总复位信号应将除ROM以外所有存储组件全部清零
  //   单级中断测试信号模拟器
  //   数码管输出
  //   数码管输出应该用寄存器锁存，否则显示数据只能一闪而过
  //   指令探针
  //   指令存储器
  //   指令字
  //   contents of rom_1 (hex, n*v repeats v):
  //   fe010113 112e23 812c23 912a23 1212823 1312623 2010413 40f073 893 73 7b7 3f078493 913 480006f 993
  //   340006f 4a783 79663 448493 200006f 4a783 f00633 12005b3 1300533 317 2c300e7 448493 198993 900793
  //   fd37d6e3 190913 900793 fb27dce3 40e073 6f fc010113 2812e23 2912c23 3212a23 3312823 3412623 4010413
  //   fca42623 fcb42423 fcc42223 7b7 3f078693 fc842703 e007b3 279793 e787b3 179793 fcc42703 e787b3 279793
  //   f687b3 fc442703 e7a023 fc442783 fff78713 e007b3 379793 e787b3 479793 737 70713 e789b3 fcc42703
  //   e007b3 179793 e787b3 179793 fcf42e23 fc842703 e007b3 179793 e787b3 179793 fcf42c23 fdc42783 678793
  //   fcf42a23 fd842783 678793 fcf42823 2200893 fd842483 280006f fdc42903 140006f 9aa03 73 498993 190913
  //   fd442783 fef946e3 148493 fd042783 fcf4cce3 893 13 3c12403 3812483 3412903 3012983 2c12a03 4010113
  //   8067 fe010113 812e23 2010413 fe042623 780006f 7b7 65478713 fec42783 379793 f707b3 47a703 7b7
  //   65478693 fec42783 379793 f687b3 7a603 7b7 3f078693 e007b3 279793 e787b3 179793 c787b3 279793 f687b3
  //   7a703 700793 f70663 793 240006f fec42783 178793 fef42623 7b7 6507a783 fec42703 f8f740e3 100793
  //   f00533 1c12403 2010113 8067 fd010113 2812623 2912423 3212223 3312023 1412e23 3010413 493 900933
  //   12009b3 87b7 78793 fff78a13 2200893 9c0006f 7b7 58078713 399793 f707b3 7a703 e007b3 179793 e787b3
  //   179793 fcf42e23 7b7 58078713 399793 f707b3 47a703 e007b3 179793 e787b3 179793 fcf42c23 fdc42783
  //   678793 fcf42a23 fd842783 678793 fcf42823 fd842483 200006f fdc42903 c0006f 73 190913 fd442783
  //   fef94ae3 148493 fd042783 fef4c0e3 198993 1800793 f737d2e3 893 13 2c12403 2812483 2412903 2012983
  //   1c12a03 3010113 8067 fc010113 2112e23 2812c23 2912a23 3212823 3312623 3412423 4010413 fca42623
  //   40f073 7b7 64878793 7a903 7b7 64878793 47a483 fcc42703 300793 4f70c63 fcc42703 300793 4e7ca63
  //   fcc42703 200793 2f70c63 fcc42703 200793 2e7ce63 fcc42783 78a63 fcc42703 100793 f70863 240006f
  //   fff48493 1c0006f 148493 140006f fff90913 c0006f 190913 13 200793 fcf42e23 7b7 64878793 47a703 7b7
  //   64878793 7a603 7b7 3f078693 e007b3 279793 e787b3 179793 c787b3 279793 f687b3 7a703 500793 f71663
  //   300793 fcf42e23 7b7 3f078713 9007b3 279793 9787b3 179793 12787b3 279793 f707b3 7a703 200793 6f71c63
  //   7b7 64878793 7a703 7b7 64878793 47a783 fdc42603 f005b3 e00533 317 bdc300e7 7b7 64878793 127a023 7b7
  //   64878793 97a223 7b7 64878793 7a703 7b7 64878793 47a783 400613 f005b3 e00533 317 b98300e7 2d40006f
  //   7b7 3f078713 9007b3 279793 9787b3 179793 12787b3 279793 f707b3 7a703 300793 6f71c63 7b7 64878793
  //   7a703 7b7 64878793 47a783 fdc42603 f005b3 e00533 317 b38300e7 7b7 64878793 127a023 7b7 64878793
  //   97a223 7b7 64878793 7a703 7b7 64878793 47a783 500613 f005b3 e00533 317 af4300e7 2300006f 7b7
  //   3f078713 9007b3 279793 9787b3 179793 12787b3 279793 f707b3 7a703 600793 2f70a63 7b7 3f078713 9007b3
  //   279793 9787b3 179793 12787b3 279793 f707b3 7a703 700793 1cf71263 1200a33 9009b3 fcc42703 300793
  //   4f70c63 fcc42703 300793 4e7ca63 fcc42703 200793 2f70c63 fcc42703 200793 2e7ce63 fcc42783 78a63
  //   fcc42703 100793 f70863 240006f fff98993 1c0006f 198993 140006f fffa0a13 c0006f 1a0a13 13 7b7
  //   3f078713 13007b3 279793 13787b3 179793 14787b3 279793 f707b3 7a703 200793 f71e63 600613 13005b3
  //   1400533 317 9dc300e7 480006f 7b7 3f078713 13007b3 279793 13787b3 179793 14787b3 279793 f707b3 7a703
  //   300793 ef71263 700613 13005b3 1400533 317 994300e7 7b7 3f078713 9007b3 279793 9787b3 179793 12787b3
  //   279793 f707b3 7a703 600793 f71e63 400613 9005b3 1200533 317 950300e7 180006f 500613 9005b3 1200533
  //   317 938300e7 7b7 64878793 7a703 7b7 64878793 47a783 fdc42603 f005b3 e00533 317 90c300e7 7b7 64878793
  //   127a023 7b7 64878793 97a223 317 a10300e7 a007b3 78c63 317 aac300e7 893 73 100006f 13 80006f 13
  //   40e073 13 3c12083 3812403 3412483 3012903 2c12983 2812a03 4010113 8067 513 317 b60300e7 13 200073
  //   100513 317 b4c300e7 13 200073 200513 317 b38300e7 13 200073 300513 317 b24300e7 13 200073
  //   JAL
  //   JALR
  //   URET
  //   I型
  //   S型
  //   U型
  //   B型
  //   J型
  //   Beq
  //   Bne
  //   MemToReg
  //   MemWrite
  //   AluOP
  //   AluSrcB
  //   RegWrite
  //   为方便自动评测，需要输出PC，IR，寄存器堆写如数据RDin
  //   RAM写使能MemWrite、RAM写入数据MDin等信号
  //   数据存储器
  //   关卡单元大小
  //   contents of rom_2 (hex, n*v repeats v):
  //   1c82 2cc4 1c82 2cc4 1c82 2cc4 2cc4 1c82 2cc4 1c82 2cc4 1c82 1c82 2cc4 1c82 2cc4 1c82 2cc4 2cc4 1c82
  //   2cc4 1c82 2cc4 1c82 1c82 2cc4 1c82 2cc4 1c82 2cc4 2cc4 1c82 2cc4 1c82 2cc4 1c82 524c 5ece 524c 524c
  //   524c 4*5ece 524c 5ece 5*524c 5ece 524c 524c 5ece 524c 5ece 6*524c 5ece 5ece 5ece 4*524c 5ece 524c
  //   5ece 7fc0 7fc0 524c 5ece 5ece 4*7fc0 524c 7fc0 7fc0 524c 524c 4*7fc0 524c 5ece 7fc0 7fc0 524c 4*7fc0
  //   5ece 5ece 524c 7fc0 7fc0 524c 5ece 524c 7fff 7fff 7fff 524c 5ece 5*7fff 524c 524c 0 2108 0 5ece 4c06
  //   524c 0 2108 0 524c 524c 524c 0 2108 0 5ece 5ece 2108 524c 524c 524c 2108 5ece 524c 7fff 7fff 7fff
  //   524c 5ece 7fff 7fc0 7fc0 7fc0 7fff 524c 7fc0 0 2108 0 7fc0 4c06 7fc0 0 2108 0 7fc0 7fc0 524c 0 2108
  //   0 7fc0 5ece 2108 524c 7fc0 7fc0 2108 5ece 2ce4 2ce4 4187 4187 4*2ce4 4187 4187 2ce4 2ce4 4187 4187
  //   2ce4 2ce4 4*4187 2ce4 2ce4 4187 4187 2ce4 2ce4 4187 4187 4*2ce4 4187 4187 4*2ce4 7fc0 7fc0 2ce4 2ce4
  //   2ce4 4*7fc0 2ce4 7fc0 7fc0 2ce4 2ce4 4*7fc0 2ce4 2ce4 7fc0 7fc0 2ce4 4*7fc0 2ce4 2ce4 2ce4 7fc0 7fc0
  //   2ce4 2ce4 6*1 4*0 1 4*2 1 4*0 1 2 1 4 2 1 4*0 1 2 6 7 2 1 4*0 1 2 3 7 2 1 4*0 1 4*2 1 4*0 6*1 35*0 3
  //   0 4 0 5 1 6 2 3 2 4 2 5 3 6 4 3 4 4 4 5 6 3 6 4 6 5 6 6 8 3 8 4 8 5 8 6 9 4 a 5 b 3 b 4 b 5 b 6 3 2
  //   3 2 4 3 3 3 4 101*0 1c82 2cc4 1c82 2cc4 1c82 2cc4 2cc4 1c82 2cc4 1c82 2cc4 1c82 1c82 2cc4 1c82 2cc4
  //   1c82 2cc4 2cc4 1c82 2cc4 1c82 2cc4 1c82 1c82 2cc4 1c82 2cc4 1c82 2cc4 2cc4 1c82 2cc4 1c82 2cc4 1c82
  //   524c 5ece 524c 524c 524c 4*5ece 524c 5ece 5*524c 5ece 524c 524c 5ece 524c 5ece 6*524c 5ece 5ece 5ece
  //   4*524c 5ece 524c 5ece 7fc0 7fc0 524c 5ece 5ece 4*7fc0 524c 7fc0 7fc0 524c 524c 4*7fc0 524c 5ece 7fc0
  //   7fc0 524c 4*7fc0 5ece 5ece 524c 7fc0 7fc0 524c 5ece 524c 7fff 7fff 7fff 524c 5ece 5*7fff 524c 524c 0
  //   2108 0 5ece 4c06 524c 0 2108 0 524c 524c 524c 0 2108 0 5ece 5ece 2108 524c 524c 524c 2108 5ece 524c
  //   7fff 7fff 7fff 524c 5ece 7fff 7fc0 7fc0 7fc0 7fff 524c 7fc0 0 2108 0 7fc0 4c06 7fc0 0 2108 0 7fc0
  //   7fc0 524c 0 2108 0 7fc0 5ece 2108 524c 7fc0 7fc0 2108 5ece 2ce4 2ce4 4187 4187 4*2ce4 4187 4187 2ce4
  //   2ce4 4187 4187 2ce4 2ce4 4*4187 2ce4 2ce4 4187 4187 2ce4 2ce4 4187 4187 4*2ce4 4187 4187 4*2ce4 7fc0
  //   7fc0 2ce4 2ce4 2ce4 4*7fc0 2ce4 7fc0 7fc0 2ce4 2ce4 4*7fc0 2ce4 2ce4 7fc0 7fc0 2ce4 4*7fc0 2ce4 2ce4
  //   2ce4 7fc0 7fc0 2ce4 2ce4 4*1 6*0 1 2 3 1 6*0 1 2 2 1 1 1 4*0 1 7 4 2 2 1 4*0 1 2 2 6 2 1 4*0 1 2 2 1
  //   1 1 4*0 4*1 37*0 3 0 4 0 5 1 6 2 3 2 4 2 5 3 6 4 3 4 4 4 5 6 3 6 4 6 5 6 6 8 3 8 4 8 5 8 6 9 4 a 5 b
  //   3 b 4 b 5 b 6 2 3 2 2 1 1 3
endmodule

module \单周期_多级中断  (
  input  IR1,
  input  IR2,
  input  IR3,
  output RegWrite,
  output MemWrite,
  output [31:0] PC,
  output [31:0] IR,
  output [31:0] RDin,
  output [31:0] MDin,
  output [31:0] LedData
);

  wire AluSrcB, and_1_out, and_2_out, and_3_out, and_4_out, and_5_out, and_6_out, and_7_out, and_8_out, B,
       Beq, BLTU, Bne, CLK, clock_1_out, comparator_1_eq, comparator_2_eq, comparator_3_eq, comparator_4_eq,
       comparator_5_eq, comparator_6_eq, comparator_7_eq, comparator_8_eq, comparator_9_eq, comparator_9_lt,
       CSRRCI, CSRRSI, d_ff_1_q, d_ff_2_q, d_ff_3_q, d_ff_4_q, d_ff_5_q, d_ff_6_q, d_ff_8_q, decoder_1_out1,
       decoder_1_out2, decoder_1_out3, demultiplexer_1_out0, demultiplexer_1_out1, demultiplexer_1_out2,
       demultiplexer_2_out0, demultiplexer_2_out1, demultiplexer_2_out2, ecall, equal, Go, halt, IE,
       Interrupt, IR1_t, IR2_t, IR3_t, IRA, IRB, IRC, J, JAL, JALR, less, LUI, MemToReg, nand_1_out,
       not_1_out, not_2_out, not_3_out, not_4_out, not_5_out, not_6_out, not_7_out, not_8_out, or_1_out,
       or_2_out, or_10_out, or_11_out, or_12_out, or_14_out, or_15_out, or_16_out, priority_encoder_1_gs,
       pull_resistor_1_node, pull_resistor_2_node, pull_resistor_3_node, Ret1, Ret2, Ret3, RST, S_type, SB,
       shield, URET, W1, W2, W3;
  wire [1:0] Inter_Num, Inter_Num_Pri, IR1_q, IR2_q, IR3_q, stack;
  wire [3:0] AluOP, multiplexer_12_out, Select;
  wire [4:0] multiplexer_1_out, multiplexer_2_out, multiplexer_13_out;
  wire [11:0] multiplexer_3_out, shifter_2_out;
  wire [12:0] CNT_num;
  wire [15:0] \总周期数 ;
  wire [19:0] shifter_3_out;
  wire [31:0] adder_2_out, adder_3_out, bit_extender_1_out, bit_extender_2_out, bit_extender_3_out,
       bit_extender_4_out, EPC, EPC1_q, EPC2_q, EPC3_q, InterAddr, mips_ram_1_p8, multiplexer_5_out,
       multiplexer_6_out, multiplexer_7_out, multiplexer_8_out, multiplexer_9_out, multiplexer_14_out,
       nextPC, PC_4, PCin, R1, R2, Result, shifter_1_out, shifter_4_out;

  Button \u_继续运行  (.out(Go));
  Button _1 (.out(IRA));
  Button _2 (.out(IRB));
  Button _3 (.out(IRC));
  LED #(.active("true")) led_1 (.in(W1));
  LED #(.active("true")) led_2 (.in(W2));
  LED #(.active("true")) led_3 (.in(W3));
  Hex_Digit_Display hex_digit_display_1 (.value(LedData[31:28]));  // open: dp
  Comparator #(.width(16), .mode("twosComplement")) comparator_1 (
    .a(\总周期数 ), .b(16'h7), .eq(comparator_1_eq));  // open: gt, lt
  Comparator #(.width(16), .mode("twosComplement")) comparator_2 (
    .a(\总周期数 ), .b(16'h241), .eq(comparator_2_eq));  // open: gt, lt
  Comparator #(.width(32), .mode("twosComplement")) comparator_3 (
    .a(R2), .b(32'h22), .eq(comparator_3_eq));  // open: gt, lt
  Comparator #(.width(32), .mode("twosComplement")) comparator_4 (
    .a(R2), .b(32'h22), .eq(comparator_4_eq));  // open: gt, lt
  Button button_1 (.out(RST));
  Hex_Digit_Display hex_digit_display_2 (.value(LedData[23:20]));  // open: dp
  Hex_Digit_Display hex_digit_display_3 (.value(LedData[27:24]));  // open: dp
  Comparator #(.width(16), .mode("twosComplement")) comparator_5 (
    .a(16'h258), .b(\总周期数 ), .eq(comparator_5_eq));  // open: gt, lt
  or or_1 (or_1_out, comparator_5_eq, comparator_6_eq);
  Comparator #(.width(16), .mode("twosComplement")) comparator_6 (
    .a(\总周期数 ), .b(16'h1), .eq(comparator_6_eq));  // open: gt, lt
  Comparator #(.width(16), .mode("twosComplement")) comparator_7 (
    .a(\总周期数 ), .b(16'h4), .eq(comparator_7_eq));  // open: gt, lt
  or or_2 (or_2_out, comparator_1_eq, comparator_2_eq);
  and and_1 (and_1_out, ecall, comparator_3_eq);
  and and_2 (and_2_out, ecall, not_1_out);
  not not_1 (not_1_out, comparator_4_eq);
  not not_2 (not_2_out, halt);
  not not_3 (not_3_out, halt);
  Counter #(.width(16), .max('hffff), .ongoal("wrap"), .trigger("rising"), .behavior("new")) counter_1 (
    .count(not_3_out), .Q(\总周期数 ), .clk(CLK), .clr(RST));  // open: load, D, carry, preset, down
  Comparator #(.width(32), .mode("twosComplement")) comparator_8 (
    .a(32'h1), .b(Result), .eq(comparator_8_eq));  // open: gt, lt
  Hex_Digit_Display hex_digit_display_4 (.value(LedData[15:12]));  // open: dp
  Hex_Digit_Display hex_digit_display_5 (.value(LedData[19:16]));  // open: dp
  Pull_Resistor #(.pull(0)) pull_resistor_1 (.node(pull_resistor_1_node));
  assign pull_resistor_1_node = or_1_out ? ~CLK : 1'bz;  // Controlled_Inverter controlled_inverter_1
  Pull_Resistor #(.pull(0)) pull_resistor_2 (.node(pull_resistor_2_node));
  assign pull_resistor_2_node = comparator_7_eq ? ~CLK : 1'bz;  // Controlled_Inverter controlled_inverter_2
  Pull_Resistor #(.pull(0)) pull_resistor_3 (.node(pull_resistor_3_node));
  assign pull_resistor_3_node = or_2_out ? ~CLK : 1'bz;  // Controlled_Inverter controlled_inverter_3
  Register #(.width(32), .trigger("rising"), .Select("low")) register_1 (
    .D(R1), .en(and_1_out), .Q(LedData), .clk(CLK), .clr(RST));
  Register #(.width(1), .trigger("rising"), .Select("low")) register_2 (
    .D(and_2_out), .en(not_2_out), .Q(halt), .clk(not_4_out), .clr(Go));
  not not_4 (not_4_out, CLK);
  Register #(.width(32), .trigger("rising"), .Select("low")) u_PC (
    .D(PCin), .en(not_5_out), .Q(PC), .clk(CLK), .clr(RST));
  not not_5 (not_5_out, halt);
  and and_3 (and_3_out, BLTU, comparator_8_eq);
  Hex_Digit_Display hex_digit_display_6 (.value(LedData[11:8]));  // open: dp
  Hex_Digit_Display hex_digit_display_7 (.value(LedData[7:4]));  // open: dp
  // Probe on \总周期数 
  not not_6 (not_6_out, equal);
  Hex_Digit_Display hex_digit_display_8 (.value(LedData[3:0]));  // open: dp
  and and_4 (and_4_out, Beq, equal);
  and and_5 (and_5_out, not_6_out, Bne);
  or or_3 (J, JAL, JALR);
  D_Flip_Flop #(.trigger("rising"), .Pre_Clr_Positions("LEGACY"), .NegatePresetClear("false"), .enable("true"), .NewFFLayout("false")) d_ff_1 (
    .clk(IR1_t), .D(1'b1), .Q(d_ff_1_q), .reset(d_ff_4_q));  // open: Qn, preset, en
  or or_4 (W1, d_ff_4_q, d_ff_1_q);
  D_Flip_Flop #(.trigger("rising"), .Pre_Clr_Positions("LEGACY"), .NegatePresetClear("false"), .enable("true"), .NewFFLayout("false")) d_ff_2 (
    .clk(IR2_t), .D(1'b1), .Q(d_ff_2_q), .reset(d_ff_5_q));  // open: Qn, preset, en
  or or_5 (W2, d_ff_5_q, d_ff_2_q);
  D_Flip_Flop #(.trigger("rising"), .Pre_Clr_Positions("LEGACY"), .NegatePresetClear("false"), .enable("true"), .NewFFLayout("false")) d_ff_3 (
    .clk(IR3_t), .D(1'b1), .Q(d_ff_3_q), .reset(d_ff_6_q));  // open: Qn, preset, en
  or or_6 (W3, d_ff_6_q, d_ff_3_q);
  // RiscV_Probe riscv_probe_1: pin names not known; wires that end beside it: IR
  or or_7 (B, and_4_out, and_3_out, and_5_out);
  or or_8 (IR1_t, IR1, IRA);
  ROM #(.addrWidth(10), .dataWidth(32), .Select("high")) rom_1 (.addr(PC[11:2]), .data(IR));
  or or_9 (IR2_t, IR2, IRB);
  or or_10 (or_10_out, d_ff_1_q, d_ff_4_q);
  and and_6 (and_6_out, or_10_out, ~Ret1);  // AND_Gate
  or or_11 (or_11_out, d_ff_2_q, d_ff_5_q);
  and and_7 (and_7_out, or_11_out, ~Ret2);  // AND_Gate
  or or_12 (or_12_out, d_ff_3_q, d_ff_6_q);
  and and_8 (and_8_out, or_12_out, ~Ret3);  // AND_Gate
  D_Flip_Flop #(.trigger("rising"), .Pre_Clr_Positions("LEGACY"), .NegatePresetClear("false"), .enable("true"), .NewFFLayout("false")) d_ff_4 (
    .clk(CLK), .D(and_6_out), .Q(d_ff_4_q));  // open: Qn, preset, en, reset
  D_Flip_Flop #(.trigger("rising"), .Pre_Clr_Positions("LEGACY"), .NegatePresetClear("false"), .enable("true"), .NewFFLayout("false")) d_ff_5 (
    .clk(CLK), .D(and_7_out), .Q(d_ff_5_q));  // open: Qn, preset, en, reset
  D_Flip_Flop #(.trigger("rising"), .Pre_Clr_Positions("LEGACY"), .NegatePresetClear("false"), .enable("true"), .NewFFLayout("false")) d_ff_6 (
    .clk(CLK), .D(and_8_out), .Q(d_ff_6_q));  // open: Qn, preset, en, reset
  \单周期硬布线控制器  \u_单周期硬布线控制器_1  (
    .Funct({IR[30], IR[25], IR[14:12]}), .OP(IR[6:2]), .ALU_OP(AluOP), .MemToReg(MemToReg),
    .MemWrite(MemWrite), .ALU_SRC(AluSrcB), .RegWrite(RegWrite), .ecall(ecall), .S_type(S_type), .Jalr(JALR),
    .Beq(Beq), .JAL(JAL), .Bne(Bne), .in_3(IR[21]), .uret(URET), .SB(SB), .BLTU(BLTU), .CSRRSI(CSRRSI),
    .CSRRCI(CSRRCI), .LUI(LUI));  // open: BLT, BGE, AUIPC
  Multiplexer #(.select(1), .width(5), .disabled("Z"), .enable("false")) multiplexer_1 (
    .in0(IR[19:15]), .in1(5'b01010), .out(multiplexer_1_out), .sel(ecall));
  Multiplexer #(.select(1), .width(5), .disabled("Z"), .enable("false")) multiplexer_2 (
    .in0(IR[24:20]), .in1(5'b10001), .out(multiplexer_2_out), .sel(ecall));
  Multiplexer #(.select(1), .width(12), .disabled("Z"), .enable("false")) multiplexer_3 (
    .in0(IR[31:20]), .in1({IR[31:25], IR[11:7]}), .out(multiplexer_3_out), .sel(S_type));
  assign bit_extender_1_out = {{12{1'b0}}, IR[31:12]};  // Bit_Extender bit_extender_1
  Shifter #(.width(32), .shift("ll")) shifter_1 (.in(bit_extender_1_out), .\dist (5'b01100), .out(shifter_1_out));
  Shifter #(.width(12), .shift("ll")) shifter_2 (
    .in({IR[31], IR[7], IR[30:25], IR[11:8]}), .\dist (4'b0001), .out(shifter_2_out));
  Shifter #(.width(20), .shift("ll")) shifter_3 (
    .in({IR[31], IR[19:12], IR[20], IR[30:21]}), .\dist (5'b00001), .out(shifter_3_out));
  or or_13 (IR3_t, IR3, IRC);
  Multiplexer #(.select(1), .width(32), .disabled("Z"), .enable("false")) multiplexer_4 (
    .in0(shifter_1_out), .in1(multiplexer_7_out), .out(RDin), .sel(not_7_out));
  not not_7 (not_7_out, LUI);
  Adder #(.width(32)) adder_1 (.a(PC), .b(32'h4), .out(PC_4));  // open: cin, cout
  assign bit_extender_2_out = {{20{shifter_2_out[11]}}, shifter_2_out};  // Bit_Extender bit_extender_2
  assign bit_extender_3_out = {{12{shifter_3_out[19]}}, shifter_3_out};  // Bit_Extender bit_extender_3
  Regifile regifile_1 (
    .Din(RDin), .Clk(CLK), .R1(R1), .R2(R2), .WE(RegWrite), .W_num(IR[11:7]), .R1_num(multiplexer_1_out),
    .R2_num(multiplexer_2_out));
  assign bit_extender_4_out = {{20{multiplexer_3_out[11]}}, multiplexer_3_out};  // Bit_Extender bit_extender_4
  Multiplexer #(.select(1), .width(32), .disabled("Z"), .enable("false")) multiplexer_5 (
    .in0(PC_4), .in1(adder_2_out), .out(multiplexer_5_out), .sel(B));
  Adder #(.width(32)) adder_2 (.a(PC), .b(bit_extender_2_out), .out(adder_2_out));  // open: cin, cout
  Adder #(.width(32)) adder_3 (.a(PC), .b(bit_extender_3_out), .out(adder_3_out));  // open: cin, cout
  Priority_Encoder #(.select(2), .disabled("Z")) priority_encoder_1 (
    .in0(1'b0), .in1(d_ff_4_q), .in2(d_ff_5_q), .in3(d_ff_6_q), .out(Inter_Num), .gs(priority_encoder_1_gs));  // open: en_out, en_in
  Multiplexer #(.select(1), .width(32), .disabled("Z"), .enable("false")) multiplexer_6 (
    .in0(R2), .in1(bit_extender_4_out), .out(multiplexer_6_out), .sel(AluSrcB));
  Multiplexer #(.select(1), .width(32), .disabled("Z"), .enable("false")) multiplexer_7 (
    .in0(multiplexer_8_out), .in1(PC_4), .out(multiplexer_7_out), .sel(J));
  and and_9 (Interrupt, priority_encoder_1_gs, shield, IE);
  D_Flip_Flop #(.trigger("rising"), .Pre_Clr_Positions("LEGACY"), .NegatePresetClear("false"), .enable("true"), .NewFFLayout("false")) d_ff_7 (
    .clk(CLK), .D(or_14_out), .Qn(IE), .en(or_15_out));  // open: Q, preset, reset
  or or_14 (or_14_out, Interrupt, CSRRCI);
  or or_15 (or_15_out, Interrupt, CSRRCI, CSRRSI, URET);
  ALU alu_1 (
    .X(R1), .Y(multiplexer_6_out), .AluOP(AluOP), .Equal(equal), .Result(Result), .out_6(less));  // open: Result_2, out_4
  Multiplexer #(.select(1), .width(32), .disabled("Z"), .enable("false")) multiplexer_8 (
    .in0(Result), .in1(mips_ram_1_p8), .out(multiplexer_8_out), .sel(MemToReg));
  Multiplexer #(.select(1), .width(32), .disabled("Z"), .enable("false")) multiplexer_9 (
    .in0(multiplexer_5_out), .in1(adder_3_out), .out(multiplexer_9_out), .sel(JAL));
  Multiplexer #(.select(2), .width(32), .disabled("Z"), .enable("false")) multiplexer_10 (
    .in1(32'h30ac), .in2(32'h3158), .in3(32'h3204), .out(InterAddr), .sel(Inter_Num));  // open: in0
  Multiplexer #(.select(1), .width(32), .disabled("Z"), .enable("false")) multiplexer_11 (
    .in0(multiplexer_9_out), .in1(Result), .out(nextPC), .sel(JALR));
  not not_8 (not_8_out, MemWrite);
  Multiplexer #(.select(2), .width(4), .disabled("Z"), .enable("false")) multiplexer_12 (
    .in0(4'b0001), .in1(4'b0010), .in2(4'b0100), .in3(4'b1000), .out(multiplexer_12_out), .sel(Result[1:0]));
  Multiplexer #(.select(2), .width(5), .disabled("Z"), .enable("false")) multiplexer_13 (
    .in0({5{1'b0}}), .in1(5'b01000), .in2(5'b10000), .in3(5'b11000), .out(multiplexer_13_out),
    .sel(Result[1:0]));
  // MIPS_RAM mips_ram_1: pin names not known; wires that end beside it: Result[11:2], MDin, MemWrite, Select, CLK, not_8_out, RST, mips_ram_1_p8
  Multiplexer #(.select(1), .width(32), .disabled("Z"), .enable("false")) multiplexer_14 (
    .in0(nextPC), .in1(InterAddr), .out(multiplexer_14_out), .sel(Interrupt));
  D_Flip_Flop #(.trigger("high"), .Pre_Clr_Positions("LEGACY"), .NegatePresetClear("false"), .enable("true"), .NewFFLayout("false")) d_ff_8 (.Q(d_ff_8_q));  // open: clk, D, Qn, preset, en, reset
  // Probe on 13'hc
  Multiplexer #(.select(1), .width(4), .disabled("Z"), .enable("false")) multiplexer_15 (
    .in0(4'b1111), .in1(multiplexer_12_out), .out(Select), .sel(SB));
  Multiplexer #(.select(1), .width(32), .disabled("Z"), .enable("false")) multiplexer_16 (
    .in0(R2), .in1(shifter_4_out), .out(MDin), .sel(SB));
  Shifter #(.width(32), .shift("ll")) shifter_4 (.in(R2), .\dist (multiplexer_13_out), .out(shifter_4_out));
  Multiplexer #(.select(1), .width(32), .disabled("Z"), .enable("false")) multiplexer_17 (
    .in0(multiplexer_14_out), .in1(EPC), .out(PCin), .sel(URET));
  Comparator #(.width(13), .mode("twosComplement")) comparator_9 (
    .a(CNT_num), .b(13'hc), .eq(comparator_9_eq), .lt(comparator_9_lt));  // open: gt
  Clock #(.highDuration(1), .lowDuration(1)) clock_1 (.out(clock_1_out));
  Comparator #(.width(2), .mode("unsigned")) comparator_10 (
    .a(Inter_Num_Pri), .b(Inter_Num), .lt(shield));  // open: gt, eq
  Counter #(.width(13), .max('h1fff), .ongoal("stay"), .trigger("rising"), .behavior("old")) counter_2 (
    .count(comparator_9_lt), .Q(CNT_num), .clk(clock_1_out));  // open: load, D, carry, clr, preset
  Pull_Resistor #(.pull(1)) pull_resistor_4 (.node(shield));
  nand nand_1 (nand_1_out, d_ff_8_q, comparator_9_eq);
  assign CLK = nand_1_out ? clock_1_out : 1'bz;  // Controlled_Buffer controlled_buffer_1
  Pull_Resistor #(.pull(1)) pull_resistor_5 (.node(CLK));
  Demultiplexer #(.select(2), .width(1), .tristate("false"), .disabled("Z"), .enable("false")) demultiplexer_1 (
    .out0(demultiplexer_1_out0), .out1(demultiplexer_1_out1), .out2(demultiplexer_1_out2), .in(Interrupt),
    .sel(stack));  // open: out3
  Register #(.width(32), .trigger("rising"), .Select("low")) EPC1 (
    .D(nextPC), .en(demultiplexer_1_out0), .Q(EPC1_q), .clk(CLK));  // open: clr
  Register #(.width(32), .trigger("rising"), .Select("low")) EPC2 (
    .D(nextPC), .en(demultiplexer_1_out1), .Q(EPC2_q), .clk(CLK));  // open: clr
  Register #(.width(32), .trigger("rising"), .Select("low")) EPC3 (
    .D(nextPC), .en(demultiplexer_1_out2), .Q(EPC3_q), .clk(CLK));  // open: clr
  Multiplexer #(.select(2), .width(32), .disabled("Z"), .enable("false")) multiplexer_18 (
    .in1(EPC1_q), .in2(EPC2_q), .in3(EPC3_q), .out(EPC), .sel(stack));  // open: in0
  or or_16 (or_16_out, URET, Interrupt);
  Counter #(.width(2), .max('h3), .ongoal("wrap"), .trigger("rising"), .behavior("new")) counter_3 (
    .count(or_16_out), .Q(stack), .clk(CLK), .down(URET));  // open: load, D, carry, clr, preset
  Demultiplexer #(.select(2), .width(1), .tristate("false"), .disabled("Z"), .enable("false")) demultiplexer_2 (
    .out0(demultiplexer_2_out0), .out1(demultiplexer_2_out1), .out2(demultiplexer_2_out2), .in(Interrupt),
    .sel(stack));  // open: out3
  Register #(.width(2), .trigger("rising"), .Select("low")) u_IR1 (
    .D(Inter_Num), .en(demultiplexer_2_out0), .Q(IR1_q), .clk(CLK));  // open: clr
  Register #(.width(2), .trigger("rising"), .Select("low")) u_IR2 (
    .D(Inter_Num), .en(demultiplexer_2_out1), .Q(IR2_q), .clk(CLK));  // open: clr
  Register #(.width(2), .trigger("rising"), .Select("low")) u_IR3 (
    .D(Inter_Num), .en(demultiplexer_2_out2), .Q(IR3_q), .clk(CLK));  // open: clr
  Multiplexer #(.select(2), .width(2), .disabled("Z"), .enable("false")) multiplexer_19 (
    .in1(IR1_q), .in2(IR2_q), .in3(IR3_q), .out(Inter_Num_Pri), .sel(stack));  // open: in0
  Decoder #(.select(2), .tristate("false"), .disabled("Z"), .enable("false")) decoder_1 (
    .out1(decoder_1_out1), .out2(decoder_1_out2), .out3(decoder_1_out3), .sel(Inter_Num_Pri));  // open: out0
  and and_10 (Ret1, URET, decoder_1_out1);
  and and_11 (Ret2, decoder_1_out2, URET);
  and and_12 (Ret3, decoder_1_out3, URET);

  // Notes on the sheet:
  //   中断源
  //   中断等待指示
  //   总复位信号应将除ROM以外所有存储组件全部清零
  //   多级中断测试信号模拟器
  //   数码管输出
  //   数码管输出应该用寄存器锁存，否则显示数据只能一闪而过
  //   指令探针
  //   指令存储器
  //   指令字
  //   contents of rom_1 (hex, n*v repeats v):
  //   7d000113 100413 1f41993 41f9d993 433 c00913 800b13 140413 f47413 800293 100313 499993 89e9b3 1300533
  //   2200893 73 406282b3 fe0294e3 140413 f00f93 1f47433 1c41413 800293 100313 49d993 89e9b3 1300533
  //   2200893 73 406282b3 fe0294e3 1c45413 406b0b33 b0463 f95ff06f 2b3 fff2c293 1029293 fff2e293 500533
  //   2200893 73 f5dff06f 1112023 410113 a12023 410113 812023 410113 1312023 410113 1412023 410113 1512023
  //   410113 1612023 410113 40e073 100b13 300a13 100a93 1600433 441413 14469b3 1300533 2200893 73 fe0416e3
  //   415a0a33 fe0a10e3 40f073 ffc10113 12b03 ffc10113 12a83 ffc10113 12a03 ffc10113 12983 ffc10113 12403
  //   ffc10113 12503 ffc10113 12883 200073 1112023 410113 a12023 410113 812023 410113 1312023 410113
  //   1412023 410113 1512023 410113 1612023 410113 40e073 200b13 300a13 100a93 1600433 441413 14469b3
  //   1300533 2200893 73 fe0416e3 415a0a33 fe0a10e3 40f073 ffc10113 12b03 ffc10113 12a83 ffc10113 12a03
  //   ffc10113 12983 ffc10113 12403 ffc10113 12503 ffc10113 12883 200073 1112023 410113 a12023 410113
  //   812023 410113 1312023 410113 1412023 410113 1512023 410113 1612023 410113 40e073 300b13 300a13
  //   100a93 1600433 441413 14469b3 1300533 2200893 73 fe0416e3 415a0a33 fe0a10e3 40f073 ffc10113 12b03
  //   ffc10113 12a83 ffc10113 12a03 ffc10113 12983 ffc10113 12403 ffc10113 12503 ffc10113 12883 200073
  //   JAL
  //   JALR
  //   URET
  //   I型
  //   S型
  //   U型
  //   B型
  //   J型
  //   Beq
  //   Bne
  //   MemToReg
  //   MemWrite
  //   AluOP
  //   AluSrcB
  //   RegWrite
  //   为方便自动评测，需要输出PC，IR，寄存器堆写如数据RDin
  //   RAM写使能MemWrite、RAM写入数据MDin等信号
  //   数据存储器
  //   控制位
  //   暂停节拍，不能为0
  //   戳工具置1进入计数暂停模式，ctrl+k时钟自动运行到对应节拍暂停
  //   ctrl+k关闭时钟连续运行，将控制位置零，进入单步调试模式调试
  //   可计数暂停的时钟源
endmodule

module \封装正确性测试  (
);

  wire IR1, IR2, IR3, MemW, RegW;
  wire [31:0] EX_PC, ID_PC, IF_PC, IR, LED, MDin, MDinr, MEM_PC, PC, RDin, RDinr, WB_PC;

  \单周期RISC_V  \u_单周期risc_v_1  (
    .IR1(IR1), .IR2(IR2), .IR3(IR3), .RegWrite(RegW), .MemWrite(MemW), .PC(PC), .IR(IR), .RDin(RDin),
    .MDin(MDin), .LedData(LED));
  \气泡流水线  \u_气泡流水线_1  (
    .RegWrite(RegW), .MemWrite(MemW), .IF_PC(IF_PC), .ID_PC(ID_PC), .EX_PC(EX_PC), .M_PC(MEM_PC),
    .WB_PC(WB_PC), .RDin(RDinr), .MDin(MDinr), .LedData(LED));
  // 单周期_单级中断 单周期_单级中断_1: pin names not known; wires that end beside it: IR1, IR3, IR2, RegW, MemW, PC, IR, RDin, MDin, LED
  \理想流水线  \u_理想流水线_1  (
    .RegWrite(RegW), .MemWrite(MemW), .IF_PC(IF_PC), .ID_PC(ID_PC), .EX_PC(EX_PC), .M_PC(MEM_PC),
    .WB_PC(WB_PC), .RDin(RDinr), .MDin(MDinr), .LedData(LED));
  \重定向流水线  \u_重定向流水线_1  (
    .RegWrite(RegW), .MemWrite(MemW), .IF_PC(IF_PC), .ID_PC(ID_PC), .EX_PC(EX_PC), .M_PC(MEM_PC),
    .WB_PC(WB_PC), .RDin(RDinr), .MDin(MDinr), .LedData(LED));
  \单周期_多级中断  \u_单周期_多级中断_1  (
    .IR1(IR1), .IR2(IR2), .IR3(IR3), .RegWrite(RegW), .MemWrite(MemW), .PC(PC), .IR(IR), .RDin(RDin),
    .MDin(MDin), .LedData(LED));

  // Notes on the sheet:
  //   单周期封装测试
  //   气泡流水封装测试
  //   单周期+单级中断封装测试
  //   请检查上面封装有无位宽不匹配，引脚标签是否和连接的标签相对应，否则无法在educoder平台上正确测试
  //   理想流水封装测试
  //   重定向流水封装测试
  //   单周期+多级中断封装测试
endmodule

module IF_ID (
  input  [31:0] IRin,
  input  [31:0] PCin,
  input  RST,
  input  EN,
  input  CLK,
  output [31:0] IRout,
  output [31:0] PCout
);

  wire [31:0] multiplexer_1_out, multiplexer_2_out;

  Register #(.width(32), .trigger("rising"), .Select("low")) register_1 (
    .D(multiplexer_1_out), .en(EN), .Q(IRout), .clk(CLK));  // open: clr
  Multiplexer #(.select(1), .width(32), .disabled("Z"), .enable("false")) multiplexer_1 (
    .in0(IRin), .in1({32{1'b0}}), .out(multiplexer_1_out), .sel(RST));
  Register #(.width(32), .trigger("rising"), .Select("low")) register_2 (
    .D(multiplexer_2_out), .en(EN), .Q(PCout), .clk(CLK));  // open: clr
  Multiplexer #(.select(1), .width(32), .disabled("Z"), .enable("false")) multiplexer_2 (
    .in0(PCin), .in1({32{1'b0}}), .out(multiplexer_2_out), .sel(RST));
endmodule

module ID_EX (
  input  JALin,
  input  SBin,
  input  JALRin,
  input  BLTUin,
  input  CSRRCIin,
  input  URETin,
  input  CSRRSIin,
  input  [4:0] W_out,
  input  LUIin,
  input  [1:0] R1Forwardin,
  input  Beqin,
  input  [1:0] R2Forwardin,
  input  Bnein,
  input  MemToRegin,
  input  MemWritein,
  input  [3:0] AluOPin,
  input  AluSrcBin,
  input  RegWritein,
  input  Stypein,
  input  haltin,
  input  [31:0] R1in,
  input  [31:0] R2in,
  input  [31:0] Iin,
  input  [31:0] Sin,
  input  [31:0] Uin,
  input  [31:0] Bin,
  input  [31:0] Jin,
  input  [31:0] IRin,
  input  [31:0] PCin,
  input  RST,
  input  EN,
  input  CLK,
  output JALout,
  output SBout,
  output JALRout,
  output BLTUout,
  output CSRRCIout,
  output URETout,
  output CSRRSIout,
  output [4:0] W_out_2,
  output LUIout,
  output [1:0] R1forwardout,
  output Beqout,
  output [1:0] R2forwardout,
  output Bneout,
  output MemToRegout,
  output MemWriteout,
  output [3:0] AluOPout,
  output AluSrcBout,
  output RegWriteout,
  output Stypeout,
  output haltout,
  output [31:0] R1out,
  output [31:0] R2out,
  output [31:0] Iout,
  output [31:0] Sout,
  output [31:0] Uout,
  output [31:0] Bout,
  output [31:0] Jout,
  output [31:0] IRout,
  output [31:0] PCout
);

  wire multiplexer_1_out, multiplexer_2_out, multiplexer_3_out, multiplexer_4_out, multiplexer_5_out,
       multiplexer_6_out, multiplexer_7_out, multiplexer_8_out, multiplexer_9_out, multiplexer_10_out,
       multiplexer_11_out, multiplexer_13_out, multiplexer_14_out, multiplexer_15_out, multiplexer_16_out,
       multiplexer_26_out;
  wire [1:0] multiplexer_28_out, multiplexer_29_out;
  wire [3:0] multiplexer_12_out;
  wire [4:0] multiplexer_27_out;
  wire [31:0] multiplexer_17_out, multiplexer_18_out, multiplexer_19_out, multiplexer_20_out,
       multiplexer_21_out, multiplexer_22_out, multiplexer_23_out, multiplexer_24_out, multiplexer_25_out;

  Multiplexer #(.select(1), .width(1), .disabled("Z"), .enable("false")) multiplexer_1 (
    .in0(JALin), .in1(1'b0), .out(multiplexer_1_out), .sel(RST));
  Multiplexer #(.select(1), .width(1), .disabled("Z"), .enable("false")) multiplexer_2 (
    .in0(SBin), .in1(1'b0), .out(multiplexer_2_out), .sel(RST));
  Multiplexer #(.select(1), .width(1), .disabled("Z"), .enable("false")) multiplexer_3 (
    .in0(JALRin), .in1(1'b0), .out(multiplexer_3_out), .sel(RST));
  Multiplexer #(.select(1), .width(1), .disabled("Z"), .enable("false")) multiplexer_4 (
    .in0(BLTUin), .in1(1'b0), .out(multiplexer_4_out), .sel(RST));
  Multiplexer #(.select(1), .width(1), .disabled("Z"), .enable("false")) multiplexer_5 (
    .in0(URETin), .in1(1'b0), .out(multiplexer_5_out), .sel(RST));
  Multiplexer #(.select(1), .width(1), .disabled("Z"), .enable("false")) multiplexer_6 (
    .in0(CSRRSIin), .in1(1'b0), .out(multiplexer_6_out), .sel(RST));
  Multiplexer #(.select(1), .width(1), .disabled("Z"), .enable("false")) multiplexer_7 (
    .in0(LUIin), .in1(1'b0), .out(multiplexer_7_out), .sel(RST));
  Multiplexer #(.select(1), .width(1), .disabled("Z"), .enable("false")) multiplexer_8 (
    .in0(Beqin), .in1(1'b0), .out(multiplexer_8_out), .sel(RST));
  Multiplexer #(.select(1), .width(1), .disabled("Z"), .enable("false")) multiplexer_9 (
    .in0(Bnein), .in1(1'b0), .out(multiplexer_9_out), .sel(RST));
  Multiplexer #(.select(1), .width(1), .disabled("Z"), .enable("false")) multiplexer_10 (
    .in0(MemToRegin), .in1(1'b0), .out(multiplexer_10_out), .sel(RST));
  Multiplexer #(.select(1), .width(1), .disabled("Z"), .enable("false")) multiplexer_11 (
    .in0(MemWritein), .in1(1'b0), .out(multiplexer_11_out), .sel(RST));
  Multiplexer #(.select(1), .width(4), .disabled("Z"), .enable("false")) multiplexer_12 (
    .in0(AluOPin), .in1(4'b0000), .out(multiplexer_12_out), .sel(RST));
  Multiplexer #(.select(1), .width(1), .disabled("Z"), .enable("false")) multiplexer_13 (
    .in0(AluSrcBin), .in1(1'b0), .out(multiplexer_13_out), .sel(RST));
  Multiplexer #(.select(1), .width(1), .disabled("Z"), .enable("false")) multiplexer_14 (
    .in0(RegWritein), .in1(1'b0), .out(multiplexer_14_out), .sel(RST));
  Multiplexer #(.select(1), .width(1), .disabled("Z"), .enable("false")) multiplexer_15 (
    .in0(Stypein), .in1(1'b0), .out(multiplexer_15_out), .sel(RST));
  Multiplexer #(.select(1), .width(1), .disabled("Z"), .enable("false")) multiplexer_16 (
    .in0(haltin), .in1(1'b0), .out(multiplexer_16_out), .sel(RST));
  Multiplexer #(.select(1), .width(32), .disabled("Z"), .enable("false")) multiplexer_17 (
    .in0(R1in), .in1({32{1'b0}}), .out(multiplexer_17_out), .sel(RST));
  Multiplexer #(.select(1), .width(32), .disabled("Z"), .enable("false")) multiplexer_18 (
    .in0(R2in), .in1({32{1'b0}}), .out(multiplexer_18_out), .sel(RST));
  Multiplexer #(.select(1), .width(32), .disabled("Z"), .enable("false")) multiplexer_19 (
    .in0(Iin), .in1({32{1'b0}}), .out(multiplexer_19_out), .sel(RST));
  Multiplexer #(.select(1), .width(32), .disabled("Z"), .enable("false")) multiplexer_20 (
    .in0(Sin), .in1({32{1'b0}}), .out(multiplexer_20_out), .sel(RST));
  Multiplexer #(.select(1), .width(32), .disabled("Z"), .enable("false")) multiplexer_21 (
    .in0(Uin), .in1({32{1'b0}}), .out(multiplexer_21_out), .sel(RST));
  Multiplexer #(.select(1), .width(32), .disabled("Z"), .enable("false")) multiplexer_22 (
    .in0(Bin), .in1({32{1'b0}}), .out(multiplexer_22_out), .sel(RST));
  Multiplexer #(.select(1), .width(32), .disabled("Z"), .enable("false")) multiplexer_23 (
    .in0(Jin), .in1({32{1'b0}}), .out(multiplexer_23_out), .sel(RST));
  Multiplexer #(.select(1), .width(32), .disabled("Z"), .enable("false")) multiplexer_24 (
    .in0(IRin), .in1({32{1'b0}}), .out(multiplexer_24_out), .sel(RST));
  Multiplexer #(.select(1), .width(32), .disabled("Z"), .enable("false")) multiplexer_25 (
    .in0(PCin), .in1({32{1'b0}}), .out(multiplexer_25_out), .sel(RST));
  Register #(.width(1), .trigger("rising"), .Select("low")) register_1 (
    .D(multiplexer_1_out), .en(EN), .Q(JALout), .clk(CLK));  // open: clr
  Register #(.width(1), .trigger("rising"), .Select("low")) register_2 (
    .D(multiplexer_2_out), .en(EN), .Q(SBout), .clk(CLK));  // open: clr
  Register #(.width(1), .trigger("rising"), .Select("low")) register_3 (
    .D(multiplexer_3_out), .en(EN), .Q(JALRout), .clk(CLK));  // open: clr
  Register #(.width(1), .trigger("rising"), .Select("low")) register_4 (
    .D(multiplexer_4_out), .en(EN), .Q(BLTUout), .clk(CLK));  // open: clr
  Register #(.width(1), .trigger("rising"), .Select("low")) register_5 (
    .D(multiplexer_5_out), .en(EN), .Q(URETout), .clk(CLK));  // open: clr
  Register #(.width(1), .trigger("rising"), .Select("low")) register_6 (
    .D(multiplexer_6_out), .en(EN), .Q(CSRRSIout), .clk(CLK));  // open: clr
  Register #(.width(1), .trigger("rising"), .Select("low")) register_7 (
    .D(multiplexer_7_out), .en(EN), .Q(LUIout), .clk(CLK));  // open: clr
  Register #(.width(1), .trigger("rising"), .Select("low")) register_8 (
    .D(multiplexer_8_out), .en(EN), .Q(Beqout), .clk(CLK));  // open: clr
  Register #(.width(1), .trigger("rising"), .Select("low")) register_9 (
    .D(multiplexer_9_out), .en(EN), .Q(Bneout), .clk(CLK));  // open: clr
  Register #(.width(1), .trigger("rising"), .Select("low")) register_10 (
    .D(multiplexer_10_out), .en(EN), .Q(MemToRegout), .clk(CLK));  // open: clr
  Register #(.width(1), .trigger("rising"), .Select("low")) register_11 (
    .D(multiplexer_11_out), .en(EN), .Q(MemWriteout), .clk(CLK));  // open: clr
  Register #(.width(4), .trigger("rising"), .Select("low")) register_12 (
    .D(multiplexer_12_out), .en(EN), .Q(AluOPout), .clk(CLK));  // open: clr
  Register #(.width(1), .trigger("rising"), .Select("low")) register_13 (
    .D(multiplexer_13_out), .en(EN), .Q(AluSrcBout), .clk(CLK));  // open: clr
  Register #(.width(1), .trigger("rising"), .Select("low")) register_14 (
    .D(multiplexer_14_out), .en(EN), .Q(RegWriteout), .clk(CLK));  // open: clr
  Register #(.width(1), .trigger("rising"), .Select("low")) register_15 (
    .D(multiplexer_15_out), .en(EN), .Q(Stypeout), .clk(CLK));  // open: clr
  Register #(.width(1), .trigger("rising"), .Select("low")) register_16 (
    .D(multiplexer_16_out), .en(EN), .Q(haltout), .clk(CLK));  // open: clr
  Register #(.width(32), .trigger("rising"), .Select("low")) register_17 (
    .D(multiplexer_17_out), .en(EN), .Q(R1out), .clk(CLK));  // open: clr
  Register #(.width(32), .trigger("rising"), .Select("low")) register_18 (
    .D(multiplexer_18_out), .en(EN), .Q(R2out), .clk(CLK));  // open: clr
  Register #(.width(32), .trigger("rising"), .Select("low")) register_19 (
    .D(multiplexer_19_out), .en(EN), .Q(Iout), .clk(CLK));  // open: clr
  Register #(.width(32), .trigger("rising"), .Select("low")) register_20 (
    .D(multiplexer_20_out), .en(EN), .Q(Sout), .clk(CLK));  // open: clr
  Register #(.width(32), .trigger("rising"), .Select("low")) register_21 (
    .D(multiplexer_21_out), .en(EN), .Q(Uout), .clk(CLK));  // open: clr
  Register #(.width(32), .trigger("rising"), .Select("low")) register_22 (
    .D(multiplexer_22_out), .en(EN), .Q(Bout), .clk(CLK));  // open: clr
  Register #(.width(32), .trigger("rising"), .Select("low")) register_23 (
    .D(multiplexer_23_out), .en(EN), .Q(Jout), .clk(CLK));  // open: clr
  Register #(.width(32), .trigger("rising"), .Select("low")) register_24 (
    .D(multiplexer_24_out), .en(EN), .Q(IRout), .clk(CLK));  // open: clr
  Register #(.width(32), .trigger("rising"), .Select("low")) register_25 (
    .D(multiplexer_25_out), .en(EN), .Q(PCout), .clk(CLK));  // open: clr
  Multiplexer #(.select(1), .width(1), .disabled("Z"), .enable("false")) multiplexer_26 (
    .in0(CSRRCIin), .in1(1'b0), .out(multiplexer_26_out), .sel(RST));
  Multiplexer #(.select(1), .width(5), .disabled("Z"), .enable("false")) multiplexer_27 (
    .in0(W_out), .in1({5{1'b0}}), .out(multiplexer_27_out), .sel(RST));
  Multiplexer #(.select(1), .width(2), .disabled("Z"), .enable("false")) multiplexer_28 (
    .in0(R1Forwardin), .in1(2'b00), .out(multiplexer_28_out), .sel(RST));
  Multiplexer #(.select(1), .width(2), .disabled("Z"), .enable("false")) multiplexer_29 (
    .in0(R2Forwardin), .in1(2'b00), .out(multiplexer_29_out), .sel(RST));
  Register #(.width(1), .trigger("rising"), .Select("low")) register_26 (
    .D(multiplexer_26_out), .en(EN), .Q(CSRRCIout), .clk(CLK));  // open: clr
  Register #(.width(5), .trigger("rising"), .Select("low")) register_27 (
    .D(multiplexer_27_out), .en(EN), .Q(W_out_2), .clk(CLK));  // open: clr
  Register #(.width(2), .trigger("rising"), .Select("low")) register_28 (
    .D(multiplexer_28_out), .en(EN), .Q(R1forwardout), .clk(CLK));  // open: clr
  Register #(.width(2), .trigger("rising"), .Select("low")) register_29 (
    .D(multiplexer_29_out), .en(EN), .Q(R2forwardout), .clk(CLK));  // open: clr
endmodule

module EX_MEM (
  input  [31:0] IRin,
  input  [31:0] PCin,
  input  haltin,
  input  Jin,
  input  [4:0] W_in,
  input  [31:0] Resultin,
  input  MemToRegin,
  input  MemWritein,
  input  RegWritein,
  input  [3:0] Selectin,
  input  [31:0] MDin,
  input  LUIin,
  input  [31:0] Uin,
  input  RST,
  input  EN,
  input  CLK,
  output [31:0] IRout,
  output [31:0] PCout,
  output haltout,
  output Jout,
  output [4:0] W_out,
  output [31:0] Resultout,
  output MemToRegout,
  output MemWriteout,
  output RegWriteout,
  output [3:0] Selectout,
  output [31:0] MDout,
  output LUIout,
  output [31:0] Uout
);

  wire multiplexer_3_out, multiplexer_4_out, multiplexer_7_out, multiplexer_8_out, multiplexer_9_out,
       multiplexer_12_out, not_1_out;
  wire [3:0] multiplexer_10_out;
  wire [4:0] multiplexer_5_out;
  wire [31:0] multiplexer_1_out, multiplexer_2_out, multiplexer_6_out, multiplexer_11_out, multiplexer_13_out;

  not not_1 (not_1_out, RST);
  Multiplexer #(.select(1), .width(32), .disabled("Z"), .enable("false")) multiplexer_1 (
    .in0(IRin), .in1({32{1'b0}}), .out(multiplexer_1_out), .sel(RST));
  Register #(.width(32), .trigger("rising"), .Select("low")) register_1 (
    .D(multiplexer_1_out), .en(EN), .Q(IRout), .clk(CLK));  // open: clr
  Multiplexer #(.select(1), .width(32), .disabled("Z"), .enable("false")) multiplexer_2 (
    .in0(PCin), .in1({32{1'b0}}), .out(multiplexer_2_out), .sel(RST));
  Register #(.width(32), .trigger("rising"), .Select("low")) register_2 (
    .D(multiplexer_2_out), .en(EN), .Q(PCout), .clk(CLK));  // open: clr
  Multiplexer #(.select(1), .width(1), .disabled("Z"), .enable("false")) multiplexer_3 (
    .in0(1'b0), .in1(haltin), .out(multiplexer_3_out), .sel(not_1_out));
  Register #(.width(1), .trigger("rising"), .Select("low")) register_3 (
    .D(multiplexer_3_out), .en(EN), .Q(haltout), .clk(CLK));  // open: clr
  Multiplexer #(.select(1), .width(1), .disabled("Z"), .enable("false")) multiplexer_4 (
    .in0(1'b0), .in1(Jin), .out(multiplexer_4_out), .sel(not_1_out));
  Register #(.width(1), .trigger("rising"), .Select("low")) register_4 (
    .D(multiplexer_4_out), .en(EN), .Q(Jout), .clk(CLK));  // open: clr
  Register #(.width(5), .trigger("rising"), .Select("low")) register_5 (
    .D(multiplexer_5_out), .en(EN), .Q(W_out), .clk(CLK));  // open: clr
  Multiplexer #(.select(1), .width(5), .disabled("Z"), .enable("false")) multiplexer_5 (
    .in0({5{1'b0}}), .in1(W_in), .out(multiplexer_5_out), .sel(not_1_out));
  Register #(.width(32), .trigger("rising"), .Select("low")) register_6 (
    .D(multiplexer_6_out), .en(EN), .Q(Resultout), .clk(CLK));  // open: clr
  Multiplexer #(.select(1), .width(32), .disabled("Z"), .enable("false")) multiplexer_6 (
    .in0({32{1'b0}}), .in1(Resultin), .out(multiplexer_6_out), .sel(not_1_out));
  Multiplexer #(.select(1), .width(1), .disabled("Z"), .enable("false")) multiplexer_7 (
    .in0(1'b0), .in1(MemToRegin), .out(multiplexer_7_out), .sel(not_1_out));
  Register #(.width(1), .trigger("rising"), .Select("low")) register_7 (
    .D(multiplexer_7_out), .en(EN), .Q(MemToRegout), .clk(CLK));  // open: clr
  Multiplexer #(.select(1), .width(1), .disabled("Z"), .enable("false")) multiplexer_8 (
    .in0(1'b0), .in1(MemWritein), .out(multiplexer_8_out), .sel(not_1_out));
  Register #(.width(1), .trigger("rising"), .Select("low")) register_8 (
    .D(multiplexer_8_out), .en(EN), .Q(MemWriteout), .clk(CLK));  // open: clr
  Multiplexer #(.select(1), .width(1), .disabled("Z"), .enable("false")) multiplexer_9 (
    .in0(1'b0), .in1(RegWritein), .out(multiplexer_9_out), .sel(not_1_out));
  Register #(.width(1), .trigger("rising"), .Select("low")) register_9 (
    .D(multiplexer_9_out), .en(EN), .Q(RegWriteout), .clk(CLK));  // open: clr
  Multiplexer #(.select(1), .width(4), .disabled("Z"), .enable("false")) multiplexer_10 (
    .in0(4'b0000), .in1(Selectin), .out(multiplexer_10_out), .sel(not_1_out));
  Register #(.width(4), .trigger("rising"), .Select("low")) register_10 (
    .D(multiplexer_10_out), .en(EN), .Q(Selectout), .clk(CLK));  // open: clr
  Multiplexer #(.select(1), .width(32), .disabled("Z"), .enable("false")) multiplexer_11 (
    .in0({32{1'b0}}), .in1(MDin), .out(multiplexer_11_out), .sel(not_1_out));
  Register #(.width(32), .trigger("rising"), .Select("low")) register_11 (
    .D(multiplexer_11_out), .en(EN), .Q(MDout), .clk(CLK));  // open: clr
  Register #(.width(1), .trigger("rising"), .Select("low")) register_12 (
    .D(multiplexer_12_out), .en(EN), .Q(LUIout), .clk(CLK));  // open: clr
  Multiplexer #(.select(1), .width(1), .disabled("Z"), .enable("false")) multiplexer_12 (
    .in0(1'b0), .in1(LUIin), .out(multiplexer_12_out), .sel(not_1_out));
  Multiplexer #(.select(1), .width(32), .disabled("Z"), .enable("false")) multiplexer_13 (
    .in0({32{1'b0}}), .in1(Uin), .out(multiplexer_13_out), .sel(not_1_out));
  Register #(.width(32), .trigger("rising"), .Select("low")) register_13 (
    .D(multiplexer_13_out), .en(EN), .Q(Uout), .clk(CLK));  // open: clr
endmodule

module MEM_WB (
  input  [31:0] IRin,
  input  [31:0] PCin,
  input  haltin,
  input  Jin,
  input  [4:0] W_in,
  input  [31:0] Resultin,
  input  MemToRegin,
  input  RegWritein,
  input  [31:0] MDdatein,
  input  LUIin,
  input  [31:0] Uin,
  input  RST,
  input  EN,
  input  CLK,
  output [31:0] IRout,
  output [31:0] PCout,
  output haltout,
  output Jout,
  output [4:0] W_out,
  output [31:0] Resultout,
  output MemToRegout,
  output RegWriteout,
  output [31:0] MDdateout,
  output LUIout,
  output [31:0] Uout
);

  wire multiplexer_3_out, multiplexer_4_out, multiplexer_7_out, multiplexer_8_out, multiplexer_11_out,
       not_1_out;
  wire [3:0] multiplexer_9_out, register_9_q, undriven;
  wire [4:0] multiplexer_5_out;
  wire [31:0] multiplexer_1_out, multiplexer_2_out, multiplexer_6_out, multiplexer_10_out, multiplexer_12_out;

  not not_1 (not_1_out, RST);
  Register #(.width(32), .trigger("rising"), .Select("low")) register_1 (
    .D(multiplexer_1_out), .en(EN), .Q(IRout), .clk(CLK));  // open: clr
  Multiplexer #(.select(1), .width(32), .disabled("Z"), .enable("false")) multiplexer_1 (
    .in0(IRin), .in1({32{1'b0}}), .out(multiplexer_1_out), .sel(RST));
  Register #(.width(32), .trigger("rising"), .Select("low")) register_2 (
    .D(multiplexer_2_out), .en(EN), .Q(PCout), .clk(CLK));  // open: clr
  Multiplexer #(.select(1), .width(32), .disabled("Z"), .enable("false")) multiplexer_2 (
    .in0(PCin), .in1({32{1'b0}}), .out(multiplexer_2_out), .sel(RST));
  Register #(.width(1), .trigger("rising"), .Select("low")) register_3 (
    .D(multiplexer_3_out), .en(EN), .Q(haltout), .clk(CLK));  // open: clr
  Multiplexer #(.select(1), .width(1), .disabled("Z"), .enable("false")) multiplexer_3 (
    .in0(1'b0), .in1(haltin), .out(multiplexer_3_out), .sel(not_1_out));
  Multiplexer #(.select(1), .width(1), .disabled("Z"), .enable("false")) multiplexer_4 (
    .in0(1'b0), .in1(Jin), .out(multiplexer_4_out), .sel(not_1_out));
  Register #(.width(1), .trigger("rising"), .Select("low")) register_4 (
    .D(multiplexer_4_out), .en(EN), .Q(Jout), .clk(CLK));  // open: clr
  Multiplexer #(.select(1), .width(5), .disabled("Z"), .enable("false")) multiplexer_5 (
    .in0({5{1'b0}}), .in1(W_in), .out(multiplexer_5_out), .sel(not_1_out));
  Register #(.width(5), .trigger("rising"), .Select("low")) register_5 (
    .D(multiplexer_5_out), .en(EN), .Q(W_out), .clk(CLK));  // open: clr
  Register #(.width(32), .trigger("rising"), .Select("low")) register_6 (
    .D(multiplexer_6_out), .en(EN), .Q(Resultout), .clk(CLK));  // open: clr
  Multiplexer #(.select(1), .width(32), .disabled("Z"), .enable("false")) multiplexer_6 (
    .in0({32{1'b0}}), .in1(Resultin), .out(multiplexer_6_out), .sel(not_1_out));
  Register #(.width(1), .trigger("rising"), .Select("low")) register_7 (
    .D(multiplexer_7_out), .en(EN), .Q(MemToRegout), .clk(CLK));  // open: clr
  Multiplexer #(.select(1), .width(1), .disabled("Z"), .enable("false")) multiplexer_7 (
    .in0(1'b0), .in1(MemToRegin), .out(multiplexer_7_out), .sel(not_1_out));
  Register #(.width(1), .trigger("rising"), .Select("low")) register_8 (
    .D(multiplexer_8_out), .en(EN), .Q(RegWriteout), .clk(CLK));  // open: clr
  Multiplexer #(.select(1), .width(1), .disabled("Z"), .enable("false")) multiplexer_8 (
    .in0(1'b0), .in1(RegWritein), .out(multiplexer_8_out), .sel(not_1_out));
  Multiplexer #(.select(1), .width(4), .disabled("Z"), .enable("false")) multiplexer_9 (
    .in0(4'b0000), .in1(undriven), .out(multiplexer_9_out), .sel(not_1_out));
  Register #(.width(4), .trigger("rising"), .Select("low")) register_9 (
    .D(multiplexer_9_out), .en(EN), .Q(register_9_q), .clk(CLK));  // open: clr
  Multiplexer #(.select(1), .width(32), .disabled("Z"), .enable("false")) multiplexer_10 (
    .in0({32{1'b0}}), .in1(MDdatein), .out(multiplexer_10_out), .sel(not_1_out));
  Register #(.width(32), .trigger("rising"), .Select("low")) register_10 (
    .D(multiplexer_10_out), .en(EN), .Q(MDdateout), .clk(CLK));  // open: clr
  Register #(.width(1), .trigger("rising"), .Select("low")) register_11 (
    .D(multiplexer_11_out), .en(EN), .Q(LUIout), .clk(CLK));  // open: clr
  Multiplexer #(.select(1), .width(1), .disabled("Z"), .enable("false")) multiplexer_11 (
    .in0(1'b0), .in1(LUIin), .out(multiplexer_11_out), .sel(not_1_out));
  Multiplexer #(.select(1), .width(32), .disabled("Z"), .enable("false")) multiplexer_12 (
    .in0({32{1'b0}}), .in1(Uin), .out(multiplexer_12_out), .sel(not_1_out));
  Register #(.width(32), .trigger("rising"), .Select("low")) register_12 (
    .D(multiplexer_12_out), .en(EN), .Q(Uout), .clk(CLK));  // open: clr
endmodule

module \数据冲突判断  (
  input  [4:0] ID_R1_num,
  input  [4:0] EX_W_num,
  input  EX_RegWrite,
  input  [4:0] ID_R2_num,
  input  [4:0] MEM_W_num,
  input  MEM_RegWrite,
  input  [4:0] OP,
  input  ecall,
  input  [4:0] Func,
  output DataHazzard
);

  wire and_1_out, and_2_out, and_3_out, and_4_out, and_5_out, and_6_out, comparator_1_eq, comparator_2_eq,
       comparator_3_eq, comparator_4_eq, comparator_5_eq, comparator_6_eq, comparator_7_eq, comparator_8_eq,
       or_1_out, or_2_out, or_3_out, or_4_out, \辅助判断数据冲突_1_r1 , \辅助判断数据冲突_1_r2 ;

  \辅助判断数据冲突  \u_辅助判断数据冲突_1  (
    .OP2(OP[0]), .OP3(OP[1]), .OP4(OP[2]), .OP5(OP[3]), .OP6(OP[4]), .F12(Func[0]), .F13(Func[1]),
    .F14(Func[2]), .F25(Func[3]), .F30(Func[4]), .R1(\辅助判断数据冲突_1_r1 ), .R2(\辅助判断数据冲突_1_r2 ));
  Comparator #(.width(5), .mode("twosComplement")) comparator_1 (
    .a(ID_R1_num), .b(EX_W_num), .eq(comparator_1_eq));  // open: gt, lt
  Comparator #(.width(5), .mode("twosComplement")) comparator_2 (
    .a(ID_R1_num), .b({5{1'b0}}), .eq(comparator_2_eq));  // open: gt, lt
  or or_1 (or_1_out, ecall, \辅助判断数据冲突_1_r1 );
  or or_2 (or_2_out, \辅助判断数据冲突_1_r2 , ecall);
  Comparator #(.width(5), .mode("twosComplement")) comparator_3 (
    .a(ID_R2_num), .b(EX_W_num), .eq(comparator_3_eq));  // open: gt, lt
  Comparator #(.width(5), .mode("twosComplement")) comparator_4 (
    .a(ID_R2_num), .b({5{1'b0}}), .eq(comparator_4_eq));  // open: gt, lt
  and and_1 (and_1_out, comparator_1_eq, EX_RegWrite, ~comparator_2_eq);  // AND_Gate
  and and_2 (and_2_out, comparator_3_eq, EX_RegWrite, ~comparator_4_eq);  // AND_Gate
  Comparator #(.width(5), .mode("twosComplement")) comparator_5 (
    .a(ID_R1_num), .b(MEM_W_num), .eq(comparator_5_eq));  // open: gt, lt
  Comparator #(.width(5), .mode("twosComplement")) comparator_6 (
    .a(ID_R1_num), .b({5{1'b0}}), .eq(comparator_6_eq));  // open: gt, lt
  Comparator #(.width(5), .mode("twosComplement")) comparator_7 (
    .a(ID_R2_num), .b(MEM_W_num), .eq(comparator_7_eq));  // open: gt, lt
  Comparator #(.width(5), .mode("twosComplement")) comparator_8 (
    .a(ID_R2_num), .b({5{1'b0}}), .eq(comparator_8_eq));  // open: gt, lt
  and and_3 (and_3_out, comparator_5_eq, MEM_RegWrite, ~comparator_6_eq);  // AND_Gate
  and and_4 (and_4_out, comparator_7_eq, MEM_RegWrite, ~comparator_8_eq);  // AND_Gate
  or or_3 (or_3_out, and_3_out, and_1_out);
  and and_5 (and_5_out, or_3_out, or_1_out);
  and and_6 (and_6_out, or_2_out, or_4_out);
  or or_4 (or_4_out, and_2_out, and_4_out);
  or or_5 (DataHazzard, and_5_out, and_6_out);
endmodule
module \辅助判断数据冲突  (
  input  OP2,
  input  OP3,
  input  OP4,
  input  OP5,
  input  OP6,
  input  F12,
  input  F13,
  input  F14,
  input  F25,
  input  F30,
  output R1,
  output R2
);

  wire and_1_out, and_2_out, and_3_out, and_4_out, and_5_out, and_6_out, and_7_out, and_8_out, and_9_out,
       and_10_out, and_11_out, and_12_out, and_13_out, and_14_out, and_15_out, and_16_out, and_17_out,
       and_18_out, and_19_out, and_20_out, and_21_out, and_22_out, and_23_out, and_24_out, and_25_out,
       and_26_out, and_27_out, and_28_out, and_29_out, and_30_out, and_31_out, and_32_out, and_33_out,
       and_34_out, and_35_out, and_36_out, and_37_out, not_1_out, not_2_out, not_3_out, not_4_out, not_5_out,
       not_6_out, not_7_out, not_8_out, not_9_out, not_10_out, not_11_out, not_12_out, not_13_out,
       not_14_out, not_15_out, not_16_out, not_17_out, not_18_out, not_19_out, not_20_out, not_21_out,
       not_22_out, not_23_out, not_24_out, not_25_out, not_26_out, not_27_out, not_28_out, not_29_out,
       not_30_out, not_31_out, not_32_out, not_33_out, not_34_out, not_35_out, not_36_out, not_37_out,
       not_38_out, not_39_out, not_40_out, not_41_out, not_42_out, not_43_out, not_44_out, not_45_out,
       not_46_out, not_47_out, not_48_out, not_49_out, not_50_out, not_51_out, not_52_out, not_53_out,
       not_54_out, not_55_out, not_56_out, not_57_out, not_58_out, not_59_out, not_60_out, not_61_out,
       not_62_out, not_63_out, not_64_out, not_65_out, not_66_out, not_67_out, not_68_out, not_69_out,
       not_70_out, not_71_out, not_72_out, not_73_out, not_74_out, not_75_out, not_76_out, not_77_out,
       not_78_out, not_79_out, not_80_out, not_81_out, not_82_out, not_83_out, not_84_out, not_85_out,
       not_86_out, not_87_out, not_88_out, not_89_out, not_90_out, not_91_out, not_92_out, not_93_out,
       not_94_out, not_95_out, not_96_out, not_97_out, not_98_out, not_99_out, not_100_out, not_101_out,
       not_102_out, not_103_out, not_104_out, not_105_out, not_106_out, not_107_out, not_108_out,
       not_109_out, not_110_out, not_111_out, not_112_out, not_113_out, not_114_out, not_115_out,
       not_116_out, not_117_out, not_118_out, not_119_out, not_120_out, not_121_out, not_122_out,
       not_123_out, not_124_out, not_125_out, not_126_out, not_127_out, not_128_out, not_129_out,
       not_130_out, not_131_out, not_132_out, not_133_out, not_134_out, not_135_out, not_136_out,
       not_137_out, not_138_out, not_139_out, not_140_out, not_141_out, not_142_out, not_143_out,
       not_144_out, not_145_out, not_146_out, not_147_out, not_148_out, not_149_out, not_150_out,
       not_151_out, not_152_out, not_153_out, not_154_out, not_155_out, not_156_out, not_157_out,
       not_158_out, not_159_out, not_160_out, not_161_out, not_162_out, not_163_out, not_164_out,
       not_165_out, not_166_out, not_167_out, not_168_out, not_169_out, not_170_out, not_171_out,
       not_172_out, not_173_out, not_174_out, not_175_out, not_176_out, not_177_out, not_178_out,
       not_179_out, not_180_out, not_181_out, not_182_out, not_183_out, not_184_out, not_185_out,
       not_186_out, not_187_out, not_188_out, not_189_out, not_190_out, not_191_out, not_192_out,
       not_193_out, not_194_out, not_195_out, not_196_out, not_197_out, not_198_out, not_199_out,
       not_200_out, not_201_out, not_202_out, not_203_out, not_204_out, not_205_out, not_206_out,
       not_207_out, not_208_out, not_209_out, not_210_out, not_211_out, not_212_out, not_213_out,
       not_214_out, not_215_out, not_216_out, not_217_out, not_218_out;

  not not_1 (not_1_out, F30);
  not not_2 (not_2_out, F25);
  not not_3 (not_3_out, F14);
  not not_4 (not_4_out, F13);
  not not_5 (not_5_out, F12);
  not not_6 (not_6_out, OP6);
  not not_7 (not_7_out, OP3);
  not not_8 (not_8_out, OP2);
  not not_9 (not_9_out, F25);
  not not_10 (not_10_out, F14);
  not not_11 (not_11_out, F13);
  not not_12 (not_12_out, F12);
  not not_13 (not_13_out, OP6);
  not not_14 (not_14_out, OP3);
  not not_15 (not_15_out, OP2);
  not not_16 (not_16_out, F30);
  not not_17 (not_17_out, F25);
  not not_18 (not_18_out, OP6);
  not not_19 (not_19_out, OP3);
  not not_20 (not_20_out, OP2);
  not not_21 (not_21_out, F30);
  not not_22 (not_22_out, F25);
  not not_23 (not_23_out, F12);
  not not_24 (not_24_out, OP6);
  not not_25 (not_25_out, OP3);
  not not_26 (not_26_out, OP2);
  not not_27 (not_27_out, F30);
  not not_28 (not_28_out, F25);
  not not_29 (not_29_out, F14);
  not not_30 (not_30_out, F12);
  not not_31 (not_31_out, OP6);
  not not_32 (not_32_out, OP3);
  not not_33 (not_33_out, OP2);
  not not_34 (not_34_out, F30);
  not not_35 (not_35_out, F25);
  not not_36 (not_36_out, F14);
  not not_37 (not_37_out, OP6);
  not not_38 (not_38_out, OP3);
  not not_39 (not_39_out, OP2);
  not not_40 (not_40_out, F14);
  not not_41 (not_41_out, F13);
  not not_42 (not_42_out, F12);
  not not_43 (not_43_out, OP6);
  not not_44 (not_44_out, OP5);
  not not_45 (not_45_out, OP3);
  not not_46 (not_46_out, OP2);
  not not_47 (not_47_out, OP6);
  not not_48 (not_48_out, OP5);
  not not_49 (not_49_out, OP3);
  not not_50 (not_50_out, OP2);
  not not_51 (not_51_out, F12);
  not not_52 (not_52_out, OP6);
  not not_53 (not_53_out, OP5);
  not not_54 (not_54_out, OP3);
  not not_55 (not_55_out, OP2);
  not not_56 (not_56_out, F13);
  not not_57 (not_57_out, F12);
  not not_58 (not_58_out, OP6);
  not not_59 (not_59_out, OP5);
  not not_60 (not_60_out, OP3);
  not not_61 (not_61_out, OP2);
  not not_62 (not_62_out, F14);
  not not_63 (not_63_out, F12);
  not not_64 (not_64_out, OP6);
  not not_65 (not_65_out, OP5);
  not not_66 (not_66_out, OP3);
  not not_67 (not_67_out, OP2);
  not not_68 (not_68_out, F30);
  not not_69 (not_69_out, F25);
  not not_70 (not_70_out, F14);
  not not_71 (not_71_out, F13);
  not not_72 (not_72_out, OP6);
  not not_73 (not_73_out, OP5);
  not not_74 (not_74_out, OP3);
  not not_75 (not_75_out, OP2);
  not not_76 (not_76_out, F30);
  not not_77 (not_77_out, F25);
  not not_78 (not_78_out, F13);
  not not_79 (not_79_out, OP6);
  not not_80 (not_80_out, OP5);
  not not_81 (not_81_out, OP3);
  not not_82 (not_82_out, OP2);
  not not_83 (not_83_out, F25);
  not not_84 (not_84_out, F13);
  not not_85 (not_85_out, OP6);
  not not_86 (not_86_out, OP5);
  not not_87 (not_87_out, OP3);
  not not_88 (not_88_out, OP2);
  not not_89 (not_89_out, F14);
  not not_90 (not_90_out, F12);
  not not_91 (not_91_out, OP6);
  not not_92 (not_92_out, OP5);
  not not_93 (not_93_out, OP4);
  not not_94 (not_94_out, OP3);
  not not_95 (not_95_out, OP2);
  not not_96 (not_96_out, F14);
  not not_97 (not_97_out, F12);
  not not_98 (not_98_out, OP6);
  not not_99 (not_99_out, OP4);
  not not_100 (not_100_out, OP3);
  not not_101 (not_101_out, OP2);
  not not_102 (not_102_out, F14);
  not not_103 (not_103_out, F13);
  not not_104 (not_104_out, F12);
  not not_105 (not_105_out, OP4);
  not not_106 (not_106_out, OP3);
  not not_107 (not_107_out, OP2);
  not not_108 (not_108_out, F14);
  not not_109 (not_109_out, F13);
  not not_110 (not_110_out, OP4);
  not not_111 (not_111_out, OP3);
  not not_112 (not_112_out, OP2);
  not not_113 (not_113_out, F14);
  not not_114 (not_114_out, F13);
  not not_115 (not_115_out, F12);
  not not_116 (not_116_out, OP4);
  not not_117 (not_117_out, OP3);
  not not_118 (not_118_out, F14);
  not not_119 (not_119_out, OP6);
  not not_120 (not_120_out, OP5);
  not not_121 (not_121_out, OP3);
  not not_122 (not_122_out, OP2);
  not not_123 (not_123_out, F14);
  not not_124 (not_124_out, F13);
  not not_125 (not_125_out, F12);
  not not_126 (not_126_out, OP6);
  not not_127 (not_127_out, OP4);
  not not_128 (not_128_out, OP3);
  not not_129 (not_129_out, OP2);
  not not_130 (not_130_out, F12);
  not not_131 (not_131_out, OP4);
  not not_132 (not_132_out, OP3);
  not not_133 (not_133_out, OP2);
  not not_134 (not_134_out, F13);
  not not_135 (not_135_out, F12);
  not not_136 (not_136_out, OP4);
  not not_137 (not_137_out, OP3);
  not not_138 (not_138_out, OP2);
  not not_139 (not_139_out, F13);
  not not_140 (not_140_out, OP4);
  not not_141 (not_141_out, OP3);
  not not_142 (not_142_out, OP2);
  not not_143 (not_143_out, F30);
  not not_144 (not_144_out, F25);
  not not_145 (not_145_out, F14);
  not not_146 (not_146_out, F13);
  not not_147 (not_147_out, F12);
  not not_148 (not_148_out, OP6);
  not not_149 (not_149_out, OP3);
  not not_150 (not_150_out, OP2);
  not not_151 (not_151_out, F25);
  not not_152 (not_152_out, F14);
  not not_153 (not_153_out, F13);
  not not_154 (not_154_out, F12);
  not not_155 (not_155_out, OP6);
  not not_156 (not_156_out, OP3);
  not not_157 (not_157_out, OP2);
  not not_158 (not_158_out, F30);
  not not_159 (not_159_out, F25);
  not not_160 (not_160_out, OP6);
  not not_161 (not_161_out, OP3);
  not not_162 (not_162_out, OP2);
  not not_163 (not_163_out, F30);
  not not_164 (not_164_out, F25);
  not not_165 (not_165_out, F12);
  not not_166 (not_166_out, OP6);
  not not_167 (not_167_out, OP3);
  not not_168 (not_168_out, OP2);
  not not_169 (not_169_out, F30);
  not not_170 (not_170_out, F25);
  not not_171 (not_171_out, F14);
  not not_172 (not_172_out, F12);
  not not_173 (not_173_out, OP6);
  not not_174 (not_174_out, OP3);
  not not_175 (not_175_out, OP2);
  not not_176 (not_176_out, F30);
  not not_177 (not_177_out, F25);
  not not_178 (not_178_out, F14);
  not not_179 (not_179_out, OP6);
  not not_180 (not_180_out, OP3);
  not not_181 (not_181_out, OP2);
  not not_182 (not_182_out, F14);
  not not_183 (not_183_out, F12);
  not not_184 (not_184_out, OP6);
  not not_185 (not_185_out, OP4);
  not not_186 (not_186_out, OP3);
  not not_187 (not_187_out, OP2);
  not not_188 (not_188_out, F14);
  not not_189 (not_189_out, F13);
  not not_190 (not_190_out, F12);
  not not_191 (not_191_out, OP4);
  not not_192 (not_192_out, OP3);
  not not_193 (not_193_out, OP2);
  not not_194 (not_194_out, F14);
  not not_195 (not_195_out, F13);
  not not_196 (not_196_out, OP4);
  not not_197 (not_197_out, OP3);
  not not_198 (not_198_out, OP2);
  not not_199 (not_199_out, F14);
  not not_200 (not_200_out, F13);
  not not_201 (not_201_out, F12);
  not not_202 (not_202_out, OP6);
  not not_203 (not_203_out, OP4);
  not not_204 (not_204_out, OP3);
  not not_205 (not_205_out, OP2);
  not not_206 (not_206_out, F12);
  not not_207 (not_207_out, OP4);
  not not_208 (not_208_out, OP3);
  not not_209 (not_209_out, OP2);
  not not_210 (not_210_out, F13);
  not not_211 (not_211_out, F12);
  not not_212 (not_212_out, OP4);
  not not_213 (not_213_out, OP3);
  not not_214 (not_214_out, OP2);
  not not_215 (not_215_out, F13);
  not not_216 (not_216_out, OP4);
  not not_217 (not_217_out, OP3);
  not not_218 (not_218_out, OP2);
  and and_1 (and_1_out, not_1_out, not_2_out, not_3_out, not_4_out, not_5_out, not_6_out, OP5, OP4, not_7_out, not_8_out);
  and and_2 (and_2_out, F30, not_9_out, not_10_out, not_11_out, not_12_out, not_13_out, OP5, OP4, not_14_out, not_15_out);
  and and_3 (and_3_out, not_16_out, not_17_out, F14, F13, F12, not_18_out, OP5, OP4, not_19_out, not_20_out);
  and and_4 (and_4_out, not_21_out, not_22_out, F14, F13, not_23_out, not_24_out, OP5, OP4, not_25_out, not_26_out);
  and and_5 (and_5_out, not_27_out, not_28_out, not_29_out, F13, not_30_out, not_31_out, OP5, OP4, not_32_out, not_33_out);
  and and_6 (and_6_out, not_34_out, not_35_out, not_36_out, F13, F12, not_37_out, OP5, OP4, not_38_out, not_39_out);
  and and_7 (and_7_out, not_40_out, not_41_out, not_42_out, not_43_out, not_44_out, OP4, not_45_out, not_46_out);
  and and_8 (and_8_out, F14, F13, F12, not_47_out, not_48_out, OP4, not_49_out, not_50_out);
  and and_9 (and_9_out, F14, F13, not_51_out, not_52_out, not_53_out, OP4, not_54_out, not_55_out);
  and and_10 (and_10_out, F14, not_56_out, not_57_out, not_58_out, not_59_out, OP4, not_60_out, not_61_out);
  and and_11 (and_11_out, not_62_out, F13, not_63_out, not_64_out, not_65_out, OP4, not_66_out, not_67_out);
  and and_12 (and_12_out, not_68_out, not_69_out, not_70_out, not_71_out, F12, not_72_out, not_73_out, OP4, not_74_out, not_75_out);
  and and_13 (and_13_out, not_76_out, not_77_out, F14, not_78_out, F12, not_79_out, not_80_out, OP4, not_81_out, not_82_out);
  and and_14 (and_14_out, F30, not_83_out, F14, not_84_out, F12, not_85_out, not_86_out, OP4, not_87_out, not_88_out);
  and and_15 (and_15_out, not_89_out, F13, not_90_out, not_91_out, not_92_out, not_93_out, not_94_out, not_95_out);
  and and_16 (and_16_out, not_96_out, F13, not_97_out, not_98_out, OP5, not_99_out, not_100_out, not_101_out);
  and and_17 (and_17_out, not_102_out, not_103_out, not_104_out, OP6, OP5, not_105_out, not_106_out, not_107_out);
  and and_18 (and_18_out, not_108_out, not_109_out, F12, OP6, OP5, not_110_out, not_111_out, not_112_out);
  and and_19 (and_19_out, not_113_out, not_114_out, not_115_out, OP6, OP5, not_116_out, not_117_out, OP2);
  and and_20 (and_20_out, not_118_out, F13, F12, not_119_out, not_120_out, OP4, not_121_out, not_122_out);
  and and_21 (and_21_out, not_123_out, not_124_out, not_125_out, not_126_out, OP5, not_127_out, not_128_out, not_129_out);
  and and_22 (and_22_out, F14, F13, not_130_out, OP6, OP5, not_131_out, not_132_out, not_133_out);
  and and_23 (and_23_out, F14, not_134_out, not_135_out, OP6, OP5, not_136_out, not_137_out, not_138_out);
  and and_24 (and_24_out, F14, not_139_out, F12, OP6, OP5, not_140_out, not_141_out, not_142_out);
  and and_25 (and_25_out, not_143_out, not_144_out, not_145_out, not_146_out, not_147_out, not_148_out, OP5, OP4, not_149_out, not_150_out);
  and and_26 (and_26_out, F30, not_151_out, not_152_out, not_153_out, not_154_out, not_155_out, OP5, OP4, not_156_out, not_157_out);
  and and_27 (and_27_out, not_158_out, not_159_out, F14, F13, F12, not_160_out, OP5, OP4, not_161_out, not_162_out);
  and and_28 (and_28_out, not_163_out, not_164_out, F14, F13, not_165_out, not_166_out, OP5, OP4, not_167_out, not_168_out);
  and and_29 (and_29_out, not_169_out, not_170_out, not_171_out, F13, not_172_out, not_173_out, OP5, OP4, not_174_out, not_175_out);
  and and_30 (and_30_out, not_176_out, not_177_out, not_178_out, F13, F12, not_179_out, OP5, OP4, not_180_out, not_181_out);
  and and_31 (and_31_out, not_182_out, F13, not_183_out, not_184_out, OP5, not_185_out, not_186_out, not_187_out);
  and and_32 (and_32_out, not_188_out, not_189_out, not_190_out, OP6, OP5, not_191_out, not_192_out, not_193_out);
  and and_33 (and_33_out, not_194_out, not_195_out, F12, OP6, OP5, not_196_out, not_197_out, not_198_out);
  and and_34 (and_34_out, not_199_out, not_200_out, not_201_out, not_202_out, OP5, not_203_out, not_204_out, not_205_out);
  and and_35 (and_35_out, F14, F13, not_206_out, OP6, OP5, not_207_out, not_208_out, not_209_out);
  and and_36 (and_36_out, F14, not_210_out, not_211_out, OP6, OP5, not_212_out, not_213_out, not_214_out);
  and and_37 (and_37_out, F14, not_215_out, F12, OP6, OP5, not_216_out, not_217_out, not_218_out);
  or or_1 (R2, and_25_out, and_26_out, and_27_out, and_28_out, and_29_out, and_30_out, and_31_out, and_32_out, and_33_out, and_34_out, and_35_out, and_36_out, and_37_out);
  or or_2 (R1, and_1_out, and_2_out, and_3_out, and_4_out, and_5_out, and_6_out, and_7_out, and_8_out, and_9_out, and_10_out, and_11_out, and_12_out, and_13_out, and_14_out, and_15_out, and_16_out, and_17_out, and_18_out, and_19_out, and_20_out, and_21_out, and_22_out, and_23_out, and_24_out);
endmodule

module \数据相关检测  (
  input  [4:0] ID_R1_num,
  input  [4:0] EX_W_num,
  input  EX_RegWrite,
  input  EX_MemToReg,
  input  [4:0] ID_R2_num,
  input  [4:0] MEM_W_num,
  input  MEM_RegWrite,
  input  [4:0] OP,
  input  ecall,
  input  [4:0] Func,
  output [1:0] R1Forward,
  output DataHazzard,
  output [1:0] R2Forward,
  output Load_Used
);

  wire and_1_out, and_2_out, and_3_out, and_4_out, and_6_out, and_7_out, and_8_out, and_9_out, and_10_out,
       and_11_out, and_12_out, and_13_out, comparator_1_eq, comparator_2_eq, comparator_3_eq,
       comparator_4_eq, comparator_5_eq, comparator_6_eq, comparator_7_eq, comparator_8_eq, comparator_9_eq,
       comparator_10_eq, comparator_11_eq, comparator_12_eq, or_3_out, or_4_out, or_5_out, R1Used, R2Used,
       \辅助判断数据冲突_1_r1 , \辅助判断数据冲突_1_r2 ;

  \辅助判断数据冲突  \u_辅助判断数据冲突_1  (
    .OP2(OP[0]), .OP3(OP[1]), .OP4(OP[2]), .OP5(OP[3]), .OP6(OP[4]), .F12(Func[0]), .F13(Func[1]),
    .F14(Func[2]), .F25(Func[3]), .F30(Func[4]), .R1(\辅助判断数据冲突_1_r1 ), .R2(\辅助判断数据冲突_1_r2 ));
  Comparator #(.width(5), .mode("twosComplement")) comparator_1 (
    .a(ID_R1_num), .b(EX_W_num), .eq(comparator_1_eq));  // open: gt, lt
  Comparator #(.width(5), .mode("twosComplement")) comparator_2 (
    .a(ID_R1_num), .b({5{1'b0}}), .eq(comparator_2_eq));  // open: gt, lt
  or or_1 (R1Used, ecall, \辅助判断数据冲突_1_r1 );
  or or_2 (R2Used, \辅助判断数据冲突_1_r2 , ecall);
  Comparator #(.width(5), .mode("twosComplement")) comparator_3 (
    .a(ID_R2_num), .b(EX_W_num), .eq(comparator_3_eq));  // open: gt, lt
  Comparator #(.width(5), .mode("twosComplement")) comparator_4 (
    .a(ID_R2_num), .b({5{1'b0}}), .eq(comparator_4_eq));  // open: gt, lt
  Comparator #(.width(5), .mode("twosComplement")) comparator_5 (
    .a(ID_R2_num), .b(EX_W_num), .eq(comparator_5_eq));  // open: gt, lt
  Comparator #(.width(5), .mode("twosComplement")) comparator_6 (
    .a(ID_R2_num), .b({5{1'b0}}), .eq(comparator_6_eq));  // open: gt, lt
  Comparator #(.width(5), .mode("twosComplement")) comparator_7 (
    .a(ID_R2_num), .b(EX_W_num), .eq(comparator_7_eq));  // open: gt, lt
  Comparator #(.width(5), .mode("twosComplement")) comparator_8 (
    .a(ID_R2_num), .b({5{1'b0}}), .eq(comparator_8_eq));  // open: gt, lt
  and and_1 (and_1_out, comparator_1_eq, EX_RegWrite, ~comparator_2_eq);  // AND_Gate
  and and_2 (and_2_out, comparator_3_eq, EX_RegWrite, ~comparator_4_eq);  // AND_Gate
  and and_3 (and_3_out, comparator_5_eq, R2Used, ~comparator_6_eq);  // AND_Gate
  and and_4 (and_4_out, comparator_7_eq, R1Used, ~comparator_8_eq);  // AND_Gate
  or or_3 (or_3_out, and_3_out, and_4_out);
  Comparator #(.width(5), .mode("twosComplement")) comparator_9 (
    .a(ID_R1_num), .b(MEM_W_num), .eq(comparator_9_eq));  // open: gt, lt
  Comparator #(.width(5), .mode("twosComplement")) comparator_10 (
    .a(ID_R1_num), .b({5{1'b0}}), .eq(comparator_10_eq));  // open: gt, lt
  Comparator #(.width(5), .mode("twosComplement")) comparator_11 (
    .a(ID_R2_num), .b(MEM_W_num), .eq(comparator_11_eq));  // open: gt, lt
  Comparator #(.width(5), .mode("twosComplement")) comparator_12 (
    .a(ID_R2_num), .b({5{1'b0}}), .eq(comparator_12_eq));  // open: gt, lt
  and and_5 (Load_Used, or_3_out, EX_MemToReg);
  and and_6 (and_6_out, comparator_9_eq, MEM_RegWrite, ~comparator_10_eq);  // AND_Gate
  and and_7 (and_7_out, comparator_11_eq, MEM_RegWrite, ~comparator_12_eq);  // AND_Gate
  and and_8 (and_8_out, R1Used, and_6_out);
  and and_9 (and_9_out, R1Used, and_1_out);
  or or_4 (or_4_out, and_6_out, and_1_out);
  and and_10 (and_10_out, or_4_out, R1Used);
  and and_11 (and_11_out, R2Used, or_5_out);
  or or_5 (or_5_out, and_2_out, and_7_out);
  and and_12 (and_12_out, and_7_out, R2Used);
  and and_13 (and_13_out, R2Used, and_2_out);
  Priority_Encoder #(.select(2), .disabled("Z")) priority_encoder_1 (
    .in0(1'b1), .in1(and_8_out), .in2(and_9_out), .out(R1Forward));  // open: in3, gs, en_out, en_in
  or or_6 (DataHazzard, and_10_out, and_11_out);
  Priority_Encoder #(.select(2), .disabled("Z")) priority_encoder_2 (
    .in0(1'b1), .in1(and_12_out), .in2(and_13_out), .out(R2Forward));  // open: in3, gs, en_out, en_in
endmodule

module sokuban (
);

  wire CLK, clock_1_out, comparator_1_eq, comparator_1_lt, d_ff_1_q, DOWN_out, Go_out, keyboard_1_avail,
       LEFT_out, nand_1_out, RIGHT_out, RST_out, UP_out, \单周期_单级中断_1_ecall ;
  wire [6:0] keyboard_1_data, \单周期_单级中断_1_x , \单周期_单级中断_1_y ;
  wire [12:0] CNT_num;
  wire [15:0] \单周期_单级中断_1_load_line , \单周期_单级中断_1_rgb ;

  D_Flip_Flop #(.trigger("high"), .Pre_Clr_Positions("LEGACY"), .NegatePresetClear("false"), .enable("true"), .NewFFLayout("false")) d_ff_1 (.Q(d_ff_1_q));  // open: clk, D, Qn, preset, en, reset
  Button LEFT (.out(LEFT_out));
  // Probe on 13'hc
  Button UP (.out(UP_out));
  Button DOWN (.out(DOWN_out));
  Button Go (.out(Go_out));
  Button RST (.out(RST_out));
  Comparator #(.width(13), .mode("twosComplement")) comparator_1 (
    .a(CNT_num), .b(13'hc), .eq(comparator_1_eq), .lt(comparator_1_lt));  // open: gt
  Clock #(.highDuration(1), .lowDuration(1)) clock_1 (.out(clock_1_out));
  Keyboard #(.Char_bit_width(7), .buflen(32), .trigger("rising")) keyboard_1 (
    .clk(CLK), .clr(RST_out), .avail(keyboard_1_avail), .data(keyboard_1_data));  // open: re
  Button RIGHT (.out(RIGHT_out));
  nand nand_1 (nand_1_out, d_ff_1_q, comparator_1_eq);
  Counter #(.width(13), .max('h1fff), .ongoal("stay"), .trigger("rising"), .behavior("old")) counter_1 (
    .count(comparator_1_lt), .Q(CNT_num), .clk(clock_1_out));  // open: load, D, carry, clr, preset
  assign CLK = nand_1_out ? clock_1_out : 1'bz;  // Controlled_Buffer controlled_buffer_1
  Pull_Resistor #(.pull(1)) pull_resistor_1 (.node(CLK));
  \单周期_单级中断  \u_单周期_单级中断_1  (
    .IR1(UP_out), .IR2(DOWN_out), .IR3(LEFT_out), .IR4(RIGHT_out), .RST(RST_out), .Go(Go_out),
    .x(\单周期_单级中断_1_x ), .y(\单周期_单级中断_1_y ), .rgb(\单周期_单级中断_1_rgb ), .ecall(\单周期_单级中断_1_ecall ),
    .FIFO(keyboard_1_avail), .Stage(keyboard_1_data), .MAP_LENGTH(16'h200),
    .LOAD_LINE(\单周期_单级中断_1_load_line ), .CLK(CLK));
  // Probe on \单周期_单级中断_1_load_line 
  // LCD_Video lcd_video_1: pin names not known; wires that end beside it: RST_out, CLK, \单周期_单级中断_1_ecall , \单周期_单级中断_1_x , \单周期_单级中断_1_y , \单周期_单级中断_1_rgb 
endmodule
