// Logisim project cpu21-riscv.circ as structural Verilog: 22 circuits, main circuit ◇单周期RISC-V
module \单周期RISC_V  (
  input  IR1,
  input  IR2,
  input  IR3,
  output RegWrite,
  output MemWrite,
  output [31:0] PC,
  output [31:0] IR,
  output [31:0] RDin,
  output [31:0] MDin,
  output [31:0] LedData
);

  wire AluSrcB, and_1_out, and_2_out, and_3_out, and_4_out, and_5_out, be, Beq, Bge, Bne, CLK, clock_1_out,
       comparator_1_eq, comparator_2_eq, comparator_2_lt, d_ff_1_q, Ecall, Equal, Go, halt, IR1_t, IR2_t,
       IR3_t, IRA, IRB, IRC, JAL, JALR, Less, MemToReg, nand_1_out, not_1_out, not_2_out, not_3_out,
       not_4_out, or_1_out, or_2_out, RS_1, RS_2, RST, S_TPYE, URET, W1, W2, W3, \单周期硬布线控制器_1_remu ;
  wire [1:0] priority_encoder_1_out;
  wire [1:1] or_6_out;
  wire [3:0] \单周期硬布线控制器_1_alu_op ;
  wire [4:0] multiplexer_2_out, multiplexer_3_out;
  wire [12:0] CNT_num;
  wire [15:0] \总周期数 ;
  wire [31:0] adder_2_out, adder_3_out, alu_1_result, alu_1_result_2, ALUResult, bit_extender_1_out,
       bit_extender_2_out, bit_extender_3_out, bit_extender_4_out, Memdata, multiplexer_1_out,
       multiplexer_4_out, multiplexer_5_out, PC_4, regifile_1_r1, shifter_1_out, shifter_2_out;

  Button \u_继续运行  (.out(Go));
  Button _1 (.out(IRA));
  Button _2 (.out(IRB));
  Button _3 (.out(IRC));
  LED #(.active("true")) led_1 (.in(W1));
  LED #(.active("true")) led_2 (.in(W2));
  LED #(.active("true")) led_3 (.in(W3));
  not not_1 (not_1_out, halt);
  Hex_Digit_Display hex_digit_display_1 (.value(LedData[31:28]));  // open: dp
  Counter #(.width(16), .max('hffff), .ongoal("wrap"), .trigger("rising"), .behavior("new")) counter_1 (
    .count(not_1_out), .Q(\总周期数 ), .clk(CLK));  // open: load, D, carry, clr, preset, down
  Hex_Digit_Display hex_digit_display_2 (.value(LedData[23:20]));  // open: dp
  Hex_Digit_Display hex_digit_display_3 (.value(LedData[27:24]));  // open: dp
  Hex_Digit_Display hex_digit_display_4 (.value(LedData[19:16]));  // open: dp
  Hex_Digit_Display hex_digit_display_5 (.value(LedData[15:12]));  // open: dp
  Hex_Digit_Display hex_digit_display_6 (.value(LedData[7:4]));  // open: dp
  Hex_Digit_Display hex_digit_display_7 (.value(LedData[11:8]));  // open: dp
  // Probe on \总周期数 
  Priority_Encoder #(.select(2), .disabled("Z")) priority_encoder_1 (
    .in0(1'b1), .in1(JALR), .in2(JAL), .in3(or_1_out), .out(priority_encoder_1_out));  // open: gs, en_out, en_in
  or or_1 (or_1_out, and_1_out, and_2_out, and_3_out);
  Multiplexer #(.select(2), .width(32), .disabled("Z"), .enable("false")) multiplexer_1 (
    .in0(PC_4), .in1(ALUResult), .in2(adder_3_out), .in3(adder_2_out), .out(multiplexer_1_out),
    .sel(priority_encoder_1_out));
  not not_2 (not_2_out, or_2_out);
  or or_2 (or_2_out, Go, halt);
  Hex_Digit_Display hex_digit_display_8 (.value(LedData[3:0]));  // open: dp
  and and_1 (and_1_out, Bne, ~Equal);  // AND_Gate
  and and_2 (and_2_out, Equal, Beq);
  and and_3 (and_3_out, Bge, be);
  Register #(.width(32), .trigger("rising"), .Select("low")) u_PC (
    .D(multiplexer_1_out), .en(not_2_out), .Q(PC), .clk(CLK), .clr(RST));
  or or_3 (IR1_t, IR1, IRA);
  // RiscV_Probe riscv_probe_1: pin names not known; wires that end beside it: IR
  Adder #(.width(32)) adder_1 (.a(PC), .b(32'h4), .out(PC_4));  // open: cin, cout
  or or_4 (IR2_t, IR2, IRB);
  ROM #(.addrWidth(10), .dataWidth(32), .Select("high")) rom_1 (.addr(PC[11:2]), .data(IR));
  Multiplexer #(.select(1), .width(5), .disabled("Z"), .enable("false")) multiplexer_2 (
    .in0(IR[19:15]), .in1(5'b10001), .out(multiplexer_2_out), .sel(Ecall));
  Multiplexer #(.select(1), .width(5), .disabled("Z"), .enable("false")) multiplexer_3 (
    .in0(IR[24:20]), .in1(5'b01010), .out(multiplexer_3_out), .sel(Ecall));
  or or_5 (IR3_t, IR3, IRC);
  \单周期硬布线控制器  \u_单周期硬布线控制器_1  (
    .Funct({IR[30], IR[25], IR[14:12]}), .OP(IR[6:2]), .ALU_OP(\单周期硬布线控制器_1_alu_op ), .MemToReg(MemToReg),
    .MemWrite(MemWrite), .ALU_SRC(AluSrcB), .RegWrite(RegWrite), .ecall(Ecall), .S_type(S_TPYE), .Jalr(JALR),
    .Beq(Beq), .JAL(JAL), .Bne(Bne), .in_3(IR[21]), .uret(URET), .RS_1(RS_1), .RS_2(RS_2),
    .REMU(\单周期硬布线控制器_1_remu ), .BLTU(Bge));  // open: LBU
  assign bit_extender_1_out = {{20{IR[31]}}, IR[31:20]};  // Bit_Extender bit_extender_1
  assign bit_extender_2_out = {{20{IR[31]}}, {IR[31:25], IR[11:7]}};  // Bit_Extender bit_extender_2
  assign bit_extender_3_out = {{20{IR[31]}}, {IR[31], IR[7], IR[30:25], IR[11:8]}};  // Bit_Extender bit_extender_3
  assign bit_extender_4_out = {{12{IR[31]}}, {IR[31], IR[19:12], IR[20], IR[30:21]}};  // Bit_Extender bit_extender_4
  Multiplexer #(.select(1), .width(32), .disabled("Z"), .enable("false")) multiplexer_4 (
    .in0(bit_extender_1_out), .in1(bit_extender_2_out), .out(multiplexer_4_out), .sel(S_TPYE));
  Shifter #(.width(32), .shift("ll")) shifter_1 (.in(bit_extender_3_out), .\dist (5'b00001), .out(shifter_1_out));
  Shifter #(.width(32), .shift("ll")) shifter_2 (.in(bit_extender_4_out), .\dist (5'b00001), .out(shifter_2_out));
  Regifile regifile_1 (
    .Din(RDin), .Clk(CLK), .R1(regifile_1_r1), .R2(MDin), .WE(RegWrite), .W_num(IR[11:7]),
    .R1_num(multiplexer_2_out), .R2_num(multiplexer_3_out));
  Adder #(.width(32)) adder_2 (.a(shifter_1_out), .b(PC), .out(adder_2_out));  // open: cin, cout
  Adder #(.width(32)) adder_3 (.a(PC), .b(shifter_2_out), .out(adder_3_out));  // open: cin, cout
  // Probe on multiplexer_5_out
  // Probe on regifile_1_r1
  Multiplexer #(.select(1), .width(32), .disabled("Z"), .enable("false")) multiplexer_5 (
    .in0(MDin), .in1(multiplexer_4_out), .out(multiplexer_5_out), .sel(AluSrcB));
  D_Flip_Flop #(.trigger("high"), .Pre_Clr_Positions("LEGACY"), .NegatePresetClear("false"), .enable("true"), .NewFFLayout("false")) d_ff_1 (.Q(d_ff_1_q));  // open: clk, D, Qn, preset, en, reset
  // Probe on 13'hc
  ALU alu_1 (
    .X(regifile_1_r1), .Y(multiplexer_5_out), .AluOP(\单周期硬布线控制器_1_alu_op ), .Equal(Equal),
    .Result(alu_1_result), .Result_2(alu_1_result_2), .out_4(be), .out_6(Less));
  not not_3 (not_3_out, comparator_1_eq);
  Comparator #(.width(32), .mode("twosComplement")) comparator_1 (
    .a(regifile_1_r1), .b(32'h22), .eq(comparator_1_eq));  // open: gt, lt
  Comparator #(.width(13), .mode("twosComplement")) comparator_2 (
    .a(CNT_num), .b(13'hc), .eq(comparator_2_eq), .lt(comparator_2_lt));  // open: gt
  Clock #(.highDuration(1), .lowDuration(1)) clock_1 (.out(clock_1_out));
  Multiplexer #(.select(1), .width(32), .disabled("Z"), .enable("false")) multiplexer_6 (
    .in0(alu_1_result), .in1(alu_1_result_2), .out(ALUResult), .sel(\单周期硬布线控制器_1_remu ));
  and and_4 (and_4_out, comparator_1_eq, Ecall);
  Counter #(.width(13), .max('h1fff), .ongoal("stay"), .trigger("rising"), .behavior("old")) counter_2 (
    .count(comparator_2_lt), .Q(CNT_num), .clk(clock_1_out));  // open: load, D, carry, clr, preset
  and and_5 (and_5_out, Ecall, not_3_out);
  nand nand_1 (nand_1_out, d_ff_1_q, comparator_2_eq);
  Register #(.width(1), .trigger("rising"), .Select("low")) register_1 (
    .D(and_5_out), .Q(halt), .clk(not_4_out), .clr(Go));  // open: en
  not not_4 (not_4_out, CLK);
  Register #(.width(32), .trigger("rising"), .Select("low")) register_2 (
    .D(MDin), .en(and_4_out), .Q(LedData), .clk(CLK));  // open: clr
  assign CLK = nand_1_out ? clock_1_out : 1'bz;  // Controlled_Buffer controlled_buffer_1
  Pull_Resistor #(.pull(1)) pull_resistor_1 (.node(CLK));
  RAM #(.addrWidth(10), .dataWidth(32), .bus("separate"), .Select("high")) ram_1 (
    .addr(ALUResult[11:2]), .din(MDin), .data(Memdata), .str(MemWrite), .sel(1'b1), .clk(CLK), .ld(1'b1));  // open: clr
  Multiplexer #(.select(2), .width(32), .disabled("Z"), .enable("false")) multiplexer_7 (
    .in0(ALUResult), .in1(Memdata), .in2(PC_4), .out(RDin), .sel({or_6_out[1], MemToReg}));  // open: in3
  or or_6 (or_6_out[1], JAL, JALR);

  // Notes on the sheet:
  //   中断源
  //   中断等待指示
  //   数码管输出应该用寄存器锁存，否则显示数据只能一闪而过
  //   数码管输出
  //   指令探针
  //   指令存储器
  //   指令字
  //   contents of rom_1 (hex, n*v repeats v):
  //   100493 100006f 100493 200913 300993 100006f 100493 200913 300993 100006f 100493 200913 300993
  //   100006f 100493 200913 300993 29c000ef 100413 100493 1f49493 900533 2200893 73 24d493 48463 fedff06f
  //   900533 2200893 73 100493 249493 900533 2200893 73 48463 fedff06f 100493 1f49493 900533 2200893 73
  //   4034d493 900533 2200893 73 4044d493 900533 2200893 73 4044d493 900533 2200893 73 4044d493 900533
  //   2200893 73 4044d493 900533 2200893 73 4044d493 900533 2200893 73 4044d493 900533 2200893 73 4044d493
  //   900533 2200893 73 100413 1f41993 41f9d993 433 c00913 300b13 140413 f47413 800293 100313 499993
  //   89e9b3 1300533 2200893 73 406282b3 fe0294e3 140413 f00f93 1f47433 1c41413 800293 100313 49d993
  //   89e9b3 1300533 2200893 73 406282b3 fe0294e3 1c45413 406b0b33 b0463 f95ff06f 2b3 fff2c293 829293
  //   ff2e293 500533 2200893 73 fff00413 493 84a023 140413 448493 84a023 140413 448493 84a023 140413
  //   448493 84a023 140413 448493 84a023 140413 448493 84a023 140413 448493 84a023 140413 448493 84a023
  //   140413 448493 84a023 140413 448493 84a023 140413 448493 84a023 140413 448493 84a023 140413 448493
  //   84a023 140413 448493 84a023 140413 448493 84a023 140413 448493 84a023 140413 448493 140413 433
  //   3c00493 42983 4aa03 149a2b3 28663 134a023 1442023 ffc48493 fe9412e3 800533 2200893 73 440413 3c00493
  //   fc9416e3 a00893 73 413 140413 800533 2200893 73 240413 800533 2200893 73 340413 800533 2200893 73
  //   440413 800533 2200893 73 540413 800533 2200893 73 640413 800533 2200893 73 740413 800533 2200893 73
  //   840413 800533 2200893 2200893 73 8067
  //   JAL
  //   JALR
  //   URET
  //   Beq
  //   Bne
  //   MemWrite
  //   AluOP
  //   AluSrcB
  //   RegWrite
  //   为方便自动评测，需要输出PC，IR，寄存器堆写如数据RDin
  //   RAM写使能MemWrite、RAM写入数据MDin等信号
  //   控制位
  //   暂停节拍，不能为0
  //   戳工具置1进入计数暂停模式，ctrl+k时钟自动运行到对应节拍暂停
  //   ctrl+k关闭时钟连续运行，将控制位置零，进入单步调试模式调试
  //   用这个时钟源需要去掉电路中的其他时钟源
  //   可计数暂停的时钟源
  //   数据存储器
endmodule

// 单周期硬布线控制器
module \单周期硬布线控制器  (
  input  [4:0] OP,
  input  [4:0] Funct,
  input  in_3,
  output [3:0] ALU_OP,
  output uret,
  output MemToReg,
  output ecall,
  output MemWrite,
  output RS_1,
  output RS_2,
  output REMU,
  output BLTU,
  output ALU_SRC,
  output RegWrite,
  output S_type,
  output Beq,
  output LBU,
  output Bne,
  output Jalr,
  output JAL
);

  wire \控制信号自动生成_1_ecall ;

  \运算控制器自动生成  \u_运算控制器自动生成_1  (
    .OP2(OP[0]), .OP3(OP[1]), .OP4(OP[2]), .OP5(OP[3]), .OP6(OP[4]), .F12(Funct[0]), .F13(Funct[1]),
    .F14(Funct[2]), .F25(Funct[3]), .F30(Funct[4]), .S0(ALU_OP[0]), .S1(ALU_OP[1]), .S2(ALU_OP[2]),
    .S3(ALU_OP[3]));
  \控制信号自动生成  \u_控制信号自动生成_1  (
    .OP2(OP[0]), .OP3(OP[1]), .OP4(OP[2]), .OP5(OP[3]), .MemToReg(MemToReg), .OP6(OP[4]), .F12(Funct[0]),
    .F13(Funct[1]), .F14(Funct[2]), .F25(Funct[3]), .F30(Funct[4]), .MemWrite(MemWrite), .RS_1(RS_1),
    .RS_2(RS_2), .REMU(REMU), .BLTU(BLTU), .ALU_SRC(ALU_SRC), .RegWrite(RegWrite),
    .ecall(\控制信号自动生成_1_ecall ), .S_Type(S_type), .BEQ(Beq), .LBU(LBU), .BNE(Bne), .JALR(Jalr), .JAL(JAL));
  and and_1 (uret, in_3, \控制信号自动生成_1_ecall );
  and and_2 (ecall, ~in_3, \控制信号自动生成_1_ecall );  // AND_Gate

  // Other names for the same wires on the sheet: IR21 = in_3; OP_CODE[4:0] = OP

  // Notes on the sheet:
  //   运算器控制器，根据指令生成运算器功能选择信号
  //   控制信号生成，产生数据通路需要的其他控制信号
endmodule

// 运算器控制器
module \运算控制器自动生成  (
  input  OP2,
  input  OP3,
  input  OP4,
  input  OP5,
  input  OP6,
  input  F12,
  input  F13,
  input  F14,
  input  F25,
  input  F30,
  output S0,
  output S1,
  output S2,
  output S3
);

  wire and_1_out, and_2_out, and_3_out, and_4_out, and_5_out, and_6_out, and_7_out, and_8_out, and_9_out,
       and_10_out, and_11_out, and_12_out, and_13_out, and_14_out, and_15_out, and_16_out, and_17_out,
       and_18_out, and_19_out, and_20_out, and_21_out, and_22_out, and_23_out, and_24_out, and_25_out,
       and_26_out, and_27_out, and_28_out, and_29_out, and_30_out, and_31_out, and_32_out, and_33_out,
       and_34_out, and_35_out, and_36_out, and_37_out, and_38_out, and_39_out, not_1_out, not_2_out,
       not_3_out, not_4_out, not_5_out, not_6_out, not_7_out, not_8_out, not_9_out, not_10_out, not_11_out,
       not_12_out, not_13_out, not_14_out, not_15_out, not_16_out, not_17_out, not_18_out, not_19_out,
       not_20_out, not_21_out, not_22_out, not_23_out, not_24_out, not_25_out, not_26_out, not_27_out,
       not_28_out, not_29_out, not_30_out, not_31_out, not_32_out, not_33_out, not_34_out, not_35_out,
       not_36_out, not_37_out, not_38_out, not_39_out, not_40_out, not_41_out, not_42_out, not_43_out,
       not_44_out, not_45_out, not_46_out, not_47_out, not_48_out, not_49_out, not_50_out, not_51_out,
       not_52_out, not_53_out, not_54_out, not_55_out, not_56_out, not_57_out, not_58_out, not_59_out,
       not_60_out, not_61_out, not_62_out, not_63_out, not_64_out, not_65_out, not_66_out, not_67_out,
       not_68_out, not_69_out, not_70_out, not_71_out, not_72_out, not_73_out, not_74_out, not_75_out,
       not_76_out, not_77_out, not_78_out, not_79_out, not_80_out, not_81_out, not_82_out, not_83_out,
       not_84_out, not_85_out, not_86_out, not_87_out, not_88_out, not_89_out, not_90_out, not_91_out,
       not_92_out, not_93_out, not_94_out, not_95_out, not_96_out, not_97_out, not_98_out, not_99_out,
       not_100_out, not_101_out, not_102_out, not_103_out, not_104_out, not_105_out, not_106_out,
       not_107_out, not_108_out, not_109_out, not_110_out, not_111_out, not_112_out, not_113_out,
       not_114_out, not_115_out, not_116_out, not_117_out, not_118_out, not_119_out, not_120_out,
       not_121_out, not_122_out, not_123_out, not_124_out, not_125_out, not_126_out, not_127_out,
       not_128_out, not_129_out, not_130_out, not_131_out, not_132_out, not_133_out, not_134_out,
       not_135_out, not_136_out, not_137_out, not_138_out, not_139_out, not_140_out, not_141_out,
       not_142_out, not_143_out, not_144_out, not_145_out, not_146_out, not_147_out, not_148_out,
       not_149_out, not_150_out, not_151_out, not_152_out, not_153_out, not_154_out, not_155_out,
       not_156_out, not_157_out, not_158_out, not_159_out, not_160_out, not_161_out, not_162_out,
       not_163_out, not_164_out, not_165_out, not_166_out, not_167_out, not_168_out, not_169_out,
       not_170_out, not_171_out, not_172_out, not_173_out, not_174_out, not_175_out, not_176_out,
       not_177_out, not_178_out, not_179_out, not_180_out, not_181_out, not_182_out, not_183_out,
       not_184_out, not_185_out, not_186_out, not_187_out, not_188_out, not_189_out, not_190_out,
       not_191_out, not_192_out, not_193_out, not_194_out, not_195_out, not_196_out, not_197_out,
       not_198_out, not_199_out, not_200_out, not_201_out, not_202_out, not_203_out, not_204_out,
       not_205_out, not_206_out, not_207_out, not_208_out, not_209_out, not_210_out, not_211_out,
       not_212_out, not_213_out, not_214_out, not_215_out, not_216_out, not_217_out, not_218_out,
       not_219_out, not_220_out, not_221_out, not_222_out, not_223_out, not_224_out, not_225_out,
       not_226_out, not_227_out, not_228_out, not_229_out, not_230_out;

  not not_1 (not_1_out, F30);
  not not_2 (not_2_out, F25);
  not not_3 (not_3_out, F14);
  not not_4 (not_4_out, F13);
  not not_5 (not_5_out, F12);
  not not_6 (not_6_out, OP6);
  not not_7 (not_7_out, OP3);
  not not_8 (not_8_out, OP2);
  not not_9 (not_9_out, F30);
  not not_10 (not_10_out, F25);
  not not_11 (not_11_out, OP6);
  not not_12 (not_12_out, OP3);
  not not_13 (not_13_out, OP2);
  not not_14 (not_14_out, F30);
  not not_15 (not_15_out, F25);
  not not_16 (not_16_out, F14);
  not not_17 (not_17_out, F12);
  not not_18 (not_18_out, OP6);
  not not_19 (not_19_out, OP3);
  not not_20 (not_20_out, OP2);
  not not_21 (not_21_out, F14);
  not not_22 (not_22_out, F13);
  not not_23 (not_23_out, F12);
  not not_24 (not_24_out, OP6);
  not not_25 (not_25_out, OP5);
  not not_26 (not_26_out, OP3);
  not not_27 (not_27_out, OP2);
  not not_28 (not_28_out, OP6);
  not not_29 (not_29_out, OP5);
  not not_30 (not_30_out, OP3);
  not not_31 (not_31_out, OP2);
  not not_32 (not_32_out, F13);
  not not_33 (not_33_out, F12);
  not not_34 (not_34_out, OP6);
  not not_35 (not_35_out, OP5);
  not not_36 (not_36_out, OP3);
  not not_37 (not_37_out, OP2);
  not not_38 (not_38_out, F14);
  not not_39 (not_39_out, F12);
  not not_40 (not_40_out, OP6);
  not not_41 (not_41_out, OP5);
  not not_42 (not_42_out, OP3);
  not not_43 (not_43_out, OP2);
  not not_44 (not_44_out, F25);
  not not_45 (not_45_out, F13);
  not not_46 (not_46_out, OP6);
  not not_47 (not_47_out, OP5);
  not not_48 (not_48_out, OP3);
  not not_49 (not_49_out, OP2);
  not not_50 (not_50_out, F30);
  not not_51 (not_51_out, F14);
  not not_52 (not_52_out, F13);
  not not_53 (not_53_out, F12);
  not not_54 (not_54_out, OP6);
  not not_55 (not_55_out, OP3);
  not not_56 (not_56_out, OP2);
  not not_57 (not_57_out, F13);
  not not_58 (not_58_out, F12);
  not not_59 (not_59_out, OP6);
  not not_60 (not_60_out, OP5);
  not not_61 (not_61_out, OP4);
  not not_62 (not_62_out, OP3);
  not not_63 (not_63_out, OP2);
  not not_64 (not_64_out, F25);
  not not_65 (not_65_out, F14);
  not not_66 (not_66_out, F13);
  not not_67 (not_67_out, F12);
  not not_68 (not_68_out, OP6);
  not not_69 (not_69_out, OP3);
  not not_70 (not_70_out, OP2);
  not not_71 (not_71_out, F30);
  not not_72 (not_72_out, F25);
  not not_73 (not_73_out, OP6);
  not not_74 (not_74_out, OP3);
  not not_75 (not_75_out, OP2);
  not not_76 (not_76_out, F30);
  not not_77 (not_77_out, F25);
  not not_78 (not_78_out, F14);
  not not_79 (not_79_out, F12);
  not not_80 (not_80_out, OP6);
  not not_81 (not_81_out, OP3);
  not not_82 (not_82_out, OP2);
  not not_83 (not_83_out, OP6);
  not not_84 (not_84_out, OP5);
  not not_85 (not_85_out, OP3);
  not not_86 (not_86_out, OP2);
  not not_87 (not_87_out, F14);
  not not_88 (not_88_out, F12);
  not not_89 (not_89_out, OP6);
  not not_90 (not_90_out, OP5);
  not not_91 (not_91_out, OP3);
  not not_92 (not_92_out, OP2);
  not not_93 (not_93_out, F30);
  not not_94 (not_94_out, F25);
  not not_95 (not_95_out, F13);
  not not_96 (not_96_out, OP6);
  not not_97 (not_97_out, OP5);
  not not_98 (not_98_out, OP3);
  not not_99 (not_99_out, OP2);
  not not_100 (not_100_out, F14);
  not not_101 (not_101_out, F13);
  not not_102 (not_102_out, F12);
  not not_103 (not_103_out, OP4);
  not not_104 (not_104_out, OP3);
  not not_105 (not_105_out, OP2);
  not not_106 (not_106_out, F14);
  not not_107 (not_107_out, F13);
  not not_108 (not_108_out, OP4);
  not not_109 (not_109_out, OP3);
  not not_110 (not_110_out, OP2);
  not not_111 (not_111_out, F14);
  not not_112 (not_112_out, F13);
  not not_113 (not_113_out, F12);
  not not_114 (not_114_out, OP4);
  not not_115 (not_115_out, OP3);
  not not_116 (not_116_out, F30);
  not not_117 (not_117_out, F14);
  not not_118 (not_118_out, F13);
  not not_119 (not_119_out, F12);
  not not_120 (not_120_out, OP6);
  not not_121 (not_121_out, OP3);
  not not_122 (not_122_out, OP2);
  not not_123 (not_123_out, F30);
  not not_124 (not_124_out, F25);
  not not_125 (not_125_out, F14);
  not not_126 (not_126_out, F13);
  not not_127 (not_127_out, F12);
  not not_128 (not_128_out, OP6);
  not not_129 (not_129_out, OP3);
  not not_130 (not_130_out, OP2);
  not not_131 (not_131_out, F25);
  not not_132 (not_132_out, F14);
  not not_133 (not_133_out, F13);
  not not_134 (not_134_out, F12);
  not not_135 (not_135_out, OP6);
  not not_136 (not_136_out, OP3);
  not not_137 (not_137_out, OP2);
  not not_138 (not_138_out, F30);
  not not_139 (not_139_out, F25);
  not not_140 (not_140_out, OP6);
  not not_141 (not_141_out, OP3);
  not not_142 (not_142_out, OP2);
  not not_143 (not_143_out, F30);
  not not_144 (not_144_out, F25);
  not not_145 (not_145_out, F14);
  not not_146 (not_146_out, OP6);
  not not_147 (not_147_out, OP3);
  not not_148 (not_148_out, OP2);
  not not_149 (not_149_out, F14);
  not not_150 (not_150_out, F13);
  not not_151 (not_151_out, F12);
  not not_152 (not_152_out, OP6);
  not not_153 (not_153_out, OP5);
  not not_154 (not_154_out, OP3);
  not not_155 (not_155_out, OP2);
  not not_156 (not_156_out, OP6);
  not not_157 (not_157_out, OP5);
  not not_158 (not_158_out, OP3);
  not not_159 (not_159_out, OP2);
  not not_160 (not_160_out, F14);
  not not_161 (not_161_out, F13);
  not not_162 (not_162_out, F12);
  not not_163 (not_163_out, OP4);
  not not_164 (not_164_out, OP3);
  not not_165 (not_165_out, OP2);
  not not_166 (not_166_out, F14);
  not not_167 (not_167_out, F13);
  not not_168 (not_168_out, OP4);
  not not_169 (not_169_out, OP3);
  not not_170 (not_170_out, OP2);
  not not_171 (not_171_out, F14);
  not not_172 (not_172_out, F13);
  not not_173 (not_173_out, F12);
  not not_174 (not_174_out, OP4);
  not not_175 (not_175_out, OP3);
  not not_176 (not_176_out, F30);
  not not_177 (not_177_out, OP6);
  not not_178 (not_178_out, OP3);
  not not_179 (not_179_out, OP2);
  not not_180 (not_180_out, F13);
  not not_181 (not_181_out, F12);
  not not_182 (not_182_out, OP6);
  not not_183 (not_183_out, OP5);
  not not_184 (not_184_out, OP4);
  not not_185 (not_185_out, OP3);
  not not_186 (not_186_out, OP2);
  not not_187 (not_187_out, F12);
  not not_188 (not_188_out, OP4);
  not not_189 (not_189_out, OP3);
  not not_190 (not_190_out, OP2);
  not not_191 (not_191_out, F30);
  not not_192 (not_192_out, F25);
  not not_193 (not_193_out, F12);
  not not_194 (not_194_out, OP6);
  not not_195 (not_195_out, OP3);
  not not_196 (not_196_out, OP2);
  not not_197 (not_197_out, F30);
  not not_198 (not_198_out, F25);
  not not_199 (not_199_out, F14);
  not not_200 (not_200_out, F12);
  not not_201 (not_201_out, OP6);
  not not_202 (not_202_out, OP3);
  not not_203 (not_203_out, OP2);
  not not_204 (not_204_out, F30);
  not not_205 (not_205_out, F25);
  not not_206 (not_206_out, F14);
  not not_207 (not_207_out, OP6);
  not not_208 (not_208_out, OP3);
  not not_209 (not_209_out, OP2);
  not not_210 (not_210_out, F12);
  not not_211 (not_211_out, OP6);
  not not_212 (not_212_out, OP5);
  not not_213 (not_213_out, OP3);
  not not_214 (not_214_out, OP2);
  not not_215 (not_215_out, F13);
  not not_216 (not_216_out, F12);
  not not_217 (not_217_out, OP6);
  not not_218 (not_218_out, OP5);
  not not_219 (not_219_out, OP3);
  not not_220 (not_220_out, OP2);
  not not_221 (not_221_out, F14);
  not not_222 (not_222_out, F12);
  not not_223 (not_223_out, OP6);
  not not_224 (not_224_out, OP5);
  not not_225 (not_225_out, OP3);
  not not_226 (not_226_out, OP2);
  not not_227 (not_227_out, F12);
  not not_228 (not_228_out, OP4);
  not not_229 (not_229_out, OP3);
  not not_230 (not_230_out, OP2);
  and and_1 (and_1_out, not_1_out, not_2_out, not_3_out, not_4_out, not_5_out, not_6_out, OP5, OP4, not_7_out, not_8_out);
  and and_2 (and_2_out, not_9_out, not_10_out, F14, F13, F12, not_11_out, OP5, OP4, not_12_out, not_13_out);
  and and_3 (and_3_out, not_14_out, not_15_out, not_16_out, F13, not_17_out, not_18_out, OP5, OP4, not_19_out, not_20_out);
  and and_4 (and_4_out, not_21_out, not_22_out, not_23_out, not_24_out, not_25_out, OP4, not_26_out, not_27_out);
  and and_5 (and_5_out, F14, F13, F12, not_28_out, not_29_out, OP4, not_30_out, not_31_out);
  and and_6 (and_6_out, F14, not_32_out, not_33_out, not_34_out, not_35_out, OP4, not_36_out, not_37_out);
  and and_7 (and_7_out, not_38_out, F13, not_39_out, not_40_out, not_41_out, OP4, not_42_out, not_43_out);
  and and_8 (and_8_out, F30, not_44_out, F14, not_45_out, F12, not_46_out, not_47_out, OP4, not_48_out, not_49_out);
  and and_9 (and_9_out, not_50_out, F25, not_51_out, not_52_out, not_53_out, not_54_out, OP5, OP4, not_55_out, not_56_out);
  and and_10 (and_10_out, F14, not_57_out, not_58_out, not_59_out, not_60_out, not_61_out, not_62_out, not_63_out);
  and and_11 (and_11_out, F30, not_64_out, not_65_out, not_66_out, not_67_out, not_68_out, OP5, OP4, not_69_out, not_70_out);
  and and_12 (and_12_out, not_71_out, not_72_out, F14, F13, F12, not_73_out, OP5, OP4, not_74_out, not_75_out);
  and and_13 (and_13_out, not_76_out, not_77_out, not_78_out, F13, not_79_out, not_80_out, OP5, OP4, not_81_out, not_82_out);
  and and_14 (and_14_out, F14, F13, F12, not_83_out, not_84_out, OP4, not_85_out, not_86_out);
  and and_15 (and_15_out, not_87_out, F13, not_88_out, not_89_out, not_90_out, OP4, not_91_out, not_92_out);
  and and_16 (and_16_out, not_93_out, not_94_out, F14, not_95_out, F12, not_96_out, not_97_out, OP4, not_98_out, not_99_out);
  and and_17 (and_17_out, not_100_out, not_101_out, not_102_out, OP6, OP5, not_103_out, not_104_out, not_105_out);
  and and_18 (and_18_out, not_106_out, not_107_out, F12, OP6, OP5, not_108_out, not_109_out, not_110_out);
  and and_19 (and_19_out, not_111_out, not_112_out, not_113_out, OP6, OP5, not_114_out, not_115_out, OP2);
  and and_20 (and_20_out, not_116_out, F25, not_117_out, not_118_out, not_119_out, not_120_out, OP5, OP4, not_121_out, not_122_out);
  and and_21 (and_21_out, not_123_out, not_124_out, not_125_out, not_126_out, not_127_out, not_128_out, OP5, OP4, not_129_out, not_130_out);
  and and_22 (and_22_out, F30, not_131_out, not_132_out, not_133_out, not_134_out, not_135_out, OP5, OP4, not_136_out, not_137_out);
  and and_23 (and_23_out, not_138_out, not_139_out, F14, F13, F12, not_140_out, OP5, OP4, not_141_out, not_142_out);
  and and_24 (and_24_out, not_143_out, not_144_out, not_145_out, F13, F12, not_146_out, OP5, OP4, not_147_out, not_148_out);
  and and_25 (and_25_out, not_149_out, not_150_out, not_151_out, not_152_out, not_153_out, OP4, not_154_out, not_155_out);
  and and_26 (and_26_out, F14, F13, F12, not_156_out, not_157_out, OP4, not_158_out, not_159_out);
  and and_27 (and_27_out, not_160_out, not_161_out, not_162_out, OP6, OP5, not_163_out, not_164_out, not_165_out);
  and and_28 (and_28_out, not_166_out, not_167_out, F12, OP6, OP5, not_168_out, not_169_out, not_170_out);
  and and_29 (and_29_out, not_171_out, not_172_out, not_173_out, OP6, OP5, not_174_out, not_175_out, OP2);
  and and_30 (and_30_out, not_176_out, F25, F14, F13, F12, not_177_out, OP5, OP4, not_178_out, not_179_out);
  and and_31 (and_31_out, F14, not_180_out, not_181_out, not_182_out, not_183_out, not_184_out, not_185_out, not_186_out);
  and and_32 (and_32_out, F14, F13, not_187_out, OP6, OP5, not_188_out, not_189_out, not_190_out);
  and and_33 (and_33_out, not_191_out, not_192_out, F14, F13, not_193_out, not_194_out, OP5, OP4, not_195_out, not_196_out);
  and and_34 (and_34_out, not_197_out, not_198_out, not_199_out, F13, not_200_out, not_201_out, OP5, OP4, not_202_out, not_203_out);
  and and_35 (and_35_out, not_204_out, not_205_out, not_206_out, F13, F12, not_207_out, OP5, OP4, not_208_out, not_209_out);
  and and_36 (and_36_out, F14, F13, not_210_out, not_211_out, not_212_out, OP4, not_213_out, not_214_out);
  and and_37 (and_37_out, F14, not_215_out, not_216_out, not_217_out, not_218_out, OP4, not_219_out, not_220_out);
  and and_38 (and_38_out, not_221_out, F13, not_222_out, not_223_out, not_224_out, OP4, not_225_out, not_226_out);
  and and_39 (and_39_out, F14, F13, not_227_out, OP6, OP5, not_228_out, not_229_out, not_230_out);
  or or_1 (S0, and_1_out, and_2_out, and_3_out, and_4_out, and_5_out, and_6_out, and_7_out, and_8_out, and_9_out, and_10_out);
  or or_2 (S1, and_11_out, and_12_out, and_13_out, and_14_out, and_15_out, and_16_out, and_17_out, and_18_out, and_19_out, and_20_out);
  or or_3 (S2, and_21_out, and_22_out, and_23_out, and_24_out, and_25_out, and_26_out, and_27_out, and_28_out, and_29_out, and_30_out, and_31_out, and_32_out);
  or or_4 (S3, and_33_out, and_34_out, and_35_out, and_36_out, and_37_out, and_38_out, and_39_out);
endmodule

// 控制信号生成
module \控制信号自动生成  (
  input  OP2,
  input  OP3,
  input  OP4,
  input  OP5,
  input  OP6,
  input  F12,
  input  F13,
  input  F14,
  input  F25,
  input  F30,
  output MemToReg,
  output MemWrite,
  output RS_1,
  output RS_2,
  output REMU,
  output BLTU,
  output ALU_SRC,
  output RegWrite,
  output ecall,
  output S_Type,
  output BEQ,
  output LBU,
  output BNE,
  output JALR,
  output JAL
);

  wire and_1_out, and_2_out, and_4_out, and_5_out, and_6_out, and_7_out, and_8_out, and_9_out, and_10_out,
       and_11_out, and_12_out, and_13_out, and_14_out, and_15_out, and_16_out, and_17_out, and_18_out,
       and_19_out, and_20_out, and_21_out, and_22_out, and_23_out, and_24_out, and_25_out, and_26_out,
       and_27_out, and_28_out, and_29_out, and_30_out, and_31_out, and_32_out, and_33_out, and_34_out,
       and_35_out, and_36_out, and_37_out, and_38_out, and_41_out, and_42_out, and_43_out, and_44_out,
       and_45_out, and_46_out, and_47_out, and_48_out, and_49_out, and_50_out, and_51_out, and_52_out,
       and_53_out, and_54_out, and_55_out, and_56_out, and_57_out, and_58_out, and_59_out, and_60_out,
       and_61_out, and_62_out, and_63_out, and_64_out, and_65_out, and_66_out, and_67_out, and_68_out,
       and_69_out, and_70_out, and_71_out, and_72_out, and_73_out, and_74_out, and_75_out, and_76_out,
       not_1_out, not_2_out, not_3_out, not_4_out, not_5_out, not_6_out, not_7_out, not_8_out, not_9_out,
       not_10_out, not_11_out, not_12_out, not_13_out, not_14_out, not_15_out, not_16_out, not_17_out,
       not_18_out, not_19_out, not_20_out, not_21_out, not_22_out, not_23_out, not_24_out, not_25_out,
       not_26_out, not_27_out, not_28_out, not_29_out, not_30_out, not_31_out, not_32_out, not_33_out,
       not_34_out, not_35_out, not_36_out, not_37_out, not_38_out, not_39_out, not_40_out, not_41_out,
       not_42_out, not_43_out, not_44_out, not_45_out, not_46_out, not_47_out, not_48_out, not_49_out,
       not_50_out, not_51_out, not_52_out, not_53_out, not_54_out, not_55_out, not_56_out, not_57_out,
       not_58_out, not_59_out, not_60_out, not_61_out, not_62_out, not_63_out, not_64_out, not_65_out,
       not_66_out, not_67_out, not_68_out, not_69_out, not_70_out, not_71_out, not_72_out, not_73_out,
       not_74_out, not_75_out, not_76_out, not_77_out, not_78_out, not_79_out, not_80_out, not_81_out,
       not_82_out, not_83_out, not_84_out, not_85_out, not_86_out, not_87_out, not_88_out, not_89_out,
       not_90_out, not_91_out, not_92_out, not_93_out, not_94_out, not_95_out, not_96_out, not_97_out,
       not_98_out, not_99_out, not_100_out, not_101_out, not_102_out, not_103_out, not_104_out, not_105_out,
       not_106_out, not_107_out, not_108_out, not_109_out, not_110_out, not_111_out, not_112_out,
       not_113_out, not_114_out, not_115_out, not_116_out, not_117_out, not_118_out, not_119_out,
       not_120_out, not_121_out, not_122_out, not_123_out, not_124_out, not_125_out, not_126_out,
       not_127_out, not_128_out, not_129_out, not_130_out, not_131_out, not_132_out, not_133_out,
       not_134_out, not_135_out, not_136_out, not_137_out, not_138_out, not_139_out, not_140_out,
       not_141_out, not_142_out, not_143_out, not_144_out, not_145_out, not_146_out, not_147_out,
       not_148_out, not_149_out, not_150_out, not_151_out, not_152_out, not_153_out, not_154_out,
       not_155_out, not_156_out, not_157_out, not_158_out, not_159_out, not_160_out, not_161_out,
       not_162_out, not_163_out, not_164_out, not_165_out, not_166_out, not_167_out, not_168_out,
       not_169_out, not_170_out, not_171_out, not_172_out, not_173_out, not_174_out, not_175_out,
       not_176_out, not_177_out, not_178_out, not_179_out, not_180_out, not_181_out, not_182_out,
       not_183_out, not_184_out, not_185_out, not_186_out, not_187_out, not_188_out, not_189_out,
       not_190_out, not_191_out, not_192_out, not_193_out, not_194_out, not_195_out, not_196_out,
       not_197_out, not_198_out, not_199_out, not_200_out, not_201_out, not_202_out, not_203_out,
       not_204_out, not_205_out, not_206_out, not_207_out, not_208_out, not_209_out, not_210_out,
       not_211_out, not_212_out, not_213_out, not_214_out, not_215_out, not_216_out, not_217_out,
       not_218_out, not_219_out, not_220_out, not_221_out, not_222_out, not_223_out, not_224_out,
       not_225_out, not_226_out, not_227_out, not_228_out, not_229_out, not_230_out, not_231_out,
       not_232_out, not_233_out, not_234_out, not_235_out, not_236_out, not_237_out, not_238_out,
       not_239_out, not_240_out, not_241_out, not_242_out, not_243_out, not_244_out, not_245_out,
       not_246_out, not_247_out, not_248_out, not_249_out, not_250_out, not_251_out, not_252_out,
       not_253_out, not_254_out, not_255_out, not_256_out, not_257_out, not_258_out, not_259_out,
       not_260_out, not_261_out, not_262_out, not_263_out, not_264_out, not_265_out, not_266_out,
       not_267_out, not_268_out, not_269_out, not_270_out, not_271_out, not_272_out, not_273_out,
       not_274_out, not_275_out, not_276_out, not_277_out, not_278_out, not_279_out, not_280_out,
       not_281_out, not_282_out, not_283_out, not_284_out, not_285_out, not_286_out, not_287_out,
       not_288_out, not_289_out, not_290_out, not_291_out, not_292_out, not_293_out, not_294_out,
       not_295_out, not_296_out, not_297_out, not_298_out, not_299_out, not_300_out, not_301_out,
       not_302_out, not_303_out, not_304_out, not_305_out, not_306_out, not_307_out, not_308_out,
       not_309_out, not_310_out, not_311_out, not_312_out, not_313_out, not_314_out, not_315_out,
       not_316_out, not_317_out, not_318_out, not_319_out, not_320_out, not_321_out, not_322_out,
       not_323_out, not_324_out, not_325_out, not_326_out, not_327_out, not_328_out, not_329_out,
       not_330_out, not_331_out, not_332_out, not_333_out, not_334_out, not_335_out, not_336_out,
       not_337_out, not_338_out, not_339_out, not_340_out, not_341_out, not_342_out, not_343_out,
       not_344_out, not_345_out, not_346_out, not_347_out, not_348_out, not_349_out, not_350_out,
       not_351_out, not_352_out, not_353_out, not_354_out, not_355_out, not_356_out, not_357_out,
       not_358_out, not_359_out, not_360_out, not_361_out, not_362_out, not_363_out, not_364_out,
       not_365_out, not_366_out, not_367_out, not_368_out, not_369_out, not_370_out, not_371_out,
       not_372_out, not_373_out, not_374_out, not_375_out, not_376_out, not_377_out, not_378_out,
       not_379_out, not_380_out, not_381_out, not_382_out, not_383_out, not_384_out, not_385_out,
       not_386_out, not_387_out, not_388_out, not_389_out, not_390_out, not_391_out, not_392_out,
       not_393_out, not_394_out, not_395_out, not_396_out, not_397_out, not_398_out, not_399_out,
       not_400_out, not_401_out, not_402_out, not_403_out, not_404_out, not_405_out, not_406_out,
       not_407_out, not_408_out, not_409_out, not_410_out, not_411_out, not_412_out, not_413_out,
       not_414_out, not_415_out, not_416_out, not_417_out, not_418_out, not_419_out, not_420_out,
       not_421_out, not_422_out, not_423_out, not_424_out, not_425_out, not_426_out, not_427_out,
       not_428_out, not_429_out, not_430_out, not_431_out, not_432_out, not_433_out, not_434_out,
       not_435_out, not_436_out, not_437_out, not_438_out, not_439_out, not_440_out, not_441_out,
       not_442_out, not_443_out, not_444_out, not_445_out, not_446_out, not_447_out, not_448_out,
       not_449_out, not_450_out, not_451_out, not_452_out, not_453_out, not_454_out, not_455_out,
       not_456_out, not_457_out, not_458_out, not_459_out, not_460_out, not_461_out, not_462_out,
       not_463_out, not_464_out, not_465_out, not_466_out, not_467_out, not_468_out, not_469_out,
       not_470_out, not_471_out, not_472_out, not_473_out, not_474_out, not_475_out, not_476_out,
       not_477_out, not_478_out, not_479_out;

  not not_1 (not_1_out, F14);
  not not_2 (not_2_out, F12);
  not not_3 (not_3_out, OP6);
  not not_4 (not_4_out, OP5);
  not not_5 (not_5_out, OP4);
  not not_6 (not_6_out, OP3);
  not not_7 (not_7_out, OP2);
  not not_8 (not_8_out, F13);
  not not_9 (not_9_out, F12);
  not not_10 (not_10_out, OP6);
  not not_11 (not_11_out, OP5);
  not not_12 (not_12_out, OP4);
  not not_13 (not_13_out, OP3);
  not not_14 (not_14_out, OP2);
  not not_15 (not_15_out, F14);
  not not_16 (not_16_out, F12);
  not not_17 (not_17_out, OP6);
  not not_18 (not_18_out, OP4);
  not not_19 (not_19_out, OP3);
  not not_20 (not_20_out, OP2);
  not not_21 (not_21_out, F30);
  not not_22 (not_22_out, F25);
  not not_23 (not_23_out, F14);
  not not_24 (not_24_out, F13);
  not not_25 (not_25_out, F12);
  not not_26 (not_26_out, OP6);
  not not_27 (not_27_out, OP3);
  not not_28 (not_28_out, OP2);
  not not_29 (not_29_out, F25);
  not not_30 (not_30_out, F14);
  not not_31 (not_31_out, F13);
  not not_32 (not_32_out, F12);
  not not_33 (not_33_out, OP6);
  not not_34 (not_34_out, OP3);
  not not_35 (not_35_out, OP2);
  not not_36 (not_36_out, F30);
  not not_37 (not_37_out, F25);
  not not_38 (not_38_out, OP6);
  not not_39 (not_39_out, OP3);
  not not_40 (not_40_out, OP2);
  not not_41 (not_41_out, F30);
  not not_42 (not_42_out, F25);
  not not_43 (not_43_out, F12);
  not not_44 (not_44_out, OP6);
  not not_45 (not_45_out, OP3);
  not not_46 (not_46_out, OP2);
  not not_47 (not_47_out, F30);
  not not_48 (not_48_out, F25);
  not not_49 (not_49_out, F14);
  not not_50 (not_50_out, F12);
  not not_51 (not_51_out, OP6);
  not not_52 (not_52_out, OP3);
  not not_53 (not_53_out, OP2);
  not not_54 (not_54_out, F30);
  not not_55 (not_55_out, F25);
  not not_56 (not_56_out, F14);
  not not_57 (not_57_out, OP6);
  not not_58 (not_58_out, OP3);
  not not_59 (not_59_out, OP2);
  not not_60 (not_60_out, F14);
  not not_61 (not_61_out, F13);
  not not_62 (not_62_out, F12);
  not not_63 (not_63_out, OP6);
  not not_64 (not_64_out, OP5);
  not not_65 (not_65_out, OP3);
  not not_66 (not_66_out, OP2);
  not not_67 (not_67_out, OP6);
  not not_68 (not_68_out, OP5);
  not not_69 (not_69_out, OP3);
  not not_70 (not_70_out, OP2);
  not not_71 (not_71_out, F12);
  not not_72 (not_72_out, OP6);
  not not_73 (not_73_out, OP5);
  not not_74 (not_74_out, OP3);
  not not_75 (not_75_out, OP2);
  not not_76 (not_76_out, F13);
  not not_77 (not_77_out, F12);
  not not_78 (not_78_out, OP6);
  not not_79 (not_79_out, OP5);
  not not_80 (not_80_out, OP3);
  not not_81 (not_81_out, OP2);
  not not_82 (not_82_out, F14);
  not not_83 (not_83_out, F12);
  not not_84 (not_84_out, OP6);
  not not_85 (not_85_out, OP5);
  not not_86 (not_86_out, OP3);
  not not_87 (not_87_out, OP2);
  not not_88 (not_88_out, F30);
  not not_89 (not_89_out, F25);
  not not_90 (not_90_out, F14);
  not not_91 (not_91_out, F13);
  not not_92 (not_92_out, OP6);
  not not_93 (not_93_out, OP5);
  not not_94 (not_94_out, OP3);
  not not_95 (not_95_out, OP2);
  not not_96 (not_96_out, F30);
  not not_97 (not_97_out, F25);
  not not_98 (not_98_out, F13);
  not not_99 (not_99_out, OP6);
  not not_100 (not_100_out, OP5);
  not not_101 (not_101_out, OP3);
  not not_102 (not_102_out, OP2);
  not not_103 (not_103_out, F25);
  not not_104 (not_104_out, F13);
  not not_105 (not_105_out, OP6);
  not not_106 (not_106_out, OP5);
  not not_107 (not_107_out, OP3);
  not not_108 (not_108_out, OP2);
  not not_109 (not_109_out, F14);
  not not_110 (not_110_out, F12);
  not not_111 (not_111_out, OP6);
  not not_112 (not_112_out, OP5);
  not not_113 (not_113_out, OP4);
  not not_114 (not_114_out, OP3);
  not not_115 (not_115_out, OP2);
  not not_116 (not_116_out, F14);
  not not_117 (not_117_out, F12);
  not not_118 (not_118_out, OP6);
  not not_119 (not_119_out, OP4);
  not not_120 (not_120_out, OP3);
  not not_121 (not_121_out, OP2);
  not not_122 (not_122_out, F14);
  not not_123 (not_123_out, F13);
  not not_124 (not_124_out, F12);
  not not_125 (not_125_out, OP4);
  not not_126 (not_126_out, OP3);
  not not_127 (not_127_out, OP2);
  not not_128 (not_128_out, F14);
  not not_129 (not_129_out, F13);
  not not_130 (not_130_out, OP4);
  not not_131 (not_131_out, OP3);
  not not_132 (not_132_out, OP2);
  not not_133 (not_133_out, F14);
  not not_134 (not_134_out, F13);
  not not_135 (not_135_out, F12);
  not not_136 (not_136_out, OP4);
  not not_137 (not_137_out, OP3);
  not not_138 (not_138_out, F30);
  not not_139 (not_139_out, F14);
  not not_140 (not_140_out, F13);
  not not_141 (not_141_out, F12);
  not not_142 (not_142_out, OP6);
  not not_143 (not_143_out, OP3);
  not not_144 (not_144_out, OP2);
  not not_145 (not_145_out, F30);
  not not_146 (not_146_out, OP6);
  not not_147 (not_147_out, OP3);
  not not_148 (not_148_out, OP2);
  not not_149 (not_149_out, F13);
  not not_150 (not_150_out, F12);
  not not_151 (not_151_out, OP6);
  not not_152 (not_152_out, OP5);
  not not_153 (not_153_out, OP4);
  not not_154 (not_154_out, OP3);
  not not_155 (not_155_out, OP2);
  not not_156 (not_156_out, F12);
  not not_157 (not_157_out, OP4);
  not not_158 (not_158_out, OP3);
  not not_159 (not_159_out, OP2);
  not not_160 (not_160_out, F30);
  not not_161 (not_161_out, F25);
  not not_162 (not_162_out, F14);
  not not_163 (not_163_out, F13);
  not not_164 (not_164_out, F12);
  not not_165 (not_165_out, OP6);
  not not_166 (not_166_out, OP3);
  not not_167 (not_167_out, OP2);
  not not_168 (not_168_out, F25);
  not not_169 (not_169_out, F14);
  not not_170 (not_170_out, F13);
  not not_171 (not_171_out, F12);
  not not_172 (not_172_out, OP6);
  not not_173 (not_173_out, OP3);
  not not_174 (not_174_out, OP2);
  not not_175 (not_175_out, F30);
  not not_176 (not_176_out, F25);
  not not_177 (not_177_out, OP6);
  not not_178 (not_178_out, OP3);
  not not_179 (not_179_out, OP2);
  not not_180 (not_180_out, F30);
  not not_181 (not_181_out, F25);
  not not_182 (not_182_out, F12);
  not not_183 (not_183_out, OP6);
  not not_184 (not_184_out, OP3);
  not not_185 (not_185_out, OP2);
  not not_186 (not_186_out, F30);
  not not_187 (not_187_out, F25);
  not not_188 (not_188_out, F14);
  not not_189 (not_189_out, F12);
  not not_190 (not_190_out, OP6);
  not not_191 (not_191_out, OP3);
  not not_192 (not_192_out, OP2);
  not not_193 (not_193_out, F30);
  not not_194 (not_194_out, F25);
  not not_195 (not_195_out, F14);
  not not_196 (not_196_out, OP6);
  not not_197 (not_197_out, OP3);
  not not_198 (not_198_out, OP2);
  not not_199 (not_199_out, F14);
  not not_200 (not_200_out, F12);
  not not_201 (not_201_out, OP6);
  not not_202 (not_202_out, OP4);
  not not_203 (not_203_out, OP3);
  not not_204 (not_204_out, OP2);
  not not_205 (not_205_out, F14);
  not not_206 (not_206_out, F13);
  not not_207 (not_207_out, F12);
  not not_208 (not_208_out, OP4);
  not not_209 (not_209_out, OP3);
  not not_210 (not_210_out, OP2);
  not not_211 (not_211_out, F14);
  not not_212 (not_212_out, F13);
  not not_213 (not_213_out, OP4);
  not not_214 (not_214_out, OP3);
  not not_215 (not_215_out, OP2);
  not not_216 (not_216_out, F30);
  not not_217 (not_217_out, F14);
  not not_218 (not_218_out, F13);
  not not_219 (not_219_out, F12);
  not not_220 (not_220_out, OP6);
  not not_221 (not_221_out, OP3);
  not not_222 (not_222_out, OP2);
  not not_223 (not_223_out, F30);
  not not_224 (not_224_out, OP6);
  not not_225 (not_225_out, OP3);
  not not_226 (not_226_out, OP2);
  not not_227 (not_227_out, F12);
  not not_228 (not_228_out, OP4);
  not not_229 (not_229_out, OP3);
  not not_230 (not_230_out, OP2);
  not not_231 (not_231_out, F30);
  not not_232 (not_232_out, OP6);
  not not_233 (not_233_out, OP3);
  not not_234 (not_234_out, OP2);
  not not_235 (not_235_out, F12);
  not not_236 (not_236_out, OP4);
  not not_237 (not_237_out, OP3);
  not not_238 (not_238_out, OP2);
  not not_239 (not_239_out, F14);
  not not_240 (not_240_out, F13);
  not not_241 (not_241_out, F12);
  not not_242 (not_242_out, OP6);
  not not_243 (not_243_out, OP5);
  not not_244 (not_244_out, OP3);
  not not_245 (not_245_out, OP2);
  not not_246 (not_246_out, OP6);
  not not_247 (not_247_out, OP5);
  not not_248 (not_248_out, OP3);
  not not_249 (not_249_out, OP2);
  not not_250 (not_250_out, F12);
  not not_251 (not_251_out, OP6);
  not not_252 (not_252_out, OP5);
  not not_253 (not_253_out, OP3);
  not not_254 (not_254_out, OP2);
  not not_255 (not_255_out, F13);
  not not_256 (not_256_out, F12);
  not not_257 (not_257_out, OP6);
  not not_258 (not_258_out, OP5);
  not not_259 (not_259_out, OP3);
  not not_260 (not_260_out, OP2);
  not not_261 (not_261_out, F14);
  not not_262 (not_262_out, F12);
  not not_263 (not_263_out, OP6);
  not not_264 (not_264_out, OP5);
  not not_265 (not_265_out, OP3);
  not not_266 (not_266_out, OP2);
  not not_267 (not_267_out, F30);
  not not_268 (not_268_out, F25);
  not not_269 (not_269_out, F14);
  not not_270 (not_270_out, F13);
  not not_271 (not_271_out, OP6);
  not not_272 (not_272_out, OP5);
  not not_273 (not_273_out, OP3);
  not not_274 (not_274_out, OP2);
  not not_275 (not_275_out, F30);
  not not_276 (not_276_out, F25);
  not not_277 (not_277_out, F13);
  not not_278 (not_278_out, OP6);
  not not_279 (not_279_out, OP5);
  not not_280 (not_280_out, OP3);
  not not_281 (not_281_out, OP2);
  not not_282 (not_282_out, F25);
  not not_283 (not_283_out, F13);
  not not_284 (not_284_out, OP6);
  not not_285 (not_285_out, OP5);
  not not_286 (not_286_out, OP3);
  not not_287 (not_287_out, OP2);
  not not_288 (not_288_out, F14);
  not not_289 (not_289_out, F12);
  not not_290 (not_290_out, OP6);
  not not_291 (not_291_out, OP5);
  not not_292 (not_292_out, OP4);
  not not_293 (not_293_out, OP3);
  not not_294 (not_294_out, OP2);
  not not_295 (not_295_out, F14);
  not not_296 (not_296_out, F12);
  not not_297 (not_297_out, OP6);
  not not_298 (not_298_out, OP4);
  not not_299 (not_299_out, OP3);
  not not_300 (not_300_out, OP2);
  not not_301 (not_301_out, F14);
  not not_302 (not_302_out, F13);
  not not_303 (not_303_out, F12);
  not not_304 (not_304_out, OP4);
  not not_305 (not_305_out, OP3);
  not not_306 (not_306_out, F13);
  not not_307 (not_307_out, F12);
  not not_308 (not_308_out, OP6);
  not not_309 (not_309_out, OP5);
  not not_310 (not_310_out, OP4);
  not not_311 (not_311_out, OP3);
  not not_312 (not_312_out, OP2);
  not not_313 (not_313_out, F30);
  not not_314 (not_314_out, F25);
  not not_315 (not_315_out, F14);
  not not_316 (not_316_out, F13);
  not not_317 (not_317_out, F12);
  not not_318 (not_318_out, OP6);
  not not_319 (not_319_out, OP3);
  not not_320 (not_320_out, OP2);
  not not_321 (not_321_out, F25);
  not not_322 (not_322_out, F14);
  not not_323 (not_323_out, F13);
  not not_324 (not_324_out, F12);
  not not_325 (not_325_out, OP6);
  not not_326 (not_326_out, OP3);
  not not_327 (not_327_out, OP2);
  not not_328 (not_328_out, F30);
  not not_329 (not_329_out, F25);
  not not_330 (not_330_out, OP6);
  not not_331 (not_331_out, OP3);
  not not_332 (not_332_out, OP2);
  not not_333 (not_333_out, F30);
  not not_334 (not_334_out, F25);
  not not_335 (not_335_out, F12);
  not not_336 (not_336_out, OP6);
  not not_337 (not_337_out, OP3);
  not not_338 (not_338_out, OP2);
  not not_339 (not_339_out, F30);
  not not_340 (not_340_out, F25);
  not not_341 (not_341_out, F14);
  not not_342 (not_342_out, F12);
  not not_343 (not_343_out, OP6);
  not not_344 (not_344_out, OP3);
  not not_345 (not_345_out, OP2);
  not not_346 (not_346_out, F30);
  not not_347 (not_347_out, F25);
  not not_348 (not_348_out, F14);
  not not_349 (not_349_out, OP6);
  not not_350 (not_350_out, OP3);
  not not_351 (not_351_out, OP2);
  not not_352 (not_352_out, F14);
  not not_353 (not_353_out, F13);
  not not_354 (not_354_out, F12);
  not not_355 (not_355_out, OP6);
  not not_356 (not_356_out, OP5);
  not not_357 (not_357_out, OP3);
  not not_358 (not_358_out, OP2);
  not not_359 (not_359_out, OP6);
  not not_360 (not_360_out, OP5);
  not not_361 (not_361_out, OP3);
  not not_362 (not_362_out, OP2);
  not not_363 (not_363_out, F12);
  not not_364 (not_364_out, OP6);
  not not_365 (not_365_out, OP5);
  not not_366 (not_366_out, OP3);
  not not_367 (not_367_out, OP2);
  not not_368 (not_368_out, F13);
  not not_369 (not_369_out, F12);
  not not_370 (not_370_out, OP6);
  not not_371 (not_371_out, OP5);
  not not_372 (not_372_out, OP3);
  not not_373 (not_373_out, OP2);
  not not_374 (not_374_out, F14);
  not not_375 (not_375_out, F12);
  not not_376 (not_376_out, OP6);
  not not_377 (not_377_out, OP5);
  not not_378 (not_378_out, OP3);
  not not_379 (not_379_out, OP2);
  not not_380 (not_380_out, F30);
  not not_381 (not_381_out, F25);
  not not_382 (not_382_out, F14);
  not not_383 (not_383_out, F13);
  not not_384 (not_384_out, OP6);
  not not_385 (not_385_out, OP5);
  not not_386 (not_386_out, OP3);
  not not_387 (not_387_out, OP2);
  not not_388 (not_388_out, F30);
  not not_389 (not_389_out, F25);
  not not_390 (not_390_out, F13);
  not not_391 (not_391_out, OP6);
  not not_392 (not_392_out, OP5);
  not not_393 (not_393_out, OP3);
  not not_394 (not_394_out, OP2);
  not not_395 (not_395_out, F25);
  not not_396 (not_396_out, F13);
  not not_397 (not_397_out, OP6);
  not not_398 (not_398_out, OP5);
  not not_399 (not_399_out, OP3);
  not not_400 (not_400_out, OP2);
  not not_401 (not_401_out, F14);
  not not_402 (not_402_out, F12);
  not not_403 (not_403_out, OP6);
  not not_404 (not_404_out, OP5);
  not not_405 (not_405_out, OP4);
  not not_406 (not_406_out, OP3);
  not not_407 (not_407_out, OP2);
  not not_408 (not_408_out, OP4);
  not not_409 (not_409_out, F14);
  not not_410 (not_410_out, F13);
  not not_411 (not_411_out, F12);
  not not_412 (not_412_out, OP4);
  not not_413 (not_413_out, OP3);
  not not_414 (not_414_out, F30);
  not not_415 (not_415_out, F14);
  not not_416 (not_416_out, F13);
  not not_417 (not_417_out, F12);
  not not_418 (not_418_out, OP6);
  not not_419 (not_419_out, OP3);
  not not_420 (not_420_out, OP2);
  not not_421 (not_421_out, F30);
  not not_422 (not_422_out, OP6);
  not not_423 (not_423_out, OP3);
  not not_424 (not_424_out, OP2);
  not not_425 (not_425_out, F13);
  not not_426 (not_426_out, F12);
  not not_427 (not_427_out, OP6);
  not not_428 (not_428_out, OP5);
  not not_429 (not_429_out, OP4);
  not not_430 (not_430_out, OP3);
  not not_431 (not_431_out, OP2);
  not not_432 (not_432_out, F30);
  not not_433 (not_433_out, F25);
  not not_434 (not_434_out, F14);
  not not_435 (not_435_out, F13);
  not not_436 (not_436_out, F12);
  not not_437 (not_437_out, OP3);
  not not_438 (not_438_out, OP2);
  not not_439 (not_439_out, F30);
  not not_440 (not_440_out, F25);
  not not_441 (not_441_out, F14);
  not not_442 (not_442_out, F13);
  not not_443 (not_443_out, F12);
  not not_444 (not_444_out, OP3);
  not not_445 (not_445_out, OP2);
  not not_446 (not_446_out, F14);
  not not_447 (not_447_out, F12);
  not not_448 (not_448_out, OP6);
  not not_449 (not_449_out, OP4);
  not not_450 (not_450_out, OP3);
  not not_451 (not_451_out, OP2);
  not not_452 (not_452_out, F12);
  not not_453 (not_453_out, OP4);
  not not_454 (not_454_out, OP3);
  not not_455 (not_455_out, OP2);
  not not_456 (not_456_out, F14);
  not not_457 (not_457_out, F13);
  not not_458 (not_458_out, F12);
  not not_459 (not_459_out, OP4);
  not not_460 (not_460_out, OP3);
  not not_461 (not_461_out, OP2);
  not not_462 (not_462_out, F13);
  not not_463 (not_463_out, F12);
  not not_464 (not_464_out, OP6);
  not not_465 (not_465_out, OP5);
  not not_466 (not_466_out, OP4);
  not not_467 (not_467_out, OP3);
  not not_468 (not_468_out, OP2);
  not not_469 (not_469_out, F14);
  not not_470 (not_470_out, F13);
  not not_471 (not_471_out, OP4);
  not not_472 (not_472_out, OP3);
  not not_473 (not_473_out, OP2);
  not not_474 (not_474_out, F14);
  not not_475 (not_475_out, F13);
  not not_476 (not_476_out, F12);
  not not_477 (not_477_out, OP4);
  not not_478 (not_478_out, OP3);
  not not_479 (not_479_out, OP4);
  and and_1 (and_1_out, not_1_out, F13, not_2_out, not_3_out, not_4_out, not_5_out, not_6_out, not_7_out);
  and and_2 (and_2_out, F14, not_8_out, not_9_out, not_10_out, not_11_out, not_12_out, not_13_out, not_14_out);
  and and_3 (MemWrite, not_15_out, F13, not_16_out, not_17_out, OP5, not_18_out, not_19_out, not_20_out);
  and and_4 (and_4_out, not_21_out, not_22_out, not_23_out, not_24_out, not_25_out, not_26_out, OP5, OP4, not_27_out, not_28_out);
  and and_5 (and_5_out, F30, not_29_out, not_30_out, not_31_out, not_32_out, not_33_out, OP5, OP4, not_34_out, not_35_out);
  and and_6 (and_6_out, not_36_out, not_37_out, F14, F13, F12, not_38_out, OP5, OP4, not_39_out, not_40_out);
  and and_7 (and_7_out, not_41_out, not_42_out, F14, F13, not_43_out, not_44_out, OP5, OP4, not_45_out, not_46_out);
  and and_8 (and_8_out, not_47_out, not_48_out, not_49_out, F13, not_50_out, not_51_out, OP5, OP4, not_52_out, not_53_out);
  and and_9 (and_9_out, not_54_out, not_55_out, not_56_out, F13, F12, not_57_out, OP5, OP4, not_58_out, not_59_out);
  and and_10 (and_10_out, not_60_out, not_61_out, not_62_out, not_63_out, not_64_out, OP4, not_65_out, not_66_out);
  and and_11 (and_11_out, F14, F13, F12, not_67_out, not_68_out, OP4, not_69_out, not_70_out);
  and and_12 (and_12_out, F14, F13, not_71_out, not_72_out, not_73_out, OP4, not_74_out, not_75_out);
  and and_13 (and_13_out, F14, not_76_out, not_77_out, not_78_out, not_79_out, OP4, not_80_out, not_81_out);
  and and_14 (and_14_out, not_82_out, F13, not_83_out, not_84_out, not_85_out, OP4, not_86_out, not_87_out);
  and and_15 (and_15_out, not_88_out, not_89_out, not_90_out, not_91_out, F12, not_92_out, not_93_out, OP4, not_94_out, not_95_out);
  and and_16 (and_16_out, not_96_out, not_97_out, F14, not_98_out, F12, not_99_out, not_100_out, OP4, not_101_out, not_102_out);
  and and_17 (and_17_out, F30, not_103_out, F14, not_104_out, F12, not_105_out, not_106_out, OP4, not_107_out, not_108_out);
  and and_18 (and_18_out, not_109_out, F13, not_110_out, not_111_out, not_112_out, not_113_out, not_114_out, not_115_out);
  and and_19 (and_19_out, not_116_out, F13, not_117_out, not_118_out, OP5, not_119_out, not_120_out, not_121_out);
  and and_20 (and_20_out, not_122_out, not_123_out, not_124_out, OP6, OP5, not_125_out, not_126_out, not_127_out);
  and and_21 (and_21_out, not_128_out, not_129_out, F12, OP6, OP5, not_130_out, not_131_out, not_132_out);
  and and_22 (and_22_out, not_133_out, not_134_out, not_135_out, OP6, OP5, not_136_out, not_137_out, OP2);
  and and_23 (and_23_out, not_138_out, F25, not_139_out, not_140_out, not_141_out, not_142_out, OP5, OP4, not_143_out, not_144_out);
  and and_24 (and_24_out, not_145_out, F25, F14, F13, F12, not_146_out, OP5, OP4, not_147_out, not_148_out);
  and and_25 (and_25_out, F14, not_149_out, not_150_out, not_151_out, not_152_out, not_153_out, not_154_out, not_155_out);
  and and_26 (and_26_out, F14, F13, not_156_out, OP6, OP5, not_157_out, not_158_out, not_159_out);
  and and_27 (and_27_out, not_160_out, not_161_out, not_162_out, not_163_out, not_164_out, not_165_out, OP5, OP4, not_166_out, not_167_out);
  and and_28 (and_28_out, F30, not_168_out, not_169_out, not_170_out, not_171_out, not_172_out, OP5, OP4, not_173_out, not_174_out);
  and and_29 (and_29_out, not_175_out, not_176_out, F14, F13, F12, not_177_out, OP5, OP4, not_178_out, not_179_out);
  and and_30 (and_30_out, not_180_out, not_181_out, F14, F13, not_182_out, not_183_out, OP5, OP4, not_184_out, not_185_out);
  and and_31 (and_31_out, not_186_out, not_187_out, not_188_out, F13, not_189_out, not_190_out, OP5, OP4, not_191_out, not_192_out);
  and and_32 (and_32_out, not_193_out, not_194_out, not_195_out, F13, F12, not_196_out, OP5, OP4, not_197_out, not_198_out);
  and and_33 (and_33_out, not_199_out, F13, not_200_out, not_201_out, OP5, not_202_out, not_203_out, not_204_out);
  and and_34 (and_34_out, not_205_out, not_206_out, not_207_out, OP6, OP5, not_208_out, not_209_out, not_210_out);
  and and_35 (and_35_out, not_211_out, not_212_out, F12, OP6, OP5, not_213_out, not_214_out, not_215_out);
  and and_36 (and_36_out, not_216_out, F25, not_217_out, not_218_out, not_219_out, not_220_out, OP5, OP4, not_221_out, not_222_out);
  and and_37 (and_37_out, not_223_out, F25, F14, F13, F12, not_224_out, OP5, OP4, not_225_out, not_226_out);
  and and_38 (and_38_out, F14, F13, not_227_out, OP6, OP5, not_228_out, not_229_out, not_230_out);
  and and_39 (REMU, not_231_out, F25, F14, F13, F12, not_232_out, OP5, OP4, not_233_out, not_234_out);
  and and_40 (BLTU, F14, F13, not_235_out, OP6, OP5, not_236_out, not_237_out, not_238_out);
  and and_41 (and_41_out, not_239_out, not_240_out, not_241_out, not_242_out, not_243_out, OP4, not_244_out, not_245_out);
  and and_42 (and_42_out, F14, F13, F12, not_246_out, not_247_out, OP4, not_248_out, not_249_out);
  and and_43 (and_43_out, F14, F13, not_250_out, not_251_out, not_252_out, OP4, not_253_out, not_254_out);
  and and_44 (and_44_out, F14, not_255_out, not_256_out, not_257_out, not_258_out, OP4, not_259_out, not_260_out);
  and and_45 (and_45_out, not_261_out, F13, not_262_out, not_263_out, not_264_out, OP4, not_265_out, not_266_out);
  and and_46 (and_46_out, not_267_out, not_268_out, not_269_out, not_270_out, F12, not_271_out, not_272_out, OP4, not_273_out, not_274_out);
  and and_47 (and_47_out, not_275_out, not_276_out, F14, not_277_out, F12, not_278_out, not_279_out, OP4, not_280_out, not_281_out);
  and and_48 (and_48_out, F30, not_282_out, F14, not_283_out, F12, not_284_out, not_285_out, OP4, not_286_out, not_287_out);
  and and_49 (and_49_out, not_288_out, F13, not_289_out, not_290_out, not_291_out, not_292_out, not_293_out, not_294_out);
  and and_50 (and_50_out, not_295_out, F13, not_296_out, not_297_out, OP5, not_298_out, not_299_out, not_300_out);
  and and_51 (and_51_out, not_301_out, not_302_out, not_303_out, OP6, OP5, not_304_out, not_305_out, OP2);
  and and_52 (and_52_out, F14, not_306_out, not_307_out, not_308_out, not_309_out, not_310_out, not_311_out, not_312_out);
  and and_53 (and_53_out, not_313_out, not_314_out, not_315_out, not_316_out, not_317_out, not_318_out, OP5, OP4, not_319_out, not_320_out);
  and and_54 (and_54_out, F30, not_321_out, not_322_out, not_323_out, not_324_out, not_325_out, OP5, OP4, not_326_out, not_327_out);
  and and_55 (and_55_out, not_328_out, not_329_out, F14, F13, F12, not_330_out, OP5, OP4, not_331_out, not_332_out);
  and and_56 (and_56_out, not_333_out, not_334_out, F14, F13, not_335_out, not_336_out, OP5, OP4, not_337_out, not_338_out);
  and and_57 (and_57_out, not_339_out, not_340_out, not_341_out, F13, not_342_out, not_343_out, OP5, OP4, not_344_out, not_345_out);
  and and_58 (and_58_out, not_346_out, not_347_out, not_348_out, F13, F12, not_349_out, OP5, OP4, not_350_out, not_351_out);
  and and_59 (and_59_out, not_352_out, not_353_out, not_354_out, not_355_out, not_356_out, OP4, not_357_out, not_358_out);
  and and_60 (and_60_out, F14, F13, F12, not_359_out, not_360_out, OP4, not_361_out, not_362_out);
  and and_61 (and_61_out, F14, F13, not_363_out, not_364_out, not_365_out, OP4, not_366_out, not_367_out);
  and and_62 (and_62_out, F14, not_368_out, not_369_out, not_370_out, not_371_out, OP4, not_372_out, not_373_out);
  and and_63 (and_63_out, not_374_out, F13, not_375_out, not_376_out, not_377_out, OP4, not_378_out, not_379_out);
  and and_64 (and_64_out, not_380_out, not_381_out, not_382_out, not_383_out, F12, not_384_out, not_385_out, OP4, not_386_out, not_387_out);
  and and_65 (and_65_out, not_388_out, not_389_out, F14, not_390_out, F12, not_391_out, not_392_out, OP4, not_393_out, not_394_out);
  and and_66 (and_66_out, F30, not_395_out, F14, not_396_out, F12, not_397_out, not_398_out, OP4, not_399_out, not_400_out);
  and and_67 (and_67_out, not_401_out, F13, not_402_out, not_403_out, not_404_out, not_405_out, not_406_out, not_407_out);
  and and_68 (and_68_out, OP6, OP5, not_408_out, OP3, OP2);
  and and_69 (and_69_out, not_409_out, not_410_out, not_411_out, OP6, OP5, not_412_out, not_413_out, OP2);
  and and_70 (and_70_out, not_414_out, F25, not_415_out, not_416_out, not_417_out, not_418_out, OP5, OP4, not_419_out, not_420_out);
  and and_71 (and_71_out, not_421_out, F25, F14, F13, F12, not_422_out, OP5, OP4, not_423_out, not_424_out);
  and and_72 (and_72_out, F14, not_425_out, not_426_out, not_427_out, not_428_out, not_429_out, not_430_out, not_431_out);
  and and_73 (and_73_out, not_432_out, not_433_out, not_434_out, not_435_out, not_436_out, OP6, OP5, OP4, not_437_out, not_438_out);
  and and_74 (and_74_out, not_439_out, not_440_out, not_441_out, not_442_out, not_443_out, OP6, OP5, OP4, not_444_out, not_445_out);
  and and_75 (and_75_out, not_446_out, F13, not_447_out, not_448_out, OP5, not_449_out, not_450_out, not_451_out);
  and and_76 (and_76_out, F14, F13, not_452_out, OP6, OP5, not_453_out, not_454_out, not_455_out);
  and and_77 (BEQ, not_456_out, not_457_out, not_458_out, OP6, OP5, not_459_out, not_460_out, not_461_out);
  and and_78 (LBU, F14, not_462_out, not_463_out, not_464_out, not_465_out, not_466_out, not_467_out, not_468_out);
  and and_79 (BNE, not_469_out, not_470_out, F12, OP6, OP5, not_471_out, not_472_out, not_473_out);
  and and_80 (JALR, not_474_out, not_475_out, not_476_out, OP6, OP5, not_477_out, not_478_out, OP2);
  and and_81 (JAL, OP6, OP5, not_479_out, OP3, OP2);
  or or_1 (MemToReg, and_1_out, and_2_out);
  or or_2 (ecall, and_73_out, and_74_out);
  or or_3 (S_Type, and_75_out, and_76_out);
  or or_4 (RS_2, and_27_out, and_28_out, and_29_out, and_30_out, and_31_out, and_32_out, and_33_out, and_34_out, and_35_out, and_36_out, and_37_out, and_38_out);
  or or_5 (ALU_SRC, and_41_out, and_42_out, and_43_out, and_44_out, and_45_out, and_46_out, and_47_out, and_48_out, and_49_out, and_50_out, and_51_out, and_52_out);
  or or_6 (RegWrite, and_53_out, and_54_out, and_55_out, and_56_out, and_57_out, and_58_out, and_59_out, and_60_out, and_61_out, and_62_out, and_63_out, and_64_out, and_65_out, and_66_out, and_67_out, and_68_out, and_69_out, and_70_out, and_71_out, and_72_out);
  or or_7 (RS_1, and_4_out, and_5_out, and_6_out, and_7_out, and_8_out, and_9_out, and_10_out, and_11_out, and_12_out, and_13_out, and_14_out, and_15_out, and_16_out, and_17_out, and_18_out, and_19_out, and_20_out, and_21_out, and_22_out, and_23_out, and_24_out, and_25_out, and_26_out);
endmodule

// ALU
module ALU (
  input  [31:0] X,
  input  [31:0] Y,
  input  [3:0] AluOP,
  output out_4,
  output Equal,
  output out_6,
  output [31:0] Result,
  output [31:0] Result_2
);

  wire [0:0] comparator_1_lt, comparator_2_lt;
  wire [31:0] adder_1_out, AND_out, divider_1_out, divider_1_rem, multiplier_1_cout, multiplier_1_out,
       NOR_out, OR_out, shifter_1_out, shifter_2_out, shifter_3_out, subtractor_1_out, XOR_out;

  assign AND_out = X & Y;  // AND_Gate AND, 32 bits wide
  assign OR_out = X | Y;  // OR_Gate OR, 32 bits wide
  Shifter #(.width(32), .shift("ll")) shifter_1 (.in(X), .\dist (Y[4:0]), .out(shifter_1_out));
  Shifter #(.width(32), .shift("ar")) shifter_2 (.in(X), .\dist (Y[4:0]), .out(shifter_2_out));
  Shifter #(.width(32), .shift("lr")) shifter_3 (.in(X), .\dist (Y[4:0]), .out(shifter_3_out));
  Multiplier #(.width(32)) multiplier_1 (.a(X), .b(Y), .out(multiplier_1_out), .cout(multiplier_1_cout));  // open: cin
  Divider #(.width(32)) divider_1 (.a(X), .b(Y), .out(divider_1_out), .rem(divider_1_rem));  // open: upper
  Adder #(.width(32)) adder_1 (.a(X), .b(Y), .out(adder_1_out));  // open: cin, cout
  Subtractor #(.width(32)) subtractor_1 (.a(X), .b(Y), .out(subtractor_1_out));  // open: bin, bout
  assign XOR_out = X ^ Y;  // XOR_Gate XOR, 32 bits wide
  assign NOR_out = ~(X | Y);  // NOR_Gate NOR, 32 bits wide
  Comparator #(.width(32), .mode("twosComplement")) comparator_1 (
    .a(X), .b(Y), .eq(Equal), .lt(comparator_1_lt[0]));  // open: gt
  Comparator #(.width(32), .mode("unsigned")) comparator_2 (.a(X), .b(Y), .lt(comparator_2_lt[0]));  // open: gt, eq
  Multiplexer #(.select(4), .width(32), .disabled("Z"), .enable("false")) multiplexer_1 (
    .in0(shifter_1_out), .in1(shifter_2_out), .in2(shifter_3_out), .in3(multiplier_1_out),
    .in4(divider_1_out), .in5(adder_1_out), .in6(subtractor_1_out), .in7(AND_out), .in8(OR_out),
    .in9(XOR_out), .in10(NOR_out), .in11({{31{1'b0}}, comparator_1_lt[0]}),
    .in12({{31{1'b0}}, comparator_2_lt[0]}), .in13({32{1'b0}}), .in14({32{1'b0}}), .in15({32{1'b0}}),
    .out(Result), .sel(AluOP));
  Multiplexer #(.select(4), .width(32), .disabled("Z"), .enable("false")) multiplexer_2 (
    .in0({32{1'b0}}), .in1({32{1'b0}}), .in2({32{1'b0}}), .in3(multiplier_1_cout), .in4(divider_1_rem),
    .in5({32{1'b0}}), .in6({32{1'b0}}), .in7({32{1'b0}}), .in8({32{1'b0}}), .in9({32{1'b0}}),
    .in10({32{1'b0}}), .in11({32{1'b0}}), .in12({32{1'b0}}), .in13({32{1'b0}}), .in14({32{1'b0}}),
    .in15({32{1'b0}}), .out(Result_2), .sel(AluOP));
  Multiplexer #(.select(4), .width(1), .disabled("Z"), .enable("false")) multiplexer_3 (
    .in0(1'b0), .in1(1'b0), .in2(1'b0), .in3(1'b0), .in4(1'b0), .in5(1'b0), .in6(1'b0), .in7(1'b0),
    .in8(1'b0), .in9(1'b0), .in10(1'b0), .in11(comparator_1_lt[0]), .in12(comparator_2_lt[0]), .in13(1'b0),
    .in14(1'b0), .in15(1'b0), .out(out_6), .sel(AluOP));
  not not_1 (out_4, out_6);

  // Other names for the same wires on the sheet: Result2[31:0] = Result_2; S[3:0] = AluOP; tunnel = out_6;
  //   tunnel_t = out_4

  // Notes on the sheet:
  //   不要改变此引脚区域内容，也不要改变ALU封装形式
  //   输入引脚
  //   输出引脚
endmodule

module Regifile (
  input  [31:0] Din,
  input  Clk,
  input  WE,
  input  [4:0] R1_num,
  input  [4:0] W_num,
  input  [4:0] R2_num,
  output [31:0] R1,
  output [31:0] R2
);

  // RegisterFile registerfile_1: pin names not known; wires that end beside it: Din, Clk, WE, W_num, R1_num, R2_num, R1, R2
endmodule

module \理想流水线  (
  output RegWrite,
  output MemWrite,
  output [31:0] IF_PC,
  output [31:0] ID_PC,
  output [31:0] EX_PC,
  output [31:0] M_PC,
  output [31:0] WB_PC,
  output [31:0] RDin,
  output [31:0] MDin,
  output [31:0] LedData
);

  wire and_1_out, and_2_out, and_3_out, and_5_out, be, CLK, clock_1_out, comparator_1_eq, comparator_1_lt,
       comparator_2_eq, d_ff_1_q, Ecall, Equal, EX_ecall, EX_halt, ex_mem_1_halt_2, ex_mem_1_jal_2,
       ex_mem_1_jalr_2, ex_mem_1_regwrite_2, Go, halt, id_ex_1_aliesrcb, id_ex_1_beq_2, id_ex_1_bltu_2,
       id_ex_1_bne_2, id_ex_1_jal_2, id_ex_1_memtoreg_2, id_ex_1_memwrite_2, id_ex_1_regwrite_2,
       id_ex_1_s_type_2, id_ex_1_uret_2, IR1, IR2, IR3, JAL, JALR, Less, mem_wb_1_halt_2, mem_wb_1_jal_2,
       mem_wb_1_jalr_2, MemToReg, nand_1_out, not_1_out, not_2_out, not_3_out, or_1_out, or_2_out,
       riscv_probe_5_p2, RS_1, RS_2, RST, S_TPYE, URET, W1, W2, W3, \单周期硬布线控制器_1_alu_src , \单周期硬布线控制器_1_beq ,
       \单周期硬布线控制器_1_bltu , \单周期硬布线控制器_1_bne , \单周期硬布线控制器_1_memtoreg , \单周期硬布线控制器_1_memwrite ,
       \单周期硬布线控制器_1_regwrite , \单周期硬布线控制器_1_remu ;
  wire [1:0] id_ex_1_jalr_2, id_ex_1_rs1_forward_2, id_ex_1_rs2_forward_2, mem_wb_1_memtoreg_2;
  wire [3:0] id_ex_1_aluop_2, \单周期硬布线控制器_1_alu_op ;
  wire [4:0] ex_mem_1_rd_2, id_ex_1_rd_2, multiplexer_2_out, multiplexer_3_out, WB_rd;
  wire [7:0] multiplexer_9_out;
  wire [12:0] CNT_num;
  wire [15:0] \LoadUse次数 , \总周期数 , \插入气泡数 , \无条件分支数 , \条件分支成功数 ;
  wire [31:0] ALU_addr, ALUResult, bit_extender_1_out, bit_extender_2_out, bit_extender_3_out,
       bit_extender_4_out, bit_extender_5_out, EX_IR, ex_mem_1_ir_2, ex_mem_1_pc_2, ex_mem_1_pc_4_2,
       id_ex_1_imm_1_2, id_ex_1_imm_2_2, id_ex_1_pc_4_2, id_ex_1_r1_2, id_ex_1_r2_2, ID_IR, if_id_1_ir_2,
       if_id_1_pc_2, if_id_1_pc_4_2, IF_IR, JumpAddr, jumpAddr_t, MEM_ALURes, MEM_IR, mem_wb_1_aluresult_2,
       mem_wb_1_pc_4_2, mem_wb_1_readdata_2, Memdata, multiplexer_1_out, multiplexer_4_out,
       multiplexer_5_out, multiplexer_6_out, multiplexer_7_out, multiplexer_8_out, multiplexer_10_out, PC_4,
       regifile_1_r1, regifile_1_r2, shifter_1_out, WB_IR;

  Button \u_总复位  (.out(RST));
  Button _1 (.out(IR1));
  Button _2 (.out(IR2));
  Button _3 (.out(IR3));
  // Probe on \总周期数 
  // Probe on \总周期数 
  Button \u_继续运行  (.out(Go));
  LED #(.active("true")) led_1 (.in(W1));
  LED #(.active("true")) led_2 (.in(W2));
  LED #(.active("true")) led_3 (.in(W3));
  Hex_Digit_Display hex_digit_display_1 (.value(LedData[31:28]));  // open: dp
  // Probe on IF_PC[19:0]
  // RiscV_Probe riscv_probe_1: pin names not known; wires that end beside it: IF_IR
  not not_1 (not_1_out, halt);
  Hex_Digit_Display hex_digit_display_2 (.value(LedData[23:20]));  // open: dp
  Hex_Digit_Display hex_digit_display_3 (.value(LedData[27:24]));  // open: dp
  // Probe on ID_PC[19:0]
  // RiscV_Probe riscv_probe_2: pin names not known; wires that end beside it: ID_IR
  Counter #(.width(16), .max('hffff), .ongoal("wrap"), .trigger("rising"), .behavior("new")) counter_1 (
    .count(not_1_out), .Q(\总周期数 ), .clk(CLK), .clr(RST));  // open: load, D, carry, preset, down
  Hex_Digit_Display hex_digit_display_4 (.value(LedData[19:16]));  // open: dp
  Hex_Digit_Display hex_digit_display_5 (.value(LedData[15:12]));  // open: dp
  Hex_Digit_Display hex_digit_display_6 (.value(LedData[7:4]));  // open: dp
  Hex_Digit_Display hex_digit_display_7 (.value(LedData[11:8]));  // open: dp
  // Probe on EX_PC[19:0]
  // RiscV_Probe riscv_probe_3: pin names not known; wires that end beside it: EX_IR
  Multiplexer #(.select(2), .width(32), .disabled("Z"), .enable("false")) multiplexer_1 (
    .in0(PC_4), .in1(ALUResult), .in2(JumpAddr), .out(multiplexer_1_out), .sel(id_ex_1_jalr_2));  // open: in3
  Hex_Digit_Display hex_digit_display_8 (.value(LedData[3:0]));  // open: dp
  not not_2 (not_2_out, or_1_out);
  or or_1 (or_1_out, Go, halt);
  // Probe on \总周期数 
  // Probe on M_PC[19:0]
  // RiscV_Probe riscv_probe_4: pin names not known; wires that end beside it: MEM_IR
  Register #(.width(32), .trigger("rising"), .Select("low")) PC (
    .D(multiplexer_1_out), .en(not_2_out), .Q(IF_PC), .clk(CLK), .clr(RST));
  Adder #(.width(32)) adder_1 (.a(IF_PC), .b(32'h4), .out(PC_4));  // open: cin, cout
  // Probe on \总周期数 
  // Probe on \无条件分支数 
  // Probe on \条件分支成功数 
  // Probe on \插入气泡数 
  // Probe on \LoadUse次数 
  // RiscV_Probe riscv_probe_5: pin names not known; wires that end beside it: IF_IR, riscv_probe_5_p2, riscv_probe_5_p2
  // Probe on IF_PC[11:0]
  // Probe on WB_PC[19:0]
  // RiscV_Probe riscv_probe_6: pin names not known; wires that end beside it: WB_IR
  or or_2 (or_2_out, id_ex_1_jalr_2[0], id_ex_1_jalr_2[1]);
  ROM #(.addrWidth(10), .dataWidth(32), .Select("high")) rom_1 (.addr(IF_PC[11:2]), .data(IF_IR));
  // Probe on EX_PC[11:0]
  // Probe on ID_PC[11:0]
  IF_ID if_id_1 (
    .IR(IF_IR), .PC(IF_PC), .PC_4(PC_4), .branch(or_2_out), .reset(RST), .IR_2(if_id_1_ir_2),
    .PC_2(if_id_1_pc_2), .PC_4_2(if_id_1_pc_4_2), .en(1'b1), .CLK(CLK));  // open: IF_PredictJump, ID_PredictJump
  // Probe on M_PC[11:0]
  D_Flip_Flop #(.trigger("high"), .Pre_Clr_Positions("LEGACY"), .NegatePresetClear("false"), .enable("true"), .NewFFLayout("false")) d_ff_1 (.Q(d_ff_1_q));  // open: clk, D, Qn, preset, en, reset
  // Probe on 13'hc
  Multiplexer #(.select(1), .width(5), .disabled("Z"), .enable("false")) multiplexer_2 (
    .in0(if_id_1_ir_2[19:15]), .in1(5'b10001), .out(multiplexer_2_out), .sel(Ecall));
  Multiplexer #(.select(1), .width(5), .disabled("Z"), .enable("false")) multiplexer_3 (
    .in0(if_id_1_ir_2[24:20]), .in1(5'b01010), .out(multiplexer_3_out), .sel(Ecall));
  // Probe on WB_PC[11:0]
  Comparator #(.width(13), .mode("twosComplement")) comparator_1 (
    .a(CNT_num), .b(13'hc), .eq(comparator_1_eq), .lt(comparator_1_lt));  // open: gt
  Clock #(.highDuration(1), .lowDuration(1)) clock_1 (.out(clock_1_out));
  \单周期硬布线控制器  \u_单周期硬布线控制器_1  (
    .Funct({if_id_1_ir_2[30], if_id_1_ir_2[25], if_id_1_ir_2[14:12]}), .OP(if_id_1_ir_2[6:2]),
    .ALU_OP(\单周期硬布线控制器_1_alu_op ), .MemToReg(\单周期硬布线控制器_1_memtoreg ), .MemWrite(\单周期硬布线控制器_1_memwrite ),
    .ALU_SRC(\单周期硬布线控制器_1_alu_src ), .RegWrite(\单周期硬布线控制器_1_regwrite ), .ecall(Ecall), .S_type(S_TPYE),
    .Jalr(JALR), .Beq(\单周期硬布线控制器_1_beq ), .JAL(JAL), .Bne(\单周期硬布线控制器_1_bne ), .in_3(if_id_1_ir_2[21]),
    .uret(URET), .RS_1(RS_1), .RS_2(RS_2), .REMU(\单周期硬布线控制器_1_remu ), .BLTU(\单周期硬布线控制器_1_bltu ));  // open: LBU
  assign bit_extender_1_out = {{20{if_id_1_ir_2[31]}}, if_id_1_ir_2[31:20]};  // Bit_Extender bit_extender_1
  assign bit_extender_2_out = {{20{if_id_1_ir_2[31]}}, {if_id_1_ir_2[31:25], if_id_1_ir_2[11:7]}};  // Bit_Extender bit_extender_2
  assign bit_extender_3_out = {{20{if_id_1_ir_2[31]}}, {if_id_1_ir_2[31], if_id_1_ir_2[7], if_id_1_ir_2[30:25], if_id_1_ir_2[11:8]}};  // Bit_Extender bit_extender_3
  assign bit_extender_4_out = {{12{if_id_1_ir_2[31]}}, {if_id_1_ir_2[31], if_id_1_ir_2[19:12], if_id_1_ir_2[20], if_id_1_ir_2[30:21]}};  // Bit_Extender bit_extender_4
  nand nand_1 (nand_1_out, d_ff_1_q, comparator_1_eq);
  Counter #(.width(13), .max('h1fff), .ongoal("stay"), .trigger("rising"), .behavior("old")) counter_2 (
    .count(comparator_1_lt), .Q(CNT_num), .clk(clock_1_out));  // open: load, D, carry, clr, preset
  Multiplexer #(.select(1), .width(32), .disabled("Z"), .enable("false")) multiplexer_4 (
    .in0(bit_extender_1_out), .in1(bit_extender_2_out), .out(multiplexer_4_out), .sel(S_TPYE));
  Multiplexer #(.select(1), .width(32), .disabled("Z"), .enable("false")) multiplexer_5 (
    .in0(bit_extender_3_out), .in1(bit_extender_4_out), .out(multiplexer_5_out), .sel(JAL));
  assign CLK = nand_1_out ? clock_1_out : 1'bz;  // Controlled_Buffer controlled_buffer_1
  Pull_Resistor #(.pull(1)) pull_resistor_1 (.node(CLK));
  Regifile regifile_1 (
    .Din(RDin), .Clk(CLK), .R1(regifile_1_r1), .R2(regifile_1_r2), .WE(RegWrite), .W_num(WB_rd),
    .R1_num(multiplexer_2_out), .R2_num(multiplexer_3_out));
  ID_EX id_ex_1 (
    .Beq(\单周期硬布线控制器_1_beq ), .Bne(\单周期硬布线控制器_1_bne ), .MemToReg(\单周期硬布线控制器_1_memtoreg ),
    .MemWrite(\单周期硬布线控制器_1_memwrite ), .AluSrcB(\单周期硬布线控制器_1_alu_src ), .RegWrite(\单周期硬布线控制器_1_regwrite ),
    .S_type(S_TPYE), .Jal(JAL), .Jalr(JALR), .Remu(\单周期硬布线控制器_1_remu ), .Aluop(\单周期硬布线控制器_1_alu_op ),
    .rd(if_id_1_ir_2[11:7]), .R1(regifile_1_r1), .R2(regifile_1_r2), .IMM_1(multiplexer_4_out),
    .IMM_2(multiplexer_5_out), .PC(if_id_1_pc_2), .PC_4(if_id_1_pc_4_2), .IR(if_id_1_ir_2), .reset(RST),
    .flush(1'b0), .Beq_2(id_ex_1_beq_2), .Bne_2(id_ex_1_bne_2), .MemToReg_2(id_ex_1_memtoreg_2),
    .MemWrite_2(id_ex_1_memwrite_2), .AlieSrcB(id_ex_1_aliesrcb), .RegWrite_2(id_ex_1_regwrite_2),
    .S_type_2(id_ex_1_s_type_2), .Jal_2(id_ex_1_jal_2), .Jalr_2(id_ex_1_jalr_2[0]),
    .Aluop_2(id_ex_1_aluop_2), .rd_2(id_ex_1_rd_2), .R1_2(id_ex_1_r1_2), .R2_2(id_ex_1_r2_2),
    .IMM_1_2(id_ex_1_imm_1_2), .IMM_2_2(id_ex_1_imm_2_2), .PC_2(EX_PC), .PC_4_2(id_ex_1_pc_4_2),
    .IR_2(EX_IR), .RS1_Forward_2(id_ex_1_rs1_forward_2), .RS2_Forward_2(id_ex_1_rs2_forward_2), .clk(CLK),
    .en(1'b1), .BLTU(\单周期硬布线控制器_1_bltu ), .BLTU_2(id_ex_1_bltu_2), .Uret(URET), .Uret_2(id_ex_1_uret_2),
    .Ecall(Ecall), .EX_ecall(EX_ecall));  // open: RS1_Forward, RS2_Forward, ID_PredictJump, Remu_2, EX_PredictJump, LBU, LBU_2
  Multiplexer #(.select(2), .width(32), .disabled("Z"), .enable("false")) multiplexer_6 (
    .in0(id_ex_1_r1_2), .in1(RDin), .in2(MEM_ALURes), .out(multiplexer_6_out), .sel(id_ex_1_rs1_forward_2));  // open: in3
  and and_1 (and_1_out, id_ex_1_bne_2, ~Equal);  // AND_Gate
  Multiplexer #(.select(2), .width(32), .disabled("Z"), .enable("false")) multiplexer_7 (
    .in0(id_ex_1_r2_2), .in1(RDin), .in2(MEM_ALURes), .out(multiplexer_7_out), .sel(id_ex_1_rs2_forward_2));  // open: in3
  or or_3 (id_ex_1_jalr_2[1], id_ex_1_jal_2, and_1_out, and_2_out, and_3_out);
  and and_2 (and_2_out, Equal, id_ex_1_beq_2);
  Multiplexer #(.select(1), .width(32), .disabled("Z"), .enable("false")) multiplexer_8 (
    .in0(multiplexer_7_out), .in1(id_ex_1_imm_1_2), .out(multiplexer_8_out), .sel(id_ex_1_aliesrcb));
  and and_3 (and_3_out, ~Equal, id_ex_1_bltu_2);  // AND_Gate
  ALU alu_1 (
    .X(multiplexer_6_out), .Y(multiplexer_8_out), .AluOP(id_ex_1_aluop_2), .Equal(Equal), .Result(ALU_addr),
    .out_4(be), .out_6(Less));  // open: Result_2
  Shifter #(.width(32), .shift("ll")) shifter_1 (.in(id_ex_1_imm_2_2), .\dist (5'b00001), .out(shifter_1_out));
  Comparator #(.width(32), .mode("twosComplement")) comparator_2 (
    .a(multiplexer_6_out), .b(32'ha), .eq(comparator_2_eq));  // open: gt, lt
  not not_3 (not_3_out, comparator_2_eq);
  Adder #(.width(32)) adder_2 (.a(shifter_1_out), .b(EX_PC), .out(jumpAddr_t));  // open: cin, cout
  and and_4 (EX_halt, comparator_2_eq, EX_ecall);
  Register #(.width(32), .trigger("rising"), .Select("low")) register_1 (
    .D(multiplexer_7_out), .en(and_5_out), .Q(LedData), .clk(CLK), .clr(RST));
  and and_5 (and_5_out, not_3_out, EX_ecall);
  EX_MEM ex_mem_1 (
    .Jal(id_ex_1_jal_2), .Jalr(id_ex_1_jalr_2[0]), .MemToReg(id_ex_1_memtoreg_2),
    .MemWrite(id_ex_1_memwrite_2), .RegWrite(id_ex_1_regwrite_2), .halt(EX_halt), .rd(id_ex_1_rd_2),
    .Result(ALU_addr), .WriteData(multiplexer_7_out), .IR(EX_IR), .PC(EX_PC), .PC_4(id_ex_1_pc_4_2),
    .reset(RST), .clk(CLK), .Jal_2(ex_mem_1_jal_2), .Jalr_2(ex_mem_1_jalr_2), .MemToReg_2(MemToReg),
    .MemWrite_2(MemWrite), .RegWrite_2(ex_mem_1_regwrite_2), .halt_2(ex_mem_1_halt_2), .rd_2(ex_mem_1_rd_2),
    .Result_2(MEM_ALURes), .WriteData_2(MDin), .IR_2(ex_mem_1_ir_2), .PC_2(ex_mem_1_pc_2),
    .PC_4_2(ex_mem_1_pc_4_2), .en(1'b1));  // open: LBU, LBU_2
  Multiplexer #(.select(2), .width(8), .disabled("Z"), .enable("false")) multiplexer_9 (
    .in0(Memdata[7:0]), .in1(Memdata[15:8]), .in2(Memdata[23:16]), .in3(Memdata[31:24]),
    .out(multiplexer_9_out), .sel(MEM_ALURes[1:0]));
  RAM #(.addrWidth(10), .dataWidth(32), .bus("separate"), .Select("high")) ram_1 (
    .addr(MEM_ALURes[11:2]), .din(MDin), .data(Memdata), .str(1'b1), .sel(CLK), .ld(1'b1), .clr(RST));  // open: clk
  assign bit_extender_5_out = {{24{1'b0}}, multiplexer_9_out};  // Bit_Extender bit_extender_5
  Multiplexer #(.select(1), .width(32), .disabled("Z"), .enable("false")) multiplexer_10 (
    .in0(Memdata), .in1(bit_extender_5_out), .out(multiplexer_10_out));  // open: sel
  or or_4 (mem_wb_1_memtoreg_2[1], mem_wb_1_jal_2, mem_wb_1_jalr_2);
  MEM_WB mem_wb_1 (
    .reset(RST), .Jal(ex_mem_1_jal_2), .Jalr(ex_mem_1_jalr_2), .MemToReg(MemToReg),
    .RegWrite(ex_mem_1_regwrite_2), .halt(ex_mem_1_halt_2), .rd(ex_mem_1_rd_2), .ALUResult(MEM_ALURes),
    .ReadData(multiplexer_10_out), .IR(ex_mem_1_ir_2), .PC(ex_mem_1_pc_2), .PC_4(ex_mem_1_pc_4_2), .clk(CLK),
    .Jal_2(mem_wb_1_jal_2), .Jalr_2(mem_wb_1_jalr_2), .MemToReg_2(mem_wb_1_memtoreg_2[0]),
    .RegWrite_2(RegWrite), .halt_2(mem_wb_1_halt_2), .out_20(WB_rd), .ALUResult_2(mem_wb_1_aluresult_2),
    .ReadData_2(mem_wb_1_readdata_2), .IR_2(WB_IR), .PC_2(WB_PC), .Pc_4_2(mem_wb_1_pc_4_2), .en(1'b1));
  Multiplexer #(.select(2), .width(32), .disabled("Z"), .enable("false")) multiplexer_11 (
    .in0(mem_wb_1_aluresult_2), .in1(mem_wb_1_readdata_2), .in2(mem_wb_1_pc_4_2), .out(RDin),
    .sel(mem_wb_1_memtoreg_2));  // open: in3
  D_Flip_Flop #(.trigger("rising"), .Pre_Clr_Positions("ABOVE_BELOW"), .NegatePresetClear("false"), .enable("true"), .NewFFLayout("true")) d_ff_2 (
    .clk(mem_wb_1_halt_2), .D(1'b1), .Q(halt), .en(1'b1), .reset(Go));  // open: Qn, preset

  // Other names for the same wires on the sheet: MEM_PC[31:0] = M_PC; WB_RegWrite = RegWrite

  // Notes on the sheet:
  //   中断源
  //   时空图监测，可删除
  //   中断等待指示
  //   数码管输出
  //   指令存储器
  //   指令探针
  //   contents of rom_1 (hex, n*v repeats v):
  //   100413 1f41993 41f9d993 433 c00913 300b13 140413 f47413 800293 100313 499993 89e9b3 1300533 2200893
  //   73 406282b3 fe0294e3 140413 f00f93 1f47433 1c41413 800293 100313 49d993 89e9b3 1300533 2200893 73
  //   406282b3 fe0294e3 1c45413 406b0b33 b0463 f95ff06f 2b3 fff2c293 829293 ff2e293 500533 2200893 73
  //   a00893 73
  //   控制位
  //   流水调试日志用
  //   暂停节拍，不能为0
  //   用这个时钟源需要去掉电路中的其他时钟源
  //   JAL
  //   JALR
  //   URET
  //   指令字
  //   戳工具置1进入计数暂停模式，ctrl+k时钟自动运行到对应节拍暂停
  //   ctrl+k关闭时钟连续运行，将控制位置零，进入单步调试模式调试
  //   Beq
  //   Bne
  //   MemWrite
  //   AluOP
  //   AluSrcB
  //   可计数暂停的时钟源
  //   为方便自动评测，需要输出流水线各段保存的PC值，注意是PC不是PC+4，另外ID段寄存器写入信息，Mem段内存写入信息也要输出
  //   数据存储器
endmodule

module \气泡流水线  (
  output RegWrite,
  output MemWrite,
  output [31:0] IF_PC,
  output [31:0] ID_PC,
  output [31:0] EX_PC,
  output [31:0] M_PC,
  output [31:0] WB_PC,
  output [31:0] RDin,
  output [31:0] MDin,
  output [31:0] LedData
);

  wire and_1_out, and_2_out, and_3_out, and_4_out, and_5_out, and_6_out, and_7_out, and_8_out, and_9_out,
       and_10_out, and_12_out, be, BranchSuc, BranchTaken, CLK, clock_1_out, comparator_1_eq,
       comparator_1_lt, comparator_2_eq, d_ff_1_q, Ecall, Equal, EX_ecall, EX_halt, ex_mem_1_halt_2,
       ex_mem_1_jal_2, ex_mem_1_jalr_2, ex_mem_1_regwrite_2, Flush, Go, halt, id_ex_1_aliesrcb,
       id_ex_1_beq_2, id_ex_1_bltu_2, id_ex_1_bne_2, id_ex_1_jal_2, id_ex_1_memtoreg_2, id_ex_1_memwrite_2,
       id_ex_1_regwrite_2, id_ex_1_s_type_2, id_ex_1_uret_2, IR1, IR2, IR3, JAL, JALR, Less, mem_wb_1_halt_2,
       mem_wb_1_jal_2, mem_wb_1_jalr_2, MemToReg, nand_1_out, not_1_out, or_1_out, or_2_out, or_3_out,
       or_4_out, or_9_out, or_10_out, riscv_probe_5_p3, RS_1, RS_2, RST, S_TPYE, stall, URET, W1, W2, W3,
       \单周期硬布线控制器_1_alu_src , \单周期硬布线控制器_1_beq , \单周期硬布线控制器_1_bltu , \单周期硬布线控制器_1_bne ,
       \单周期硬布线控制器_1_memtoreg , \单周期硬布线控制器_1_memwrite , \单周期硬布线控制器_1_regwrite , \单周期硬布线控制器_1_remu , \无条件跳转 ;
  wire [1:0] id_ex_1_jalr_2, id_ex_1_rs1_forward_2, id_ex_1_rs2_forward_2, mem_wb_1_memtoreg_2;
  wire [3:0] id_ex_1_aluop_2, \单周期硬布线控制器_1_alu_op ;
  wire [4:0] ex_mem_1_rd_2, id_ex_1_rd_2, multiplexer_2_out, multiplexer_3_out, WB_rd;
  wire [7:0] multiplexer_9_out;
  wire [12:0] CNT_num;
  wire [15:0] \LoadUse次数 , \总周期数 , \插入气泡数 , \无条件分支数 , \条件分支成功数 ;
  wire [31:0] ALU_addr, ALUResult, bit_extender_1_out, bit_extender_2_out, bit_extender_3_out,
       bit_extender_4_out, bit_extender_5_out, EX_IR, ex_mem_1_ir_2, ex_mem_1_pc_4_2, id_ex_1_imm_1_2,
       id_ex_1_imm_2_2, id_ex_1_pc_4_2, id_ex_1_r1_2, id_ex_1_r2_2, ID_IR, if_id_1_pc_4_2, IF_IR, jumpAddr,
       MEM_ALURes, MEM_IR, mem_wb_1_aluresult_2, mem_wb_1_pc_4_2, mem_wb_1_readdata_2, Memdata,
       multiplexer_1_out, multiplexer_4_out, multiplexer_5_out, multiplexer_6_out, multiplexer_7_out,
       multiplexer_8_out, multiplexer_10_out, PC_4, regifile_1_r1, regifile_1_r2, shifter_1_out, WB_IR;

  Button \u_总复位  (.out(RST));
  Button _1 (.out(IR1));
  Button _2 (.out(IR2));
  Button _3 (.out(IR3));
  // Probe on \总周期数 
  // Probe on \总周期数 
  Button \u_继续运行  (.out(Go));
  LED #(.active("true")) led_1 (.in(W1));
  LED #(.active("true")) led_2 (.in(W2));
  LED #(.active("true")) led_3 (.in(W3));
  Hex_Digit_Display hex_digit_display_1 (.value(LedData[31:28]));  // open: dp
  // Probe on IF_PC[19:0]
  // RiscV_Probe riscv_probe_1: pin names not known; wires that end beside it: IF_IR
  and and_1 (and_1_out, ~halt, CLK);  // AND_Gate
  and and_2 (and_2_out, ~halt, CLK);  // AND_Gate
  and and_3 (and_3_out, ~halt, CLK);  // AND_Gate
  Hex_Digit_Display hex_digit_display_2 (.value(LedData[23:20]));  // open: dp
  Hex_Digit_Display hex_digit_display_3 (.value(LedData[27:24]));  // open: dp
  // Probe on ID_PC[19:0]
  // RiscV_Probe riscv_probe_2: pin names not known; wires that end beside it: ID_IR
  or or_1 (or_1_out, Go, ~halt);  // OR_Gate
  Counter #(.width(16), .max('hffff), .ongoal("wrap"), .trigger("rising"), .behavior("new")) counter_1 (
    .count(CLK), .Q(\总周期数 ), .clk(and_1_out), .clr(RST));  // open: load, D, carry, preset, down
  Counter #(.width(16), .max('hffff), .ongoal("wrap"), .trigger("rising"), .behavior("new")) counter_2 (
    .count(BranchSuc), .Q(\条件分支成功数 ), .clk(and_2_out), .clr(RST));  // open: load, D, carry, preset, down
  Counter #(.width(16), .max('hffff), .ongoal("wrap"), .trigger("rising"), .behavior("new")) counter_3 (
    .count(stall), .Q(\LoadUse次数 ), .clk(and_3_out), .clr(RST));  // open: load, D, carry, preset, down
  Hex_Digit_Display hex_digit_display_4 (.value(LedData[15:12]));  // open: dp
  Hex_Digit_Display hex_digit_display_5 (.value(LedData[19:16]));  // open: dp
  and and_4 (and_4_out, ~stall, or_1_out);  // AND_Gate
  Hex_Digit_Display hex_digit_display_6 (.value(LedData[7:4]));  // open: dp
  Hex_Digit_Display hex_digit_display_7 (.value(LedData[11:8]));  // open: dp
  // Probe on EX_PC[19:0]
  // RiscV_Probe riscv_probe_3: pin names not known; wires that end beside it: EX_IR
  Multiplexer #(.select(2), .width(32), .disabled("Z"), .enable("false")) multiplexer_1 (
    .in0(PC_4), .in1(ALUResult), .in2(jumpAddr), .out(multiplexer_1_out), .sel(id_ex_1_jalr_2));  // open: in3
  Hex_Digit_Display hex_digit_display_8 (.value(LedData[3:0]));  // open: dp
  // Probe on \总周期数 
  // Probe on M_PC[19:0]
  // RiscV_Probe riscv_probe_4: pin names not known; wires that end beside it: MEM_IR
  Register #(.width(32), .trigger("rising"), .Select("low")) PC (
    .D(multiplexer_1_out), .en(and_4_out), .Q(IF_PC), .clk(CLK), .clr(RST));
  Adder #(.width(32)) adder_1 (.a(IF_PC), .b(32'h4), .out(PC_4));  // open: cin, cout
  or or_2 (or_2_out, Go, ~halt);  // OR_Gate
  // Probe on \总周期数 
  // Probe on \无条件分支数 
  // Probe on \条件分支成功数 
  // Probe on \插入气泡数 
  // Probe on \LoadUse次数 
  // RiscV_Probe riscv_probe_5: pin names not known; wires that end beside it: halt, IF_IR, riscv_probe_5_p3, riscv_probe_5_p3
  and and_5 (and_5_out, ~stall, or_2_out);  // AND_Gate
  // Probe on IF_PC[11:0]
  // Probe on WB_PC[19:0]
  // RiscV_Probe riscv_probe_6: pin names not known; wires that end beside it: WB_IR
  or or_3 (or_3_out, id_ex_1_jalr_2[0], id_ex_1_jalr_2[1]);
  ROM #(.addrWidth(10), .dataWidth(32), .Select("high")) rom_1 (.addr(IF_PC[11:2]), .data(IF_IR));
  and and_6 (and_6_out, ~halt, CLK);  // AND_Gate
  and and_7 (and_7_out, ~halt, CLK);  // AND_Gate
  // Probe on EX_PC[11:0]
  // Probe on ID_PC[11:0]
  IF_ID if_id_1 (
    .IR(IF_IR), .PC(IF_PC), .PC_4(PC_4), .branch(or_3_out), .reset(RST), .IR_2(ID_IR), .PC_2(ID_PC),
    .PC_4_2(if_id_1_pc_4_2), .en(and_5_out), .CLK(CLK));  // open: IF_PredictJump, ID_PredictJump
  Counter #(.width(16), .max('hffff), .ongoal("wrap"), .trigger("rising"), .behavior("new")) counter_4 (
    .count(Flush), .Q(\插入气泡数 ), .clk(and_6_out), .clr(RST));  // open: load, D, carry, preset, down
  Counter #(.width(16), .max('hffff), .ongoal("wrap"), .trigger("rising"), .behavior("new")) counter_5 (
    .count(\无条件跳转 ), .Q(\无条件分支数 ), .clk(and_7_out), .clr(RST));  // open: load, D, carry, preset, down
  // Probe on M_PC[11:0]
  D_Flip_Flop #(.trigger("high"), .Pre_Clr_Positions("LEGACY"), .NegatePresetClear("false"), .enable("true"), .NewFFLayout("false")) d_ff_1 (.Q(d_ff_1_q));  // open: clk, D, Qn, preset, en, reset
  // Probe on 13'hc
  \气泡处理逻辑  \u_气泡处理逻辑_1  (
    .IR(ID_IR), .BranchTaken(BranchTaken), .Ecall(Ecall), .RS1_used(RS_1), .EX_RegWrite(id_ex_1_regwrite_2),
    .EX_rd(id_ex_1_rd_2), .RS2_used(RS_2), .MEM_RegWrite(ex_mem_1_regwrite_2), .MEM_rd(ex_mem_1_rd_2),
    .stall(stall), .flush(Flush));
  Multiplexer #(.select(1), .width(5), .disabled("Z"), .enable("false")) multiplexer_2 (
    .in0(ID_IR[19:15]), .in1(5'b10001), .out(multiplexer_2_out), .sel(Ecall));
  Multiplexer #(.select(1), .width(5), .disabled("Z"), .enable("false")) multiplexer_3 (
    .in0(ID_IR[24:20]), .in1(5'b01010), .out(multiplexer_3_out), .sel(Ecall));
  // Probe on WB_PC[11:0]
  Comparator #(.width(13), .mode("twosComplement")) comparator_1 (
    .a(CNT_num), .b(13'hc), .eq(comparator_1_eq), .lt(comparator_1_lt));  // open: gt
  Clock #(.highDuration(1), .lowDuration(1)) clock_1 (.out(clock_1_out));
  \单周期硬布线控制器  \u_单周期硬布线控制器_1  (
    .Funct({ID_IR[30], ID_IR[25], ID_IR[14:12]}), .OP(ID_IR[6:2]), .ALU_OP(\单周期硬布线控制器_1_alu_op ),
    .MemToReg(\单周期硬布线控制器_1_memtoreg ), .MemWrite(\单周期硬布线控制器_1_memwrite ), .ALU_SRC(\单周期硬布线控制器_1_alu_src ),
    .RegWrite(\单周期硬布线控制器_1_regwrite ), .ecall(Ecall), .S_type(S_TPYE), .Jalr(JALR), .Beq(\单周期硬布线控制器_1_beq ),
    .JAL(JAL), .Bne(\单周期硬布线控制器_1_bne ), .in_3(ID_IR[21]), .uret(URET), .RS_1(RS_1), .RS_2(RS_2),
    .REMU(\单周期硬布线控制器_1_remu ), .BLTU(\单周期硬布线控制器_1_bltu ));  // open: LBU
  assign bit_extender_1_out = {{20{ID_IR[31]}}, ID_IR[31:20]};  // Bit_Extender bit_extender_1
  assign bit_extender_2_out = {{20{ID_IR[31]}}, {ID_IR[31:25], ID_IR[11:7]}};  // Bit_Extender bit_extender_2
  assign bit_extender_3_out = {{20{ID_IR[31]}}, {ID_IR[31], ID_IR[7], ID_IR[30:25], ID_IR[11:8]}};  // Bit_Extender bit_extender_3
  assign bit_extender_4_out = {{12{ID_IR[31]}}, {ID_IR[31], ID_IR[19:12], ID_IR[20], ID_IR[30:21]}};  // Bit_Extender bit_extender_4
  nand nand_1 (nand_1_out, d_ff_1_q, comparator_1_eq);
  Counter #(.width(13), .max('h1fff), .ongoal("stay"), .trigger("rising"), .behavior("old")) counter_6 (
    .count(comparator_1_lt), .Q(CNT_num), .clk(clock_1_out));  // open: load, D, carry, clr, preset
  Multiplexer #(.select(1), .width(32), .disabled("Z"), .enable("false")) multiplexer_4 (
    .in0(bit_extender_1_out), .in1(bit_extender_2_out), .out(multiplexer_4_out), .sel(S_TPYE));
  Multiplexer #(.select(1), .width(32), .disabled("Z"), .enable("false")) multiplexer_5 (
    .in0(bit_extender_3_out), .in1(bit_extender_4_out), .out(multiplexer_5_out), .sel(JAL));
  assign CLK = nand_1_out ? clock_1_out : 1'bz;  // Controlled_Buffer controlled_buffer_1
  or or_4 (or_4_out, Go, ~halt);  // OR_Gate
  Pull_Resistor #(.pull(1)) pull_resistor_1 (.node(CLK));
  or or_5 (BranchTaken, id_ex_1_jalr_2[0], id_ex_1_jalr_2[1]);
  Regifile regifile_1 (
    .Din(RDin), .Clk(CLK), .R1(regifile_1_r1), .R2(regifile_1_r2), .WE(RegWrite), .W_num(WB_rd),
    .R1_num(multiplexer_2_out), .R2_num(multiplexer_3_out));
  ID_EX id_ex_1 (
    .Beq(\单周期硬布线控制器_1_beq ), .Bne(\单周期硬布线控制器_1_bne ), .MemToReg(\单周期硬布线控制器_1_memtoreg ),
    .MemWrite(\单周期硬布线控制器_1_memwrite ), .AluSrcB(\单周期硬布线控制器_1_alu_src ), .RegWrite(\单周期硬布线控制器_1_regwrite ),
    .S_type(S_TPYE), .Jal(JAL), .Jalr(JALR), .Remu(\单周期硬布线控制器_1_remu ), .Aluop(\单周期硬布线控制器_1_alu_op ),
    .rd(ID_IR[11:7]), .R1(regifile_1_r1), .R2(regifile_1_r2), .IMM_1(multiplexer_4_out),
    .IMM_2(multiplexer_5_out), .PC(ID_PC), .PC_4(if_id_1_pc_4_2), .IR(ID_IR), .reset(RST), .flush(Flush),
    .Beq_2(id_ex_1_beq_2), .Bne_2(id_ex_1_bne_2), .MemToReg_2(id_ex_1_memtoreg_2),
    .MemWrite_2(id_ex_1_memwrite_2), .AlieSrcB(id_ex_1_aliesrcb), .RegWrite_2(id_ex_1_regwrite_2),
    .S_type_2(id_ex_1_s_type_2), .Jal_2(id_ex_1_jal_2), .Jalr_2(id_ex_1_jalr_2[0]),
    .Aluop_2(id_ex_1_aluop_2), .rd_2(id_ex_1_rd_2), .R1_2(id_ex_1_r1_2), .R2_2(id_ex_1_r2_2),
    .IMM_1_2(id_ex_1_imm_1_2), .IMM_2_2(id_ex_1_imm_2_2), .PC_2(EX_PC), .PC_4_2(id_ex_1_pc_4_2),
    .IR_2(EX_IR), .RS1_Forward_2(id_ex_1_rs1_forward_2), .RS2_Forward_2(id_ex_1_rs2_forward_2), .clk(CLK),
    .en(or_4_out), .BLTU(\单周期硬布线控制器_1_bltu ), .BLTU_2(id_ex_1_bltu_2), .Uret(URET), .Uret_2(id_ex_1_uret_2),
    .Ecall(Ecall), .EX_ecall(EX_ecall));  // open: RS1_Forward, RS2_Forward, ID_PredictJump, Remu_2, EX_PredictJump, LBU, LBU_2
  or or_6 (\无条件跳转 , id_ex_1_jal_2, id_ex_1_jalr_2[0]);
  Multiplexer #(.select(2), .width(32), .disabled("Z"), .enable("false")) multiplexer_6 (
    .in0(id_ex_1_r1_2), .in1(RDin), .in2(MEM_ALURes), .out(multiplexer_6_out), .sel(id_ex_1_rs1_forward_2));  // open: in3
  or or_7 (id_ex_1_jalr_2[1], BranchSuc, id_ex_1_jal_2);
  and and_8 (and_8_out, id_ex_1_bne_2, ~Equal);  // AND_Gate
  Multiplexer #(.select(2), .width(32), .disabled("Z"), .enable("false")) multiplexer_7 (
    .in0(id_ex_1_r2_2), .in1(RDin), .in2(MEM_ALURes), .out(multiplexer_7_out), .sel(id_ex_1_rs2_forward_2));  // open: in3
  or or_8 (BranchSuc, and_8_out, and_9_out, and_10_out);
  and and_9 (and_9_out, Equal, id_ex_1_beq_2);
  Multiplexer #(.select(1), .width(32), .disabled("Z"), .enable("false")) multiplexer_8 (
    .in0(multiplexer_7_out), .in1(id_ex_1_imm_1_2), .out(multiplexer_8_out), .sel(id_ex_1_aliesrcb));
  and and_10 (and_10_out, ~Equal, id_ex_1_bltu_2);  // AND_Gate
  ALU alu_1 (
    .X(multiplexer_6_out), .Y(multiplexer_8_out), .AluOP(id_ex_1_aluop_2), .Equal(Equal), .Result(ALU_addr),
    .out_4(be), .out_6(Less));  // open: Result_2
  Shifter #(.width(32), .shift("ll")) shifter_1 (.in(id_ex_1_imm_2_2), .\dist (5'b00001), .out(shifter_1_out));
  Comparator #(.width(32), .mode("twosComplement")) comparator_2 (
    .a(multiplexer_6_out), .b(32'ha), .eq(comparator_2_eq));  // open: gt, lt
  not not_1 (not_1_out, comparator_2_eq);
  Adder #(.width(32)) adder_2 (.a(shifter_1_out), .b(EX_PC), .out(jumpAddr));  // open: cin, cout
  and and_11 (EX_halt, comparator_2_eq, EX_ecall);
  Register #(.width(32), .trigger("rising"), .Select("low")) register_1 (
    .D(multiplexer_7_out), .en(and_12_out), .Q(LedData), .clk(CLK), .clr(RST));
  and and_12 (and_12_out, not_1_out, EX_ecall);
  or or_9 (or_9_out, Go, ~halt);  // OR_Gate
  EX_MEM ex_mem_1 (
    .Jal(id_ex_1_jal_2), .Jalr(id_ex_1_jalr_2[0]), .MemToReg(id_ex_1_memtoreg_2),
    .MemWrite(id_ex_1_memwrite_2), .RegWrite(id_ex_1_regwrite_2), .halt(EX_halt), .rd(id_ex_1_rd_2),
    .Result(ALU_addr), .WriteData(multiplexer_7_out), .IR(EX_IR), .PC(EX_PC), .PC_4(id_ex_1_pc_4_2),
    .reset(RST), .clk(CLK), .Jal_2(ex_mem_1_jal_2), .Jalr_2(ex_mem_1_jalr_2), .MemToReg_2(MemToReg),
    .MemWrite_2(MemWrite), .RegWrite_2(ex_mem_1_regwrite_2), .halt_2(ex_mem_1_halt_2), .rd_2(ex_mem_1_rd_2),
    .Result_2(MEM_ALURes), .WriteData_2(MDin), .IR_2(ex_mem_1_ir_2), .PC_2(M_PC), .PC_4_2(ex_mem_1_pc_4_2),
    .en(or_9_out));  // open: LBU, LBU_2
  Multiplexer #(.select(2), .width(8), .disabled("Z"), .enable("false")) multiplexer_9 (
    .in0(Memdata[7:0]), .in1(Memdata[15:8]), .in2(Memdata[23:16]), .in3(Memdata[31:24]),
    .out(multiplexer_9_out), .sel(MEM_ALURes[1:0]));
  RAM #(.addrWidth(10), .dataWidth(32), .bus("separate"), .Select("high")) ram_1 (
    .addr(MEM_ALURes[11:2]), .din(MDin), .data(Memdata), .str(1'b1), .sel(CLK), .ld(1'b1), .clr(RST));  // open: clk
  assign bit_extender_5_out = {{24{1'b0}}, multiplexer_9_out};  // Bit_Extender bit_extender_5
  Multiplexer #(.select(1), .width(32), .disabled("Z"), .enable("false")) multiplexer_10 (
    .in0(Memdata), .in1(bit_extender_5_out), .out(multiplexer_10_out));  // open: sel
  or or_10 (or_10_out, Go, ~halt);  // OR_Gate
  or or_11 (mem_wb_1_memtoreg_2[1], mem_wb_1_jal_2, mem_wb_1_jalr_2);
  MEM_WB mem_wb_1 (
    .reset(RST), .Jal(ex_mem_1_jal_2), .Jalr(ex_mem_1_jalr_2), .MemToReg(MemToReg),
    .RegWrite(ex_mem_1_regwrite_2), .halt(ex_mem_1_halt_2), .rd(ex_mem_1_rd_2), .ALUResult(MEM_ALURes),
    .ReadData(multiplexer_10_out), .IR(ex_mem_1_ir_2), .PC(M_PC), .PC_4(ex_mem_1_pc_4_2), .clk(CLK),
    .Jal_2(mem_wb_1_jal_2), .Jalr_2(mem_wb_1_jalr_2), .MemToReg_2(mem_wb_1_memtoreg_2[0]),
    .RegWrite_2(RegWrite), .halt_2(mem_wb_1_halt_2), .out_20(WB_rd), .ALUResult_2(mem_wb_1_aluresult_2),
    .ReadData_2(mem_wb_1_readdata_2), .IR_2(WB_IR), .PC_2(WB_PC), .Pc_4_2(mem_wb_1_pc_4_2), .en(or_10_out));
  Multiplexer #(.select(2), .width(32), .disabled("Z"), .enable("false")) multiplexer_11 (
    .in0(mem_wb_1_aluresult_2), .in1(mem_wb_1_readdata_2), .in2(mem_wb_1_pc_4_2), .out(RDin),
    .sel(mem_wb_1_memtoreg_2));  // open: in3
  D_Flip_Flop #(.trigger("rising"), .Pre_Clr_Positions("ABOVE_BELOW"), .NegatePresetClear("false"), .enable("true"), .NewFFLayout("true")) d_ff_2 (
    .clk(mem_wb_1_halt_2), .D(1'b1), .Q(halt), .en(1'b1), .reset(Go));  // open: Qn, preset

  // Other names for the same wires on the sheet: MEM_PC[31:0] = M_PC; WB_RegWrite = RegWrite

  // Notes on the sheet:
  //   中断源
  //   时空图监测，可删除
  //   中断等待指示
  //   数码管输出
  //   指令存储器
  //   指令探针
  //   contents of rom_1 (hex, n*v repeats v):
  //   100493 100006f 100493 200913 300993 100006f 100493 200913 300993 100006f 100493 200913 300993
  //   100006f 100493 200913 300993 29c000ef 100413 100493 1f49493 900533 2200893 73 24d493 48463 fedff06f
  //   900533 2200893 73 100493 249493 900533 2200893 73 48463 fedff06f 100493 1f49493 900533 2200893 73
  //   4034d493 900533 2200893 73 4044d493 900533 2200893 73 4044d493 900533 2200893 73 4044d493 900533
  //   2200893 73 4044d493 900533 2200893 73 4044d493 900533 2200893 73 4044d493 900533 2200893 73 4044d493
  //   900533 2200893 73 100413 1f41993 41f9d993 433 c00913 300b13 140413 f47413 800293 100313 499993
  //   89e9b3 1300533 2200893 73 406282b3 fe0294e3 140413 f00f93 1f47433 1c41413 800293 100313 49d993
  //   89e9b3 1300533 2200893 73 406282b3 fe0294e3 1c45413 406b0b33 b0463 f95ff06f 2b3 fff2c293 829293
  //   ff2e293 500533 2200893 73 fff00413 493 84a023 140413 448493 84a023 140413 448493 84a023 140413
  //   448493 84a023 140413 448493 84a023 140413 448493 84a023 140413 448493 84a023 140413 448493 84a023
  //   140413 448493 84a023 140413 448493 84a023 140413 448493 84a023 140413 448493 84a023 140413 448493
  //   84a023 140413 448493 84a023 140413 448493 84a023 140413 448493 84a023 140413 448493 140413 433
  //   3c00493 42983 4aa03 149a2b3 28663 134a023 1442023 ffc48493 fe9412e3 800533 2200893 73 440413 3c00493
  //   fc9416e3 a00893 73 413 140413 800533 2200893 73 240413 800533 2200893 73 340413 800533 2200893 73
  //   440413 800533 2200893 73 540413 800533 2200893 73 640413 800533 2200893 73 740413 800533 2200893 73
  //   840413 800533 2200893 2200893 73 8067
  //   控制位
  //   流水调试日志用
  //   暂停节拍，不能为0
  //   用这个时钟源需要去掉电路中的其他时钟源
  //   JAL
  //   JALR
  //   URET
  //   指令字
  //   戳工具置1进入计数暂停模式，ctrl+k时钟自动运行到对应节拍暂停
  //   ctrl+k关闭时钟连续运行，将控制位置零，进入单步调试模式调试
  //   Beq
  //   Bne
  //   MemWrite
  //   AluOP
  //   AluSrcB
  //   可计数暂停的时钟源
  //   为方便自动评测，需要输出流水线各段保存的PC值，注意是PC不是PC+4，另外ID段寄存器写入信息，Mem段内存写入信息也要输出
  //   数据存储器
endmodule
module \重定向流水线  (
  output RegWrite,
  output MemWrite,
  output [31:0] IF_PC,
  output [31:0] ID_PC,
  output [31:0] EX_PC,
  output [31:0] M_PC,
  output [31:0] WB_PC,
  output [31:0] RDin,
  output [31:0] MDin,
  output [31:0] LedData
);

  wire alu_1_out_6, and_1_out, and_2_out, and_3_out, and_4_out, and_5_out, and_6_out, and_7_out, and_8_out,
       and_9_out, and_10_out, and_11_out, and_12_out, be, BranchSuc, BranchTaken, CLK, clock_1_out,
       comparator_1_eq, comparator_1_lt, comparator_2_eq, d_ff_1_q, Ecall, Equal, EX_ecall, EX_halt,
       ex_mem_1_halt_2, ex_mem_1_jal_2, ex_mem_1_jalr_2, ex_mem_1_regwrite_2, Flush, Go, halt,
       id_ex_1_aliesrcb, id_ex_1_beq_2, id_ex_1_bltu_2, id_ex_1_bne_2, id_ex_1_jal_2, id_ex_1_lbu_2,
       id_ex_1_memtoreg_2, id_ex_1_memwrite_2, id_ex_1_regwrite_2, IR1, IR2, IR3, JAL, JALR, LBU,
       mem_wb_1_halt_2, mem_wb_1_jal_2, mem_wb_1_jalr_2, MemToReg, nand_1_out, not_1_out, not_2_out,
       not_3_out, not_4_out, not_5_out, or_1_out, or_2_out, or_3_out, or_4_out, or_9_out, or_10_out, remu,
       riscv_probe_5_p2, RS_1, RS_2, RST, S_TPYE, stall, URET, W1, W2, W3, \单周期硬布线控制器_1_alu_src ,
       \单周期硬布线控制器_1_beq , \单周期硬布线控制器_1_bltu , \单周期硬布线控制器_1_bne , \单周期硬布线控制器_1_lbu , \单周期硬布线控制器_1_memtoreg ,
       \单周期硬布线控制器_1_memwrite , \单周期硬布线控制器_1_regwrite , \单周期硬布线控制器_1_remu , \无条件跳转 ;
  wire [1:0] id_ex_1_jalr_2, id_ex_1_rs1_forward_2, id_ex_1_rs2_forward_2, mem_wb_1_memtoreg_2,
       \重定向处理逻辑_1_rs1_forward , \重定向处理逻辑_1_rs2_forward ;
  wire [3:0] id_ex_1_aluop_2, \单周期硬布线控制器_1_alu_op ;
  wire [4:0] ex_mem_1_rd_2, id_ex_1_rd_2, multiplexer_2_out, multiplexer_3_out, WB_rd;
  wire [7:0] multiplexer_10_out;
  wire [12:0] CNT_num;
  wire [15:0] \LoadUse次数 , \总周期数 , \插入气泡数 , \无条件分支数 , \条件分支成功数 ;
  wire [31:0] alu_1_result_2, ALU_addr, bit_extender_1_out, bit_extender_2_out, bit_extender_3_out,
       bit_extender_4_out, bit_extender_5_out, EX_IR, ex_mem_1_pc_4_2, id_ex_1_imm_1_2, id_ex_1_imm_2_2,
       id_ex_1_pc_4_2, id_ex_1_r1_2, id_ex_1_r2_2, ID_IR, if_id_1_pc_4_2, IF_IR, jumpAddr, MEM_ALURes,
       MEM_IR, mem_wb_1_aluresult_2, mem_wb_1_pc_4_2, mem_wb_1_readdata_2, Memdata, multiplexer_1_out,
       multiplexer_4_out, multiplexer_5_out, multiplexer_6_out, multiplexer_7_out, multiplexer_8_out,
       multiplexer_9_out, multiplexer_11_out, PC_4, regifile_1_r1, regifile_1_r2, shifter_1_out, WB_IR;

  Button \u_总复位  (.out(RST));
  Button _1 (.out(IR1));
  Button _2 (.out(IR2));
  Button _3 (.out(IR3));
  // Probe on \总周期数 
  // Probe on \总周期数 
  LED #(.active("true")) led_1 (.in(W1));
  LED #(.active("true")) led_2 (.in(W2));
  LED #(.active("true")) led_3 (.in(W3));
  Hex_Digit_Display hex_digit_display_1 (.value(LedData[31:28]));  // open: dp
  // Probe on IF_PC[19:0]
  // RiscV_Probe riscv_probe_1: pin names not known; wires that end beside it: IF_IR
  // Probe on id_ex_1_jalr_2
  Hex_Digit_Display hex_digit_display_2 (.value(LedData[27:24]));  // open: dp
  Hex_Digit_Display hex_digit_display_3 (.value(LedData[23:20]));  // open: dp
  // Probe on ID_PC[19:0]
  // RiscV_Probe riscv_probe_2: pin names not known; wires that end beside it: ID_IR
  and and_1 (and_1_out, ~stall, ~halt);  // AND_Gate
  or or_1 (or_1_out, and_1_out, Go);
  Hex_Digit_Display hex_digit_display_4 (.value(LedData[19:16]));  // open: dp
  Hex_Digit_Display hex_digit_display_5 (.value(LedData[15:12]));  // open: dp
  Multiplexer #(.select(2), .width(32), .disabled("Z"), .enable("false")) multiplexer_1 (
    .in0(PC_4), .in1(ALU_addr), .in2(jumpAddr), .out(multiplexer_1_out), .sel(id_ex_1_jalr_2));  // open: in3
  Hex_Digit_Display hex_digit_display_6 (.value(LedData[11:8]));  // open: dp
  Hex_Digit_Display hex_digit_display_7 (.value(LedData[7:4]));  // open: dp
  // Probe on EX_PC[19:0]
  // RiscV_Probe riscv_probe_3: pin names not known; wires that end beside it: EX_IR
  not not_1 (not_1_out, CLK);
  Hex_Digit_Display hex_digit_display_8 (.value(LedData[3:0]));  // open: dp
  // Probe on \重定向处理逻辑_1_rs2_forward 
  // Probe on \重定向处理逻辑_1_rs1_forward 
  Register #(.width(32), .trigger("falling"), .Select("low")) PC (
    .D(multiplexer_1_out), .en(or_1_out), .Q(IF_PC), .clk(not_1_out), .clr(RST));
  Counter #(.width(16), .max('hffff), .ongoal("wrap"), .trigger("rising"), .behavior("new")) counter_1 (
    .count(CLK), .Q(\总周期数 ), .clk(and_2_out), .clr(RST));  // open: load, D, carry, preset, down
  and and_2 (and_2_out, ~halt, CLK);  // AND_Gate
  Counter #(.width(16), .max('hffff), .ongoal("wrap"), .trigger("rising"), .behavior("new")) counter_2 (
    .count(BranchSuc), .Q(\条件分支成功数 ), .clk(and_3_out), .clr(RST));  // open: load, D, carry, preset, down
  and and_3 (and_3_out, ~halt, CLK);  // AND_Gate
  Counter #(.width(16), .max('hffff), .ongoal("wrap"), .trigger("rising"), .behavior("new")) counter_3 (
    .count(stall), .Q(\LoadUse次数 ), .clk(and_4_out), .clr(RST));  // open: load, D, carry, preset, down
  and and_4 (and_4_out, ~halt, CLK);  // AND_Gate
  // Probe on \总周期数 
  // Probe on M_PC[19:0]
  // RiscV_Probe riscv_probe_4: pin names not known; wires that end beside it: MEM_IR
  \重定向处理逻辑  \u_重定向处理逻辑_1  (
    .RS1_used(RS_1), .BranchTaken(BranchTaken), .EX_rd(id_ex_1_rd_2), .IR(ID_IR), .RS2_used(RS_2),
    .Ecall(Ecall), .MEM_rd(ex_mem_1_rd_2), .EX_RegWrite(id_ex_1_regwrite_2),
    .EX_MemToReg(id_ex_1_memtoreg_2), .MEM_RegWrite(ex_mem_1_regwrite_2), .Stall(stall), .Flush(Flush),
    .RS1_Forward(\重定向处理逻辑_1_rs1_forward ), .RS2_Forward(\重定向处理逻辑_1_rs2_forward ));
  Button \u_继续运行  (.out(Go));
  // RiscV_Probe riscv_probe_5: pin names not known; wires that end beside it: IF_IR, riscv_probe_5_p2, riscv_probe_5_p2
  Adder #(.width(32)) adder_1 (.a(IF_PC), .b(32'h4), .out(PC_4));  // open: cin, cout
  or or_2 (or_2_out, Go, ~halt);  // OR_Gate
  // Probe on \总周期数 
  // Probe on \无条件分支数 
  // Probe on \条件分支成功数 
  // Probe on \插入气泡数 
  // Probe on \LoadUse次数 
  or or_3 (or_3_out, id_ex_1_jalr_2[0], id_ex_1_jalr_2[1]);
  ROM #(.addrWidth(10), .dataWidth(32), .Select("high")) rom_1 (.addr(IF_PC[11:2]), .data(IF_IR));
  and and_5 (and_5_out, ~stall, or_2_out);  // AND_Gate
  // Probe on IF_PC[11:0]
  // Probe on WB_PC[19:0]
  // RiscV_Probe riscv_probe_6: pin names not known; wires that end beside it: WB_IR
  IF_ID if_id_1 (
    .IR(IF_IR), .PC(IF_PC), .PC_4(PC_4), .branch(or_3_out), .reset(RST), .IR_2(ID_IR), .PC_2(ID_PC),
    .PC_4_2(if_id_1_pc_4_2), .en(and_5_out), .CLK(CLK));  // open: IF_PredictJump, ID_PredictJump
  // Probe on ID_PC[11:0]
  // Probe on EX_PC[11:0]
  Multiplexer #(.select(1), .width(5), .disabled("Z"), .enable("false")) multiplexer_2 (
    .in0(ID_IR[19:15]), .in1(5'b10001), .out(multiplexer_2_out), .sel(Ecall));
  Multiplexer #(.select(1), .width(5), .disabled("Z"), .enable("false")) multiplexer_3 (
    .in0(ID_IR[24:20]), .in1(5'b01010), .out(multiplexer_3_out), .sel(Ecall));
  // Probe on M_PC[11:0]
  D_Flip_Flop #(.trigger("high"), .Pre_Clr_Positions("LEGACY"), .NegatePresetClear("false"), .enable("true"), .NewFFLayout("false")) d_ff_1 (.Q(d_ff_1_q));  // open: clk, D, Qn, preset, en, reset
  // Probe on 13'hc
  \单周期硬布线控制器  \u_单周期硬布线控制器_1  (
    .Funct({ID_IR[30], ID_IR[25], ID_IR[14:12]}), .OP(ID_IR[6:2]), .ALU_OP(\单周期硬布线控制器_1_alu_op ),
    .MemToReg(\单周期硬布线控制器_1_memtoreg ), .MemWrite(\单周期硬布线控制器_1_memwrite ), .ALU_SRC(\单周期硬布线控制器_1_alu_src ),
    .RegWrite(\单周期硬布线控制器_1_regwrite ), .ecall(Ecall), .S_type(S_TPYE), .Jalr(JALR), .Beq(\单周期硬布线控制器_1_beq ),
    .JAL(JAL), .Bne(\单周期硬布线控制器_1_bne ), .in_3(ID_IR[21]), .uret(URET), .RS_1(RS_1), .RS_2(RS_2),
    .REMU(\单周期硬布线控制器_1_remu ), .BLTU(\单周期硬布线控制器_1_bltu ), .LBU(\单周期硬布线控制器_1_lbu ));
  assign bit_extender_1_out = {{20{ID_IR[31]}}, ID_IR[31:20]};  // Bit_Extender bit_extender_1
  assign bit_extender_2_out = {{20{ID_IR[31]}}, {ID_IR[31:25], ID_IR[11:7]}};  // Bit_Extender bit_extender_2
  assign bit_extender_3_out = {{20{ID_IR[31]}}, {ID_IR[31], ID_IR[7], ID_IR[30:25], ID_IR[11:8]}};  // Bit_Extender bit_extender_3
  assign bit_extender_4_out = {{12{ID_IR[31]}}, {ID_IR[31], ID_IR[19:12], ID_IR[20], ID_IR[30:21]}};  // Bit_Extender bit_extender_4
  // Probe on WB_PC[11:0]
  Comparator #(.width(13), .mode("twosComplement")) comparator_1 (
    .a(CNT_num), .b(13'hc), .eq(comparator_1_eq), .lt(comparator_1_lt));  // open: gt
  Clock #(.highDuration(1), .lowDuration(1)) clock_1 (.out(clock_1_out));
  not not_2 (not_2_out, CLK);
  Multiplexer #(.select(1), .width(32), .disabled("Z"), .enable("false")) multiplexer_4 (
    .in0(bit_extender_1_out), .in1(bit_extender_2_out), .out(multiplexer_4_out), .sel(S_TPYE));
  Multiplexer #(.select(1), .width(32), .disabled("Z"), .enable("false")) multiplexer_5 (
    .in0(bit_extender_3_out), .in1(bit_extender_4_out), .out(multiplexer_5_out), .sel(JAL));
  nand nand_1 (nand_1_out, d_ff_1_q, comparator_1_eq);
  Counter #(.width(13), .max('h1fff), .ongoal("stay"), .trigger("rising"), .behavior("old")) counter_4 (
    .count(comparator_1_lt), .Q(CNT_num), .clk(clock_1_out));  // open: load, D, carry, clr, preset
  or or_4 (or_4_out, Go, ~halt);  // OR_Gate
  Counter #(.width(16), .max('hffff), .ongoal("wrap"), .trigger("rising"), .behavior("new")) counter_5 (
    .count(Flush), .Q(\插入气泡数 ), .clk(and_6_out), .clr(RST));  // open: load, D, carry, preset, down
  and and_6 (and_6_out, ~halt, CLK);  // AND_Gate
  Counter #(.width(16), .max('hffff), .ongoal("wrap"), .trigger("rising"), .behavior("new")) counter_6 (
    .count(\无条件跳转 ), .Q(\无条件分支数 ), .clk(and_7_out), .clr(RST));  // open: load, D, carry, preset, down
  and and_7 (and_7_out, ~halt, CLK);  // AND_Gate
  assign CLK = nand_1_out ? clock_1_out : 1'bz;  // Controlled_Buffer controlled_buffer_1
  Regifile regifile_1 (
    .Din(RDin), .Clk(not_2_out), .R1(regifile_1_r1), .R2(regifile_1_r2), .WE(RegWrite), .W_num(WB_rd),
    .R1_num(multiplexer_2_out), .R2_num(multiplexer_3_out));
  // Probe on multiplexer_7_out
  Pull_Resistor #(.pull(1)) pull_resistor_1 (.node(CLK));
  or or_5 (BranchTaken, id_ex_1_jalr_2[0], id_ex_1_jalr_2[1]);
  ID_EX id_ex_1 (
    .Beq(\单周期硬布线控制器_1_beq ), .Bne(\单周期硬布线控制器_1_bne ), .MemToReg(\单周期硬布线控制器_1_memtoreg ),
    .MemWrite(\单周期硬布线控制器_1_memwrite ), .AluSrcB(\单周期硬布线控制器_1_alu_src ), .RegWrite(\单周期硬布线控制器_1_regwrite ),
    .S_type(S_TPYE), .Jal(JAL), .Jalr(JALR), .Remu(\单周期硬布线控制器_1_remu ), .Aluop(\单周期硬布线控制器_1_alu_op ),
    .rd(ID_IR[11:7]), .R1(regifile_1_r1), .R2(regifile_1_r2), .IMM_1(multiplexer_4_out),
    .IMM_2(multiplexer_5_out), .PC(ID_PC), .PC_4(if_id_1_pc_4_2), .IR(ID_IR),
    .RS1_Forward(\重定向处理逻辑_1_rs1_forward ), .RS2_Forward(\重定向处理逻辑_1_rs2_forward ), .reset(RST), .flush(Flush),
    .Beq_2(id_ex_1_beq_2), .Bne_2(id_ex_1_bne_2), .MemToReg_2(id_ex_1_memtoreg_2),
    .MemWrite_2(id_ex_1_memwrite_2), .AlieSrcB(id_ex_1_aliesrcb), .RegWrite_2(id_ex_1_regwrite_2),
    .Jal_2(id_ex_1_jal_2), .Jalr_2(id_ex_1_jalr_2[0]), .Remu_2(remu), .Aluop_2(id_ex_1_aluop_2),
    .rd_2(id_ex_1_rd_2), .R1_2(id_ex_1_r1_2), .R2_2(id_ex_1_r2_2), .IMM_1_2(id_ex_1_imm_1_2),
    .IMM_2_2(id_ex_1_imm_2_2), .PC_2(EX_PC), .PC_4_2(id_ex_1_pc_4_2), .IR_2(EX_IR),
    .RS1_Forward_2(id_ex_1_rs1_forward_2), .RS2_Forward_2(id_ex_1_rs2_forward_2), .clk(CLK), .en(or_4_out),
    .BLTU(\单周期硬布线控制器_1_bltu ), .BLTU_2(id_ex_1_bltu_2), .Uret(URET), .Ecall(Ecall), .EX_ecall(EX_ecall),
    .LBU(\单周期硬布线控制器_1_lbu ), .LBU_2(id_ex_1_lbu_2));  // open: ID_PredictJump, S_type_2, EX_PredictJump, Uret_2
  // Probe on id_ex_1_rs1_forward_2
  or or_6 (\无条件跳转 , id_ex_1_jal_2, id_ex_1_jalr_2[0]);
  Multiplexer #(.select(2), .width(32), .disabled("Z"), .enable("false")) multiplexer_6 (
    .in0(id_ex_1_r1_2), .in1(RDin), .in2(MEM_ALURes), .out(multiplexer_6_out), .sel(id_ex_1_rs1_forward_2));  // open: in3
  // Probe on id_ex_1_rs2_forward_2
  or or_7 (id_ex_1_jalr_2[1], BranchSuc, id_ex_1_jal_2);
  and and_8 (and_8_out, id_ex_1_bne_2, ~Equal);  // AND_Gate
  Multiplexer #(.select(2), .width(32), .disabled("Z"), .enable("false")) multiplexer_7 (
    .in0(id_ex_1_r2_2), .in1(RDin), .in2(MEM_ALURes), .out(multiplexer_7_out), .sel(id_ex_1_rs2_forward_2));  // open: in3
  or or_8 (BranchSuc, and_8_out, and_9_out, and_10_out);
  and and_9 (and_9_out, Equal, id_ex_1_beq_2);
  // Probe on multiplexer_6_out
  // Probe on multiplexer_8_out
  Multiplexer #(.select(1), .width(32), .disabled("Z"), .enable("false")) multiplexer_8 (
    .in0(multiplexer_7_out), .in1(id_ex_1_imm_1_2), .out(multiplexer_8_out), .sel(id_ex_1_aliesrcb));
  and and_10 (and_10_out, alu_1_out_6, id_ex_1_bltu_2);
  ALU alu_1 (
    .X(multiplexer_6_out), .Y(multiplexer_8_out), .AluOP(id_ex_1_aluop_2), .Equal(Equal), .Result(ALU_addr),
    .Result_2(alu_1_result_2), .out_4(be), .out_6(alu_1_out_6));
  Shifter #(.width(32), .shift("ll")) shifter_1 (.in(id_ex_1_imm_2_2), .\dist (5'b00001), .out(shifter_1_out));
  Comparator #(.width(32), .mode("twosComplement")) comparator_2 (
    .a(multiplexer_6_out), .b(32'h22), .eq(comparator_2_eq));  // open: gt, lt
  not not_3 (not_3_out, comparator_2_eq);
  Multiplexer #(.select(1), .width(32), .disabled("Z"), .enable("false")) multiplexer_9 (
    .in0(ALU_addr), .in1(alu_1_result_2), .out(multiplexer_9_out), .sel(remu));
  Adder #(.width(32)) adder_2 (.a(shifter_1_out), .b(EX_PC), .out(jumpAddr));  // open: cin, cout
  // Probe on multiplexer_6_out
  and and_11 (and_11_out, not_3_out, EX_ecall);
  Register #(.width(32), .trigger("rising"), .Select("low")) register_1 (
    .D(multiplexer_7_out), .en(and_12_out), .Q(LedData), .clk(CLK), .clr(RST));
  and and_12 (and_12_out, comparator_2_eq, EX_ecall);
  // Probe on multiplexer_9_out
  or or_9 (or_9_out, Go, ~halt);  // OR_Gate
  Register #(.width(1), .trigger("rising"), .Select("low")) register_2 (
    .D(and_11_out), .Q(EX_halt), .clk(not_4_out), .clr(Go));  // open: en
  not not_4 (not_4_out, CLK);
  EX_MEM ex_mem_1 (
    .Jal(id_ex_1_jal_2), .Jalr(id_ex_1_jalr_2[0]), .MemToReg(id_ex_1_memtoreg_2),
    .MemWrite(id_ex_1_memwrite_2), .RegWrite(id_ex_1_regwrite_2), .halt(EX_halt), .rd(id_ex_1_rd_2),
    .Result(multiplexer_9_out), .WriteData(multiplexer_7_out), .IR(EX_IR), .PC(EX_PC), .PC_4(id_ex_1_pc_4_2),
    .reset(RST), .clk(CLK), .Jal_2(ex_mem_1_jal_2), .Jalr_2(ex_mem_1_jalr_2), .MemToReg_2(MemToReg),
    .MemWrite_2(MemWrite), .RegWrite_2(ex_mem_1_regwrite_2), .halt_2(ex_mem_1_halt_2), .rd_2(ex_mem_1_rd_2),
    .Result_2(MEM_ALURes), .WriteData_2(MDin), .IR_2(MEM_IR), .PC_2(M_PC), .PC_4_2(ex_mem_1_pc_4_2),
    .en(or_9_out), .LBU(id_ex_1_lbu_2), .LBU_2(LBU));
  // Probe on MEM_ALURes
  RAM #(.addrWidth(10), .dataWidth(32), .bus("separate"), .Select("high")) ram_1 (
    .addr(MEM_ALURes[11:2]), .din(MDin), .data(Memdata), .str(MemWrite), .sel(1'b1), .clk(CLK), .ld(1'b1),
    .clr(RST));
  Multiplexer #(.select(2), .width(8), .disabled("Z"), .enable("false")) multiplexer_10 (
    .in0(Memdata[7:0]), .in1(Memdata[15:8]), .in2(Memdata[23:16]), .in3(Memdata[31:24]),
    .out(multiplexer_10_out), .sel(MEM_ALURes[1:0]));
  assign bit_extender_5_out = {{24{1'b0}}, multiplexer_10_out};  // Bit_Extender bit_extender_5
  Multiplexer #(.select(1), .width(32), .disabled("Z"), .enable("false")) multiplexer_11 (
    .in0(Memdata), .in1(bit_extender_5_out), .out(multiplexer_11_out), .sel(LBU));
  or or_10 (or_10_out, Go, ~halt);  // OR_Gate
  or or_11 (mem_wb_1_memtoreg_2[1], mem_wb_1_jal_2, mem_wb_1_jalr_2);
  MEM_WB mem_wb_1 (
    .reset(RST), .Jal(ex_mem_1_jal_2), .Jalr(ex_mem_1_jalr_2), .MemToReg(MemToReg),
    .RegWrite(ex_mem_1_regwrite_2), .halt(ex_mem_1_halt_2), .rd(ex_mem_1_rd_2), .ALUResult(MEM_ALURes),
    .ReadData(multiplexer_11_out), .IR(MEM_IR), .PC(M_PC), .PC_4(ex_mem_1_pc_4_2), .clk(CLK),
    .Jal_2(mem_wb_1_jal_2), .Jalr_2(mem_wb_1_jalr_2), .MemToReg_2(mem_wb_1_memtoreg_2[0]),
    .RegWrite_2(RegWrite), .halt_2(mem_wb_1_halt_2), .out_20(WB_rd), .ALUResult_2(mem_wb_1_aluresult_2),
    .ReadData_2(mem_wb_1_readdata_2), .IR_2(WB_IR), .PC_2(WB_PC), .Pc_4_2(mem_wb_1_pc_4_2), .en(or_10_out));
  Multiplexer #(.select(2), .width(32), .disabled("Z"), .enable("false")) multiplexer_12 (
    .in0(mem_wb_1_aluresult_2), .in1(mem_wb_1_readdata_2), .in2(mem_wb_1_pc_4_2), .out(RDin),
    .sel(mem_wb_1_memtoreg_2));  // open: in3
  Register #(.width(1), .trigger("rising"), .Select("low")) register_3 (
    .D(mem_wb_1_halt_2), .Q(halt), .clk(not_5_out), .clr(Go));  // open: en
  not not_5 (not_5_out, CLK);
  // Probe on RDin

  // Other names for the same wires on the sheet: MEM_PC[31:0] = M_PC; WB_RegWrite = RegWrite

  // Notes on the sheet:
  //   中断源
  //   时空图监测，可删除
  //   中断等待指示
  //   MUL REMU LBU BLTU
  //   87540110
  //   数码管输出
  //   0x00001111 0x00002222 0x00004444 0x00008888  ……  0x40000000 0x80000000 0x00000000
  //   0x00000081 0x00000082 0x00000083  …… 0x0000009e 0x0000009f 0x000000a0
  //   指令探针
  //   指令存储器
  //   contents of rom_1 (hex, n*v repeats v):
  //   100493 100006f 100493 200913 300993 100006f 100493 200913 300993 100006f 100493 200913 300993
  //   100006f 100493 200913 300993 3c0000ef 100413 100493 1f49493 900533 2200893 73 24d493 48463 fedff06f
  //   900533 2200893 73 100493 249493 900533 2200893 73 48463 fedff06f 100493 1f49493 900533 2200893 73
  //   4034d493 900533 2200893 73 4044d493 900533 2200893 73 4044d493 900533 2200893 73 4044d493 900533
  //   2200893 73 4044d493 900533 2200893 73 4044d493 900533 2200893 73 4044d493 900533 2200893 73 4044d493
  //   900533 2200893 73 100413 1f41993 41f9d993 433 c00913 300b13 140413 f47413 800293 100313 499993
  //   89e9b3 1300533 2200893 73 406282b3 fe0294e3 140413 f00f93 1f47433 1c41413 800293 100313 49d993
  //   89e9b3 1300533 2200893 73 406282b3 fe0294e3 1c45413 406b0b33 b0463 f95ff06f 2b3 fff2c293 829293
  //   ff2e293 500533 2200893 73 fff00413 493 84a023 140413 448493 84a023 140413 448493 84a023 140413
  //   448493 84a023 140413 448493 84a023 140413 448493 84a023 140413 448493 84a023 140413 448493 84a023
  //   140413 448493 84a023 140413 448493 84a023 140413 448493 84a023 140413 448493 84a023 140413 448493
  //   84a023 140413 448493 84a023 140413 448493 84a023 140413 448493 84a023 140413 448493 140413 433
  //   3c00493 42983 4aa03 149a2b3 28663 134a023 1442023 ffc48493 fe9412e3 800533 2200893 73 440413 3c00493
  //   fc9416e3 a00893 73 200293 1100493 849493 1148493 900533 2200893 73 2000e13 25484b3 900533 2200893 73
  //   fffe0e13 fe0e16e3 a00893 73 8800493 849493 4848493 8700913 891913 5490913 2997933 1091913 11096913
  //   1200533 2200893 73 a00893 73 313 1000e13 8400493 849493 8348493 400913 891913 490913 849493 8248493
  //   849493 8148493 891913 490913 891913 490913 932023 12484b3 430313 fffe0e13 fe0e18e3 2000e13 313 34483
  //   900533 2200893 73 130313 fffe0e13 fe0e14e3 a00893 73 ff100493 900533 2200893 73 148493 fe9068e3
  //   900533 2200893 73 a00893 73 413 140413 800533 2200893 73 240413 800533 2200893 73 340413 800533
  //   2200893 73 440413 800533 2200893 73 540413 800533 2200893 73 640413 800533 2200893 73 740413 800533
  //   2200893 73 840413 800533 2200893 2200893 73 8067
  //   0xfffffff1 0xfffffff2 0xfffffff3 0xfffffff4 0xfffffff5 0xfffffff6 0xfffffff7 0xfffffff8 0xfffffff9 0xfffffffa 0xfffffffb 0xfffffffc 0xfffffffd 0xfffffffe 0xffffffff 0x00000000
  //   控制位
  //   JAL
  //   JALR
  //   URET
  //   指令字
  //   流水调试日志用
  //   暂停节拍，不能为0
  //   MemWrite
  //   AluOP
  //   AluSrcB
  //   戳工具置1进入计数暂停模式，ctrl+k时钟自动运行到对应节拍暂停
  //   ctrl+k关闭时钟连续运行，将控制位置零，进入单步调试模式调试
  //   Beq
  //   Bne
  //   可计数暂停的时钟源
  //   为方便自动评测，需要输出流水线各段保存的PC值，注意是PC不是PC+4，另外ID段寄存器写入信息，Mem段内存写入信息也要输出
  //   数据存储器
endmodule

module \中断按键参考电路  (
  input  \同步清零信号 ,
  output \与中断屏蔽位与 
);

  wire \_1号中断_out , and_1_out, clock_1_out, d_ff_1_q, or_1_out, or_2_out;

  Clock #(.highDuration(1), .lowDuration(1)) clock_1 (.out(clock_1_out));
  Button \_1号中断  (.out(\_1号中断_out ));
  or or_1 (or_1_out, \与中断屏蔽位与 , d_ff_1_q);
  LED #(.active("true")) \_1号中断等待指示灯  (.in(or_1_out));
  D_Flip_Flop #(.trigger("rising"), .Pre_Clr_Positions("LEGACY"), .NegatePresetClear("false"), .enable("true"), .NewFFLayout("false")) d_ff_1 (
    .clk(\_1号中断_out ), .D(1'b1), .Q(d_ff_1_q), .reset(\与中断屏蔽位与 ));  // open: Qn, preset, en
  or or_2 (or_2_out, d_ff_1_q, \与中断屏蔽位与 );
  and and_1 (and_1_out, or_2_out, ~\同步清零信号 );  // AND_Gate
  D_Flip_Flop #(.trigger("rising"), .Pre_Clr_Positions("LEGACY"), .NegatePresetClear("false"), .enable("true"), .NewFFLayout("false")) IR1 (
    .clk(clock_1_out), .D(and_1_out), .Q(\与中断屏蔽位与 ));  // open: Qn, preset, en, reset

  // Notes on the sheet:
  //   中断信号采样参考电路
  //   Reset 
endmodule

module \单周期_单级中断  (
  input  IR1,
  input  IR2,
  input  IR3,
  output RegWrite,
  output MemWrite,
  output [31:0] PC,
  output [31:0] IR,
  output [31:0] RDin,
  output [31:0] MDin,
  output [31:0] LedData
);

  wire CLK, clock_1_out, comparator_1_eq, comparator_2_eq, comparator_3_eq, comparator_4_eq, comparator_5_eq,
       comparator_5_lt, d_ff_1_q, Go, IR1_t, IR2_t, IR3_t, IRA, IRB, IRC, nand_1_out, or_1_out, W1, W2, W3;
  wire [12:0] CNT_num;
  wire [15:0] \总周期数 ;

  Button \u_继续运行  (.out(Go));
  Button _1 ();  // open: out
  Button _2 ();  // open: out
  Button _3 ();  // open: out
  LED #(.active("true")) led_1 (.in(W1));
  LED #(.active("true")) led_2 (.in(W2));
  LED #(.active("true")) led_3 (.in(W3));
  Hex_Digit_Display hex_digit_display_1 (.value(LedData[31:28]));  // open: dp
  Comparator #(.width(16), .mode("twosComplement")) comparator_1 (
    .a(16'h23b), .b(\总周期数 ), .eq(comparator_1_eq));  // open: gt, lt
  Comparator #(.width(16), .mode("twosComplement")) comparator_2 (
    .a(\总周期数 ), .b(16'h1), .eq(comparator_2_eq));  // open: gt, lt
  Comparator #(.width(16), .mode("twosComplement")) comparator_3 (
    .a(\总周期数 ), .b(16'h4), .eq(comparator_3_eq));  // open: gt, lt
  Comparator #(.width(16), .mode("twosComplement")) comparator_4 (
    .a(\总周期数 ), .b(16'h7), .eq(comparator_4_eq));  // open: gt, lt
  Hex_Digit_Display hex_digit_display_2 (.value(LedData[27:24]));  // open: dp
  Hex_Digit_Display hex_digit_display_3 (.value(LedData[23:20]));  // open: dp
  or or_1 (or_1_out, comparator_1_eq, comparator_2_eq);
  assign IRA = or_1_out ? ~CLK : 1'bz;  // Controlled_Inverter controlled_inverter_1
  assign IRB = comparator_3_eq ? ~CLK : 1'bz;  // Controlled_Inverter controlled_inverter_2
  assign IRC = comparator_4_eq ? ~CLK : 1'bz;  // Controlled_Inverter controlled_inverter_3
  Hex_Digit_Display hex_digit_display_4 (.value(LedData[15:12]));  // open: dp
  Hex_Digit_Display hex_digit_display_5 (.value(LedData[19:16]));  // open: dp
  Pull_Resistor #(.pull(0)) pull_resistor_1 (.node(IRA));
  Pull_Resistor #(.pull(0)) pull_resistor_2 (.node(IRB));
  Pull_Resistor #(.pull(0)) pull_resistor_3 (.node(IRC));
  Hex_Digit_Display hex_digit_display_6 (.value(LedData[7:4]));  // open: dp
  Hex_Digit_Display hex_digit_display_7 (.value(LedData[11:8]));  // open: dp
  // Probe on \总周期数 
  Hex_Digit_Display hex_digit_display_8 (.value(LedData[3:0]));  // open: dp
  or or_2 (IR1_t, IR1, IRA);
  or or_3 (IR2_t, IR2, IRB);
  or or_4 (IR3_t, IR3, IRC);
  D_Flip_Flop #(.trigger("high"), .Pre_Clr_Positions("LEGACY"), .NegatePresetClear("false"), .enable("true"), .NewFFLayout("false")) d_ff_1 (.Q(d_ff_1_q));  // open: clk, D, Qn, preset, en, reset
  // Probe on 13'hc
  Comparator #(.width(13), .mode("twosComplement")) comparator_5 (
    .a(CNT_num), .b(13'hc), .eq(comparator_5_eq), .lt(comparator_5_lt));  // open: gt
  Clock #(.highDuration(1), .lowDuration(1)) clock_1 (.out(clock_1_out));
  Counter #(.width(13), .max('h1fff), .ongoal("stay"), .trigger("rising"), .behavior("old")) counter_1 (
    .count(comparator_5_lt), .Q(CNT_num), .clk(clock_1_out));  // open: load, D, carry, clr, preset
  nand nand_1 (nand_1_out, d_ff_1_q, comparator_5_eq);
  assign CLK = nand_1_out ? clock_1_out : 1'bz;  // Controlled_Buffer controlled_buffer_1
  Pull_Resistor #(.pull(1)) pull_resistor_4 (.node(CLK));

  // Notes on the sheet:
  //   中断源
  //   中断等待指示
  //   总复位信号应将除ROM以外所有存储组件全部清零
  //   单级中断测试信号模拟器
  //   数码管输出
  //   数码管输出应该用寄存器锁存，否则显示数据只能一闪而过
  //   为方便自动评测，需要输出PC，IR，寄存器堆写如数据RDin
  //   RAM写使能MemWrite、RAM写入数据MDin等信号
  //   控制位
  //   暂停节拍，不能为0
  //   戳工具置1进入计数暂停模式，ctrl+k时钟自动运行到对应节拍暂停
  //   ctrl+k关闭时钟连续运行，将控制位置零，进入单步调试模式调试
  //   可计数暂停的时钟源
endmodule

module \单周期_多级中断  (
  input  IR1,
  input  IR2,
  input  IR3,
  output RegWrite,
  output MemWrite,
  output [31:0] PC,
  output [31:0] IR,
  output [31:0] RDin,
  output [31:0] MDin,
  output [31:0] LedData
);

  wire CLK, clock_1_out, comparator_1_eq, comparator_2_eq, comparator_3_eq, comparator_4_eq, comparator_5_eq,
       comparator_6_eq, comparator_6_lt, d_ff_1_q, Go, IR1_t, IR2_t, IR3_t, IRA, IRB, IRC, nand_1_out,
       or_1_out, or_2_out, W1, W2, W3;
  wire [12:0] CNT_num;
  wire [15:0] \总周期数 ;

  Button \u_继续运行  (.out(Go));
  Button _1 ();  // open: out
  Button _2 ();  // open: out
  Button _3 ();  // open: out
  LED #(.active("true")) led_1 (.in(W1));
  LED #(.active("true")) led_2 (.in(W2));
  LED #(.active("true")) led_3 (.in(W3));
  Hex_Digit_Display hex_digit_display_1 (.value(LedData[31:28]));  // open: dp
  Comparator #(.width(16), .mode("twosComplement")) comparator_1 (
    .a(\总周期数 ), .b(16'h7), .eq(comparator_1_eq));  // open: gt, lt
  Comparator #(.width(16), .mode("twosComplement")) comparator_2 (
    .a(\总周期数 ), .b(16'h241), .eq(comparator_2_eq));  // open: gt, lt
  Hex_Digit_Display hex_digit_display_2 (.value(LedData[27:24]));  // open: dp
  Hex_Digit_Display hex_digit_display_3 (.value(LedData[23:20]));  // open: dp
  Comparator #(.width(16), .mode("twosComplement")) comparator_3 (
    .a(16'h258), .b(\总周期数 ), .eq(comparator_3_eq));  // open: gt, lt
  or or_1 (or_1_out, comparator_3_eq, comparator_4_eq);
  Comparator #(.width(16), .mode("twosComplement")) comparator_4 (
    .a(\总周期数 ), .b(16'h1), .eq(comparator_4_eq));  // open: gt, lt
  Comparator #(.width(16), .mode("twosComplement")) comparator_5 (
    .a(\总周期数 ), .b(16'h4), .eq(comparator_5_eq));  // open: gt, lt
  or or_2 (or_2_out, comparator_1_eq, comparator_2_eq);
  Hex_Digit_Display hex_digit_display_4 (.value(LedData[19:16]));  // open: dp
  Hex_Digit_Display hex_digit_display_5 (.value(LedData[15:12]));  // open: dp
  Pull_Resistor #(.pull(0)) pull_resistor_1 (.node(IRA));
  assign IRA = or_1_out ? ~CLK : 1'bz;  // Controlled_Inverter controlled_inverter_1
  Pull_Resistor #(.pull(0)) pull_resistor_2 (.node(IRB));
  assign IRB = comparator_5_eq ? ~CLK : 1'bz;  // Controlled_Inverter controlled_inverter_2
  Pull_Resistor #(.pull(0)) pull_resistor_3 (.node(IRC));
  assign IRC = or_2_out ? ~CLK : 1'bz;  // Controlled_Inverter controlled_inverter_3
  Hex_Digit_Display hex_digit_display_6 (.value(LedData[7:4]));  // open: dp
  Hex_Digit_Display hex_digit_display_7 (.value(LedData[11:8]));  // open: dp
  // Probe on \总周期数 
  Hex_Digit_Display hex_digit_display_8 (.value(LedData[3:0]));  // open: dp
  or or_3 (IR1_t, IR1, IRA);
  or or_4 (IR2_t, IR2, IRB);
  or or_5 (IR3_t, IR3, IRC);
  D_Flip_Flop #(.trigger("high"), .Pre_Clr_Positions("LEGACY"), .NegatePresetClear("false"), .enable("true"), .NewFFLayout("false")) d_ff_1 (.Q(d_ff_1_q));  // open: clk, D, Qn, preset, en, reset
  // Probe on 13'hc
  Comparator #(.width(13), .mode("twosComplement")) comparator_6 (
    .a(CNT_num), .b(13'hc), .eq(comparator_6_eq), .lt(comparator_6_lt));  // open: gt
  Clock #(.highDuration(1), .lowDuration(1)) clock_1 (.out(clock_1_out));
  Counter #(.width(13), .max('h1fff), .ongoal("stay"), .trigger("rising"), .behavior("old")) counter_1 (
    .count(comparator_6_lt), .Q(CNT_num), .clk(clock_1_out));  // open: load, D, carry, clr, preset
  nand nand_1 (nand_1_out, d_ff_1_q, comparator_6_eq);
  assign CLK = nand_1_out ? clock_1_out : 1'bz;  // Controlled_Buffer controlled_buffer_1
  Pull_Resistor #(.pull(1)) pull_resistor_4 (.node(CLK));

  // Notes on the sheet:
  //   中断源
  //   中断等待指示
  //   总复位信号应将除ROM以外所有存储组件全部清零
  //   多级中断测试信号模拟器
  //   数码管输出
  //   数码管输出应该用寄存器锁存，否则显示数据只能一闪而过
  //   为方便自动评测，需要输出PC，IR，寄存器堆写如数据RDin
  //   RAM写使能MemWrite、RAM写入数据MDin等信号
  //   控制位
  //   暂停节拍，不能为0
  //   戳工具置1进入计数暂停模式，ctrl+k时钟自动运行到对应节拍暂停
  //   ctrl+k关闭时钟连续运行，将控制位置零，进入单步调试模式调试
  //   可计数暂停的时钟源
endmodule

module \封装正确性测试  (
);

  wire IR1, IR2, IR3, MemW, RegW;
  wire [31:0] EX_PC, ID_PC, IF_PC, IR, LED, MDin, MDinr, MEM_PC, PC, RDin, RDinr, WB_PC;

  \单周期RISC_V  \u_单周期risc_v_1  (
    .IR1(IR1), .IR2(IR2), .IR3(IR3), .RegWrite(RegW), .MemWrite(MemW), .PC(PC), .IR(IR), .RDin(RDin),
    .MDin(MDin), .LedData(LED));
  \气泡流水线  \u_气泡流水线_1  (
    .RegWrite(RegW), .MemWrite(MemW), .IF_PC(IF_PC), .ID_PC(ID_PC), .EX_PC(EX_PC), .M_PC(MEM_PC),
    .WB_PC(WB_PC), .RDin(RDinr), .MDin(MDinr), .LedData(LED));
  \单周期_单级中断  \u_单周期_单级中断_1  (
    .IR1(IR1), .IR2(IR2), .IR3(IR3), .RegWrite(RegW), .MemWrite(MemW), .PC(PC), .IR(IR), .RDin(RDin),
    .MDin(MDin), .LedData(LED));
  \理想流水线  \u_理想流水线_1  (
    .RegWrite(RegW), .MemWrite(MemW), .IF_PC(IF_PC), .ID_PC(ID_PC), .EX_PC(EX_PC), .M_PC(MEM_PC),
    .WB_PC(WB_PC), .RDin(RDinr), .MDin(MDinr), .LedData(LED));
  \重定向流水线  \u_重定向流水线_1  (
    .RegWrite(RegW), .MemWrite(MemW), .IF_PC(IF_PC), .ID_PC(ID_PC), .EX_PC(EX_PC), .M_PC(MEM_PC),
    .WB_PC(WB_PC), .RDin(RDinr), .MDin(MDinr), .LedData(LED));
  \单周期_多级中断  \u_单周期_多级中断_1  (
    .IR1(IR1), .IR2(IR2), .IR3(IR3), .RegWrite(RegW), .MemWrite(MemW), .PC(PC), .IR(IR), .RDin(RDin),
    .MDin(MDin), .LedData(LED));

  // Notes on the sheet:
  //   单周期封装测试
  //   气泡流水封装测试
  //   单周期+单级中断封装测试
  //   请检查上面封装有无位宽不匹配，引脚标签是否和连接的标签相对应，否则无法在educoder平台上正确测试
  //   理想流水封装测试
  //   重定向流水封装测试
  //   单周期+多级中断封装测试
endmodule

module IF_ID (
  input  [31:0] IR,
  input  [31:0] PC,
  input  [31:0] PC_4,
  input  IF_PredictJump,
  input  branch,
  input  reset,
  input  en,
  input  CLK,
  output [31:0] IR_2,
  output [31:0] PC_2,
  output [31:0] PC_4_2,
  output ID_PredictJump
);

  wire multiplexer_4_out, or_1_out;
  wire [31:0] multiplexer_1_out, multiplexer_2_out, multiplexer_3_out;

  Multiplexer #(.select(1), .width(32), .disabled("Z"), .enable("false")) multiplexer_1 (
    .in0(IR), .in1({32{1'b0}}), .out(multiplexer_1_out), .sel(or_1_out));
  Multiplexer #(.select(1), .width(32), .disabled("Z"), .enable("false")) multiplexer_2 (
    .in0(PC), .in1({32{1'b0}}), .out(multiplexer_2_out), .sel(or_1_out));
  Multiplexer #(.select(1), .width(32), .disabled("Z"), .enable("false")) multiplexer_3 (
    .in0(PC_4), .in1({32{1'b0}}), .out(multiplexer_3_out), .sel(or_1_out));
  Multiplexer #(.select(1), .width(1), .disabled("Z"), .enable("false")) multiplexer_4 (
    .in0(IF_PredictJump), .in1(1'b0), .out(multiplexer_4_out));  // open: sel
  or or_1 (or_1_out, branch, reset);
  Register #(.width(32), .trigger("rising"), .Select("low")) register_1 (
    .D(multiplexer_1_out), .en(en), .Q(IR_2), .clk(CLK));  // open: clr
  Register #(.width(32), .trigger("rising"), .Select("low")) register_2 (
    .D(multiplexer_2_out), .en(en), .Q(PC_2), .clk(CLK));  // open: clr
  Register #(.width(32), .trigger("rising"), .Select("low")) register_3 (
    .D(multiplexer_3_out), .en(en), .Q(PC_4_2), .clk(CLK));  // open: clr
  Register #(.width(1), .trigger("rising"), .Select("low")) register_4 (
    .D(multiplexer_4_out), .en(or_1_out), .Q(ID_PredictJump), .clk(CLK));  // open: clr
endmodule

module EX_MEM (
  input  LBU,
  input  Jal,
  input  Jalr,
  input  MemToReg,
  input  MemWrite,
  input  RegWrite,
  input  halt,
  input  [4:0] rd,
  input  [31:0] Result,
  input  [31:0] WriteData,
  input  [31:0] IR,
  input  [31:0] PC,
  input  [31:0] PC_4,
  input  reset,
  input  clk,
  input  en,
  output LBU_2,
  output Jal_2,
  output Jalr_2,
  output MemToReg_2,
  output MemWrite_2,
  output RegWrite_2,
  output halt_2,
  output [4:0] rd_2,
  output [31:0] Result_2,
  output [31:0] WriteData_2,
  output [31:0] IR_2,
  output [31:0] PC_2,
  output [31:0] PC_4_2
);

  wire multiplexer_1_out, multiplexer_2_out, multiplexer_3_out, multiplexer_4_out, multiplexer_5_out,
       multiplexer_6_out, multiplexer_7_out;
  wire [4:0] multiplexer_8_out;
  wire [31:0] multiplexer_9_out, multiplexer_10_out, multiplexer_11_out, multiplexer_12_out,
       multiplexer_13_out;

  Multiplexer #(.select(1), .width(1), .disabled("Z"), .enable("false")) multiplexer_1 (
    .in0(LBU), .in1(1'b0), .out(multiplexer_1_out), .sel(reset));
  Multiplexer #(.select(1), .width(1), .disabled("Z"), .enable("false")) multiplexer_2 (
    .in0(Jal), .in1(1'b0), .out(multiplexer_2_out), .sel(reset));
  Multiplexer #(.select(1), .width(1), .disabled("Z"), .enable("false")) multiplexer_3 (
    .in0(Jalr), .in1(1'b0), .out(multiplexer_3_out), .sel(reset));
  Multiplexer #(.select(1), .width(1), .disabled("Z"), .enable("false")) multiplexer_4 (
    .in0(MemToReg), .in1(1'b0), .out(multiplexer_4_out), .sel(reset));
  Multiplexer #(.select(1), .width(1), .disabled("Z"), .enable("false")) multiplexer_5 (
    .in0(MemWrite), .in1(1'b0), .out(multiplexer_5_out), .sel(reset));
  Multiplexer #(.select(1), .width(1), .disabled("Z"), .enable("false")) multiplexer_6 (
    .in0(RegWrite), .in1(1'b0), .out(multiplexer_6_out), .sel(reset));
  Multiplexer #(.select(1), .width(1), .disabled("Z"), .enable("false")) multiplexer_7 (
    .in0(halt), .in1(1'b0), .out(multiplexer_7_out), .sel(reset));
  Multiplexer #(.select(1), .width(5), .disabled("Z"), .enable("false")) multiplexer_8 (
    .in0(rd), .in1({5{1'b0}}), .out(multiplexer_8_out), .sel(reset));
  Multiplexer #(.select(1), .width(32), .disabled("Z"), .enable("false")) multiplexer_9 (
    .in0(Result), .in1({32{1'b0}}), .out(multiplexer_9_out), .sel(reset));
  Multiplexer #(.select(1), .width(32), .disabled("Z"), .enable("false")) multiplexer_10 (
    .in0(WriteData), .in1({32{1'b0}}), .out(multiplexer_10_out), .sel(reset));
  Multiplexer #(.select(1), .width(32), .disabled("Z"), .enable("false")) multiplexer_11 (
    .in0(IR), .in1({32{1'b0}}), .out(multiplexer_11_out), .sel(reset));
  Multiplexer #(.select(1), .width(32), .disabled("Z"), .enable("false")) multiplexer_12 (
    .in0(PC), .in1({32{1'b0}}), .out(multiplexer_12_out), .sel(reset));
  Multiplexer #(.select(1), .width(32), .disabled("Z"), .enable("false")) multiplexer_13 (
    .in0(PC_4), .in1({32{1'b0}}), .out(multiplexer_13_out), .sel(reset));
  Register #(.width(1), .trigger("rising"), .Select("low")) register_1 (
    .D(multiplexer_1_out), .en(en), .Q(LBU_2), .clk(clk));  // open: clr
  Register #(.width(1), .trigger("rising"), .Select("low")) register_2 (
    .D(multiplexer_2_out), .en(en), .Q(Jal_2), .clk(clk));  // open: clr
  Register #(.width(1), .trigger("rising"), .Select("low")) register_3 (
    .D(multiplexer_3_out), .en(en), .Q(Jalr_2), .clk(clk));  // open: clr
  Register #(.width(1), .trigger("rising"), .Select("low")) register_4 (
    .D(multiplexer_4_out), .en(en), .Q(MemToReg_2), .clk(clk));  // open: clr
  Register #(.width(1), .trigger("rising"), .Select("low")) register_5 (
    .D(multiplexer_5_out), .en(en), .Q(MemWrite_2), .clk(clk));  // open: clr
  Register #(.width(1), .trigger("rising"), .Select("low")) register_6 (
    .D(multiplexer_6_out), .en(en), .Q(RegWrite_2), .clk(clk));  // open: clr
  Register #(.width(1), .trigger("rising"), .Select("low")) register_7 (
    .D(multiplexer_7_out), .en(en), .Q(halt_2), .clk(clk));  // open: clr
  Register #(.width(5), .trigger("rising"), .Select("low")) register_8 (
    .D(multiplexer_8_out), .en(en), .Q(rd_2), .clk(clk));  // open: clr
  Register #(.width(32), .trigger("rising"), .Select("low")) register_9 (
    .D(multiplexer_9_out), .en(en), .Q(Result_2), .clk(clk));  // open: clr
  Register #(.width(32), .trigger("rising"), .Select("low")) register_10 (
    .D(multiplexer_10_out), .en(en), .Q(WriteData_2), .clk(clk));  // open: clr
  Register #(.width(32), .trigger("rising"), .Select("low")) register_11 (
    .D(multiplexer_11_out), .en(en), .Q(IR_2), .clk(clk));  // open: clr
  Register #(.width(32), .trigger("rising"), .Select("low")) register_12 (
    .D(multiplexer_12_out), .en(en), .Q(PC_2), .clk(clk));  // open: clr
  Register #(.width(32), .trigger("rising"), .Select("low")) register_13 (
    .D(multiplexer_13_out), .en(en), .Q(PC_4_2), .clk(clk));  // open: clr
endmodule

module ID_EX (
  input  LBU,
  input  Ecall,
  input  Uret,
  input  BLTU,
  input  Beq,
  input  Bne,
  input  MemToReg,
  input  MemWrite,
  input  AluSrcB,
  input  RegWrite,
  input  S_type,
  input  Jal,
  input  Jalr,
  input  Remu,
  input  [3:0] Aluop,
  input  [4:0] rd,
  input  [31:0] R1,
  input  [31:0] R2,
  input  [31:0] IMM_1,
  input  [31:0] IMM_2,
  input  [31:0] PC,
  input  [31:0] PC_4,
  input  [31:0] IR,
  input  [1:0] RS1_Forward,
  input  [1:0] RS2_Forward,
  input  ID_PredictJump,
  input  clk,
  input  reset,
  input  flush,
  input  en,
  output LBU_2,
  output EX_ecall,
  output Uret_2,
  output BLTU_2,
  output Beq_2,
  output Bne_2,
  output MemToReg_2,
  output MemWrite_2,
  output AlieSrcB,
  output RegWrite_2,
  output S_type_2,
  output Jal_2,
  output Jalr_2,
  output Remu_2,
  output [3:0] Aluop_2,
  output [4:0] rd_2,
  output [31:0] R1_2,
  output [31:0] R2_2,
  output [31:0] IMM_1_2,
  output [31:0] IMM_2_2,
  output [31:0] PC_2,
  output [31:0] PC_4_2,
  output [31:0] IR_2,
  output [1:0] RS1_Forward_2,
  output [1:0] RS2_Forward_2,
  output EX_PredictJump
);

  wire multiplexer_1_out, multiplexer_2_out, multiplexer_3_out, multiplexer_4_out, multiplexer_5_out,
       multiplexer_6_out, multiplexer_7_out, multiplexer_8_out, multiplexer_9_out, multiplexer_10_out,
       multiplexer_11_out, multiplexer_12_out, multiplexer_13_out, multiplexer_14_out, multiplexer_26_out,
       or_1_out;
  wire [1:0] multiplexer_24_out, multiplexer_25_out;
  wire [3:0] multiplexer_15_out;
  wire [4:0] multiplexer_16_out;
  wire [31:0] multiplexer_17_out, multiplexer_18_out, multiplexer_19_out, multiplexer_20_out,
       multiplexer_21_out, multiplexer_22_out, multiplexer_23_out;

  Multiplexer #(.select(1), .width(1), .disabled("Z"), .enable("false")) multiplexer_1 (
    .in0(LBU), .in1(1'b0), .out(multiplexer_1_out), .sel(or_1_out));
  Multiplexer #(.select(1), .width(1), .disabled("Z"), .enable("false")) multiplexer_2 (
    .in0(Ecall), .in1(1'b0), .out(multiplexer_2_out), .sel(or_1_out));
  Multiplexer #(.select(1), .width(1), .disabled("Z"), .enable("false")) multiplexer_3 (
    .in0(Uret), .in1(1'b0), .out(multiplexer_3_out), .sel(or_1_out));
  Multiplexer #(.select(1), .width(1), .disabled("Z"), .enable("false")) multiplexer_4 (
    .in0(BLTU), .in1(1'b0), .out(multiplexer_4_out), .sel(or_1_out));
  Multiplexer #(.select(1), .width(1), .disabled("Z"), .enable("false")) multiplexer_5 (
    .in0(Beq), .in1(1'b0), .out(multiplexer_5_out), .sel(or_1_out));
  Multiplexer #(.select(1), .width(1), .disabled("Z"), .enable("false")) multiplexer_6 (
    .in0(Bne), .in1(1'b0), .out(multiplexer_6_out), .sel(or_1_out));
  Multiplexer #(.select(1), .width(1), .disabled("Z"), .enable("false")) multiplexer_7 (
    .in0(MemToReg), .in1(1'b0), .out(multiplexer_7_out), .sel(or_1_out));
  Multiplexer #(.select(1), .width(1), .disabled("Z"), .enable("false")) multiplexer_8 (
    .in0(MemWrite), .in1(1'b0), .out(multiplexer_8_out), .sel(or_1_out));
  Multiplexer #(.select(1), .width(1), .disabled("Z"), .enable("false")) multiplexer_9 (
    .in0(AluSrcB), .in1(1'b0), .out(multiplexer_9_out), .sel(or_1_out));
  Multiplexer #(.select(1), .width(1), .disabled("Z"), .enable("false")) multiplexer_10 (
    .in0(RegWrite), .in1(1'b0), .out(multiplexer_10_out), .sel(or_1_out));
  Multiplexer #(.select(1), .width(1), .disabled("Z"), .enable("false")) multiplexer_11 (
    .in0(S_type), .in1(1'b0), .out(multiplexer_11_out), .sel(or_1_out));
  Multiplexer #(.select(1), .width(1), .disabled("Z"), .enable("false")) multiplexer_12 (
    .in0(Jal), .in1(1'b0), .out(multiplexer_12_out), .sel(or_1_out));
  Multiplexer #(.select(1), .width(1), .disabled("Z"), .enable("false")) multiplexer_13 (
    .in0(Jalr), .in1(1'b0), .out(multiplexer_13_out), .sel(or_1_out));
  Multiplexer #(.select(1), .width(1), .disabled("Z"), .enable("false")) multiplexer_14 (
    .in0(Remu), .in1(1'b0), .out(multiplexer_14_out), .sel(or_1_out));
  Multiplexer #(.select(1), .width(4), .disabled("Z"), .enable("false")) multiplexer_15 (
    .in0(Aluop), .in1(4'b0000), .out(multiplexer_15_out), .sel(or_1_out));
  Multiplexer #(.select(1), .width(5), .disabled("Z"), .enable("false")) multiplexer_16 (
    .in0(rd), .in1({5{1'b0}}), .out(multiplexer_16_out), .sel(or_1_out));
  Multiplexer #(.select(1), .width(32), .disabled("Z"), .enable("false")) multiplexer_17 (
    .in0(R1), .in1({32{1'b0}}), .out(multiplexer_17_out), .sel(or_1_out));
  Multiplexer #(.select(1), .width(32), .disabled("Z"), .enable("false")) multiplexer_18 (
    .in0(R2), .in1({32{1'b0}}), .out(multiplexer_18_out), .sel(or_1_out));
  Multiplexer #(.select(1), .width(32), .disabled("Z"), .enable("false")) multiplexer_19 (
    .in0(IMM_1), .in1({32{1'b0}}), .out(multiplexer_19_out), .sel(or_1_out));
  Multiplexer #(.select(1), .width(32), .disabled("Z"), .enable("false")) multiplexer_20 (
    .in0(IMM_2), .in1({32{1'b0}}), .out(multiplexer_20_out), .sel(or_1_out));
  Multiplexer #(.select(1), .width(32), .disabled("Z"), .enable("false")) multiplexer_21 (
    .in0(PC), .in1({32{1'b0}}), .out(multiplexer_21_out), .sel(or_1_out));
  Multiplexer #(.select(1), .width(32), .disabled("Z"), .enable("false")) multiplexer_22 (
    .in0(PC_4), .in1({32{1'b0}}), .out(multiplexer_22_out), .sel(or_1_out));
  Multiplexer #(.select(1), .width(32), .disabled("Z"), .enable("false")) multiplexer_23 (
    .in0(IR), .in1({32{1'b0}}), .out(multiplexer_23_out), .sel(or_1_out));
  Multiplexer #(.select(1), .width(2), .disabled("Z"), .enable("false")) multiplexer_24 (
    .in0(RS1_Forward), .in1(2'b00), .out(multiplexer_24_out), .sel(or_1_out));
  Multiplexer #(.select(1), .width(2), .disabled("Z"), .enable("false")) multiplexer_25 (
    .in0(RS2_Forward), .in1(2'b00), .out(multiplexer_25_out), .sel(or_1_out));
  Multiplexer #(.select(1), .width(1), .disabled("Z"), .enable("false")) multiplexer_26 (
    .in0(ID_PredictJump), .in1(1'b0), .out(multiplexer_26_out), .sel(or_1_out));
  or or_1 (or_1_out, reset, flush);
  Register #(.width(1), .trigger("rising"), .Select("low")) register_1 (
    .D(multiplexer_1_out), .en(en), .Q(LBU_2), .clk(clk));  // open: clr
  Register #(.width(1), .trigger("rising"), .Select("low")) register_2 (
    .D(multiplexer_2_out), .en(en), .Q(EX_ecall), .clk(clk));  // open: clr
  Register #(.width(1), .trigger("rising"), .Select("low")) register_3 (
    .D(multiplexer_3_out), .en(en), .Q(Uret_2), .clk(clk));  // open: clr
  Register #(.width(1), .trigger("rising"), .Select("low")) register_4 (
    .D(multiplexer_4_out), .en(en), .Q(BLTU_2), .clk(clk));  // open: clr
  Register #(.width(1), .trigger("rising"), .Select("low")) register_5 (
    .D(multiplexer_5_out), .en(en), .Q(Beq_2), .clk(clk));  // open: clr
  Register #(.width(1), .trigger("rising"), .Select("low")) register_6 (
    .D(multiplexer_6_out), .en(en), .Q(Bne_2), .clk(clk));  // open: clr
  Register #(.width(1), .trigger("rising"), .Select("low")) register_7 (
    .D(multiplexer_7_out), .en(en), .Q(MemToReg_2), .clk(clk));  // open: clr
  Register #(.width(1), .trigger("rising"), .Select("low")) register_8 (
    .D(multiplexer_8_out), .en(en), .Q(MemWrite_2), .clk(clk));  // open: clr
  Register #(.width(1), .trigger("rising"), .Select("low")) register_9 (
    .D(multiplexer_9_out), .en(en), .Q(AlieSrcB), .clk(clk));  // open: clr
  Register #(.width(1), .trigger("rising"), .Select("low")) register_10 (
    .D(multiplexer_10_out), .en(en), .Q(RegWrite_2), .clk(clk));  // open: clr
  Register #(.width(1), .trigger("rising"), .Select("low")) register_11 (
    .D(multiplexer_11_out), .en(en), .Q(S_type_2), .clk(clk));  // open: clr
  Register #(.width(1), .trigger("rising"), .Select("low")) register_12 (
    .D(multiplexer_12_out), .en(en), .Q(Jal_2), .clk(clk));  // open: clr
  Register #(.width(1), .trigger("rising"), .Select("low")) register_13 (
    .D(multiplexer_13_out), .en(en), .Q(Jalr_2), .clk(clk));  // open: clr
  Register #(.width(1), .trigger("rising"), .Select("low")) register_14 (
    .D(multiplexer_14_out), .en(en), .Q(Remu_2), .clk(clk));  // open: clr
  Register #(.width(4), .trigger("rising"), .Select("low")) register_15 (
    .D(multiplexer_15_out), .en(en), .Q(Aluop_2), .clk(clk));  // open: clr
  Register #(.width(5), .trigger("rising"), .Select("low")) register_16 (
    .D(multiplexer_16_out), .en(en), .Q(rd_2), .clk(clk));  // open: clr
  Register #(.width(32), .trigger("rising"), .Select("low")) register_17 (
    .D(multiplexer_17_out), .en(en), .Q(R1_2), .clk(clk));  // open: clr
  Register #(.width(32), .trigger("rising"), .Select("low")) register_18 (
    .D(multiplexer_18_out), .en(en), .Q(R2_2), .clk(clk));  // open: clr
  Register #(.width(32), .trigger("rising"), .Select("low")) register_19 (
    .D(multiplexer_19_out), .en(en), .Q(IMM_1_2), .clk(clk));  // open: clr
  Register #(.width(32), .trigger("rising"), .Select("low")) register_20 (
    .D(multiplexer_20_out), .en(en), .Q(IMM_2_2), .clk(clk));  // open: clr
  Register #(.width(32), .trigger("rising"), .Select("low")) register_21 (
    .D(multiplexer_21_out), .en(en), .Q(PC_2), .clk(clk));  // open: clr
  Register #(.width(32), .trigger("rising"), .Select("low")) register_22 (
    .D(multiplexer_22_out), .en(en), .Q(PC_4_2), .clk(clk));  // open: clr
  Register #(.width(32), .trigger("rising"), .Select("low")) register_23 (
    .D(multiplexer_23_out), .en(en), .Q(IR_2), .clk(clk));  // open: clr
  Register #(.width(2), .trigger("rising"), .Select("low")) register_24 (
    .D(multiplexer_24_out), .en(en), .Q(RS1_Forward_2), .clk(clk));  // open: clr
  Register #(.width(2), .trigger("rising"), .Select("low")) register_25 (
    .D(multiplexer_25_out), .en(en), .Q(RS2_Forward_2), .clk(clk));  // open: clr
  Register #(.width(1), .trigger("rising"), .Select("low")) register_26 (
    .D(multiplexer_26_out), .en(en), .Q(EX_PredictJump), .clk(clk));  // open: clr
endmodule

module MEM_WB (
  input  en,
  input  clk,
  input  reset,
  input  Jal,
  input  Jalr,
  input  MemToReg,
  input  RegWrite,
  input  halt,
  input  [4:0] rd,
  input  [31:0] ALUResult,
  input  [31:0] ReadData,
  input  [31:0] IR,
  input  [31:0] PC,
  input  [31:0] PC_4,
  output Jal_2,
  output Jalr_2,
  output MemToReg_2,
  output RegWrite_2,
  output halt_2,
  output [4:0] out_20,
  output [31:0] ALUResult_2,
  output [31:0] ReadData_2,
  output [31:0] IR_2,
  output [31:0] PC_2,
  output [31:0] Pc_4_2
);

  wire multiplexer_1_out, multiplexer_2_out, multiplexer_3_out, multiplexer_4_out, multiplexer_5_out;
  wire [4:0] multiplexer_6_out;
  wire [31:0] multiplexer_7_out, multiplexer_8_out, multiplexer_9_out, multiplexer_10_out, multiplexer_11_out;

  Multiplexer #(.select(1), .width(1), .disabled("Z"), .enable("false")) multiplexer_1 (
    .in0(Jal), .in1(1'b0), .out(multiplexer_1_out), .sel(reset));
  Multiplexer #(.select(1), .width(1), .disabled("Z"), .enable("false")) multiplexer_2 (
    .in0(Jalr), .in1(1'b0), .out(multiplexer_2_out), .sel(reset));
  Multiplexer #(.select(1), .width(1), .disabled("Z"), .enable("false")) multiplexer_3 (
    .in0(MemToReg), .in1(1'b0), .out(multiplexer_3_out), .sel(reset));
  Multiplexer #(.select(1), .width(1), .disabled("Z"), .enable("false")) multiplexer_4 (
    .in0(RegWrite), .in1(1'b0), .out(multiplexer_4_out), .sel(reset));
  Multiplexer #(.select(1), .width(1), .disabled("Z"), .enable("false")) multiplexer_5 (
    .in0(halt), .in1(1'b0), .out(multiplexer_5_out), .sel(reset));
  Multiplexer #(.select(1), .width(5), .disabled("Z"), .enable("false")) multiplexer_6 (
    .in0(rd), .in1({5{1'b0}}), .out(multiplexer_6_out), .sel(reset));
  Multiplexer #(.select(1), .width(32), .disabled("Z"), .enable("false")) multiplexer_7 (
    .in0(ALUResult), .in1({32{1'b0}}), .out(multiplexer_7_out), .sel(reset));
  Multiplexer #(.select(1), .width(32), .disabled("Z"), .enable("false")) multiplexer_8 (
    .in0(ReadData), .in1({32{1'b0}}), .out(multiplexer_8_out), .sel(reset));
  Multiplexer #(.select(1), .width(32), .disabled("Z"), .enable("false")) multiplexer_9 (
    .in0(IR), .in1({32{1'b0}}), .out(multiplexer_9_out), .sel(reset));
  Multiplexer #(.select(1), .width(32), .disabled("Z"), .enable("false")) multiplexer_10 (
    .in0(PC), .in1({32{1'b0}}), .out(multiplexer_10_out), .sel(reset));
  Multiplexer #(.select(1), .width(32), .disabled("Z"), .enable("false")) multiplexer_11 (
    .in0(PC_4), .in1({32{1'b0}}), .out(multiplexer_11_out), .sel(reset));
  Register #(.width(1), .trigger("rising"), .Select("low")) register_1 (
    .D(multiplexer_1_out), .en(en), .Q(Jal_2), .clk(clk));  // open: clr
  Register #(.width(1), .trigger("rising"), .Select("low")) register_2 (
    .D(multiplexer_2_out), .en(en), .Q(Jalr_2), .clk(clk));  // open: clr
  Register #(.width(1), .trigger("rising"), .Select("low")) register_3 (
    .D(multiplexer_3_out), .en(en), .Q(MemToReg_2), .clk(clk));  // open: clr
  Register #(.width(1), .trigger("rising"), .Select("low")) register_4 (
    .D(multiplexer_4_out), .en(en), .Q(RegWrite_2), .clk(clk));  // open: clr
  Register #(.width(1), .trigger("rising"), .Select("low")) register_5 (
    .D(multiplexer_5_out), .en(en), .Q(halt_2), .clk(clk));  // open: clr
  Register #(.width(5), .trigger("rising"), .Select("low")) register_6 (
    .D(multiplexer_6_out), .en(en), .Q(out_20), .clk(clk));  // open: clr
  Register #(.width(32), .trigger("rising"), .Select("low")) register_7 (
    .D(multiplexer_7_out), .en(en), .Q(ALUResult_2), .clk(clk));  // open: clr
  Register #(.width(32), .trigger("rising"), .Select("low")) register_8 (
    .D(multiplexer_8_out), .en(en), .Q(ReadData_2), .clk(clk));  // open: clr
  Register #(.width(32), .trigger("rising"), .Select("low")) register_9 (
    .D(multiplexer_9_out), .en(en), .Q(IR_2), .clk(clk));  // open: clr
  Register #(.width(32), .trigger("rising"), .Select("low")) register_10 (
    .D(multiplexer_10_out), .en(en), .Q(PC_2), .clk(clk));  // open: clr
  Register #(.width(32), .trigger("rising"), .Select("low")) register_11 (
    .D(multiplexer_11_out), .en(en), .Q(Pc_4_2), .clk(clk));  // open: clr
endmodule

module \气泡处理逻辑  (
  input  [31:0] IR,
  input  BranchTaken,
  input  Ecall,
  input  RS1_used,
  input  EX_RegWrite,
  input  [4:0] EX_rd,
  input  RS2_used,
  input  MEM_RegWrite,
  input  [4:0] MEM_rd,
  output stall,
  output flush
);

  wire and_1_out, and_2_out, and_3_out, and_4_out, comparator_1_eq, comparator_2_eq, comparator_3_eq,
       comparator_4_eq, comparator_5_eq, comparator_6_eq, comparator_7_eq, comparator_8_eq, comparator_9_eq,
       comparator_10_eq, comparator_11_eq, comparator_12_eq, or_1_out, or_2_out;

  Comparator #(.width(5), .mode("twosComplement")) comparator_1 (
    .a({5{1'b0}}), .b(IR[19:15]), .eq(comparator_1_eq));  // open: gt, lt
  Comparator #(.width(5), .mode("twosComplement")) comparator_2 (
    .a(IR[19:15]), .b(EX_rd), .eq(comparator_2_eq));  // open: gt, lt
  Comparator #(.width(5), .mode("twosComplement")) comparator_3 (
    .a({5{1'b0}}), .b(IR[19:15]), .eq(comparator_3_eq));  // open: gt, lt
  Comparator #(.width(5), .mode("twosComplement")) comparator_4 (
    .a(IR[19:15]), .b(MEM_rd), .eq(comparator_4_eq));  // open: gt, lt
  Comparator #(.width(5), .mode("twosComplement")) comparator_5 (
    .a({5{1'b0}}), .b(IR[24:20]), .eq(comparator_5_eq));  // open: gt, lt
  Comparator #(.width(5), .mode("twosComplement")) comparator_6 (
    .a(IR[24:20]), .b(EX_rd), .eq(comparator_6_eq));  // open: gt, lt
  Comparator #(.width(5), .mode("twosComplement")) comparator_7 (
    .a({5{1'b0}}), .b(IR[24:20]), .eq(comparator_7_eq));  // open: gt, lt
  Comparator #(.width(5), .mode("twosComplement")) comparator_8 (
    .a(IR[24:20]), .b(MEM_rd), .eq(comparator_8_eq));  // open: gt, lt
  Comparator #(.width(5), .mode("twosComplement")) comparator_9 (
    .a(5'b10001), .b(EX_rd), .eq(comparator_9_eq));  // open: gt, lt
  Comparator #(.width(5), .mode("twosComplement")) comparator_10 (
    .a(EX_rd), .b(5'b01010), .eq(comparator_10_eq));  // open: gt, lt
  Comparator #(.width(5), .mode("twosComplement")) comparator_11 (
    .a(5'b10001), .b(MEM_rd), .eq(comparator_11_eq));  // open: gt, lt
  Comparator #(.width(5), .mode("twosComplement")) comparator_12 (
    .a(MEM_rd), .b(5'b01010), .eq(comparator_12_eq));  // open: gt, lt
  or or_1 (or_1_out, comparator_9_eq, comparator_10_eq);
  or or_2 (or_2_out, comparator_11_eq, comparator_12_eq);
  and and_1 (and_1_out, RS1_used, ~comparator_1_eq, comparator_2_eq, EX_RegWrite);  // AND_Gate
  and and_2 (and_2_out, RS1_used, ~comparator_3_eq, comparator_4_eq, MEM_RegWrite);  // AND_Gate
  and and_3 (and_3_out, RS2_used, ~comparator_5_eq, comparator_6_eq, EX_RegWrite);  // AND_Gate
  and and_4 (and_4_out, RS2_used, ~comparator_7_eq, comparator_8_eq, MEM_RegWrite);  // AND_Gate
  or or_3 (stall, and_1_out, and_2_out, and_3_out, and_4_out, or_1_out, or_2_out);
  or or_4 (flush, stall, BranchTaken);

  // Other names for the same wires on the sheet: DataHazzard = stall; RS1[4:0] = IR[19:15]; RS2[4:0] = IR[24:20]
endmodule

module \重定向处理逻辑  (
  input  RS1_used,
  input  BranchTaken,
  input  [4:0] EX_rd,
  input  [31:0] IR,
  input  RS2_used,
  input  Ecall,
  input  [4:0] MEM_rd,
  input  EX_RegWrite,
  input  EX_MemToReg,
  input  MEM_RegWrite,
  output Stall,
  output Flush,
  output [1:0] RS1_Forward,
  output [1:0] RS2_Forward
);

  wire and_1_out, and_2_out, and_3_out, and_4_out, and_5_out, and_6_out, and_7_out, and_8_out, and_9_out,
       and_10_out, and_11_out, and_12_out, and_17_out, and_18_out, and_19_out, and_20_out, and_21_out,
       and_22_out, and_23_out, and_24_out, comparator_1_eq, comparator_2_eq, comparator_3_eq,
       comparator_4_eq, comparator_5_eq, comparator_6_eq, comparator_7_eq, comparator_8_eq, comparator_9_eq,
       comparator_10_eq, comparator_11_eq, comparator_12_eq, comparator_13_eq, comparator_14_eq,
       comparator_15_eq, comparator_16_eq, Ecall1, Ecall2, Ecall3, Ecall4, or_3_out, or_5_out;

  and and_1 (and_1_out, Ecall, EX_RegWrite);
  and and_2 (and_2_out, Ecall, MEM_RegWrite);
  and and_3 (and_3_out, Ecall, EX_RegWrite);
  and and_4 (and_4_out, Ecall, MEM_RegWrite);
  Comparator #(.width(5), .mode("twosComplement")) comparator_1 (
    .a(EX_rd), .b(IR[19:15]), .eq(comparator_1_eq));  // open: gt, lt
  Comparator #(.width(5), .mode("twosComplement")) comparator_2 (
    .a(IR[19:15]), .b({5{1'b0}}), .eq(comparator_2_eq));  // open: gt, lt
  Comparator #(.width(5), .mode("twosComplement")) comparator_3 (
    .a({5{1'b0}}), .b(IR[24:20]), .eq(comparator_3_eq));  // open: gt, lt
  Comparator #(.width(5), .mode("twosComplement")) comparator_4 (
    .a(IR[24:20]), .b(EX_rd), .eq(comparator_4_eq));  // open: gt, lt
  Comparator #(.width(5), .mode("twosComplement")) comparator_5 (
    .a(EX_rd), .b(IR[19:15]), .eq(comparator_5_eq));  // open: gt, lt
  Comparator #(.width(5), .mode("twosComplement")) comparator_6 (
    .a(IR[19:15]), .b({5{1'b0}}), .eq(comparator_6_eq));  // open: gt, lt
  Comparator #(.width(5), .mode("twosComplement")) comparator_7 (
    .a({5{1'b0}}), .b(IR[19:15]), .eq(comparator_7_eq));  // open: gt, lt
  Comparator #(.width(5), .mode("twosComplement")) comparator_8 (
    .a(IR[19:15]), .b(MEM_rd), .eq(comparator_8_eq));  // open: gt, lt
  Comparator #(.width(5), .mode("twosComplement")) comparator_9 (
    .a(EX_rd), .b(IR[24:20]), .eq(comparator_9_eq));  // open: gt, lt
  Comparator #(.width(5), .mode("twosComplement")) comparator_10 (
    .a(IR[24:20]), .b({5{1'b0}}), .eq(comparator_10_eq));  // open: gt, lt
  Comparator #(.width(5), .mode("twosComplement")) comparator_11 (
    .a({5{1'b0}}), .b(IR[24:20]), .eq(comparator_11_eq));  // open: gt, lt
  Comparator #(.width(5), .mode("twosComplement")) comparator_12 (
    .a(IR[24:20]), .b(MEM_rd), .eq(comparator_12_eq));  // open: gt, lt
  and and_5 (and_5_out, RS1_used, ~comparator_2_eq);  // AND_Gate
  and and_6 (and_6_out, ~comparator_3_eq, RS2_used);  // AND_Gate
  and and_7 (and_7_out, comparator_5_eq, ~comparator_6_eq);  // AND_Gate
  and and_8 (and_8_out, ~comparator_7_eq, comparator_8_eq);  // AND_Gate
  and and_9 (and_9_out, comparator_9_eq, ~comparator_10_eq);  // AND_Gate
  and and_10 (and_10_out, ~comparator_11_eq, comparator_12_eq);  // AND_Gate
  and and_11 (and_11_out, comparator_1_eq, and_5_out, EX_MemToReg);
  and and_12 (and_12_out, EX_MemToReg, and_6_out, comparator_4_eq);
  Comparator #(.width(5), .mode("twosComplement")) comparator_13 (
    .a(EX_rd), .b(5'b10001), .eq(comparator_13_eq));  // open: gt, lt
  and and_13 (Ecall1, comparator_13_eq, and_1_out);
  and and_14 (Ecall2, and_2_out, comparator_14_eq);
  Comparator #(.width(5), .mode("twosComplement")) comparator_14 (
    .a(MEM_rd), .b(5'b10001), .eq(comparator_14_eq));  // open: gt, lt
  Comparator #(.width(5), .mode("twosComplement")) comparator_15 (
    .a(EX_rd), .b(5'b01010), .eq(comparator_15_eq));  // open: gt, lt
  and and_15 (Ecall3, comparator_15_eq, and_3_out);
  and and_16 (Ecall4, and_4_out, comparator_16_eq);
  Comparator #(.width(5), .mode("twosComplement")) comparator_16 (
    .a(MEM_rd), .b(5'b01010), .eq(comparator_16_eq));  // open: gt, lt
  or or_1 (Stall, and_11_out, and_12_out);
  and and_17 (and_17_out, and_7_out, and_18_out);
  and and_18 (and_18_out, EX_RegWrite, RS1_used);
  and and_19 (and_19_out, RS1_used, MEM_RegWrite);
  and and_20 (and_20_out, and_19_out, and_8_out);
  and and_21 (and_21_out, and_9_out, and_22_out);
  and and_22 (and_22_out, EX_RegWrite, RS2_used);
  and and_23 (and_23_out, RS2_used, MEM_RegWrite);
  and and_24 (and_24_out, and_23_out, and_10_out);
  or or_2 (RS1_Forward[1], Ecall1, and_17_out);
  or or_3 (or_3_out, Ecall2, and_20_out);
  or or_4 (RS2_Forward[1], Ecall3, and_21_out);
  or or_5 (or_5_out, Ecall4, and_24_out);
  and and_25 (RS1_Forward[0], ~RS1_Forward[1], or_3_out);  // AND_Gate
  and and_26 (RS2_Forward[0], ~RS2_Forward[1], or_5_out);  // AND_Gate
  or or_6 (Flush, Stall, BranchTaken);

  // Other names for the same wires on the sheet: RS1[4:0] = IR[19:15]; RS2[4:0] = IR[24:20]; LoadUse = Stall
endmodule

module BHB (
);

  wire and_17_out, and_18_out, and_19_out, and_28_out, and_29_out, and_30_out, and_31_out, and_32_out,
       and_33_out, and_34_out, and_35_out, BranchTaken, clk, comparator_1_eq, comparator_2_eq,
       comparator_3_eq, comparator_4_eq, comparator_5_eq, comparator_6_eq, comparator_7_eq, comparator_8_eq,
       comparator_9_eq, comparator_10_eq, comparator_11_eq, comparator_12_eq, comparator_13_eq,
       comparator_14_eq, comparator_15_eq, comparator_16_eq, d_ff_1_q, d_ff_2_q, d_ff_3_q, d_ff_4_q,
       d_ff_5_q, d_ff_6_q, d_ff_7_q, d_ff_8_q, decoder_1_out0, decoder_1_out1, decoder_1_out2,
       decoder_1_out3, decoder_1_out4, decoder_1_out5, decoder_1_out6, decoder_1_out7, demultiplexer_1_out0,
       demultiplexer_1_out1, demultiplexer_1_out2, demultiplexer_1_out3, demultiplexer_1_out4,
       demultiplexer_1_out5, demultiplexer_1_out6, demultiplexer_1_out7, EX_Branch, EX_Hit, EX_Miss,
       ID_PredictJump, L0, L1, L2, L3, L4, L5, L6, L7, M0, M1, M2, M3, M4, M5, M6, M7, not_1_out, not_2_out,
       not_3_out, not_4_out, not_5_out, not_6_out, not_7_out, not_8_out, or_1_out, or_2_out, or_3_out,
       or_4_out, or_5_out, or_6_out, or_7_out, or_8_out, or_9_out, or_10_out, or_12_out, or_13_out,
       or_14_out, or_15_out, or_16_out, or_17_out, or_18_out, or_19_out, priority_encoder_1_gs, v0, v1, v2,
       v3, v4, v5, v6, v7, Wirte0, Wirte1, Wirte2, Wirte3, Wirte4, Wirte5, Wirte6, Wirte7, Write0, Write1,
       Write2, Write3, Write4, Write5, Write6, Write7;
  wire [0:0] controlled_buffer_9_out, controlled_buffer_10_out, controlled_buffer_11_out,
       controlled_buffer_12_out, controlled_buffer_13_out, controlled_buffer_14_out,
       controlled_buffer_15_out, controlled_buffer_16_out;
  wire [1:0] fsm_1_nexthigh, fsm_2_nexthigh, fsm_3_nexthigh, fsm_4_nexthigh, fsm_5_nexthigh, fsm_6_nexthigh,
       fsm_7_nexthigh, fsm_8_nexthigh, Predict0, Predict1, Predict2, Predict3, Predict4, Predict5, Predict6,
       Predict7;
  wire [2:0] max_1_maxid, max_2_maxid, max_3_maxid, max_4_maxid, max_5_maxid, max_6_maxid, max_7_maxid,
       priority_encoder_1_out;
  wire [15:0] C0, C1, C2, C3, C4, C5, C6, C7, max_1_max, max_2_max, max_3_max, max_4_max, max_5_max,
       max_6_max;
  wire [31:0] EX_BranchAddr, EX_PC, IF_PC, JumpAddr, register_25_q, register_26_q, register_27_q,
       register_28_q, register_29_q, register_30_q, register_31_q, register_32_q, Tag, Tag0, Tag1, Tag2,
       Tag3, Tag4, Tag5, Tag6, Tag7;

  Register #(.width(1), .trigger("rising"), .Select("low")) register_1 (
    .D(1'b1), .en(Write0), .Q(v0), .clk(clk));  // open: clr
  Register #(.width(1), .trigger("rising"), .Select("low")) register_2 (
    .D(1'b1), .en(Write1), .Q(v1), .clk(clk));  // open: clr
  Register #(.width(1), .trigger("rising"), .Select("low")) register_3 (
    .D(1'b1), .en(Write2), .Q(v2), .clk(clk));  // open: clr
  Register #(.width(1), .trigger("rising"), .Select("low")) register_4 (
    .D(1'b1), .en(Write3), .Q(v3), .clk(clk));  // open: clr
  Register #(.width(1), .trigger("rising"), .Select("low")) register_5 (
    .D(1'b1), .en(Write4), .Q(v4), .clk(clk));  // open: clr
  Register #(.width(1), .trigger("rising"), .Select("low")) register_6 (
    .D(1'b1), .en(Write5), .Q(v5), .clk(clk));  // open: clr
  Register #(.width(1), .trigger("rising"), .Select("low")) register_7 (
    .D(1'b1), .en(Write6), .Q(v6), .clk(clk));  // open: clr
  Register #(.width(1), .trigger("rising"), .Select("low")) register_8 (
    .D(1'b1), .en(Write7), .Q(v7), .clk(clk));  // open: clr
  Register #(.width(32), .trigger("rising"), .Select("low")) register_9 (
    .D(Tag), .en(Write0), .Q(Tag0), .clk(clk));  // open: clr
  Register #(.width(32), .trigger("rising"), .Select("low")) register_10 (
    .D(Tag), .en(Write1), .Q(Tag1), .clk(clk));  // open: clr
  Register #(.width(32), .trigger("rising"), .Select("low")) register_11 (
    .D(Tag), .en(Write2), .Q(Tag2), .clk(clk));  // open: clr
  Register #(.width(32), .trigger("rising"), .Select("low")) register_12 (
    .D(Tag), .en(Write3), .Q(Tag3), .clk(clk));  // open: clr
  Register #(.width(32), .trigger("rising"), .Select("low")) register_13 (
    .D(Tag), .en(Write4), .Q(Tag4), .clk(clk));  // open: clr
  Register #(.width(32), .trigger("rising"), .Select("low")) register_14 (
    .D(Tag), .en(Write5), .Q(Tag5), .clk(clk));  // open: clr
  Register #(.width(32), .trigger("rising"), .Select("low")) register_15 (
    .D(Tag), .en(Write6), .Q(Tag6), .clk(clk));  // open: clr
  Register #(.width(32), .trigger("rising"), .Select("low")) register_16 (
    .D(Tag), .en(Write7), .Q(Tag7), .clk(clk));  // open: clr
  Register #(.width(16), .trigger("rising"), .Select("low")) register_17 (
    .en(Write0), .Q(C0), .clk(clk), .clr(d_ff_1_q));  // open: D
  or or_1 (or_1_out, Write0, L0);
  Register #(.width(16), .trigger("rising"), .Select("low")) register_18 (
    .en(Write1), .Q(C1), .clk(clk), .clr(d_ff_2_q));  // open: D
  or or_2 (or_2_out, Write1, L1);
  Register #(.width(16), .trigger("rising"), .Select("low")) register_19 (
    .en(Write2), .Q(C2), .clk(clk), .clr(d_ff_3_q));  // open: D
  or or_3 (or_3_out, Write2, L2);
  Register #(.width(16), .trigger("rising"), .Select("low")) register_20 (
    .en(Write3), .Q(C3), .clk(clk), .clr(d_ff_4_q));  // open: D
  or or_4 (or_4_out, Write3, L3);
  Register #(.width(16), .trigger("rising"), .Select("low")) register_21 (
    .en(Write4), .Q(C4), .clk(clk), .clr(d_ff_5_q));  // open: D
  or or_5 (or_5_out, Write4, L4);
  Register #(.width(16), .trigger("rising"), .Select("low")) register_22 (
    .en(Write5), .Q(C5), .clk(clk), .clr(d_ff_6_q));  // open: D
  or or_6 (or_6_out, Write5, L5);
  Register #(.width(16), .trigger("rising"), .Select("low")) register_23 (
    .en(Write6), .Q(C6), .clk(clk), .clr(d_ff_7_q));  // open: D
  or or_7 (or_7_out, Write6, L6);
  Register #(.width(16), .trigger("rising"), .Select("low")) register_24 (
    .en(Write7), .Q(C7), .clk(clk), .clr(d_ff_8_q));  // open: D
  or or_8 (or_8_out, Write7, L7);
  D_Flip_Flop #(.trigger("rising"), .Pre_Clr_Positions("ABOVE_BELOW"), .NegatePresetClear("false"), .enable("false"), .NewFFLayout("false")) d_ff_1 (
    .clk(clk), .D(or_1_out), .Q(d_ff_1_q));  // open: Qn, preset, reset
  D_Flip_Flop #(.trigger("rising"), .Pre_Clr_Positions("ABOVE_BELOW"), .NegatePresetClear("false"), .enable("false"), .NewFFLayout("false")) d_ff_2 (
    .clk(clk), .D(or_2_out), .Q(d_ff_2_q));  // open: Qn, preset, reset
  D_Flip_Flop #(.trigger("rising"), .Pre_Clr_Positions("ABOVE_BELOW"), .NegatePresetClear("false"), .enable("false"), .NewFFLayout("false")) d_ff_3 (
    .clk(clk), .D(or_3_out), .Q(d_ff_3_q));  // open: Qn, preset, reset
  D_Flip_Flop #(.trigger("rising"), .Pre_Clr_Positions("ABOVE_BELOW"), .NegatePresetClear("false"), .enable("false"), .NewFFLayout("false")) d_ff_4 (
    .clk(clk), .D(or_4_out), .Q(d_ff_4_q));  // open: Qn, preset, reset
  D_Flip_Flop #(.trigger("rising"), .Pre_Clr_Positions("ABOVE_BELOW"), .NegatePresetClear("false"), .enable("false"), .NewFFLayout("false")) d_ff_5 (
    .clk(clk), .D(or_5_out), .Q(d_ff_5_q));  // open: Qn, preset, reset
  D_Flip_Flop #(.trigger("rising"), .Pre_Clr_Positions("ABOVE_BELOW"), .NegatePresetClear("false"), .enable("false"), .NewFFLayout("false")) d_ff_6 (
    .clk(clk), .D(or_6_out), .Q(d_ff_6_q));  // open: Qn, preset, reset
  D_Flip_Flop #(.trigger("rising"), .Pre_Clr_Positions("ABOVE_BELOW"), .NegatePresetClear("false"), .enable("false"), .NewFFLayout("false")) d_ff_7 (
    .clk(clk), .D(or_7_out), .Q(d_ff_7_q));  // open: Qn, preset, reset
  D_Flip_Flop #(.trigger("rising"), .Pre_Clr_Positions("ABOVE_BELOW"), .NegatePresetClear("false"), .enable("false"), .NewFFLayout("false")) d_ff_8 (
    .clk(clk), .D(or_8_out), .Q(d_ff_8_q));  // open: Qn, preset, reset
  Register #(.width(32), .trigger("rising"), .Select("low")) register_25 (
    .D(EX_BranchAddr), .en(Write0), .Q(register_25_q), .clk(clk));  // open: clr
  Register #(.width(32), .trigger("rising"), .Select("low")) register_26 (
    .D(EX_BranchAddr), .en(Write1), .Q(register_26_q), .clk(clk));  // open: clr
  Register #(.width(32), .trigger("rising"), .Select("low")) register_27 (
    .D(EX_BranchAddr), .en(Write2), .Q(register_27_q), .clk(clk));  // open: clr
  Register #(.width(32), .trigger("rising"), .Select("low")) register_28 (
    .D(EX_BranchAddr), .en(Write3), .Q(register_28_q), .clk(clk));  // open: clr
  Register #(.width(32), .trigger("rising"), .Select("low")) register_29 (
    .D(EX_BranchAddr), .en(Write4), .Q(register_29_q), .clk(clk));  // open: clr
  Register #(.width(32), .trigger("rising"), .Select("low")) register_30 (
    .D(EX_BranchAddr), .en(Write5), .Q(register_30_q), .clk(clk));  // open: clr
  Register #(.width(32), .trigger("rising"), .Select("low")) register_31 (
    .D(EX_BranchAddr), .en(Write6), .Q(register_31_q), .clk(clk));  // open: clr
  Register #(.width(32), .trigger("rising"), .Select("low")) register_32 (
    .D(EX_BranchAddr), .en(Write7), .Q(register_32_q), .clk(clk));  // open: clr
  assign JumpAddr = L0 ? register_25_q : 32'bz;  // Controlled_Buffer controlled_buffer_1
  assign JumpAddr = L1 ? register_26_q : 32'bz;  // Controlled_Buffer controlled_buffer_2
  assign JumpAddr = L2 ? register_27_q : 32'bz;  // Controlled_Buffer controlled_buffer_3
  assign JumpAddr = L3 ? register_28_q : 32'bz;  // Controlled_Buffer controlled_buffer_4
  assign JumpAddr = L4 ? register_29_q : 32'bz;  // Controlled_Buffer controlled_buffer_5
  assign JumpAddr = L5 ? register_30_q : 32'bz;  // Controlled_Buffer controlled_buffer_6
  assign JumpAddr = L6 ? register_31_q : 32'bz;  // Controlled_Buffer controlled_buffer_7
  assign JumpAddr = L7 ? register_32_q : 32'bz;  // Controlled_Buffer controlled_buffer_8
  Comparator #(.width(32), .mode("twosComplement")) comparator_1 (
    .a(EX_PC), .b(Tag0), .eq(comparator_1_eq));  // open: gt, lt
  Comparator #(.width(32), .mode("twosComplement")) comparator_2 (
    .a(Tag0), .b(IF_PC), .eq(comparator_2_eq));  // open: gt, lt
  Comparator #(.width(32), .mode("twosComplement")) comparator_3 (
    .a(EX_PC), .b(Tag1), .eq(comparator_3_eq));  // open: gt, lt
  Comparator #(.width(32), .mode("twosComplement")) comparator_4 (
    .a(Tag1), .b(IF_PC), .eq(comparator_4_eq));  // open: gt, lt
  Comparator #(.width(32), .mode("twosComplement")) comparator_5 (
    .a(EX_PC), .b(Tag2), .eq(comparator_5_eq));  // open: gt, lt
  Comparator #(.width(32), .mode("twosComplement")) comparator_6 (
    .a(Tag2), .b(IF_PC), .eq(comparator_6_eq));  // open: gt, lt
  Comparator #(.width(32), .mode("twosComplement")) comparator_7 (
    .a(EX_PC), .b(Tag3), .eq(comparator_7_eq));  // open: gt, lt
  Comparator #(.width(32), .mode("twosComplement")) comparator_8 (
    .a(Tag3), .b(IF_PC), .eq(comparator_8_eq));  // open: gt, lt
  Comparator #(.width(32), .mode("twosComplement")) comparator_9 (
    .a(EX_PC), .b(Tag4), .eq(comparator_9_eq));  // open: gt, lt
  Comparator #(.width(32), .mode("twosComplement")) comparator_10 (
    .a(Tag4), .b(IF_PC), .eq(comparator_10_eq));  // open: gt, lt
  Comparator #(.width(32), .mode("twosComplement")) comparator_11 (
    .a(EX_PC), .b(Tag5), .eq(comparator_11_eq));  // open: gt, lt
  Comparator #(.width(32), .mode("twosComplement")) comparator_12 (
    .a(Tag5), .b(IF_PC), .eq(comparator_12_eq));  // open: gt, lt
  Comparator #(.width(32), .mode("twosComplement")) comparator_13 (
    .a(EX_PC), .b(Tag6), .eq(comparator_13_eq));  // open: gt, lt
  Comparator #(.width(32), .mode("twosComplement")) comparator_14 (
    .a(Tag6), .b(IF_PC), .eq(comparator_14_eq));  // open: gt, lt
  Comparator #(.width(32), .mode("twosComplement")) comparator_15 (
    .a(EX_PC), .b(Tag7), .eq(comparator_15_eq));  // open: gt, lt
  Comparator #(.width(32), .mode("twosComplement")) comparator_16 (
    .a(Tag7), .b(IF_PC), .eq(comparator_16_eq));  // open: gt, lt
  and and_1 (M0, comparator_1_eq, v0);
  and and_2 (L0, v0, comparator_2_eq);
  and and_3 (M1, comparator_3_eq, v1);
  and and_4 (L1, v1, comparator_4_eq);
  and and_5 (M2, comparator_5_eq, v2);
  and and_6 (L2, v2, comparator_6_eq);
  and and_7 (M3, comparator_7_eq, v3);
  and and_8 (L3, v3, comparator_8_eq);
  and and_9 (M4, comparator_9_eq, v4);
  and and_10 (L4, v4, comparator_10_eq);
  and and_11 (M5, comparator_11_eq, v5);
  and and_12 (L5, v5, comparator_12_eq);
  and and_13 (M6, comparator_13_eq, v6);
  and and_14 (L6, v6, comparator_14_eq);
  and and_15 (M7, comparator_15_eq, v7);
  and and_16 (L7, v7, comparator_16_eq);
  not not_1 (not_1_out, v0);
  not not_2 (not_2_out, v1);
  not not_3 (not_3_out, v2);
  not not_4 (not_4_out, v3);
  not not_5 (not_5_out, v4);
  not not_6 (not_6_out, v5);
  not not_7 (not_7_out, v6);
  not not_8 (not_8_out, v7);
  and and_17 (and_17_out, v0, v1, v2, v3);
  and and_18 (and_18_out, v4, v5, v6, v7);
  or or_9 (or_9_out, M0, M1, M2, M3);
  or or_10 (or_10_out, M4, M5, M6, M7);
  Priority_Encoder #(.select(3), .disabled("Z")) priority_encoder_1 (
    .in0(not_1_out), .in1(not_2_out), .in2(not_3_out), .in3(not_4_out), .in4(not_5_out), .in5(not_6_out),
    .in6(not_7_out), .in7(not_8_out), .out(priority_encoder_1_out), .gs(priority_encoder_1_gs));  // open: en_out, en_in
  and and_19 (and_19_out, and_17_out, and_18_out);
  MAX max_1 (.X(C0), .Y(C1), .Xid(3'b000), .Yid(3'b001), .MAX(max_1_max), .MAXID(max_1_maxid));
  MAX max_2 (.X(C2), .Y(C3), .Xid(3'b010), .Yid(3'b011), .MAX(max_2_max), .MAXID(max_2_maxid));
  MAX max_3 (.X(C4), .Y(C5), .Xid(3'b100), .Yid(3'b101), .MAX(max_3_max), .MAXID(max_3_maxid));
  MAX max_4 (.X(C6), .Y(C7), .Xid(3'b110), .Yid(3'b111), .MAX(max_4_max), .MAXID(max_4_maxid));
  or or_11 (EX_Hit, or_9_out, or_10_out);
  not not_9 (EX_Miss, EX_Hit);
  Decoder #(.select(3), .tristate("false"), .disabled(0), .enable("true")) decoder_1 (
    .out0(decoder_1_out0), .out1(decoder_1_out1), .out2(decoder_1_out2), .out3(decoder_1_out3),
    .out4(decoder_1_out4), .out5(decoder_1_out5), .out6(decoder_1_out6), .out7(decoder_1_out7),
    .sel(priority_encoder_1_out), .en(priority_encoder_1_gs));
  Demultiplexer #(.select(3), .width(1), .tristate("false"), .disabled(0), .enable("false")) demultiplexer_1 (
    .out0(demultiplexer_1_out0), .out1(demultiplexer_1_out1), .out2(demultiplexer_1_out2),
    .out3(demultiplexer_1_out3), .out4(demultiplexer_1_out4), .out5(demultiplexer_1_out5),
    .out6(demultiplexer_1_out6), .out7(demultiplexer_1_out7), .in(and_19_out), .sel(max_7_maxid));
  MAX max_5 (.X(max_1_max), .Y(max_2_max), .Xid(max_1_maxid), .Yid(max_2_maxid), .MAX(max_5_max), .MAXID(max_5_maxid));
  MAX max_6 (.X(max_3_max), .Y(max_4_max), .Xid(max_3_maxid), .Yid(max_4_maxid), .MAX(max_6_max), .MAXID(max_6_maxid));
  MAX max_7 (.X(max_5_max), .Y(max_6_max), .Xid(max_5_maxid), .Yid(max_6_maxid), .MAXID(max_7_maxid));  // open: MAX
  or or_12 (or_12_out, decoder_1_out0, demultiplexer_1_out0);
  or or_13 (or_13_out, decoder_1_out1, demultiplexer_1_out1);
  or or_14 (or_14_out, decoder_1_out2, demultiplexer_1_out2);
  or or_15 (or_15_out, decoder_1_out3, demultiplexer_1_out3);
  or or_16 (or_16_out, decoder_1_out4, demultiplexer_1_out4);
  or or_17 (or_17_out, decoder_1_out5, demultiplexer_1_out5);
  or or_18 (or_18_out, decoder_1_out6, demultiplexer_1_out6);
  or or_19 (or_19_out, decoder_1_out7, demultiplexer_1_out7);
  and and_20 (Wirte0, or_12_out, EX_Branch, EX_Miss);
  and and_21 (Wirte1, or_13_out, EX_Branch, EX_Miss);
  and and_22 (Wirte2, or_14_out, EX_Branch, EX_Miss);
  and and_23 (Wirte3, or_15_out, EX_Branch, EX_Miss);
  and and_24 (Wirte4, or_16_out, EX_Branch, EX_Miss);
  and and_25 (Wirte5, or_17_out, EX_Branch, EX_Miss);
  and and_26 (Wirte6, or_18_out, EX_Branch, EX_Miss);
  and and_27 (Wirte7, or_19_out, EX_Branch, EX_Miss);
  Pull_Resistor #(.pull(0)) pull_resistor_1 (.node(ID_PredictJump));
  assign {ID_PredictJump, controlled_buffer_9_out[0]} = L0 ? Predict0 : 2'bz;  // Controlled_Buffer controlled_buffer_9
  assign {ID_PredictJump, controlled_buffer_10_out[0]} = L1 ? Predict1 : 2'bz;  // Controlled_Buffer controlled_buffer_10
  assign {ID_PredictJump, controlled_buffer_11_out[0]} = L2 ? Predict2 : 2'bz;  // Controlled_Buffer controlled_buffer_11
  assign {ID_PredictJump, controlled_buffer_12_out[0]} = L3 ? Predict3 : 2'bz;  // Controlled_Buffer controlled_buffer_12
  assign {ID_PredictJump, controlled_buffer_13_out[0]} = L4 ? Predict4 : 2'bz;  // Controlled_Buffer controlled_buffer_13
  assign {ID_PredictJump, controlled_buffer_14_out[0]} = L5 ? Predict5 : 2'bz;  // Controlled_Buffer controlled_buffer_14
  assign {ID_PredictJump, controlled_buffer_15_out[0]} = L6 ? Predict6 : 2'bz;  // Controlled_Buffer controlled_buffer_15
  assign {ID_PredictJump, controlled_buffer_16_out[0]} = L7 ? Predict7 : 2'bz;  // Controlled_Buffer controlled_buffer_16
  FSM fsm_1 (
    .High(Predict0[1]), .Low(Predict0[0]), .Jump(BranchTaken), .NextHigh(fsm_1_nexthigh[0]),
    .NextLow(fsm_1_nexthigh[1]));
  FSM fsm_2 (
    .High(Predict1[1]), .Low(Predict1[0]), .Jump(BranchTaken), .NextHigh(fsm_2_nexthigh[0]),
    .NextLow(fsm_2_nexthigh[1]));
  FSM fsm_3 (
    .High(Predict2[1]), .Low(Predict2[0]), .Jump(BranchTaken), .NextHigh(fsm_3_nexthigh[0]),
    .NextLow(fsm_3_nexthigh[1]));
  and and_28 (and_28_out, EX_Branch, M0);
  and and_29 (and_29_out, EX_Branch, M1);
  and and_30 (and_30_out, EX_Branch, M2);
  and and_31 (and_31_out, EX_Branch, M3);
  FSM fsm_4 (
    .High(Predict3[1]), .Low(Predict3[0]), .Jump(BranchTaken), .NextHigh(fsm_4_nexthigh[0]),
    .NextLow(fsm_4_nexthigh[1]));
  and and_32 (and_32_out, EX_Branch, M4);
  FSM fsm_5 (
    .High(Predict4[1]), .Low(Predict4[0]), .Jump(BranchTaken), .NextHigh(fsm_5_nexthigh[0]),
    .NextLow(fsm_5_nexthigh[1]));
  and and_33 (and_33_out, EX_Branch, M5);
  FSM fsm_6 (
    .High(Predict5[1]), .Low(Predict5[0]), .Jump(BranchTaken), .NextHigh(fsm_6_nexthigh[0]),
    .NextLow(fsm_6_nexthigh[1]));
  and and_34 (and_34_out, EX_Branch, M6);
  FSM fsm_7 (
    .High(Predict6[1]), .Low(Predict6[0]), .Jump(BranchTaken), .NextHigh(fsm_7_nexthigh[0]),
    .NextLow(fsm_7_nexthigh[1]));
  and and_35 (and_35_out, EX_Branch, M7);
  FSM fsm_8 (
    .High(Predict7[1]), .Low(Predict7[0]), .Jump(BranchTaken), .NextHigh(fsm_8_nexthigh[0]),
    .NextLow(fsm_8_nexthigh[1]));
  Register #(.width(2), .trigger("rising"), .Select("low")) register_33 (
    .D(fsm_1_nexthigh), .en(and_28_out), .Q(Predict0), .clk(clk));  // open: clr
  Register #(.width(2), .trigger("rising"), .Select("low")) register_34 (
    .D(fsm_2_nexthigh), .en(and_29_out), .Q(Predict1), .clk(clk));  // open: clr
  Register #(.width(2), .trigger("rising"), .Select("low")) register_35 (
    .D(fsm_3_nexthigh), .en(and_30_out), .Q(Predict2), .clk(clk));  // open: clr
  Register #(.width(2), .trigger("rising"), .Select("low")) register_36 (
    .D(fsm_4_nexthigh), .en(and_31_out), .Q(Predict3), .clk(clk));  // open: clr
  Register #(.width(2), .trigger("rising"), .Select("low")) register_37 (
    .D(fsm_5_nexthigh), .en(and_32_out), .Q(Predict4), .clk(clk));  // open: clr
  Register #(.width(2), .trigger("rising"), .Select("low")) register_38 (
    .D(fsm_6_nexthigh), .en(and_33_out), .Q(Predict5), .clk(clk));  // open: clr
  Register #(.width(2), .trigger("rising"), .Select("low")) register_39 (
    .D(fsm_7_nexthigh), .en(and_34_out), .Q(Predict6), .clk(clk));  // open: clr
  Register #(.width(2), .trigger("rising"), .Select("low")) register_40 (
    .D(fsm_8_nexthigh), .en(and_35_out), .Q(Predict7), .clk(clk));  // open: clr
endmodule

module MAX (
  input  [15:0] X,
  input  [15:0] Y,
  input  [2:0] Xid,
  input  [2:0] Yid,
  output [15:0] MAX,
  output [2:0] MAXID
);

  wire comparator_1_eq, comparator_1_lt, or_1_out;

  Comparator #(.width(16), .mode("twosComplement")) comparator_1 (
    .a(X), .b(Y), .eq(comparator_1_eq), .lt(comparator_1_lt));  // open: gt
  Multiplexer #(.select(1), .width(16), .disabled("Z"), .enable("false")) multiplexer_1 (
    .in0(X), .in1(Y), .out(MAX), .sel(or_1_out));
  or or_1 (or_1_out, comparator_1_eq, comparator_1_lt);
  Multiplexer #(.select(1), .width(3), .disabled("Z"), .enable("false")) multiplexer_2 (
    .in0(Xid), .in1(Yid), .out(MAXID), .sel(or_1_out));
endmodule

module FSM (
  input  High,
  input  Low,
  input  Jump,
  output NextHigh,
  output NextLow
);

  wire and_1_out, and_2_out, and_3_out, and_4_out, not_1_out, not_2_out, not_3_out, not_4_out, not_5_out;

  not not_1 (not_1_out, Low);
  not not_2 (not_2_out, High);
  not not_3 (not_3_out, Low);
  not not_4 (not_4_out, Low);
  not not_5 (not_5_out, Jump);
  and and_1 (and_1_out, Low, Jump);
  and and_2 (and_2_out, High, not_1_out);
  and and_3 (and_3_out, not_2_out, not_3_out, Jump);
  and and_4 (and_4_out, High, not_4_out, not_5_out);
  or or_1 (NextHigh, and_1_out, and_2_out);
  or or_2 (NextLow, and_3_out, and_4_out);
endmodule
